// Logisim project cpu28_EX_branch.circ as structural Verilog: 28 circuits, main circuit ◇单周期MIPS
module \单周期MIPS  (
  input  IR1,
  input  IR2,
  input  IR3,
  output RegWrite,
  output MemWrite,
  output [31:0] PC,
  output [31:0] IR,
  output [31:0] RDin,
  output [31:0] MDin,
  output [31:0] LedData
);

  wire and_2_out, and_3_out, and_4_out, and_5_out, BLTZ, Branch, CLK, clock_2_out, comparator_1_eq,
       comparator_1_lt, comparator_2_lt, d_ff_1_q, en, Go, IR1_t, IR2_t, IR3_t, IRA, IRB, IRC, JAL, Led, LH,
       mips_alu_1_equal, nand_1_out, not_1_out, or_4_out, RegDst, register_2_q, SignedExt, SRAV, Syscall, W1,
       W2, W3, XORI, \单周期硬布线控制器_1_alu_src , \单周期硬布线控制器_1_beq , \单周期硬布线控制器_1_bne , \单周期硬布线控制器_1_jmp ,
       \单周期硬布线控制器_1_jr , \单周期硬布线控制器_1_memtoreg ;
  wire [3:0] \单周期硬布线控制器_1_alu_op ;
  wire [4:0] multiplexer_5_out, multiplexer_6_out, multiplexer_7_out, multiplexer_8_out, multiplexer_12_out;
  wire [12:0] CNT_num;
  wire [15:0] multiplexer_13_out, \总周期数 ;
  wire [31:0] adder_1_out, adder_2_out, bit_extender_1_out, bit_extender_2_out, bit_extender_3_out,
       bit_extender_4_out, mips_alu_1_result, multiplexer_1_out, multiplexer_2_out, multiplexer_3_out,
       multiplexer_4_out, multiplexer_10_out, multiplexer_11_out, multiplexer_14_out, multiplexer_15_out,
       ram_1_data, rs, shifter_1_out, shifter_2_out;

  Clock #(.highDuration(1), .lowDuration(1)) clock_1 ();  // open: out
  Button _1 (.out(IRA));
  Button _2 (.out(IRB));
  Button _3 (.out(IRC));
  Multiplexer #(.select(1), .width(32), .disabled("Z"), .enable("false")) multiplexer_1 (
    .in0(adder_1_out), .in1(adder_2_out), .out(multiplexer_1_out), .sel(or_4_out));
  Button \u_继续运行  (.out(Go));
  LED #(.active("true")) led_1 (.in(W1));
  LED #(.active("true")) led_2 (.in(W2));
  LED #(.active("true")) led_3 (.in(W3));
  Multiplexer #(.select(1), .width(32), .disabled("Z"), .enable("false")) multiplexer_2 (
    .in0(multiplexer_1_out), .in1(adder_2_out), .out(multiplexer_2_out), .sel(Branch));
  D_Flip_Flop #(.trigger("high"), .Pre_Clr_Positions("LEGACY"), .NegatePresetClear("false"), .enable("true"), .NewFFLayout("false")) d_ff_1 (.Q(d_ff_1_q));  // open: clk, D, Qn, preset, en, reset
  // Probe on 13'h5
  Hex_Digit_Display hex_digit_display_1 (.value(LedData[31:28]));  // open: dp
  Multiplexer #(.select(1), .width(32), .disabled("Z"), .enable("false")) multiplexer_3 (
    .in0(multiplexer_2_out), .in1(multiplexer_4_out), .out(multiplexer_3_out), .sel(\单周期硬布线控制器_1_jmp ));
  Multiplexer #(.select(1), .width(32), .disabled("Z"), .enable("false")) multiplexer_4 (
    .in0(shifter_2_out), .in1(rs), .out(multiplexer_4_out), .sel(\单周期硬布线控制器_1_jr ));
  Comparator #(.width(13), .mode("twosComplement")) comparator_1 (
    .a(CNT_num), .b(13'h5), .eq(comparator_1_eq), .lt(comparator_1_lt));  // open: gt
  Clock #(.highDuration(1), .lowDuration(1)) clock_2 (.out(clock_2_out));
  Hex_Digit_Display hex_digit_display_2 (.value(LedData[23:20]));  // open: dp
  Hex_Digit_Display hex_digit_display_3 (.value(LedData[27:24]));  // open: dp
  Register #(.width(32), .trigger("rising"), .Select("low")) u_PC (
    .D(multiplexer_3_out), .en(en), .Q(PC), .clk(CLK));  // open: clr
  nand nand_1 (nand_1_out, d_ff_1_q, comparator_1_eq);
  Counter #(.width(13), .max('h1fff), .ongoal("stay"), .trigger("rising"), .behavior("old")) counter_1 (
    .count(comparator_1_lt), .Q(CNT_num), .clk(clock_2_out));  // open: load, D, carry, clr, preset
  Hex_Digit_Display hex_digit_display_4 (.value(LedData[19:16]));  // open: dp
  Hex_Digit_Display hex_digit_display_5 (.value(LedData[15:12]));  // open: dp
  Adder #(.width(32)) adder_1 (.a(PC), .b(32'h4), .out(adder_1_out));  // open: cin, cout
  Comparator #(.width(32), .mode("twosComplement")) comparator_2 (
    .a(rs), .b({32{1'b0}}), .lt(comparator_2_lt));  // open: gt, eq
  assign CLK = nand_1_out ? clock_2_out : 1'bz;  // Controlled_Buffer controlled_buffer_1
  Hex_Digit_Display hex_digit_display_6 (.value(LedData[7:4]));  // open: dp
  Hex_Digit_Display hex_digit_display_7 (.value(LedData[11:8]));  // open: dp
  // Probe on \总周期数 
  // Mips_Probe mips_probe_1: pin names not known; wires that end beside it: IR
  ROM #(.addrWidth(10), .dataWidth(32), .Select("high")) rom_1 (.addr(PC[11:2]), .data(IR));
  and and_1 (Branch, comparator_2_lt, BLTZ);
  Pull_Resistor #(.pull(1)) pull_resistor_1 (.node(CLK));
  Hex_Digit_Display hex_digit_display_8 (.value(LedData[3:0]));  // open: dp
  Multiplexer #(.select(1), .width(5), .disabled("Z"), .enable("false")) multiplexer_5 (
    .in0(IR[25:21]), .in1(5'b00100), .out(multiplexer_5_out), .sel(Syscall));
  Multiplexer #(.select(1), .width(5), .disabled("Z"), .enable("false")) multiplexer_6 (
    .in0(IR[20:16]), .in1(5'b00010), .out(multiplexer_6_out), .sel(Syscall));
  Multiplexer #(.select(1), .width(5), .disabled("Z"), .enable("false")) multiplexer_7 (
    .in0(IR[20:16]), .in1(IR[15:11]), .out(multiplexer_7_out), .sel(RegDst));
  Counter #(.width(16), .max('hffff), .ongoal("wrap"), .trigger("rising"), .behavior("old")) counter_2 (
    .count(en), .Q(\总周期数 ), .clk(CLK));  // open: load, D, carry, clr, preset
  or or_1 (IR1_t, IR1, IRA);
  \单周期硬布线控制器  \u_单周期硬布线控制器_1  (
    .OP(IR[31:26]), .Func(IR[5:0]), .ALU_OP(\单周期硬布线控制器_1_alu_op ), .MemToReg(\单周期硬布线控制器_1_memtoreg ),
    .MemWrite(MemWrite), .BLTZ(BLTZ), .LH(LH), .SRAV(SRAV), .XORI(XORI), .ALU_SRC(\单周期硬布线控制器_1_alu_src ),
    .RegWrite(RegWrite), .SysCALL(Syscall), .SignedExt(SignedExt), .RegDst(RegDst), .Beq(\单周期硬布线控制器_1_beq ),
    .Bne(\单周期硬布线控制器_1_bne ), .JR(\单周期硬布线控制器_1_jr ), .JMP(\单周期硬布线控制器_1_jmp ), .JAL(JAL));
  Multiplexer #(.select(1), .width(5), .disabled("Z"), .enable("false")) multiplexer_8 (
    .in0(multiplexer_7_out), .in1({5{1'b1}}), .out(multiplexer_8_out), .sel(JAL));
  Multiplexer #(.select(1), .width(32), .disabled("Z"), .enable("false")) multiplexer_9 (
    .in0(multiplexer_14_out), .in1(adder_1_out), .out(RDin), .sel(JAL));
  or or_2 (IR2_t, IR2, IRB);
  and and_2 (and_2_out, Syscall, Led);
  assign bit_extender_1_out = {{16{1'b0}}, IR[15:0]};  // Bit_Extender bit_extender_1
  assign bit_extender_2_out = {{16{IR[15]}}, IR[15:0]};  // Bit_Extender bit_extender_2
  assign bit_extender_3_out = {{6{IR[25]}}, IR[25:0]};  // Bit_Extender bit_extender_3
  and and_3 (and_3_out, \单周期硬布线控制器_1_beq , mips_alu_1_equal);
  Register #(.width(32), .trigger("rising"), .Select("low")) register_1 (
    .D(rs), .en(and_2_out), .Q(LedData), .clk(CLK));  // open: clr
  \MIPS_Regfile_上升沿  \mips_regfile_上升沿_1  (
    .Din(RDin), .Clk(CLK), .R1(rs), .R2(MDin), .WE(RegWrite), .W_num(multiplexer_8_out),
    .R1_num(multiplexer_5_out), .R2_num(multiplexer_6_out));
  Multiplexer #(.select(1), .width(32), .disabled("Z"), .enable("false")) multiplexer_10 (
    .in0(bit_extender_1_out), .in1(bit_extender_2_out), .out(multiplexer_10_out), .sel(SignedExt));
  or or_3 (IR3_t, IR3, IRC);
  Multiplexer #(.select(1), .width(32), .disabled("Z"), .enable("false")) multiplexer_11 (
    .in0(MDin), .in1(multiplexer_10_out), .out(multiplexer_11_out), .sel(\单周期硬布线控制器_1_alu_src ));
  Comparator #(.width(32), .mode("twosComplement")) comparator_3 (.a(32'h22), .b(MDin), .eq(Led));  // open: gt, lt
  and and_4 (and_4_out, ~mips_alu_1_equal, \单周期硬布线控制器_1_bne );  // AND_Gate
  MIPS_ALU mips_alu_1 (
    .X(rs), .Y(multiplexer_11_out), .AluOP(\单周期硬布线控制器_1_alu_op ), .Equal(mips_alu_1_equal),
    .Result(mips_alu_1_result), .shamt(multiplexer_12_out));  // open: Result_2
  not not_1 (not_1_out, Led);
  Shifter #(.width(32), .shift("ll")) shifter_1 (.in(multiplexer_10_out), .\dist (5'b00010), .out(shifter_1_out));
  Shifter #(.width(32), .shift("ll")) shifter_2 (.in(bit_extender_3_out), .\dist (5'b00010), .out(shifter_2_out));
  Multiplexer #(.select(1), .width(5), .disabled("Z"), .enable("false")) multiplexer_12 (
    .in0(IR[10:6]), .in1(rs[4:0]), .out(multiplexer_12_out), .sel(SRAV));
  and and_5 (and_5_out, Syscall, not_1_out);
  Adder #(.width(32)) adder_2 (.a(shifter_1_out), .b(adder_1_out), .out(adder_2_out));  // open: cin, cout
  or or_4 (or_4_out, and_3_out, and_4_out);
  Register #(.width(1), .trigger("rising"), .Select("low")) register_2 (
    .D(Syscall), .en(and_5_out), .Q(register_2_q), .clk(CLK), .clr(Go));
  not not_2 (en, register_2_q);
  Multiplexer #(.select(1), .width(16), .disabled("Z"), .enable("false")) multiplexer_13 (
    .in0(ram_1_data[15:0]), .in1(ram_1_data[31:16]), .out(multiplexer_13_out), .sel(mips_alu_1_result[1]));
  RAM #(.addrWidth(10), .dataWidth(32), .bus("separate"), .Select("high")) ram_1 (
    .addr(mips_alu_1_result[11:2]), .din(MDin), .data(ram_1_data), .str(MemWrite), .clk(CLK), .ld(1'b1));  // open: sel, clr
  assign bit_extender_4_out = {{16{multiplexer_13_out[15]}}, multiplexer_13_out};  // Bit_Extender bit_extender_4
  Multiplexer #(.select(1), .width(32), .disabled("Z"), .enable("false")) multiplexer_14 (
    .in0(mips_alu_1_result), .in1(multiplexer_15_out), .out(multiplexer_14_out), .sel(\单周期硬布线控制器_1_memtoreg ));
  Multiplexer #(.select(1), .width(32), .disabled("Z"), .enable("false")) multiplexer_15 (
    .in0(ram_1_data), .in1(bit_extender_4_out), .out(multiplexer_15_out), .sel(LH));

  // Notes on the sheet:
  //   中断源
  //   控制位
  //   中断等待指示
  //   总复位信号应将除ROM以外所有存储组件全部清零
  //   暂停节拍，不能为0
  //   戳工具置1进入计数暂停模式，ctrl+k时钟自动运行到对应节拍暂停
  //   数码管输出
  //   指令存储器
  //   可计数暂停的时钟源
  //   数码管输出应该用寄存器锁存，否则显示数据只能一闪而过
  //   指令字
  //   contents of rom_1 (hex, n*v repeats v):
  //   20110001 8000c05 20110001 20120002 20130003 8000c09 20110001 20120002 20130003 8000c0d 20110001
  //   20120002 20130003 8000c11 20110001 20120002 20130003 c000cf7 20100001 20110001 118fc0 112020
  //   20020022 c 118882 12200001 8000c15 112020 20020022 c 20110001 118880 112020 20020022 c 12200001
  //   8000c1f 20110001 118fc0 112020 20020022 c 1188c3 112020 20020022 c 118903 112020 20020022 c 118903
  //   112020 20020022 c 118903 112020 20020022 c 118903 112020 20020022 c 118903 112020 20020022 c 118903
  //   112020 20020022 c 118903 112020 20020022 c 20100001 109fc0 139fc3 8021 2012000c 24160003 26100001
  //   3210000f 20080008 20090001 139900 2709825 132020 20020022 c 1094022 1500fff9 22100001 2018000f
  //   2188024 108700 20080008 20090001 139902 2709825 132021 20020022 c 1094022 1500fff9 108702 2c9b022
  //   12c00001 8000c50 4020 1084027 84400 3508ffff 82021 20020022 c 2010ffff 20110000 ae300000 22100001
  //   22310004 ae300000 22100001 22310004 ae300000 22100001 22310004 ae300000 22100001 22310004 ae300000
  //   22100001 22310004 ae300000 22100001 22310004 ae300000 22100001 22310004 ae300000 22100001 22310004
  //   ae300000 22100001 22310004 ae300000 22100001 22310004 ae300000 22100001 22310004 ae300000 22100001
  //   22310004 ae300000 22100001 22310004 ae300000 22100001 22310004 ae300000 22100001 22310004 ae300000
  //   22100001 22310004 22100001 8020 2011003c 8e130000 8e340000 274402a 11000002 ae330000 ae140000
  //   2231fffc 1611fff8 102020 20020022 c 22100004 2011003c 1611fff2 20020032 c 20080001 20090003 20110876
  //   118d00 112020 20020022 c 200b0008 1118807 1318807 112020 20020022 c 216bffff 1560fff9 2002000a c
  //   2008ffff 20117777 112020 20020022 c 200b0010 3a31ffff 112020 20020022 c 216bffff 1560fffa 2002000a c
  //   20090000 200b0010 34118483 20120404 118c00 129400 36318281 22520404 ad310000 2328820 21290004
  //   216bffff 1560fffb 200b0020 20090000 85310000 112020 20020022 c 21290002 216bffff 1560fff9 2002000a c
  //   2011fff1 112020 20020022 c 22310001 620fffb 2002000a c 20100000 22100001 102020 20020022 c 22100002
  //   102020 20020022 c 22100003 102020 20020022 c 22100004 102020 20020022 c 22100005 102020 20020022 c
  //   22100006 102020 20020022 c 22100007 102020 20020022 c 22100008 102020 20020022 20020022 c 3e00008
  //   OP
  //   Func
  //   rs
  //   rt
  //   rd
  //   imm
  //   shamt
  //   JMP
  //   JR
  //   OP
  //   Func
  //   SysCALL
  //   Beq
  //   Bne
  //   AluOP
  //   AluSrcB
  //   RegWrite
  //   JAL
  //   RegDst
  //   MemToReg
  //   MemWrite
  //   为方便自动评测，需要输出PC，IR，寄存器堆写如数据RDin
  //   RAM写使能MemWrite、RAM写入数据MDin等信号
endmodule

// 单周期硬布线控制器
module \单周期硬布线控制器  (
  input  [5:0] OP,
  input  [5:0] Func,
  output [3:0] ALU_OP,
  output MemToReg,
  output MemWrite,
  output BLTZ,
  output LH,
  output SRAV,
  output XORI,
  output ALU_SRC,
  output RegWrite,
  output SysCALL,
  output SignedExt,
  output RegDst,
  output Beq,
  output Bne,
  output JR,
  output JMP,
  output JAL
);

  \运算控制器自动生成  \u_运算控制器自动生成_1  (
    .OP0(OP[0]), .OP1(OP[1]), .OP2(OP[2]), .OP3(OP[3]), .OP4(OP[4]), .OP5(OP[5]), .F0(Func[0]), .F1(Func[1]),
    .F2(Func[2]), .F3(Func[3]), .F4(Func[4]), .F5(Func[5]), .S0(ALU_OP[0]), .S1(ALU_OP[1]), .S2(ALU_OP[2]),
    .S3(ALU_OP[3]));
  \控制信号自动生成  \u_控制信号自动生成_1  (
    .OP0(OP[0]), .OP1(OP[1]), .OP2(OP[2]), .OP3(OP[3]), .OP4(OP[4]), .OP5(OP[5]), .F0(Func[0]), .F1(Func[1]),
    .F2(Func[2]), .F3(Func[3]), .F4(Func[4]), .F5(Func[5]), .MemToReg(MemToReg), .MemWrite(MemWrite),
    .BLTZ(BLTZ), .LH(LH), .SRAV(SRAV), .XORI(XORI), .ALU_SRC(ALU_SRC), .RegWrite(RegWrite),
    .SysCALL(SysCALL), .SignedExt(SignedExt), .RegDst(RegDst), .BEQ(Beq), .BNE(Bne), .JR(JR), .JUMP(JMP),
    .JAL(JAL));

  // Other names for the same wires on the sheet: OP_CODE[5:0] = OP

  // Notes on the sheet:
  //   运算器控制器，根据指令生成运算器功能选择信号
  //   控制信号生成，产生数据通路需要的其他控制信号
endmodule

// 运算器控制器
module \运算控制器自动生成  (
  input  OP0,
  input  OP1,
  input  OP2,
  input  OP3,
  input  OP4,
  input  OP5,
  input  F0,
  input  F1,
  input  F2,
  input  F3,
  input  F4,
  input  F5,
  output S0,
  output S1,
  output S2,
  output S3
);

  wire and_1_out, and_2_out, and_3_out, and_4_out, and_5_out, and_6_out, and_7_out, and_8_out, and_9_out,
       and_10_out, and_11_out, and_12_out, and_13_out, and_14_out, and_15_out, and_16_out, and_17_out,
       and_18_out, and_19_out, and_20_out, and_21_out, and_22_out, and_23_out, and_24_out, and_25_out,
       and_26_out, and_27_out, and_28_out, and_29_out, and_30_out, and_31_out, and_32_out, and_33_out,
       and_34_out, and_35_out, and_36_out, and_37_out, and_38_out, and_39_out, not_1_out, not_2_out,
       not_3_out, not_4_out, not_5_out, not_6_out, not_7_out, not_8_out, not_9_out, not_10_out, not_11_out,
       not_12_out, not_13_out, not_14_out, not_15_out, not_16_out, not_17_out, not_18_out, not_19_out,
       not_20_out, not_21_out, not_22_out, not_23_out, not_24_out, not_25_out, not_26_out, not_27_out,
       not_28_out, not_29_out, not_30_out, not_31_out, not_32_out, not_33_out, not_34_out, not_35_out,
       not_36_out, not_37_out, not_38_out, not_39_out, not_40_out, not_41_out, not_42_out, not_43_out,
       not_44_out, not_45_out, not_46_out, not_47_out, not_48_out, not_49_out, not_50_out, not_51_out,
       not_52_out, not_53_out, not_54_out, not_55_out, not_56_out, not_57_out, not_58_out, not_59_out,
       not_60_out, not_61_out, not_62_out, not_63_out, not_64_out, not_65_out, not_66_out, not_67_out,
       not_68_out, not_69_out, not_70_out, not_71_out, not_72_out, not_73_out, not_74_out, not_75_out,
       not_76_out, not_77_out, not_78_out, not_79_out, not_80_out, not_81_out, not_82_out, not_83_out,
       not_84_out, not_85_out, not_86_out, not_87_out, not_88_out, not_89_out, not_90_out, not_91_out,
       not_92_out, not_93_out, not_94_out, not_95_out, not_96_out, not_97_out, not_98_out, not_99_out,
       not_100_out, not_101_out, not_102_out, not_103_out, not_104_out, not_105_out, not_106_out,
       not_107_out, not_108_out, not_109_out, not_110_out, not_111_out, not_112_out, not_113_out,
       not_114_out, not_115_out, not_116_out, not_117_out, not_118_out, not_119_out, not_120_out,
       not_121_out, not_122_out, not_123_out, not_124_out, not_125_out, not_126_out, not_127_out,
       not_128_out, not_129_out, not_130_out, not_131_out, not_132_out, not_133_out, not_134_out,
       not_135_out, not_136_out, not_137_out, not_138_out, not_139_out, not_140_out, not_141_out,
       not_142_out, not_143_out, not_144_out, not_145_out, not_146_out, not_147_out, not_148_out,
       not_149_out, not_150_out, not_151_out, not_152_out, not_153_out, not_154_out, not_155_out,
       not_156_out, not_157_out, not_158_out, not_159_out, not_160_out, not_161_out, not_162_out,
       not_163_out, not_164_out, not_165_out, not_166_out, not_167_out, not_168_out, not_169_out,
       not_170_out, not_171_out, not_172_out, not_173_out, not_174_out, not_175_out, not_176_out,
       not_177_out, not_178_out, not_179_out, not_180_out, not_181_out, not_182_out, not_183_out,
       not_184_out, not_185_out, not_186_out, not_187_out, not_188_out, not_189_out, not_190_out,
       not_191_out, not_192_out, not_193_out, not_194_out, not_195_out, not_196_out, not_197_out,
       not_198_out, not_199_out, not_200_out, not_201_out, not_202_out, not_203_out, not_204_out,
       not_205_out, not_206_out, not_207_out, not_208_out, not_209_out, not_210_out, not_211_out,
       not_212_out, not_213_out, not_214_out, not_215_out, not_216_out, not_217_out, not_218_out,
       not_219_out, not_220_out, not_221_out, not_222_out, not_223_out, not_224_out, not_225_out,
       not_226_out, not_227_out, not_228_out, not_229_out, not_230_out, not_231_out, not_232_out,
       not_233_out, not_234_out, not_235_out, not_236_out, not_237_out, not_238_out, not_239_out,
       not_240_out, not_241_out, not_242_out, not_243_out, not_244_out, not_245_out, not_246_out,
       not_247_out, not_248_out, not_249_out, not_250_out, not_251_out, not_252_out, not_253_out,
       not_254_out, not_255_out, not_256_out, not_257_out, not_258_out, not_259_out;

  not not_1 (not_1_out, OP5);
  not not_2 (not_2_out, OP4);
  not not_3 (not_3_out, OP3);
  not not_4 (not_4_out, OP2);
  not not_5 (not_5_out, OP1);
  not not_6 (not_6_out, OP0);
  not not_7 (not_7_out, F5);
  not not_8 (not_8_out, F4);
  not not_9 (not_9_out, F3);
  not not_10 (not_10_out, F2);
  not not_11 (not_11_out, OP5);
  not not_12 (not_12_out, OP4);
  not not_13 (not_13_out, OP3);
  not not_14 (not_14_out, OP2);
  not not_15 (not_15_out, OP1);
  not not_16 (not_16_out, OP0);
  not not_17 (not_17_out, F4);
  not not_18 (not_18_out, F3);
  not not_19 (not_19_out, F2);
  not not_20 (not_20_out, F1);
  not not_21 (not_21_out, F0);
  not not_22 (not_22_out, OP5);
  not not_23 (not_23_out, OP4);
  not not_24 (not_24_out, OP3);
  not not_25 (not_25_out, OP2);
  not not_26 (not_26_out, OP1);
  not not_27 (not_27_out, OP0);
  not not_28 (not_28_out, F4);
  not not_29 (not_29_out, F3);
  not not_30 (not_30_out, F2);
  not not_31 (not_31_out, F1);
  not not_32 (not_32_out, OP5);
  not not_33 (not_33_out, OP4);
  not not_34 (not_34_out, OP3);
  not not_35 (not_35_out, OP2);
  not not_36 (not_36_out, OP1);
  not not_37 (not_37_out, OP0);
  not not_38 (not_38_out, F4);
  not not_39 (not_39_out, F3);
  not not_40 (not_40_out, F1);
  not not_41 (not_41_out, F0);
  not not_42 (not_42_out, OP5);
  not not_43 (not_43_out, OP4);
  not not_44 (not_44_out, OP3);
  not not_45 (not_45_out, OP2);
  not not_46 (not_46_out, OP1);
  not not_47 (not_47_out, OP0);
  not not_48 (not_48_out, F4);
  not not_49 (not_49_out, F2);
  not not_50 (not_50_out, F0);
  not not_51 (not_51_out, OP5);
  not not_52 (not_52_out, OP4);
  not not_53 (not_53_out, OP2);
  not not_54 (not_54_out, OP1);
  not not_55 (not_55_out, OP0);
  not not_56 (not_56_out, OP5);
  not not_57 (not_57_out, OP4);
  not not_58 (not_58_out, OP1);
  not not_59 (not_59_out, OP0);
  not not_60 (not_60_out, OP5);
  not not_61 (not_61_out, OP4);
  not not_62 (not_62_out, OP2);
  not not_63 (not_63_out, OP1);
  not not_64 (not_64_out, OP5);
  not not_65 (not_65_out, OP4);
  not not_66 (not_66_out, OP2);
  not not_67 (not_67_out, OP0);
  not not_68 (not_68_out, OP4);
  not not_69 (not_69_out, OP3);
  not not_70 (not_70_out, OP2);
  not not_71 (not_71_out, OP4);
  not not_72 (not_72_out, OP2);
  not not_73 (not_73_out, OP5);
  not not_74 (not_74_out, OP4);
  not not_75 (not_75_out, OP3);
  not not_76 (not_76_out, OP2);
  not not_77 (not_77_out, OP1);
  not not_78 (not_78_out, OP0);
  not not_79 (not_79_out, F5);
  not not_80 (not_80_out, F4);
  not not_81 (not_81_out, F3);
  not not_82 (not_82_out, OP5);
  not not_83 (not_83_out, OP4);
  not not_84 (not_84_out, OP0);
  not not_85 (not_85_out, OP4);
  not not_86 (not_86_out, OP3);
  not not_87 (not_87_out, OP2);
  not not_88 (not_88_out, OP1);
  not not_89 (not_89_out, OP5);
  not not_90 (not_90_out, OP4);
  not not_91 (not_91_out, OP3);
  not not_92 (not_92_out, OP2);
  not not_93 (not_93_out, OP1);
  not not_94 (not_94_out, OP0);
  not not_95 (not_95_out, F5);
  not not_96 (not_96_out, F4);
  not not_97 (not_97_out, F3);
  not not_98 (not_98_out, F2);
  not not_99 (not_99_out, F0);
  not not_100 (not_100_out, OP5);
  not not_101 (not_101_out, OP4);
  not not_102 (not_102_out, OP3);
  not not_103 (not_103_out, OP2);
  not not_104 (not_104_out, OP1);
  not not_105 (not_105_out, OP0);
  not not_106 (not_106_out, F4);
  not not_107 (not_107_out, F3);
  not not_108 (not_108_out, F2);
  not not_109 (not_109_out, F0);
  not not_110 (not_110_out, OP5);
  not not_111 (not_111_out, OP4);
  not not_112 (not_112_out, OP3);
  not not_113 (not_113_out, OP2);
  not not_114 (not_114_out, OP1);
  not not_115 (not_115_out, OP0);
  not not_116 (not_116_out, F4);
  not not_117 (not_117_out, F3);
  not not_118 (not_118_out, F1);
  not not_119 (not_119_out, F0);
  not not_120 (not_120_out, OP5);
  not not_121 (not_121_out, OP4);
  not not_122 (not_122_out, OP3);
  not not_123 (not_123_out, OP2);
  not not_124 (not_124_out, OP1);
  not not_125 (not_125_out, OP0);
  not not_126 (not_126_out, F4);
  not not_127 (not_127_out, F3);
  not not_128 (not_128_out, OP5);
  not not_129 (not_129_out, OP4);
  not not_130 (not_130_out, OP3);
  not not_131 (not_131_out, OP2);
  not not_132 (not_132_out, OP1);
  not not_133 (not_133_out, OP0);
  not not_134 (not_134_out, F4);
  not not_135 (not_135_out, F2);
  not not_136 (not_136_out, F0);
  not not_137 (not_137_out, OP5);
  not not_138 (not_138_out, OP4);
  not not_139 (not_139_out, OP1);
  not not_140 (not_140_out, OP0);
  not not_141 (not_141_out, OP5);
  not not_142 (not_142_out, OP4);
  not not_143 (not_143_out, OP2);
  not not_144 (not_144_out, OP0);
  not not_145 (not_145_out, OP5);
  not not_146 (not_146_out, OP4);
  not not_147 (not_147_out, OP3);
  not not_148 (not_148_out, OP2);
  not not_149 (not_149_out, OP1);
  not not_150 (not_150_out, OP0);
  not not_151 (not_151_out, F4);
  not not_152 (not_152_out, F3);
  not not_153 (not_153_out, F2);
  not not_154 (not_154_out, F1);
  not not_155 (not_155_out, F0);
  not not_156 (not_156_out, OP5);
  not not_157 (not_157_out, OP4);
  not not_158 (not_158_out, OP3);
  not not_159 (not_159_out, OP2);
  not not_160 (not_160_out, OP1);
  not not_161 (not_161_out, OP0);
  not not_162 (not_162_out, F4);
  not not_163 (not_163_out, F3);
  not not_164 (not_164_out, F2);
  not not_165 (not_165_out, F1);
  not not_166 (not_166_out, OP5);
  not not_167 (not_167_out, OP4);
  not not_168 (not_168_out, OP3);
  not not_169 (not_169_out, OP2);
  not not_170 (not_170_out, OP1);
  not not_171 (not_171_out, OP0);
  not not_172 (not_172_out, F4);
  not not_173 (not_173_out, F3);
  not not_174 (not_174_out, F2);
  not not_175 (not_175_out, F0);
  not not_176 (not_176_out, OP5);
  not not_177 (not_177_out, OP4);
  not not_178 (not_178_out, OP3);
  not not_179 (not_179_out, OP2);
  not not_180 (not_180_out, OP1);
  not not_181 (not_181_out, OP0);
  not not_182 (not_182_out, F4);
  not not_183 (not_183_out, F3);
  not not_184 (not_184_out, F1);
  not not_185 (not_185_out, F0);
  not not_186 (not_186_out, OP5);
  not not_187 (not_187_out, OP4);
  not not_188 (not_188_out, OP3);
  not not_189 (not_189_out, OP2);
  not not_190 (not_190_out, OP1);
  not not_191 (not_191_out, OP0);
  not not_192 (not_192_out, F4);
  not not_193 (not_193_out, F2);
  not not_194 (not_194_out, OP5);
  not not_195 (not_195_out, OP4);
  not not_196 (not_196_out, OP2);
  not not_197 (not_197_out, OP1);
  not not_198 (not_198_out, OP0);
  not not_199 (not_199_out, OP5);
  not not_200 (not_200_out, OP4);
  not not_201 (not_201_out, OP1);
  not not_202 (not_202_out, OP0);
  not not_203 (not_203_out, OP5);
  not not_204 (not_204_out, OP4);
  not not_205 (not_205_out, OP2);
  not not_206 (not_206_out, OP1);
  not not_207 (not_207_out, OP4);
  not not_208 (not_208_out, OP3);
  not not_209 (not_209_out, OP2);
  not not_210 (not_210_out, OP4);
  not not_211 (not_211_out, OP2);
  not not_212 (not_212_out, OP4);
  not not_213 (not_213_out, OP3);
  not not_214 (not_214_out, OP2);
  not not_215 (not_215_out, OP1);
  not not_216 (not_216_out, OP5);
  not not_217 (not_217_out, OP4);
  not not_218 (not_218_out, OP3);
  not not_219 (not_219_out, OP2);
  not not_220 (not_220_out, OP1);
  not not_221 (not_221_out, OP0);
  not not_222 (not_222_out, F4);
  not not_223 (not_223_out, F3);
  not not_224 (not_224_out, F1);
  not not_225 (not_225_out, OP5);
  not not_226 (not_226_out, OP4);
  not not_227 (not_227_out, OP3);
  not not_228 (not_228_out, OP2);
  not not_229 (not_229_out, OP1);
  not not_230 (not_230_out, OP0);
  not not_231 (not_231_out, F4);
  not not_232 (not_232_out, F3);
  not not_233 (not_233_out, OP5);
  not not_234 (not_234_out, OP4);
  not not_235 (not_235_out, OP3);
  not not_236 (not_236_out, OP2);
  not not_237 (not_237_out, OP1);
  not not_238 (not_238_out, OP0);
  not not_239 (not_239_out, F4);
  not not_240 (not_240_out, F2);
  not not_241 (not_241_out, F0);
  not not_242 (not_242_out, OP5);
  not not_243 (not_243_out, OP4);
  not not_244 (not_244_out, OP3);
  not not_245 (not_245_out, OP2);
  not not_246 (not_246_out, OP1);
  not not_247 (not_247_out, OP0);
  not not_248 (not_248_out, F4);
  not not_249 (not_249_out, F2);
  not not_250 (not_250_out, OP5);
  not not_251 (not_251_out, OP4);
  not not_252 (not_252_out, OP2);
  not not_253 (not_253_out, OP0);
  not not_254 (not_254_out, OP5);
  not not_255 (not_255_out, OP4);
  not not_256 (not_256_out, OP1);
  not not_257 (not_257_out, OP5);
  not not_258 (not_258_out, OP4);
  not not_259 (not_259_out, OP0);
  and and_1 (and_1_out, not_1_out, not_2_out, not_3_out, not_4_out, not_5_out, not_6_out, not_7_out, not_8_out, not_9_out, not_10_out, F1, F0);
  and and_2 (and_2_out, not_11_out, not_12_out, not_13_out, not_14_out, not_15_out, not_16_out, F5, not_17_out, not_18_out, not_19_out, not_20_out, not_21_out);
  and and_3 (and_3_out, not_22_out, not_23_out, not_24_out, not_25_out, not_26_out, not_27_out, F5, not_28_out, not_29_out, not_30_out, not_31_out, F0);
  and and_4 (and_4_out, not_32_out, not_33_out, not_34_out, not_35_out, not_36_out, not_37_out, F5, not_38_out, not_39_out, F2, not_40_out, not_41_out);
  and and_5 (and_5_out, not_42_out, not_43_out, not_44_out, not_45_out, not_46_out, not_47_out, F5, not_48_out, F3, not_49_out, F1, not_50_out);
  and and_6 (and_6_out, not_51_out, not_52_out, OP3, not_53_out, not_54_out, not_55_out);
  and and_7 (and_7_out, not_56_out, not_57_out, OP3, OP2, not_58_out, not_59_out);
  and and_8 (and_8_out, not_60_out, not_61_out, OP3, not_62_out, not_63_out, OP0);
  and and_9 (and_9_out, not_64_out, not_65_out, OP3, not_66_out, OP1, not_67_out);
  and and_10 (and_10_out, OP5, not_68_out, not_69_out, not_70_out, OP1, OP0);
  and and_11 (and_11_out, OP5, not_71_out, OP3, not_72_out, OP1, OP0);
  and and_12 (and_12_out, not_73_out, not_74_out, not_75_out, not_76_out, not_77_out, not_78_out, not_79_out, not_80_out, not_81_out, F2, F1, F0);
  and and_13 (and_13_out, not_82_out, not_83_out, OP3, OP2, OP1, not_84_out);
  and and_14 (and_14_out, OP5, not_85_out, not_86_out, not_87_out, not_88_out, OP0);
  and and_15 (and_15_out, not_89_out, not_90_out, not_91_out, not_92_out, not_93_out, not_94_out, not_95_out, not_96_out, not_97_out, not_98_out, F1, not_99_out);
  and and_16 (and_16_out, not_100_out, not_101_out, not_102_out, not_103_out, not_104_out, not_105_out, F5, not_106_out, not_107_out, not_108_out, F1, not_109_out);
  and and_17 (and_17_out, not_110_out, not_111_out, not_112_out, not_113_out, not_114_out, not_115_out, F5, not_116_out, not_117_out, F2, not_118_out, not_119_out);
  and and_18 (and_18_out, not_120_out, not_121_out, not_122_out, not_123_out, not_124_out, not_125_out, F5, not_126_out, not_127_out, F2, F1, F0);
  and and_19 (and_19_out, not_128_out, not_129_out, not_130_out, not_131_out, not_132_out, not_133_out, F5, not_134_out, F3, not_135_out, F1, not_136_out);
  and and_20 (and_20_out, not_137_out, not_138_out, OP3, OP2, not_139_out, not_140_out);
  and and_21 (and_21_out, not_141_out, not_142_out, OP3, not_143_out, OP1, not_144_out);
  and and_22 (and_22_out, not_145_out, not_146_out, not_147_out, not_148_out, not_149_out, not_150_out, F5, not_151_out, not_152_out, not_153_out, not_154_out, not_155_out);
  and and_23 (and_23_out, not_156_out, not_157_out, not_158_out, not_159_out, not_160_out, not_161_out, F5, not_162_out, not_163_out, not_164_out, not_165_out, F0);
  and and_24 (and_24_out, not_166_out, not_167_out, not_168_out, not_169_out, not_170_out, not_171_out, F5, not_172_out, not_173_out, not_174_out, F1, not_175_out);
  and and_25 (and_25_out, not_176_out, not_177_out, not_178_out, not_179_out, not_180_out, not_181_out, F5, not_182_out, not_183_out, F2, not_184_out, not_185_out);
  and and_26 (and_26_out, not_186_out, not_187_out, not_188_out, not_189_out, not_190_out, not_191_out, F5, not_192_out, F3, not_193_out, F1, F0);
  and and_27 (and_27_out, not_194_out, not_195_out, OP3, not_196_out, not_197_out, not_198_out);
  and and_28 (and_28_out, not_199_out, not_200_out, OP3, OP2, not_201_out, not_202_out);
  and and_29 (and_29_out, not_203_out, not_204_out, OP3, not_205_out, not_206_out, OP0);
  and and_30 (and_30_out, OP5, not_207_out, not_208_out, not_209_out, OP1, OP0);
  and and_31 (and_31_out, OP5, not_210_out, OP3, not_211_out, OP1, OP0);
  and and_32 (and_32_out, OP5, not_212_out, not_213_out, not_214_out, not_215_out, OP0);
  and and_33 (and_33_out, not_216_out, not_217_out, not_218_out, not_219_out, not_220_out, not_221_out, F5, not_222_out, not_223_out, F2, not_224_out, F0);
  and and_34 (and_34_out, not_225_out, not_226_out, not_227_out, not_228_out, not_229_out, not_230_out, F5, not_231_out, not_232_out, F2, F1, F0);
  and and_35 (and_35_out, not_233_out, not_234_out, not_235_out, not_236_out, not_237_out, not_238_out, F5, not_239_out, F3, not_240_out, F1, not_241_out);
  and and_36 (and_36_out, not_242_out, not_243_out, not_244_out, not_245_out, not_246_out, not_247_out, F5, not_248_out, F3, not_249_out, F1, F0);
  and and_37 (and_37_out, not_250_out, not_251_out, OP3, not_252_out, OP1, not_253_out);
  and and_38 (and_38_out, not_254_out, not_255_out, OP3, OP2, not_256_out, OP0);
  and and_39 (and_39_out, not_257_out, not_258_out, OP3, OP2, OP1, not_259_out);
  or or_1 (S1, and_15_out, and_16_out, and_17_out, and_18_out, and_19_out, and_20_out, and_21_out);
  or or_2 (S2, and_22_out, and_23_out, and_24_out, and_25_out, and_26_out, and_27_out, and_28_out, and_29_out, and_30_out, and_31_out, and_32_out);
  or or_3 (S3, and_33_out, and_34_out, and_35_out, and_36_out, and_37_out, and_38_out, and_39_out);
  or or_4 (S0, and_1_out, and_2_out, and_3_out, and_4_out, and_5_out, and_6_out, and_7_out, and_8_out, and_9_out, and_10_out, and_11_out, and_12_out, and_13_out, and_14_out);
endmodule

// 控制信号生成
module \控制信号自动生成  (
  input  OP0,
  input  OP1,
  input  OP2,
  input  OP3,
  input  OP4,
  input  OP5,
  input  F0,
  input  F1,
  input  F2,
  input  F3,
  input  F4,
  input  F5,
  output MemToReg,
  output MemWrite,
  output BLTZ,
  output LH,
  output SRAV,
  output XORI,
  output ALU_SRC,
  output RegWrite,
  output SysCALL,
  output SignedExt,
  output RegDst,
  output BEQ,
  output BNE,
  output JR,
  output JUMP,
  output JAL
);

  wire and_7_out, and_8_out, and_9_out, and_10_out, and_11_out, and_12_out, and_13_out, and_14_out,
       and_15_out, and_16_out, and_17_out, and_18_out, and_19_out, and_21_out, and_22_out, and_23_out,
       and_24_out, and_25_out, and_26_out, and_27_out, and_28_out, and_29_out, and_30_out, and_31_out,
       and_32_out, and_33_out, and_34_out, and_38_out, and_39_out, not_1_out, not_2_out, not_3_out,
       not_4_out, not_5_out, not_6_out, not_7_out, not_8_out, not_9_out, not_10_out, not_11_out, not_12_out,
       not_13_out, not_14_out, not_15_out, not_16_out, not_17_out, not_18_out, not_19_out, not_20_out,
       not_21_out, not_22_out, not_23_out, not_24_out, not_25_out, not_26_out, not_27_out, not_28_out,
       not_29_out, not_30_out, not_31_out, not_32_out, not_33_out, not_34_out, not_35_out, not_36_out,
       not_37_out, not_38_out, not_39_out, not_40_out, not_41_out, not_42_out, not_43_out, not_44_out,
       not_45_out, not_46_out, not_47_out, not_48_out, not_49_out, not_50_out, not_51_out, not_52_out,
       not_53_out, not_54_out, not_55_out, not_56_out, not_57_out, not_58_out, not_59_out, not_60_out,
       not_61_out, not_62_out, not_63_out, not_64_out, not_65_out, not_66_out, not_67_out, not_68_out,
       not_69_out, not_70_out, not_71_out, not_72_out, not_73_out, not_74_out, not_75_out, not_76_out,
       not_77_out, not_78_out, not_79_out, not_80_out, not_81_out, not_82_out, not_83_out, not_84_out,
       not_85_out, not_86_out, not_87_out, not_88_out, not_89_out, not_90_out, not_91_out, not_92_out,
       not_93_out, not_94_out, not_95_out, not_96_out, not_97_out, not_98_out, not_99_out, not_100_out,
       not_101_out, not_102_out, not_103_out, not_104_out, not_105_out, not_106_out, not_107_out,
       not_108_out, not_109_out, not_110_out, not_111_out, not_112_out, not_113_out, not_114_out,
       not_115_out, not_116_out, not_117_out, not_118_out, not_119_out, not_120_out, not_121_out,
       not_122_out, not_123_out, not_124_out, not_125_out, not_126_out, not_127_out, not_128_out,
       not_129_out, not_130_out, not_131_out, not_132_out, not_133_out, not_134_out, not_135_out,
       not_136_out, not_137_out, not_138_out, not_139_out, not_140_out, not_141_out, not_142_out,
       not_143_out, not_144_out, not_145_out, not_146_out, not_147_out, not_148_out, not_149_out,
       not_150_out, not_151_out, not_152_out, not_153_out, not_154_out, not_155_out, not_156_out,
       not_157_out, not_158_out, not_159_out, not_160_out, not_161_out, not_162_out, not_163_out,
       not_164_out, not_165_out, not_166_out, not_167_out, not_168_out, not_169_out, not_170_out,
       not_171_out, not_172_out, not_173_out, not_174_out, not_175_out, not_176_out, not_177_out,
       not_178_out, not_179_out, not_180_out, not_181_out, not_182_out, not_183_out, not_184_out,
       not_185_out, not_186_out, not_187_out, not_188_out, not_189_out, not_190_out, not_191_out,
       not_192_out, not_193_out, not_194_out, not_195_out, not_196_out, not_197_out, not_198_out,
       not_199_out, not_200_out, not_201_out, not_202_out, not_203_out, not_204_out, not_205_out,
       not_206_out, not_207_out, not_208_out, not_209_out, not_210_out, not_211_out, not_212_out,
       not_213_out, not_214_out, not_215_out, not_216_out;

  not not_1 (not_1_out, OP2);
  not not_2 (not_2_out, OP3);
  not not_3 (not_3_out, OP4);
  not not_4 (not_4_out, OP2);
  not not_5 (not_5_out, OP4);
  not not_6 (not_6_out, OP1);
  not not_7 (not_7_out, OP2);
  not not_8 (not_8_out, OP3);
  not not_9 (not_9_out, OP4);
  not not_10 (not_10_out, OP5);
  not not_11 (not_11_out, OP1);
  not not_12 (not_12_out, OP2);
  not not_13 (not_13_out, OP3);
  not not_14 (not_14_out, OP4);
  not not_15 (not_15_out, OP0);
  not not_16 (not_16_out, OP1);
  not not_17 (not_17_out, OP2);
  not not_18 (not_18_out, OP3);
  not not_19 (not_19_out, OP4);
  not not_20 (not_20_out, OP5);
  not not_21 (not_21_out, F3);
  not not_22 (not_22_out, F4);
  not not_23 (not_23_out, F5);
  not not_24 (not_24_out, OP0);
  not not_25 (not_25_out, OP4);
  not not_26 (not_26_out, OP5);
  not not_27 (not_27_out, OP0);
  not not_28 (not_28_out, OP4);
  not not_29 (not_29_out, OP5);
  not not_30 (not_30_out, OP1);
  not not_31 (not_31_out, OP4);
  not not_32 (not_32_out, OP5);
  not not_33 (not_33_out, OP2);
  not not_34 (not_34_out, OP3);
  not not_35 (not_35_out, OP4);
  not not_36 (not_36_out, OP2);
  not not_37 (not_37_out, OP4);
  not not_38 (not_38_out, OP0);
  not not_39 (not_39_out, OP1);
  not not_40 (not_40_out, OP2);
  not not_41 (not_41_out, OP4);
  not not_42 (not_42_out, OP5);
  not not_43 (not_43_out, F0);
  not not_44 (not_44_out, F2);
  not not_45 (not_45_out, F3);
  not not_46 (not_46_out, F4);
  not not_47 (not_47_out, OP0);
  not not_48 (not_48_out, OP1);
  not not_49 (not_49_out, OP2);
  not not_50 (not_50_out, OP4);
  not not_51 (not_51_out, OP5);
  not not_52 (not_52_out, F1);
  not not_53 (not_53_out, F3);
  not not_54 (not_54_out, F4);
  not not_55 (not_55_out, OP0);
  not not_56 (not_56_out, OP1);
  not not_57 (not_57_out, OP2);
  not not_58 (not_58_out, OP4);
  not not_59 (not_59_out, OP5);
  not not_60 (not_60_out, F2);
  not not_61 (not_61_out, F4);
  not not_62 (not_62_out, OP0);
  not not_63 (not_63_out, OP1);
  not not_64 (not_64_out, OP2);
  not not_65 (not_65_out, OP4);
  not not_66 (not_66_out, OP5);
  not not_67 (not_67_out, F3);
  not not_68 (not_68_out, F4);
  not not_69 (not_69_out, F5);
  not not_70 (not_70_out, OP0);
  not not_71 (not_71_out, OP1);
  not not_72 (not_72_out, OP2);
  not not_73 (not_73_out, OP4);
  not not_74 (not_74_out, OP5);
  not not_75 (not_75_out, F3);
  not not_76 (not_76_out, F4);
  not not_77 (not_77_out, OP0);
  not not_78 (not_78_out, OP4);
  not not_79 (not_79_out, OP5);
  not not_80 (not_80_out, OP1);
  not not_81 (not_81_out, OP4);
  not not_82 (not_82_out, OP5);
  not not_83 (not_83_out, OP2);
  not not_84 (not_84_out, OP3);
  not not_85 (not_85_out, OP4);
  not not_86 (not_86_out, OP2);
  not not_87 (not_87_out, OP3);
  not not_88 (not_88_out, OP4);
  not not_89 (not_89_out, OP0);
  not not_90 (not_90_out, OP1);
  not not_91 (not_91_out, OP2);
  not not_92 (not_92_out, OP3);
  not not_93 (not_93_out, OP4);
  not not_94 (not_94_out, OP5);
  not not_95 (not_95_out, F0);
  not not_96 (not_96_out, F1);
  not not_97 (not_97_out, F4);
  not not_98 (not_98_out, F5);
  not not_99 (not_99_out, OP5);
  not not_100 (not_100_out, OP4);
  not not_101 (not_101_out, OP3);
  not not_102 (not_102_out, OP1);
  not not_103 (not_103_out, OP0);
  not not_104 (not_104_out, OP5);
  not not_105 (not_105_out, OP4);
  not not_106 (not_106_out, OP3);
  not not_107 (not_107_out, OP1);
  not not_108 (not_108_out, OP5);
  not not_109 (not_109_out, OP4);
  not not_110 (not_110_out, OP2);
  not not_111 (not_111_out, OP1);
  not not_112 (not_112_out, OP0);
  not not_113 (not_113_out, OP5);
  not not_114 (not_114_out, OP4);
  not not_115 (not_115_out, OP2);
  not not_116 (not_116_out, OP1);
  not not_117 (not_117_out, OP5);
  not not_118 (not_118_out, OP4);
  not not_119 (not_119_out, OP2);
  not not_120 (not_120_out, OP0);
  not not_121 (not_121_out, OP4);
  not not_122 (not_122_out, OP3);
  not not_123 (not_123_out, OP2);
  not not_124 (not_124_out, OP4);
  not not_125 (not_125_out, OP2);
  not not_126 (not_126_out, OP4);
  not not_127 (not_127_out, OP3);
  not not_128 (not_128_out, OP2);
  not not_129 (not_129_out, OP1);
  not not_130 (not_130_out, OP5);
  not not_131 (not_131_out, OP4);
  not not_132 (not_132_out, OP3);
  not not_133 (not_133_out, OP2);
  not not_134 (not_134_out, OP1);
  not not_135 (not_135_out, OP0);
  not not_136 (not_136_out, OP1);
  not not_137 (not_137_out, OP2);
  not not_138 (not_138_out, OP3);
  not not_139 (not_139_out, OP4);
  not not_140 (not_140_out, OP5);
  not not_141 (not_141_out, F0);
  not not_142 (not_142_out, F2);
  not not_143 (not_143_out, F3);
  not not_144 (not_144_out, F4);
  not not_145 (not_145_out, OP0);
  not not_146 (not_146_out, OP1);
  not not_147 (not_147_out, OP2);
  not not_148 (not_148_out, OP3);
  not not_149 (not_149_out, OP4);
  not not_150 (not_150_out, OP5);
  not not_151 (not_151_out, F1);
  not not_152 (not_152_out, F3);
  not not_153 (not_153_out, F4);
  not not_154 (not_154_out, OP0);
  not not_155 (not_155_out, OP1);
  not not_156 (not_156_out, OP2);
  not not_157 (not_157_out, OP3);
  not not_158 (not_158_out, OP4);
  not not_159 (not_159_out, OP5);
  not not_160 (not_160_out, F2);
  not not_161 (not_161_out, F4);
  not not_162 (not_162_out, OP0);
  not not_163 (not_163_out, OP1);
  not not_164 (not_164_out, OP2);
  not not_165 (not_165_out, OP3);
  not not_166 (not_166_out, OP4);
  not not_167 (not_167_out, OP5);
  not not_168 (not_168_out, F3);
  not not_169 (not_169_out, F4);
  not not_170 (not_170_out, F5);
  not not_171 (not_171_out, OP0);
  not not_172 (not_172_out, OP1);
  not not_173 (not_173_out, OP2);
  not not_174 (not_174_out, OP3);
  not not_175 (not_175_out, OP4);
  not not_176 (not_176_out, OP5);
  not not_177 (not_177_out, F3);
  not not_178 (not_178_out, F4);
  not not_179 (not_179_out, OP0);
  not not_180 (not_180_out, OP1);
  not not_181 (not_181_out, OP3);
  not not_182 (not_182_out, OP4);
  not not_183 (not_183_out, OP5);
  not not_184 (not_184_out, OP1);
  not not_185 (not_185_out, OP3);
  not not_186 (not_186_out, OP4);
  not not_187 (not_187_out, OP5);
  not not_188 (not_188_out, OP0);
  not not_189 (not_189_out, OP1);
  not not_190 (not_190_out, OP2);
  not not_191 (not_191_out, OP3);
  not not_192 (not_192_out, OP4);
  not not_193 (not_193_out, OP5);
  not not_194 (not_194_out, F0);
  not not_195 (not_195_out, F1);
  not not_196 (not_196_out, F2);
  not not_197 (not_197_out, F4);
  not not_198 (not_198_out, F5);
  not not_199 (not_199_out, OP0);
  not not_200 (not_200_out, OP2);
  not not_201 (not_201_out, OP3);
  not not_202 (not_202_out, OP4);
  not not_203 (not_203_out, OP5);
  not not_204 (not_204_out, F0);
  not not_205 (not_205_out, F1);
  not not_206 (not_206_out, F2);
  not not_207 (not_207_out, F4);
  not not_208 (not_208_out, F5);
  not not_209 (not_209_out, OP2);
  not not_210 (not_210_out, OP3);
  not not_211 (not_211_out, OP4);
  not not_212 (not_212_out, OP5);
  not not_213 (not_213_out, OP2);
  not not_214 (not_214_out, OP3);
  not not_215 (not_215_out, OP4);
  not not_216 (not_216_out, OP5);
  and and_1 (MemToReg, OP0, not_1_out, not_2_out, not_3_out, OP5);
  and and_2 (MemWrite, OP0, OP1, not_4_out, OP3, not_5_out, OP5);
  and and_3 (BLTZ, OP0, not_6_out, not_7_out, not_8_out, not_9_out, not_10_out);
  and and_4 (LH, OP0, not_11_out, not_12_out, not_13_out, not_14_out, OP5);
  and and_5 (SRAV, not_15_out, not_16_out, not_17_out, not_18_out, not_19_out, not_20_out, F0, F1, F2, not_21_out, not_22_out, not_23_out);
  and and_6 (XORI, not_24_out, OP1, OP2, OP3, not_25_out, not_26_out);
  and and_7 (and_7_out, not_27_out, OP3, not_28_out, not_29_out);
  and and_8 (and_8_out, not_30_out, OP3, not_31_out, not_32_out);
  and and_9 (and_9_out, OP0, not_33_out, not_34_out, not_35_out, OP5);
  and and_10 (and_10_out, OP0, OP1, not_36_out, not_37_out, OP5);
  and and_11 (and_11_out, not_38_out, not_39_out, not_40_out, not_41_out, not_42_out, not_43_out, not_44_out, not_45_out, not_46_out);
  and and_12 (and_12_out, not_47_out, not_48_out, not_49_out, not_50_out, not_51_out, not_52_out, not_53_out, not_54_out, F5);
  and and_13 (and_13_out, not_55_out, not_56_out, not_57_out, not_58_out, not_59_out, F1, not_60_out, F3, not_61_out, F5);
  and and_14 (and_14_out, not_62_out, not_63_out, not_64_out, not_65_out, not_66_out, F0, F1, not_67_out, not_68_out, not_69_out);
  and and_15 (and_15_out, not_70_out, not_71_out, not_72_out, not_73_out, not_74_out, F0, F1, F2, not_75_out, not_76_out);
  and and_16 (and_16_out, not_77_out, OP3, not_78_out, not_79_out);
  and and_17 (and_17_out, not_80_out, OP3, not_81_out, not_82_out);
  and and_18 (and_18_out, OP0, not_83_out, not_84_out, not_85_out, OP5);
  and and_19 (and_19_out, OP0, OP1, not_86_out, not_87_out, not_88_out);
  and and_20 (SysCALL, not_89_out, not_90_out, not_91_out, not_92_out, not_93_out, not_94_out, not_95_out, not_96_out, F2, F3, not_97_out, not_98_out);
  and and_21 (and_21_out, not_99_out, not_100_out, not_101_out, OP2, not_102_out, not_103_out);
  and and_22 (and_22_out, not_104_out, not_105_out, not_106_out, OP2, not_107_out, OP0);
  and and_23 (and_23_out, not_108_out, not_109_out, OP3, not_110_out, not_111_out, not_112_out);
  and and_24 (and_24_out, not_113_out, not_114_out, OP3, not_115_out, not_116_out, OP0);
  and and_25 (and_25_out, not_117_out, not_118_out, OP3, not_119_out, OP1, not_120_out);
  and and_26 (and_26_out, OP5, not_121_out, not_122_out, not_123_out, OP1, OP0);
  and and_27 (and_27_out, OP5, not_124_out, OP3, not_125_out, OP1, OP0);
  and and_28 (and_28_out, OP5, not_126_out, not_127_out, not_128_out, not_129_out, OP0);
  and and_29 (and_29_out, not_130_out, not_131_out, not_132_out, not_133_out, not_134_out, OP0);
  and and_30 (and_30_out, not_135_out, not_136_out, not_137_out, not_138_out, not_139_out, not_140_out, not_141_out, not_142_out, not_143_out, not_144_out);
  and and_31 (and_31_out, not_145_out, not_146_out, not_147_out, not_148_out, not_149_out, not_150_out, not_151_out, not_152_out, not_153_out, F5);
  and and_32 (and_32_out, not_154_out, not_155_out, not_156_out, not_157_out, not_158_out, not_159_out, F1, not_160_out, F3, not_161_out, F5);
  and and_33 (and_33_out, not_162_out, not_163_out, not_164_out, not_165_out, not_166_out, not_167_out, F0, F1, not_168_out, not_169_out, not_170_out);
  and and_34 (and_34_out, not_171_out, not_172_out, not_173_out, not_174_out, not_175_out, not_176_out, F0, F1, F2, not_177_out, not_178_out);
  and and_35 (BEQ, not_179_out, not_180_out, OP2, not_181_out, not_182_out, not_183_out);
  and and_36 (BNE, OP0, not_184_out, OP2, not_185_out, not_186_out, not_187_out);
  and and_37 (JR, not_188_out, not_189_out, not_190_out, not_191_out, not_192_out, not_193_out, not_194_out, not_195_out, not_196_out, F3, not_197_out, not_198_out);
  and and_38 (and_38_out, not_199_out, not_200_out, not_201_out, not_202_out, not_203_out, not_204_out, not_205_out, not_206_out, F3, not_207_out, not_208_out);
  and and_39 (and_39_out, OP1, not_209_out, not_210_out, not_211_out, not_212_out);
  and and_40 (JAL, OP0, OP1, not_213_out, not_214_out, not_215_out, not_216_out);
  or or_1 (ALU_SRC, and_7_out, and_8_out, and_9_out, and_10_out);
  or or_2 (RegWrite, and_11_out, and_12_out, and_13_out, and_14_out, and_15_out, and_16_out, and_17_out, and_18_out, and_19_out);
  or or_3 (SignedExt, and_21_out, and_22_out, and_23_out, and_24_out, and_25_out, and_26_out, and_27_out, and_28_out, and_29_out);
  or or_4 (RegDst, and_30_out, and_31_out, and_32_out, and_33_out, and_34_out);
  or or_5 (JUMP, and_38_out, and_39_out);
endmodule

// ALU
module MIPS_ALU (
  input  [4:0] shamt,
  input  [31:0] X,
  input  [31:0] Y,
  input  [3:0] AluOP,
  output Equal,
  output [31:0] Result,
  output [31:0] Result_2
);

  wire [0:0] comparator_1_lt, comparator_2_lt;
  wire [31:0] adder_1_out, AND_out, divider_1_out, divider_1_rem, multiplier_1_cout, multiplier_1_out,
       NOR_out, OR_out, shifter_1_out, shifter_2_out, shifter_3_out, subtractor_1_out, XOR_out;

  assign AND_out = X & Y;  // AND_Gate AND, 32 bits wide
  assign OR_out = X | Y;  // OR_Gate OR, 32 bits wide
  Shifter #(.width(32), .shift("ll")) shifter_1 (.in(Y), .\dist (shamt), .out(shifter_1_out));
  Shifter #(.width(32), .shift("ar")) shifter_2 (.in(Y), .\dist (shamt), .out(shifter_2_out));
  Shifter #(.width(32), .shift("lr")) shifter_3 (.in(Y), .\dist (shamt), .out(shifter_3_out));
  Multiplier #(.width(32)) multiplier_1 (.a(X), .b(Y), .out(multiplier_1_out), .cout(multiplier_1_cout));  // open: cin
  Divider #(.width(32)) divider_1 (.a(X), .b(Y), .out(divider_1_out), .rem(divider_1_rem));  // open: upper
  Adder #(.width(32)) adder_1 (.a(X), .b(Y), .out(adder_1_out));  // open: cin, cout
  Subtractor #(.width(32)) subtractor_1 (.a(X), .b(Y), .out(subtractor_1_out));  // open: bin, bout
  assign XOR_out = X ^ Y;  // XOR_Gate XOR, 32 bits wide
  assign NOR_out = ~(X | Y);  // NOR_Gate NOR, 32 bits wide
  Comparator #(.width(32), .mode("twosComplement")) comparator_1 (
    .a(X), .b(Y), .eq(Equal), .lt(comparator_1_lt[0]));  // open: gt
  Comparator #(.width(32), .mode("unsigned")) comparator_2 (.a(X), .b(Y), .lt(comparator_2_lt[0]));  // open: gt, eq
  Multiplexer #(.select(4), .width(32), .disabled("Z"), .enable("false")) multiplexer_1 (
    .in0(shifter_1_out), .in1(shifter_2_out), .in2(shifter_3_out), .in3(multiplier_1_out),
    .in4(divider_1_out), .in5(adder_1_out), .in6(subtractor_1_out), .in7(AND_out), .in8(OR_out),
    .in9(XOR_out), .in10(NOR_out), .in11({{31{1'b0}}, comparator_1_lt[0]}),
    .in12({{31{1'b0}}, comparator_2_lt[0]}), .in13({32{1'b0}}), .in14({32{1'b0}}), .in15({32{1'b0}}),
    .out(Result), .sel(AluOP));
  Multiplexer #(.select(4), .width(32), .disabled("Z"), .enable("false")) multiplexer_2 (
    .in0({32{1'b0}}), .in1({32{1'b0}}), .in2({32{1'b0}}), .in3(multiplier_1_cout), .in4(divider_1_rem),
    .in5({32{1'b0}}), .in6({32{1'b0}}), .in7({32{1'b0}}), .in8({32{1'b0}}), .in9({32{1'b0}}),
    .in10({32{1'b0}}), .in11({32{1'b0}}), .in12({32{1'b0}}), .in13({32{1'b0}}), .in14({32{1'b0}}),
    .in15({32{1'b0}}), .out(Result_2), .sel(AluOP));

  // Other names for the same wires on the sheet: Result2[31:0] = Result_2; S[3:0] = AluOP

  // Notes on the sheet:
  //   不要改变此引脚区域内容，也不要改变ALU封装形式
  //   输入引脚
  //   输出引脚
endmodule

module MIPS_Regifile (
  input  [31:0] Din,
  input  Clk,
  input  WE,
  input  [4:0] R1_num,
  input  [4:0] W_num,
  input  [4:0] R2_num,
  output [31:0] R1,
  output [31:0] R2
);

  // RegisterFile registerfile_1: pin names not known; wires that end beside it: Din, Clk, WE, W_num, R1_num, R2_num, R1, R2
endmodule

module \MIPS_Regfile_上升沿  (
  input  [31:0] Din,
  input  Clk,
  input  WE,
  input  [4:0] R1_num,
  input  [4:0] W_num,
  input  [4:0] R2_num,
  output [31:0] R1,
  output [31:0] R2
);

  // RegisterFile registerfile_1: pin names not known; wires that end beside it: Din, Clk, WE, W_num, R1_num, R2_num, R1, R2
endmodule

module \理想流水线  (
  output RegWrite,
  output MemWrite,
  output [31:0] IF_PC,
  output [31:0] ID_PC,
  output [31:0] EX_PC,
  output [31:0] M_PC,
  output [31:0] WB_PC,
  output [31:0] RDin,
  output [31:0] MDin,
  output [31:0] LedData
);

  wire and_1_out, and_2_out, and_3_out, and_4_out, BLTZ, CLK, clock_1_out, clock_2_out, comparator_2_lt,
       comparator_3_eq, comparator_3_lt, d_ff_1_q, equal, EX_BLTZ, EX_BRANCH, ex_mem_1_ctout16,
       \ex_mem_1_传输状态out_表明当前传输数据有效 , EX_SRAV, Go, \ID_EX_传输状态out_表明当前传输数据有效 , \if_id_1_传输状态out_表明当前传输数据有效 ,
       IR1, IR2, IR3, Led, MEM_LH, mem_wb_1_ctout16_5, nand_1_out, not_1_out, or_1_out, or_2_out,
       register_1_q, RST, W1, W2, W3;
  wire [2:0] ID_EX_ctrl4_2;
  wire [3:0] CTRL4, ex_mem_1_ctout16_2;
  wire [4:0] ex_mem_1_wbout5, ID_EX_shout5_3, ID_EX_wbout5, mem_wb_1_wbout5, multiplexer_2_out,
       multiplexer_3_out, multiplexer_4_out, multiplexer_5_out, multiplexer_7_out;
  wire [12:0] CNT_num;
  wire [15:0] CTRL, EX_CTRL, ex_mem_1_ctout16_6, \LoadUse次数 , mem_wb_1_ctout16_6, \总周期数 , \插入气泡数 , \无条件分支数 ,
       \条件分支成功数 ;
  wire [31:0] adder_1_out, adder_2_out, adder_3_out, adder_4_out, bit_extender_1_out, bit_extender_2_out,
       bit_extender_3_out, EX_IR, ex_mem_1_aluout32, ex_mem_1_irout32, ex_mem_1_ledout32, EX_R1,
       ID_EX_irout32, ID_EX_r1out32_2, ID_EX_r1out32_3, ID_EX_r2out32, ID_IR, if_id_1_irout32, IF_IR, IR,
       MEM_IR, mem_wb_1_aluout32, mem_wb_1_mdout32, mips_alu_1_result, mips_ram_1_dataout,
       mips_regifile_1_r1, mips_regifile_1_r2, multiplexer_1_out, multiplexer_6_out, multiplexer_8_out,
       multiplexer_9_out, multiplexer_10_out, multiplexer_11_out, multiplexer_12_out, multiplexer_13_out,
       register_2_q, rom_1_data, shifter_1_out, shifter_2_out, WB_IR;

  Button \u_总复位  (.out(RST));
  Button _1 (.out(IR1));
  Button _2 (.out(IR2));
  Button _3 (.out(IR3));
  // Probe on \总周期数 
  // Probe on \总周期数 
  Button \u_继续运行  (.out(Go));
  LED #(.active("true")) led_1 (.in(W1));
  LED #(.active("true")) led_2 (.in(W2));
  LED #(.active("true")) led_3 (.in(W3));
  and and_1 (and_1_out, mem_wb_1_ctout16_6[4], ~mem_wb_1_ctout16_5);  // AND_Gate
  Hex_Digit_Display hex_digit_display_1 (.value(LedData[31:28]));  // open: dp
  // Probe on IF_PC[19:0]
  // Mips_Probe mips_probe_1: pin names not known; wires that end beside it: IF_IR
  Register #(.width(1), .trigger("rising"), .Select("low")) register_1 (
    .D(mem_wb_1_ctout16_6[4]), .en(and_1_out), .Q(register_1_q), .clk(CLK), .clr(or_1_out));
  or or_1 (or_1_out, RST, Go);
  Multiplexer #(.select(1), .width(32), .disabled("Z"), .enable("false")) multiplexer_1 (
    .in0(adder_1_out), .in1(multiplexer_12_out), .out(multiplexer_1_out), .sel(or_2_out));
  or or_2 (or_2_out, EX_BRANCH, BLTZ, EX_CTRL[15]);
  Hex_Digit_Display hex_digit_display_2 (.value(LedData[23:20]));  // open: dp
  Hex_Digit_Display hex_digit_display_3 (.value(LedData[27:24]));  // open: dp
  // Probe on ID_PC[19:0]
  // Mips_Probe mips_probe_2: pin names not known; wires that end beside it: ID_IR
  Register #(.width(32), .trigger("rising"), .Select("low")) PC (
    .D(multiplexer_1_out), .en(not_1_out), .Q(IF_PC), .clk(CLK), .clr(RST));
  Counter #(.width(16), .max('hffff), .ongoal("wrap"), .trigger("rising"), .behavior("old")) counter_1 (
    .count(not_1_out), .Q(\总周期数 ), .clk(CLK), .clr(RST));  // open: load, D, carry, preset
  not not_1 (not_1_out, register_1_q);
  Hex_Digit_Display hex_digit_display_4 (.value(LedData[15:12]));  // open: dp
  Hex_Digit_Display hex_digit_display_5 (.value(LedData[19:16]));  // open: dp
  Adder #(.width(32)) adder_1 (.a(IF_PC), .b(32'h4), .out(adder_1_out));  // open: cin, cout
  Hex_Digit_Display hex_digit_display_6 (.value(LedData[7:4]));  // open: dp
  Hex_Digit_Display hex_digit_display_7 (.value(LedData[11:8]));  // open: dp
  Clock #(.highDuration(1), .lowDuration(1)) clock_1 (.out(clock_1_out));
  // Probe on EX_PC[19:0]
  // Mips_Probe mips_probe_3: pin names not known; wires that end beside it: clock_1_out, EX_IR, CLK
  ROM #(.addrWidth(10), .dataWidth(32), .Select("high")) rom_1 (.addr(IF_PC[11:2]), .data(rom_1_data));
  Hex_Digit_Display hex_digit_display_8 (.value(LedData[3:0]));  // open: dp
  IF_ID if_id_1 (
    .IRin32(rom_1_data), .PCin32(IF_PC), .\传输状态In_表明当前传输数据有效 (1'b1), .CLK(CLK), .IRout32(if_id_1_irout32),
    .PCout32(ID_PC), .\传输状态Out_表明当前传输数据有效 (\if_id_1_传输状态out_表明当前传输数据有效 ), .\同步清零_气泡_高电平有效 (RST),
    .\使能端_低电平有效_stall_高电平有效 (register_1_q));  // open: CTin16, CTout16
  // Probe on \总周期数 
  // Probe on M_PC[19:0]
  // Mips_Probe mips_probe_4: pin names not known; wires that end beside it: MEM_IR
  // Probe on \总周期数 
  // Probe on \无条件分支数 
  // Probe on \条件分支成功数 
  // Probe on \插入气泡数 
  // Probe on \LoadUse次数 
  // Probe on IF_PC[11:0]
  // Probe on WB_PC[19:0]
  // Mips_Probe mips_probe_5: pin names not known; wires that end beside it: WB_IR
  Multiplexer #(.select(1), .width(5), .disabled("Z"), .enable("false")) multiplexer_2 (
    .in0(if_id_1_irout32[25:21]), .in1(5'b00100), .out(multiplexer_2_out), .sel(CTRL[4]));
  Multiplexer #(.select(1), .width(5), .disabled("Z"), .enable("false")) multiplexer_3 (
    .in0(if_id_1_irout32[20:16]), .in1(5'b00010), .out(multiplexer_3_out), .sel(CTRL[4]));
  Multiplexer #(.select(1), .width(5), .disabled("Z"), .enable("false")) multiplexer_4 (
    .in0(if_id_1_irout32[20:16]), .in1(if_id_1_irout32[15:11]), .out(multiplexer_4_out), .sel(CTRL[5]));
  Multiplexer #(.select(1), .width(5), .disabled("Z"), .enable("false")) multiplexer_5 (
    .in0(multiplexer_4_out), .in1({5{1'b1}}), .out(multiplexer_5_out), .sel(CTRL[6]));
  // Probe on EX_PC[11:0]
  // Probe on ID_PC[11:0]
  \单周期硬布线控制器  \u_单周期硬布线控制器_1  (
    .OP(if_id_1_irout32[31:26]), .Func(if_id_1_irout32[5:0]), .ALU_OP(CTRL[3:0]), .MemToReg(CTRL[10]),
    .MemWrite(CTRL[9]), .BLTZ(CTRL4[3]), .LH(CTRL4[2]), .SRAV(CTRL4[1]), .XORI(CTRL4[0]), .ALU_SRC(CTRL[8]),
    .RegWrite(CTRL[7]), .SysCALL(CTRL[4]), .SignedExt(CTRL[13]), .RegDst(CTRL[5]), .Beq(CTRL[12]),
    .Bne(CTRL[11]), .JR(CTRL[14]), .JMP(CTRL[15]), .JAL(CTRL[6]));
  assign bit_extender_1_out = {{16{1'b0}}, if_id_1_irout32[15:0]};  // Bit_Extender bit_extender_1
  assign bit_extender_2_out = {{16{if_id_1_irout32[15]}}, if_id_1_irout32[15:0]};  // Bit_Extender bit_extender_2
  assign bit_extender_3_out = {{6{if_id_1_irout32[25]}}, if_id_1_irout32[25:0]};  // Bit_Extender bit_extender_3
  // Probe on M_PC[11:0]
  MIPS_Regifile mips_regifile_1 (
    .Din(RDin), .Clk(CLK), .R1(mips_regifile_1_r1), .R2(mips_regifile_1_r2), .WE(RegWrite),
    .W_num(mem_wb_1_wbout5), .R1_num(multiplexer_2_out), .R2_num(multiplexer_3_out));
  Multiplexer #(.select(1), .width(32), .disabled("Z"), .enable("false")) multiplexer_6 (
    .in0(bit_extender_1_out), .in1(bit_extender_2_out), .out(multiplexer_6_out), .sel(CTRL[13]));
  // Probe on WB_PC[11:0]
  Shifter #(.width(32), .shift("ll")) shifter_1 (.in(bit_extender_3_out), .\dist (5'b00010), .out(shifter_1_out));
  ID_EX ID_EX (
    .R1in32(mips_regifile_1_r1), .R2in32(mips_regifile_1_r2), .IRin32(IR), .PCin32(ID_PC),
    .IMMin32(multiplexer_6_out), .WBin5(multiplexer_5_out), .SHin5(if_id_1_irout32[10:6]), .CTin16(CTRL),
    .\传输状态In_表明当前传输数据有效 (\if_id_1_传输状态out_表明当前传输数据有效 ), .CLK(CLK), .R1out32(EX_R1), .R2out32(ID_EX_r2out32),
    .IRout32(ID_EX_irout32), .PCout32(EX_PC), .R1out32_2(ID_EX_r1out32_2), .WBout5(ID_EX_wbout5),
    .SHout5_3(ID_EX_shout5_3), .CTout16(EX_CTRL), .\传输状态Out_表明当前传输数据有效 (\ID_EX_传输状态out_表明当前传输数据有效 ),
    .\同步清零_气泡_高电平有效 (RST), .\使能端_低电平有效_stall_高电平有效 (register_1_q), ._26in32(shifter_1_out),
    .R1out32_3(ID_EX_r1out32_3), .CTRL4(CTRL4),
    .CTRL4_2({EX_BLTZ, ID_EX_ctrl4_2[2], EX_SRAV, ID_EX_ctrl4_2[0]}));  // open: FWR1in2, WBout5_2, FWR2in2, SHout5_4, ERETin1_2, SHout5_2, ERETin1, SHout5
  Register #(.width(32), .trigger("rising"), .Select("low")) register_2 (
    .D(EX_R1), .en(and_2_out), .Q(register_2_q), .clk(CLK));  // open: clr
  and and_2 (and_2_out, Led, EX_CTRL[4]);
  Shifter #(.width(32), .shift("ll")) shifter_2 (.in(ID_EX_r1out32_2), .\dist (5'b00010), .out(shifter_2_out));
  Multiplexer #(.select(1), .width(5), .disabled("Z"), .enable("false")) multiplexer_7 (
    .in0(ID_EX_shout5_3), .in1(EX_R1[4:0]), .out(multiplexer_7_out), .sel(EX_SRAV));
  Adder #(.width(32)) adder_2 (.a(EX_PC), .b(32'h4), .out(adder_2_out));  // open: cin, cout
  Multiplexer #(.select(1), .width(32), .disabled("Z"), .enable("false")) multiplexer_8 (
    .in0(ID_EX_r2out32), .in1(ID_EX_r1out32_2), .out(multiplexer_8_out), .sel(EX_CTRL[8]));
  Comparator #(.width(32), .mode("twosComplement")) comparator_1 (
    .a(ID_EX_r2out32), .b(32'h22), .eq(Led));  // open: gt, lt
  Adder #(.width(32)) adder_3 (.a(shifter_2_out), .b(adder_2_out), .out(adder_3_out));  // open: cin, cout
  MIPS_ALU mips_alu_1 (
    .X(EX_R1), .Y(multiplexer_8_out), .AluOP(EX_CTRL[3:0]), .Equal(equal), .Result(mips_alu_1_result),
    .shamt(multiplexer_7_out));  // open: Result_2
  Multiplexer #(.select(1), .width(32), .disabled("Z"), .enable("false")) multiplexer_9 (
    .in0(ID_EX_r1out32_3), .in1(EX_R1), .out(multiplexer_9_out), .sel(EX_CTRL[14]));
  Multiplexer #(.select(1), .width(32), .disabled("Z"), .enable("false")) multiplexer_10 (
    .in0(adder_2_out), .in1(adder_3_out), .out(multiplexer_10_out), .sel(EX_BRANCH));
  EX_MEM ex_mem_1 (
    .ALUin32(mips_alu_1_result), .Memin32(ID_EX_r2out32), .IRin32(ID_EX_irout32), .PCin32(EX_PC),
    .WBin5(ID_EX_wbout5), .CTin16_2(EX_CTRL), .\传输状态In_表明当前传输数据有效 (\ID_EX_传输状态out_表明当前传输数据有效 ), .CLK(CLK),
    .ALUout32(ex_mem_1_aluout32), .Memout32(MDin), .IRout32(ex_mem_1_irout32), .PCout32(M_PC),
    .WBout5(ex_mem_1_wbout5), .CTout16_6({ex_mem_1_ctout16_6[15:10], MemWrite, ex_mem_1_ctout16_6[8:0]}),
    .\传输状态Out_表明当前传输数据有效 (\ex_mem_1_传输状态out_表明当前传输数据有效 ), .\同步清零_气泡_高电平有效 (RST),
    .\使能端_低电平有效_stall_高电平有效 (register_1_q), .LEDin32(register_2_q), .LEDout32(ex_mem_1_ledout32),
    .CTin16(Led), .CTout16(ex_mem_1_ctout16), .CTin4({EX_BLTZ, ID_EX_ctrl4_2[2], EX_SRAV, ID_EX_ctrl4_2[0]}),
    .CTout16_2({ex_mem_1_ctout16_2[3], MEM_LH, ex_mem_1_ctout16_2[1:0]}));  // open: Resullt2, CTout16_3, ERETin2, CTout16_4, ERETin2_2, CTout16_5
  Multiplexer #(.select(1), .width(32), .disabled("Z"), .enable("false")) multiplexer_11 (
    .in0(multiplexer_10_out), .in1(adder_3_out), .out(multiplexer_11_out), .sel(BLTZ));
  Multiplexer #(.select(1), .width(32), .disabled("Z"), .enable("false")) multiplexer_12 (
    .in0(multiplexer_11_out), .in1(multiplexer_9_out), .out(multiplexer_12_out), .sel(EX_CTRL[15]));
  MIPS_RAM mips_ram_1 (
    .\字节地址 (ex_mem_1_aluout32[11:2]), .Din(MDin), .DataOut(mips_ram_1_dataout), .CLK(CLK), .WE(MemWrite),
    .Mode(ex_mem_1_aluout32[1]), .LH(MEM_LH));
  MEM_WB mem_wb_1 (
    .ALUin32(ex_mem_1_aluout32), .MDin32(mips_ram_1_dataout), .IRin32(ex_mem_1_irout32), .PCin32(M_PC),
    .WBin5(ex_mem_1_wbout5), .CTin16_2({ex_mem_1_ctout16_6[15:10], MemWrite, ex_mem_1_ctout16_6[8:0]}),
    .\传输状态In_表明当前传输数据有效 (\ex_mem_1_传输状态out_表明当前传输数据有效 ), .CLK(CLK), .ALUout32(mem_wb_1_aluout32),
    .MDout32(mem_wb_1_mdout32), .PCout32(WB_PC), .WBout5(mem_wb_1_wbout5),
    .CTout16_6({mem_wb_1_ctout16_6[15:8], RegWrite, mem_wb_1_ctout16_6[6:0]}), .\同步清零_气泡_高电平有效 (RST),
    .\使能端_低电平有效_stall_高电平有效 (register_1_q), .LEDin32(ex_mem_1_ledout32), .LEDout32(LedData),
    .CTin16(ex_mem_1_ctout16), .CTout16_5(mem_wb_1_ctout16_5),
    .CTin4({ex_mem_1_ctout16_2[3], MEM_LH, ex_mem_1_ctout16_2[1:0]}));  // open: IRout32, 传输状态Out_表明当前传输数据有效, CTout16, CTout16_2, RE2in32, ERETin1, CTout16_3, ERETin1_2, CTout16_4
  Multiplexer #(.select(1), .width(32), .disabled("Z"), .enable("false")) multiplexer_13 (
    .in0(mem_wb_1_aluout32), .in1(mem_wb_1_mdout32), .out(multiplexer_13_out), .sel(mem_wb_1_ctout16_6[10]));
  Adder #(.width(32)) adder_4 (.a(WB_PC), .b(32'h4), .out(adder_4_out));  // open: cin, cout
  Multiplexer #(.select(1), .width(32), .disabled("Z"), .enable("false")) multiplexer_14 (
    .in0(multiplexer_13_out), .in1(adder_4_out), .out(RDin), .sel(mem_wb_1_ctout16_6[6]));
  Comparator #(.width(32), .mode("twosComplement")) comparator_2 (
    .a(EX_R1), .b({32{1'b0}}), .lt(comparator_2_lt));  // open: gt, eq
  and and_3 (and_3_out, equal, EX_CTRL[12]);
  and and_4 (and_4_out, ~equal, EX_CTRL[11]);  // AND_Gate
  and and_5 (BLTZ, comparator_2_lt, EX_BLTZ);
  D_Flip_Flop #(.trigger("high"), .Pre_Clr_Positions("LEGACY"), .NegatePresetClear("false"), .enable("true"), .NewFFLayout("false")) d_ff_1 (.Q(d_ff_1_q));  // open: clk, D, Qn, preset, en, reset
  // Probe on 13'hc
  or or_3 (EX_BRANCH, and_3_out, and_4_out);
  Comparator #(.width(13), .mode("twosComplement")) comparator_3 (
    .a(CNT_num), .b(13'hc), .eq(comparator_3_eq), .lt(comparator_3_lt));  // open: gt
  Clock #(.highDuration(1), .lowDuration(1)) clock_2 (.out(clock_2_out));
  nand nand_1 (nand_1_out, d_ff_1_q, comparator_3_eq);
  Counter #(.width(13), .max('h1fff), .ongoal("stay"), .trigger("rising"), .behavior("old")) counter_2 (
    .count(comparator_3_lt), .Q(CNT_num), .clk(clock_2_out));  // open: load, D, carry, clr, preset
  assign CLK = nand_1_out ? clock_2_out : 1'bz;  // Controlled_Buffer controlled_buffer_1
  Pull_Resistor #(.pull(1)) pull_resistor_1 (.node(CLK));

  // Other names for the same wires on the sheet: SignedExt = CTRL[13]; EX_JR = EX_CTRL[14]; EX_JMP = EX_CTRL[15];
  //   MEM_PC[31:0] = M_PC

  // Notes on the sheet:
  //   中断源
  //   时空图监测，可删除
  //   中断等待指示
  //   数码管输出
  //   指令存储器
  //   contents of rom_1 (hex, n*v repeats v):
  //   20100000 20110000 20120000 20130000 36100000 36310001 36520002 36730003 ae100000 ae110004 ae120008
  //   ae13000c 2002000a 20110000 20120000 20130000 c
  //   OP
  //   rs
  //   rt
  //   rd
  //   Func
  //   JMP
  //   JR
  //   OP
  //   Func
  //   Syscall
  //   Beq
  //   Bne
  //   MemToReg
  //   MemWrite
  //   AluOP
  //   AluSrcB
  //   RegWrite
  //   JAL
  //   RegDst
  //   流水调试日志用
  //   Syscall
  //   AluOP
  //   AluSrcB
  //   RegWrite
  //   为方便自动评测，需要输出流水线各段保存的PC值，注意是PC不是PC+4，另外ID段寄存器写入信息，Mem段内存写入信息也要输出
  //   MemWrite
  //   JAL
  //   MemToReg
  //   Bne
  //   控制位
  //   暂停节拍，不能为0
  //   戳工具置1进入计数暂停模式，ctrl+k时钟自动运行到对应节拍暂停
  //   ctrl+k关闭时钟连续运行，将控制位置零，进入单步调试模式调试
  //   用这个时钟源需要去掉电路中的其他时钟源
  //   可计数暂停的时钟源
endmodule

module \气泡流水线  (
  output RegWrite,
  output MemWrite,
  output [31:0] IF_PC,
  output [31:0] ID_PC,
  output [31:0] EX_PC,
  output [31:0] M_PC,
  output [31:0] WB_PC,
  output [31:0] RDin,
  output [31:0] MDin,
  output [31:0] LedData
);

  wire and_1_out, and_2_out, and_3_out, and_4_out, and_5_out, and_6_out, BLTZ, BRANCH, CLK, clock_1_out,
       clock_2_out, comparator_1_eq, comparator_1_lt, comparator_3_lt, d_ff_1_q, equal, EX_BLTZ, EX_BRANCH,
       ex_mem_1_ctout16, \ex_mem_1_传输状态out_表明当前传输数据有效 , EX_SRAV, Go, \ID_EX_传输状态out_表明当前传输数据有效 ,
       \if_id_1_传输状态out_表明当前传输数据有效 , IR1, IR2, IR3, Led, MEM_LH, Mem_RegWrite, mem_wb_1_ctout16_5,
       nand_1_out, not_1_out, or_1_out, or_3_out, or_4_out, or_5_out, or_6_out, register_1_q, RST, W1, W2,
       W3, \数据相关 ;
  wire [2:0] ID_EX_ctrl4_2;
  wire [3:0] CTRL4, ex_mem_1_ctout16_2;
  wire [4:0] ex_mem_1_wbout5, ID_EX_shout5_3, ID_EX_wbout5, mem_wb_1_wbout5, multiplexer_2_out,
       multiplexer_3_out, multiplexer_4_out, multiplexer_5_out, multiplexer_8_out;
  wire [12:0] CNT_num;
  wire [15:0] CTRL, EX_CTRL, ex_mem_1_ctout16_6, \LoadUse次数 , mem_wb_1_ctout16_6, \总周期数 , \插入气泡数 , \无条件分支数 ,
       \条件分支成功数 ;
  wire [31:0] adder_1_out, adder_2_out, adder_3_out, adder_4_out, bit_extender_1_out, bit_extender_2_out,
       bit_extender_3_out, EX_IR, ex_mem_1_aluout32, ex_mem_1_ledout32, EX_R1, ID_EX_r1out32_2,
       ID_EX_r1out32_3, ID_EX_r2out32, ID_IR, IF_IR, MEM_IR, mem_wb_1_aluout32, mem_wb_1_mdout32,
       mips_alu_1_result, mips_ram_1_dataout, mips_regifile_1_r1, mips_regifile_1_r2, multiplexer_1_out,
       multiplexer_6_out, multiplexer_7_out, multiplexer_9_out, multiplexer_10_out, multiplexer_11_out,
       multiplexer_12_out, multiplexer_13_out, register_2_q, shifter_1_out, shifter_2_out, WB_IR;

  Button \u_总复位  (.out(RST));
  Button _1 (.out(IR1));
  Button _2 (.out(IR2));
  Button _3 (.out(IR3));
  // Probe on \总周期数 
  // Probe on \总周期数 
  Button \u_继续运行  (.out(Go));
  LED #(.active("true")) led_1 (.in(W1));
  LED #(.active("true")) led_2 (.in(W2));
  LED #(.active("true")) led_3 (.in(W3));
  Hex_Digit_Display hex_digit_display_1 (.value(LedData[31:28]));  // open: dp
  // Probe on IF_PC[19:0]
  // Mips_Probe mips_probe_1: pin names not known; wires that end beside it: IF_IR
  and and_1 (and_1_out, mem_wb_1_ctout16_6[4], ~mem_wb_1_ctout16_5);  // AND_Gate
  Hex_Digit_Display hex_digit_display_2 (.value(LedData[23:20]));  // open: dp
  Hex_Digit_Display hex_digit_display_3 (.value(LedData[27:24]));  // open: dp
  // Probe on ID_PC[19:0]
  // Mips_Probe mips_probe_2: pin names not known; wires that end beside it: ID_IR
  // Probe on IF_PC
  Register #(.width(32), .trigger("rising"), .Select("low")) PC (
    .D(multiplexer_1_out), .en(and_2_out), .Q(IF_PC), .clk(CLK), .clr(RST));
  and and_2 (and_2_out, ~\数据相关 , not_1_out);  // AND_Gate
  Counter #(.width(16), .max('hffff), .ongoal("wrap"), .trigger("rising"), .behavior("old")) counter_1 (
    .count(not_1_out), .Q(\总周期数 ), .clk(CLK), .clr(RST));  // open: load, D, carry, preset
  Register #(.width(1), .trigger("rising"), .Select("low")) register_1 (
    .D(mem_wb_1_ctout16_6[4]), .en(and_1_out), .Q(register_1_q), .clk(CLK), .clr(or_1_out));
  or or_1 (or_1_out, RST, Go);
  Multiplexer #(.select(1), .width(32), .disabled("Z"), .enable("false")) multiplexer_1 (
    .in0(adder_1_out), .in1(multiplexer_12_out), .out(multiplexer_1_out), .sel(BRANCH));
  or or_2 (BRANCH, EX_BRANCH, BLTZ, EX_CTRL[15]);
  Hex_Digit_Display hex_digit_display_4 (.value(LedData[15:12]));  // open: dp
  Hex_Digit_Display hex_digit_display_5 (.value(LedData[19:16]));  // open: dp
  Adder #(.width(32)) adder_1 (.a(IF_PC), .b(32'h4), .out(adder_1_out));  // open: cin, cout
  and and_3 (and_3_out, \数据相关 , not_1_out);
  not not_1 (not_1_out, register_1_q);
  Hex_Digit_Display hex_digit_display_6 (.value(LedData[11:8]));  // open: dp
  Hex_Digit_Display hex_digit_display_7 (.value(LedData[7:4]));  // open: dp
  Clock #(.highDuration(1), .lowDuration(1)) clock_1 (.out(clock_1_out));
  // Probe on EX_PC[19:0]
  // Mips_Probe mips_probe_3: pin names not known; wires that end beside it: clock_1_out, EX_IR, CLK
  Counter #(.width(16), .max('hffff), .ongoal("wrap"), .trigger("rising"), .behavior("old")) counter_2 (
    .count(and_3_out), .Q(\插入气泡数 ), .clk(CLK), .clr(RST));  // open: load, D, carry, preset
  Hex_Digit_Display hex_digit_display_8 (.value(LedData[3:0]));  // open: dp
  or or_3 (or_3_out, RST, BRANCH);
  // Mips_Probe mips_probe_4: pin names not known; wires that end beside it: IF_IR
  ROM #(.addrWidth(10), .dataWidth(32), .Select("high")) rom_1 (.addr(IF_PC[11:2]), .data(IF_IR));
  or or_4 (or_4_out, \数据相关 , register_1_q);
  // Probe on \总周期数 
  // Probe on M_PC[19:0]
  // Mips_Probe mips_probe_5: pin names not known; wires that end beside it: MEM_IR
  \数据相关检测  \u_数据相关检测_1  (
    .ID_R1(multiplexer_2_out), .EX_WriteReg(ID_EX_wbout5), .EX_RegWrite(EX_CTRL[7]),
    .MEM_WriteReg(ex_mem_1_wbout5), .MEM_RegWrite(Mem_RegWrite), .OP(ID_IR[31:26]), .Func(ID_IR[5:0]),
    .ID_R2(multiplexer_3_out), .\数据相关 (\数据相关 ));
  IF_ID if_id_1 (
    .IRin32(IF_IR), .PCin32(IF_PC), .\传输状态In_表明当前传输数据有效 (1'b1), .CLK(CLK), .IRout32(ID_IR), .PCout32(ID_PC),
    .\传输状态Out_表明当前传输数据有效 (\if_id_1_传输状态out_表明当前传输数据有效 ), .\同步清零_气泡_高电平有效 (or_3_out),
    .\使能端_低电平有效_stall_高电平有效 (or_4_out));  // open: CTin16, CTout16
  // Probe on \总周期数 
  // Probe on \无条件分支数 
  // Probe on \条件分支成功数 
  // Probe on \插入气泡数 
  // Probe on \LoadUse次数 
  // Probe on IF_PC[11:0]
  // Probe on WB_PC[19:0]
  // Mips_Probe mips_probe_6: pin names not known; wires that end beside it: WB_IR
  Multiplexer #(.select(1), .width(5), .disabled("Z"), .enable("false")) multiplexer_2 (
    .in0(ID_IR[25:21]), .in1(5'b00100), .out(multiplexer_2_out), .sel(CTRL[4]));
  Multiplexer #(.select(1), .width(5), .disabled("Z"), .enable("false")) multiplexer_3 (
    .in0(ID_IR[20:16]), .in1(5'b00010), .out(multiplexer_3_out), .sel(CTRL[4]));
  Multiplexer #(.select(1), .width(5), .disabled("Z"), .enable("false")) multiplexer_4 (
    .in0(ID_IR[20:16]), .in1(ID_IR[15:11]), .out(multiplexer_4_out), .sel(CTRL[5]));
  // Probe on EX_PC[11:0]
  // Probe on ID_PC[11:0]
  \单周期硬布线控制器  \u_单周期硬布线控制器_1  (
    .OP(ID_IR[31:26]), .Func(ID_IR[5:0]), .ALU_OP(CTRL[3:0]), .MemToReg(CTRL[10]), .MemWrite(CTRL[9]),
    .BLTZ(CTRL4[3]), .LH(CTRL4[2]), .SRAV(CTRL4[1]), .XORI(CTRL4[0]), .ALU_SRC(CTRL[8]), .RegWrite(CTRL[7]),
    .SysCALL(CTRL[4]), .SignedExt(CTRL[13]), .RegDst(CTRL[5]), .Beq(CTRL[12]), .Bne(CTRL[11]), .JR(CTRL[14]),
    .JMP(CTRL[15]), .JAL(CTRL[6]));
  Multiplexer #(.select(1), .width(5), .disabled("Z"), .enable("false")) multiplexer_5 (
    .in0(multiplexer_4_out), .in1({5{1'b1}}), .out(multiplexer_5_out), .sel(CTRL[6]));
  // Probe on M_PC[11:0]
  D_Flip_Flop #(.trigger("high"), .Pre_Clr_Positions("LEGACY"), .NegatePresetClear("false"), .enable("true"), .NewFFLayout("false")) d_ff_1 (.Q(d_ff_1_q));  // open: clk, D, Qn, preset, en, reset
  // Probe on 13'hc
  assign bit_extender_1_out = {{16{1'b0}}, ID_IR[15:0]};  // Bit_Extender bit_extender_1
  assign bit_extender_2_out = {{16{ID_IR[15]}}, ID_IR[15:0]};  // Bit_Extender bit_extender_2
  assign bit_extender_3_out = {{6{ID_IR[25]}}, ID_IR[25:0]};  // Bit_Extender bit_extender_3
  // Probe on WB_PC[11:0]
  Comparator #(.width(13), .mode("twosComplement")) comparator_1 (
    .a(CNT_num), .b(13'hc), .eq(comparator_1_eq), .lt(comparator_1_lt));  // open: gt
  Clock #(.highDuration(1), .lowDuration(1)) clock_2 (.out(clock_2_out));
  MIPS_Regifile mips_regifile_1 (
    .Din(RDin), .Clk(CLK), .R1(mips_regifile_1_r1), .R2(mips_regifile_1_r2), .WE(RegWrite),
    .W_num(mem_wb_1_wbout5), .R1_num(multiplexer_2_out), .R2_num(multiplexer_3_out));
  Multiplexer #(.select(1), .width(32), .disabled("Z"), .enable("false")) multiplexer_6 (
    .in0(bit_extender_1_out), .in1(bit_extender_2_out), .out(multiplexer_6_out), .sel(CTRL[13]));
  Shifter #(.width(32), .shift("ll")) shifter_1 (.in(bit_extender_3_out), .\dist (5'b00010), .out(shifter_1_out));
  nand nand_1 (nand_1_out, d_ff_1_q, comparator_1_eq);
  Counter #(.width(13), .max('h1fff), .ongoal("stay"), .trigger("rising"), .behavior("old")) counter_3 (
    .count(comparator_1_lt), .Q(CNT_num), .clk(clock_2_out));  // open: load, D, carry, clr, preset
  assign CLK = nand_1_out ? clock_2_out : 1'bz;  // Controlled_Buffer controlled_buffer_1
  or or_5 (or_5_out, RST, \数据相关 , BRANCH);
  ID_EX ID_EX (
    .R1in32(mips_regifile_1_r1), .R2in32(mips_regifile_1_r2), .IRin32(ID_IR), .PCin32(ID_PC),
    .IMMin32(multiplexer_6_out), .WBin5(multiplexer_5_out), .SHin5(ID_IR[10:6]), .CTin16(CTRL),
    .\传输状态In_表明当前传输数据有效 (\if_id_1_传输状态out_表明当前传输数据有效 ), .CLK(CLK), .R1out32(EX_R1), .R2out32(ID_EX_r2out32),
    .IRout32(EX_IR), .PCout32(EX_PC), .R1out32_2(ID_EX_r1out32_2), .WBout5(ID_EX_wbout5),
    .SHout5_3(ID_EX_shout5_3), .CTout16(EX_CTRL), .\传输状态Out_表明当前传输数据有效 (\ID_EX_传输状态out_表明当前传输数据有效 ),
    .\同步清零_气泡_高电平有效 (or_5_out), .\使能端_低电平有效_stall_高电平有效 (register_1_q), ._26in32(shifter_1_out),
    .R1out32_3(ID_EX_r1out32_3), .CTRL4(CTRL4),
    .CTRL4_2({EX_BLTZ, ID_EX_ctrl4_2[2], EX_SRAV, ID_EX_ctrl4_2[0]}));  // open: FWR1in2, WBout5_2, FWR2in2, SHout5_4, ERETin1_2, SHout5_2, ERETin1, SHout5
  Pull_Resistor #(.pull(1)) pull_resistor_1 (.node(CLK));
  and and_4 (and_4_out, Led, EX_CTRL[4]);
  Register #(.width(32), .trigger("rising"), .Select("low")) register_2 (
    .D(EX_R1), .en(and_4_out), .Q(register_2_q), .clk(CLK));  // open: clr
  Multiplexer #(.select(1), .width(32), .disabled("Z"), .enable("false")) multiplexer_7 (
    .in0(ID_EX_r2out32), .in1(ID_EX_r1out32_2), .out(multiplexer_7_out), .sel(EX_CTRL[8]));
  Shifter #(.width(32), .shift("ll")) shifter_2 (.in(ID_EX_r1out32_2), .\dist (5'b00010), .out(shifter_2_out));
  Multiplexer #(.select(1), .width(5), .disabled("Z"), .enable("false")) multiplexer_8 (
    .in0(ID_EX_shout5_3), .in1(EX_R1[4:0]), .out(multiplexer_8_out), .sel(EX_SRAV));
  Adder #(.width(32)) adder_2 (.a(EX_PC), .b(32'h4), .out(adder_2_out));  // open: cin, cout
  MIPS_ALU mips_alu_1 (
    .X(EX_R1), .Y(multiplexer_7_out), .AluOP(EX_CTRL[3:0]), .Equal(equal), .Result(mips_alu_1_result),
    .shamt(multiplexer_8_out));  // open: Result_2
  Comparator #(.width(32), .mode("twosComplement")) comparator_2 (
    .a(ID_EX_r2out32), .b(32'h22), .eq(Led));  // open: gt, lt
  Adder #(.width(32)) adder_3 (.a(shifter_2_out), .b(adder_2_out), .out(adder_3_out));  // open: cin, cout
  Multiplexer #(.select(1), .width(32), .disabled("Z"), .enable("false")) multiplexer_9 (
    .in0(adder_2_out), .in1(adder_3_out), .out(multiplexer_9_out), .sel(EX_BRANCH));
  Multiplexer #(.select(1), .width(32), .disabled("Z"), .enable("false")) multiplexer_10 (
    .in0(ID_EX_r1out32_3), .in1(EX_R1), .out(multiplexer_10_out), .sel(EX_CTRL[14]));
  Multiplexer #(.select(1), .width(32), .disabled("Z"), .enable("false")) multiplexer_11 (
    .in0(multiplexer_9_out), .in1(adder_3_out), .out(multiplexer_11_out), .sel(BLTZ));
  EX_MEM ex_mem_1 (
    .ALUin32(mips_alu_1_result), .Memin32(ID_EX_r2out32), .IRin32(EX_IR), .PCin32(EX_PC),
    .WBin5(ID_EX_wbout5), .CTin16_2(EX_CTRL), .\传输状态In_表明当前传输数据有效 (\ID_EX_传输状态out_表明当前传输数据有效 ), .CLK(CLK),
    .ALUout32(ex_mem_1_aluout32), .Memout32(MDin), .IRout32(MEM_IR), .PCout32(M_PC),
    .WBout5(ex_mem_1_wbout5),
    .CTout16_6({ex_mem_1_ctout16_6[15:10], MemWrite, ex_mem_1_ctout16_6[8], Mem_RegWrite, ex_mem_1_ctout16_6[6:0]}),
    .\传输状态Out_表明当前传输数据有效 (\ex_mem_1_传输状态out_表明当前传输数据有效 ), .\同步清零_气泡_高电平有效 (RST),
    .\使能端_低电平有效_stall_高电平有效 (register_1_q), .LEDin32(register_2_q), .LEDout32(ex_mem_1_ledout32),
    .CTin16(Led), .CTout16(ex_mem_1_ctout16), .CTin4({EX_BLTZ, ID_EX_ctrl4_2[2], EX_SRAV, ID_EX_ctrl4_2[0]}),
    .CTout16_2({ex_mem_1_ctout16_2[3], MEM_LH, ex_mem_1_ctout16_2[1:0]}));  // open: Resullt2, CTout16_3, ERETin2, CTout16_4, ERETin2_2, CTout16_5
  Multiplexer #(.select(1), .width(32), .disabled("Z"), .enable("false")) multiplexer_12 (
    .in0(multiplexer_11_out), .in1(multiplexer_10_out), .out(multiplexer_12_out), .sel(EX_CTRL[15]));
  MIPS_RAM mips_ram_1 (
    .\字节地址 (ex_mem_1_aluout32[11:2]), .Din(MDin), .DataOut(mips_ram_1_dataout), .CLK(CLK), .WE(MemWrite),
    .Mode(ex_mem_1_aluout32[1]), .LH(MEM_LH));
  MEM_WB mem_wb_1 (
    .ALUin32(ex_mem_1_aluout32), .MDin32(mips_ram_1_dataout), .IRin32(MEM_IR), .PCin32(M_PC),
    .WBin5(ex_mem_1_wbout5),
    .CTin16_2({ex_mem_1_ctout16_6[15:10], MemWrite, ex_mem_1_ctout16_6[8], Mem_RegWrite, ex_mem_1_ctout16_6[6:0]}),
    .\传输状态In_表明当前传输数据有效 (\ex_mem_1_传输状态out_表明当前传输数据有效 ), .CLK(CLK), .ALUout32(mem_wb_1_aluout32),
    .MDout32(mem_wb_1_mdout32), .IRout32(WB_IR), .PCout32(WB_PC), .WBout5(mem_wb_1_wbout5),
    .CTout16_6({mem_wb_1_ctout16_6[15:8], RegWrite, mem_wb_1_ctout16_6[6:0]}), .\同步清零_气泡_高电平有效 (RST),
    .\使能端_低电平有效_stall_高电平有效 (register_1_q), .LEDin32(ex_mem_1_ledout32), .LEDout32(LedData),
    .CTin16(ex_mem_1_ctout16), .CTout16_5(mem_wb_1_ctout16_5),
    .CTin4({ex_mem_1_ctout16_2[3], MEM_LH, ex_mem_1_ctout16_2[1:0]}));  // open: 传输状态Out_表明当前传输数据有效, CTout16, CTout16_2, RE2in32, ERETin1, CTout16_3, ERETin1_2, CTout16_4
  Multiplexer #(.select(1), .width(32), .disabled("Z"), .enable("false")) multiplexer_13 (
    .in0(mem_wb_1_aluout32), .in1(mem_wb_1_mdout32), .out(multiplexer_13_out), .sel(mem_wb_1_ctout16_6[10]));
  Multiplexer #(.select(1), .width(32), .disabled("Z"), .enable("false")) multiplexer_14 (
    .in0(multiplexer_13_out), .in1(adder_4_out), .out(RDin), .sel(mem_wb_1_ctout16_6[6]));
  Adder #(.width(32)) adder_4 (.a(WB_PC), .b(32'h4), .out(adder_4_out));  // open: cin, cout
  or or_6 (or_6_out, BLTZ, EX_BRANCH);
  Counter #(.width(16), .max('hffff), .ongoal("wrap"), .trigger("rising"), .behavior("old")) counter_4 (
    .count(EX_CTRL[15]), .Q(\无条件分支数 ), .clk(CLK), .clr(RST));  // open: load, D, carry, preset
  Counter #(.width(16), .max('hffff), .ongoal("wrap"), .trigger("rising"), .behavior("old")) counter_5 (
    .count(or_6_out), .Q(\条件分支成功数 ), .clk(CLK), .clr(RST));  // open: load, D, carry, preset
  Comparator #(.width(32), .mode("twosComplement")) comparator_3 (
    .a(EX_R1), .b({32{1'b0}}), .lt(comparator_3_lt));  // open: gt, eq
  and and_5 (and_5_out, equal, EX_CTRL[12]);
  and and_6 (and_6_out, ~equal, EX_CTRL[11]);  // AND_Gate
  and and_7 (BLTZ, comparator_3_lt, EX_BLTZ);
  or or_7 (EX_BRANCH, and_5_out, and_6_out);

  // Other names for the same wires on the sheet: SignedExt = CTRL[13]; EX_RegWrite = EX_CTRL[7]; EX_JR = EX_CTRL[14];
  //   EX_JMP = EX_CTRL[15]; MEM_PC[31:0] = M_PC

  // Notes on the sheet:
  //   中断源
  //   时空图监测，可删除
  //   中断等待指示
  //   数码管输出
  //   指令存储器
  //   contents of rom_1 (hex, n*v repeats v):
  //   20110001 8000c05 20110001 20120002 20130003 8000c09 20110001 20120002 20130003 8000c0d 20110001
  //   20120002 20130003 8000c11 20110001 20120002 20130003 c000cf7 20100001 20110001 118fc0 112020
  //   20020022 c 118882 12200001 8000c15 112020 20020022 c 20110001 118880 112020 20020022 c 12200001
  //   8000c1f 20110001 118fc0 112020 20020022 c 1188c3 112020 20020022 c 118903 112020 20020022 c 118903
  //   112020 20020022 c 118903 112020 20020022 c 118903 112020 20020022 c 118903 112020 20020022 c 118903
  //   112020 20020022 c 118903 112020 20020022 c 20100001 109fc0 139fc3 8021 2012000c 24160003 26100001
  //   3210000f 20080008 20090001 139900 2709825 132020 20020022 c 1094022 1500fff9 22100001 2018000f
  //   2188024 108700 20080008 20090001 139902 2709825 132021 20020022 c 1094022 1500fff9 108702 2c9b022
  //   12c00001 8000c50 4020 1084027 84400 3508ffff 82021 20020022 c 2010ffff 20110000 ae300000 22100001
  //   22310004 ae300000 22100001 22310004 ae300000 22100001 22310004 ae300000 22100001 22310004 ae300000
  //   22100001 22310004 ae300000 22100001 22310004 ae300000 22100001 22310004 ae300000 22100001 22310004
  //   ae300000 22100001 22310004 ae300000 22100001 22310004 ae300000 22100001 22310004 ae300000 22100001
  //   22310004 ae300000 22100001 22310004 ae300000 22100001 22310004 ae300000 22100001 22310004 ae300000
  //   22100001 22310004 22100001 8020 2011003c 8e130000 8e340000 274402a 11000002 ae330000 ae140000
  //   2231fffc 1611fff8 102020 20020022 c 22100004 2011003c 1611fff2 20020032 c 20080001 20090003 20110876
  //   118d00 112020 20020022 c 200b0008 1118807 1318807 112020 20020022 c 216bffff 1560fff9 2002000a c
  //   2008ffff 20117777 112020 20020022 c 200b0010 3a31ffff 112020 20020022 c 216bffff 1560fffa 2002000a c
  //   20090000 200b0010 34118483 20120404 118c00 129400 36318281 22520404 ad310000 2328820 21290004
  //   216bffff 1560fffb 200b0020 20090000 85310000 112020 20020022 c 21290002 216bffff 1560fff9 2002000a c
  //   2011fff1 112020 20020022 c 22310001 620fffb 2002000a c 20100000 22100001 102020 20020022 c 22100002
  //   102020 20020022 c 22100003 102020 20020022 c 22100004 102020 20020022 c 22100005 102020 20020022 c
  //   22100006 102020 20020022 c 22100007 102020 20020022 c 22100008 102020 20020022 20020022 c 3e00008
  //   OP
  //   Func
  //   rs
  //   rt
  //   rd
  //   JMP
  //   JR
  //   OP
  //   Func
  //   Syscall
  //   控制位
  //   Beq
  //   Bne
  //   AluOP
  //   AluSrcB
  //   RegWrite
  //   JAL
  //   RegDst
  //   流水调试日志用
  //   暂停节拍，不能为0
  //   MemToReg
  //   MemWrite
  //   戳工具置1进入计数暂停模式，ctrl+k时钟自动运行到对应节拍暂停
  //   ctrl+k关闭时钟连续运行，将控制位置零，进入单步调试模式调试
  //   可计数暂停的时钟源
  //   Syscall
  //   AluSrcB
  //   RegWrite
  //   AluOP
  //   为方便自动评测，需要输出流水线各段保存的PC值，注意是PC不是PC+4，另外ID段寄存器写入信息，Mem段内存写入信息也要输出
  //   MemWrite
  //   JAL
  //   Bne
endmodule
module \重定向流水线  (
  output RegWrite,
  output MemWrite,
  output [31:0] IF_PC,
  output [31:0] ID_PC,
  output [31:0] EX_PC,
  output [31:0] M_PC,
  output [31:0] WB_PC,
  output [31:0] RDin,
  output [31:0] MDin,
  output [31:0] LedData
);

  wire and_1_out, and_2_out, and_3_out, and_4_out, and_5_out, and_6_out, BLTZ, BRANCH, CLK, clock_1_out,
       clock_2_out, comparator_1_eq, comparator_1_lt, comparator_3_lt, d_ff_1_q, equal, EX_BLTZ, EX_BRANCH,
       ex_mem_1_ctout16, \ex_mem_1_传输状态out_表明当前传输数据有效 , EX_SRAV, Go, \ID_EX_传输状态out_表明当前传输数据有效 ,
       \if_id_1_传输状态out_表明当前传输数据有效 , IR1, IR2, IR3, Led, \load_use相关 , MEM_LH, Mem_MemToReg, Mem_RegWrite,
       mem_wb_1_ctout16_5, nand_1_out, not_1_out, or_1_out, or_3_out, or_4_out, or_5_out, or_6_out,
       register_1_q, RST, W1, W2, W3;
  wire [1:0] F, ForwardR1, ForwardR2, ID_EX_wbout5_2;
  wire [2:0] ID_EX_ctrl4_2;
  wire [3:0] CTRL4, ex_mem_1_ctout16_2;
  wire [4:0] ex_mem_1_wbout5, ID_EX_shout5_3, ID_EX_wbout5, mem_wb_1_wbout5, multiplexer_2_out,
       multiplexer_3_out, multiplexer_4_out, multiplexer_5_out, multiplexer_8_out;
  wire [12:0] CNT_num;
  wire [15:0] adder_5_out, CTRL, EX_CTRL, ex_mem_1_ctout16_6, \LoadUse次数 , mem_wb_1_ctout16_6,
       multiplier_1_out, \总周期数 , \插入气泡数 , \无条件分支数 , \条件分支成功数 ;
  wire [31:0] adder_1_out, adder_2_out, adder_3_out, adder_4_out, ALURes, bit_extender_1_out,
       bit_extender_2_out, bit_extender_3_out, EX_IR, ex_mem_1_ledout32, EX_R1, EX_R2, EXALU, ID_EX_r1out32,
       ID_EX_r1out32_2, ID_EX_r1out32_3, ID_IR, IF_IR, MEM_IR, mips_alu_1_result, mips_ram_1_dataout,
       mips_regifile_1_r1, mips_regifile_1_r2, multiplexer_1_out, multiplexer_6_out, multiplexer_9_out,
       multiplexer_10_out, multiplexer_11_out, multiplexer_12_out, multiplexer_13_out, multiplexer_14_out,
       R2, RD, register_2_q, shifter_1_out, shifter_2_out, WB_IR;

  Button \u_总复位  (.out(RST));
  Button _1 (.out(IR1));
  Button _2 (.out(IR2));
  Button _3 (.out(IR3));
  // Probe on \总周期数 
  // Probe on \总周期数 
  Button \u_继续运行  (.out(Go));
  LED #(.active("true")) led_1 (.in(W1));
  LED #(.active("true")) led_2 (.in(W2));
  LED #(.active("true")) led_3 (.in(W3));
  Hex_Digit_Display hex_digit_display_1 (.value(LedData[31:28]));  // open: dp
  // Probe on IF_PC[19:0]
  // Mips_Probe mips_probe_1: pin names not known; wires that end beside it: IF_IR
  Hex_Digit_Display hex_digit_display_2 (.value(LedData[27:24]));  // open: dp
  Hex_Digit_Display hex_digit_display_3 (.value(LedData[23:20]));  // open: dp
  // Probe on ID_PC[19:0]
  // Mips_Probe mips_probe_2: pin names not known; wires that end beside it: ID_IR
  and and_1 (and_1_out, mem_wb_1_ctout16_6[4], ~mem_wb_1_ctout16_5);  // AND_Gate
  Hex_Digit_Display hex_digit_display_4 (.value(LedData[15:12]));  // open: dp
  Hex_Digit_Display hex_digit_display_5 (.value(LedData[19:16]));  // open: dp
  and and_2 (and_2_out, ~\load_use相关 , not_1_out);  // AND_Gate
  Register #(.width(1), .trigger("rising"), .Select("low")) register_1 (
    .D(mem_wb_1_ctout16_6[4]), .en(and_1_out), .Q(register_1_q), .clk(CLK), .clr(or_1_out));
  or or_1 (or_1_out, RST, Go);
  Multiplexer #(.select(1), .width(32), .disabled("Z"), .enable("false")) multiplexer_1 (
    .in0(adder_1_out), .in1(multiplexer_13_out), .out(multiplexer_1_out), .sel(BRANCH));
  or or_2 (BRANCH, EX_BRANCH, BLTZ, EX_CTRL[15]);
  Hex_Digit_Display hex_digit_display_6 (.value(LedData[7:4]));  // open: dp
  Hex_Digit_Display hex_digit_display_7 (.value(LedData[11:8]));  // open: dp
  Clock #(.highDuration(1), .lowDuration(1)) clock_1 (.out(clock_1_out));
  // Probe on EX_PC[19:0]
  // Mips_Probe mips_probe_3: pin names not known; wires that end beside it: clock_1_out, EX_IR, CLK
  Register #(.width(32), .trigger("rising"), .Select("low")) PC (
    .D(multiplexer_1_out), .en(and_2_out), .Q(IF_PC), .clk(CLK), .clr(RST));
  Counter #(.width(16), .max('hffff), .ongoal("wrap"), .trigger("rising"), .behavior("old")) counter_1 (
    .count(not_1_out), .Q(\总周期数 ), .clk(CLK), .clr(RST));  // open: load, D, carry, preset
  not not_1 (not_1_out, register_1_q);
  Hex_Digit_Display hex_digit_display_8 (.value(LedData[3:0]));  // open: dp
  Adder #(.width(32)) adder_1 (.a(IF_PC), .b(32'h4), .out(adder_1_out));  // open: cin, cout
  and and_3 (and_3_out, \load_use相关 , not_1_out);
  // Probe on \总周期数 
  // Probe on M_PC[19:0]
  // Mips_Probe mips_probe_4: pin names not known; wires that end beside it: MEM_IR
  \load_use相关检测  \load_use相关检测_1  (
    .MEM_MemToReg(Mem_MemToReg), .ID_R1(multiplexer_2_out), .EX_WriteReg(ID_EX_wbout5),
    .EX_RegWrite(EX_CTRL[7]), .MEM_WriteReg(ex_mem_1_wbout5), .MEM_RegWrite(Mem_RegWrite), .OP(ID_IR[31:26]),
    .Func(ID_IR[5:0]), .ID_R2(multiplexer_3_out), .ForwardToR1(ForwardR1), .\Load_Use相关 (\load_use相关 ),
    .ForwardToR2(ForwardR2), .EX_MemToReg(EX_CTRL[10]));
  ROM #(.addrWidth(10), .dataWidth(32), .Select("high")) rom_1 (.addr(IF_PC[11:2]), .data(IF_IR));
  Counter #(.width(16), .max('hffff), .ongoal("wrap"), .trigger("rising"), .behavior("old")) counter_2 (
    .count(and_3_out), .Q(\LoadUse次数 ), .clk(CLK), .clr(RST));  // open: load, D, carry, preset
  // Probe on \总周期数 
  // Probe on \无条件分支数 
  // Probe on \条件分支成功数 
  // Probe on \插入气泡数 
  // Probe on \LoadUse次数 
  or or_3 (or_3_out, RST, BRANCH);
  IF_ID if_id_1 (
    .IRin32(IF_IR), .PCin32(IF_PC), .\传输状态In_表明当前传输数据有效 (1'b1), .CLK(CLK), .IRout32(ID_IR), .PCout32(ID_PC),
    .\传输状态Out_表明当前传输数据有效 (\if_id_1_传输状态out_表明当前传输数据有效 ), .\同步清零_气泡_高电平有效 (or_3_out),
    .\使能端_低电平有效_stall_高电平有效 (or_4_out));  // open: CTin16, CTout16
  or or_4 (or_4_out, \load_use相关 , register_1_q);
  // Probe on IF_PC[11:0]
  // Probe on WB_PC[19:0]
  // Mips_Probe mips_probe_5: pin names not known; wires that end beside it: WB_IR
  // Probe on EX_PC[11:0]
  // Probe on ID_PC[11:0]
  // Probe on M_PC[11:0]
  D_Flip_Flop #(.trigger("high"), .Pre_Clr_Positions("LEGACY"), .NegatePresetClear("false"), .enable("true"), .NewFFLayout("false")) d_ff_1 (.Q(d_ff_1_q));  // open: clk, D, Qn, preset, en, reset
  // Probe on 13'hc
  Multiplexer #(.select(1), .width(5), .disabled("Z"), .enable("false")) multiplexer_2 (
    .in0(ID_IR[25:21]), .in1(5'b00100), .out(multiplexer_2_out), .sel(CTRL[4]));
  Multiplexer #(.select(1), .width(5), .disabled("Z"), .enable("false")) multiplexer_3 (
    .in0(ID_IR[20:16]), .in1(5'b00010), .out(multiplexer_3_out), .sel(CTRL[4]));
  Multiplexer #(.select(1), .width(5), .disabled("Z"), .enable("false")) multiplexer_4 (
    .in0(ID_IR[20:16]), .in1(ID_IR[15:11]), .out(multiplexer_4_out), .sel(CTRL[5]));
  Multiplexer #(.select(1), .width(5), .disabled("Z"), .enable("false")) multiplexer_5 (
    .in0(multiplexer_4_out), .in1({5{1'b1}}), .out(multiplexer_5_out), .sel(CTRL[6]));
  // Probe on WB_PC[11:0]
  Comparator #(.width(13), .mode("twosComplement")) comparator_1 (
    .a(CNT_num), .b(13'hc), .eq(comparator_1_eq), .lt(comparator_1_lt));  // open: gt
  Clock #(.highDuration(1), .lowDuration(1)) clock_2 (.out(clock_2_out));
  \单周期硬布线控制器  \u_单周期硬布线控制器_1  (
    .OP(ID_IR[31:26]), .Func(ID_IR[5:0]), .ALU_OP(CTRL[3:0]), .MemToReg(CTRL[10]), .MemWrite(CTRL[9]),
    .BLTZ(CTRL4[3]), .LH(CTRL4[2]), .SRAV(CTRL4[1]), .XORI(CTRL4[0]), .ALU_SRC(CTRL[8]), .RegWrite(CTRL[7]),
    .SysCALL(CTRL[4]), .SignedExt(CTRL[13]), .RegDst(CTRL[5]), .Beq(CTRL[12]), .Bne(CTRL[11]), .JR(CTRL[14]),
    .JMP(CTRL[15]), .JAL(CTRL[6]));
  assign bit_extender_1_out = {{16{1'b0}}, ID_IR[15:0]};  // Bit_Extender bit_extender_1
  assign bit_extender_2_out = {{16{ID_IR[15]}}, ID_IR[15:0]};  // Bit_Extender bit_extender_2
  assign bit_extender_3_out = {{6{ID_IR[25]}}, ID_IR[25:0]};  // Bit_Extender bit_extender_3
  nand nand_1 (nand_1_out, d_ff_1_q, comparator_1_eq);
  Counter #(.width(13), .max('h1fff), .ongoal("stay"), .trigger("rising"), .behavior("old")) counter_3 (
    .count(comparator_1_lt), .Q(CNT_num), .clk(clock_2_out));  // open: load, D, carry, clr, preset
  MIPS_Regifile mips_regifile_1 (
    .Din(RDin), .Clk(CLK), .R1(mips_regifile_1_r1), .R2(mips_regifile_1_r2), .WE(RegWrite),
    .W_num(mem_wb_1_wbout5), .R1_num(multiplexer_2_out), .R2_num(multiplexer_3_out));
  Multiplexer #(.select(1), .width(32), .disabled("Z"), .enable("false")) multiplexer_6 (
    .in0(bit_extender_1_out), .in1(bit_extender_2_out), .out(multiplexer_6_out), .sel(CTRL[13]));
  assign CLK = nand_1_out ? clock_2_out : 1'bz;  // Controlled_Buffer controlled_buffer_1
  Shifter #(.width(32), .shift("ll")) shifter_1 (.in(bit_extender_3_out), .\dist (5'b00010), .out(shifter_1_out));
  Pull_Resistor #(.pull(1)) pull_resistor_1 (.node(CLK));
  or or_5 (or_5_out, RST, \load_use相关 , BRANCH);
  ID_EX ID_EX (
    .R1in32(mips_regifile_1_r1), .R2in32(mips_regifile_1_r2), .IRin32(ID_IR), .PCin32(ID_PC),
    .IMMin32(multiplexer_6_out), .WBin5(multiplexer_5_out), .SHin5(ID_IR[10:6]), .CTin16(CTRL),
    .\传输状态In_表明当前传输数据有效 (\if_id_1_传输状态out_表明当前传输数据有效 ), .CLK(CLK), .R1out32(ID_EX_r1out32), .R2out32(EX_R2),
    .IRout32(EX_IR), .PCout32(EX_PC), .R1out32_2(ID_EX_r1out32_2), .WBout5(ID_EX_wbout5),
    .SHout5_3(ID_EX_shout5_3), .CTout16(EX_CTRL), .\传输状态Out_表明当前传输数据有效 (\ID_EX_传输状态out_表明当前传输数据有效 ),
    .\同步清零_气泡_高电平有效 (or_5_out), .\使能端_低电平有效_stall_高电平有效 (register_1_q), ._26in32(shifter_1_out),
    .R1out32_3(ID_EX_r1out32_3), .FWR1in2(ForwardR1), .WBout5_2(ID_EX_wbout5_2), .FWR2in2(ForwardR2),
    .SHout5_4(F), .CTRL4(CTRL4), .CTRL4_2({EX_BLTZ, ID_EX_ctrl4_2[2], EX_SRAV, ID_EX_ctrl4_2[0]}));  // open: ERETin1_2, SHout5_2, ERETin1, SHout5
  Register #(.width(32), .trigger("rising"), .Select("low")) register_2 (
    .D(EX_R1), .en(and_4_out), .Q(register_2_q), .clk(CLK));  // open: clr
  and and_4 (and_4_out, Led, EX_CTRL[4]);
  Multiplexer #(.select(2), .width(32), .disabled("Z"), .enable("false")) multiplexer_7 (
    .in0(ID_EX_r1out32), .in1(ALURes), .in2(RD), .in3(EXALU), .out(EX_R1), .sel(ID_EX_wbout5_2));
  Shifter #(.width(32), .shift("ll")) shifter_2 (.in(ID_EX_r1out32_2), .\dist (5'b00010), .out(shifter_2_out));
  Multiplexer #(.select(1), .width(5), .disabled("Z"), .enable("false")) multiplexer_8 (
    .in0(ID_EX_shout5_3), .in1(EX_R1[4:0]), .out(multiplexer_8_out), .sel(EX_SRAV));
  Adder #(.width(32)) adder_2 (.a(EX_PC), .b(32'h4), .out(adder_2_out));  // open: cin, cout
  Multiplexer #(.select(1), .width(32), .disabled("Z"), .enable("false")) multiplexer_9 (
    .in0(R2), .in1(ID_EX_r1out32_2), .out(multiplexer_9_out), .sel(EX_CTRL[8]));
  Comparator #(.width(32), .mode("twosComplement")) comparator_2 (.a(R2), .b(32'h22), .eq(Led));  // open: gt, lt
  Adder #(.width(32)) adder_3 (.a(shifter_2_out), .b(adder_2_out), .out(adder_3_out));  // open: cin, cout
  MIPS_ALU mips_alu_1 (
    .X(EX_R1), .Y(multiplexer_9_out), .AluOP(EX_CTRL[3:0]), .Equal(equal), .Result(mips_alu_1_result),
    .shamt(multiplexer_8_out));  // open: Result_2
  Multiplexer #(.select(1), .width(32), .disabled("Z"), .enable("false")) multiplexer_10 (
    .in0(ID_EX_r1out32_3), .in1(EX_R1), .out(multiplexer_10_out), .sel(EX_CTRL[14]));
  Multiplexer #(.select(1), .width(32), .disabled("Z"), .enable("false")) multiplexer_11 (
    .in0(adder_2_out), .in1(adder_3_out), .out(multiplexer_11_out), .sel(EX_BRANCH));
  EX_MEM ex_mem_1 (
    .ALUin32(mips_alu_1_result), .Memin32(R2), .IRin32(EX_IR), .PCin32(EX_PC), .WBin5(ID_EX_wbout5),
    .CTin16_2(EX_CTRL), .\传输状态In_表明当前传输数据有效 (\ID_EX_传输状态out_表明当前传输数据有效 ), .CLK(CLK), .ALUout32(EXALU),
    .Memout32(MDin), .IRout32(MEM_IR), .PCout32(M_PC), .WBout5(ex_mem_1_wbout5),
    .CTout16_6({ex_mem_1_ctout16_6[15:11], Mem_MemToReg, MemWrite, ex_mem_1_ctout16_6[8], Mem_RegWrite, ex_mem_1_ctout16_6[6:0]}),
    .\传输状态Out_表明当前传输数据有效 (\ex_mem_1_传输状态out_表明当前传输数据有效 ), .\同步清零_气泡_高电平有效 (RST),
    .\使能端_低电平有效_stall_高电平有效 (register_1_q), .LEDin32(register_2_q), .LEDout32(ex_mem_1_ledout32),
    .CTin16(Led), .CTout16(ex_mem_1_ctout16), .CTin4({EX_BLTZ, ID_EX_ctrl4_2[2], EX_SRAV, ID_EX_ctrl4_2[0]}),
    .CTout16_2({ex_mem_1_ctout16_2[3], MEM_LH, ex_mem_1_ctout16_2[1:0]}));  // open: Resullt2, CTout16_3, ERETin2, CTout16_4, ERETin2_2, CTout16_5
  Multiplexer #(.select(1), .width(32), .disabled("Z"), .enable("false")) multiplexer_12 (
    .in0(multiplexer_11_out), .in1(adder_3_out), .out(multiplexer_12_out), .sel(BLTZ));
  Multiplexer #(.select(1), .width(32), .disabled("Z"), .enable("false")) multiplexer_13 (
    .in0(multiplexer_12_out), .in1(multiplexer_10_out), .out(multiplexer_13_out), .sel(EX_CTRL[15]));
  MIPS_RAM mips_ram_1 (
    .\字节地址 (EXALU[11:2]), .Din(MDin), .DataOut(mips_ram_1_dataout), .CLK(CLK), .WE(MemWrite),
    .Mode(EXALU[1]), .LH(MEM_LH));
  MEM_WB mem_wb_1 (
    .ALUin32(EXALU), .MDin32(mips_ram_1_dataout), .IRin32(MEM_IR), .PCin32(M_PC), .WBin5(ex_mem_1_wbout5),
    .CTin16_2({ex_mem_1_ctout16_6[15:11], Mem_MemToReg, MemWrite, ex_mem_1_ctout16_6[8], Mem_RegWrite, ex_mem_1_ctout16_6[6:0]}),
    .\传输状态In_表明当前传输数据有效 (\ex_mem_1_传输状态out_表明当前传输数据有效 ), .CLK(CLK), .ALUout32(ALURes), .MDout32(RD),
    .IRout32(WB_IR), .PCout32(WB_PC), .WBout5(mem_wb_1_wbout5),
    .CTout16_6({mem_wb_1_ctout16_6[15:8], RegWrite, mem_wb_1_ctout16_6[6:0]}), .\同步清零_气泡_高电平有效 (RST),
    .\使能端_低电平有效_stall_高电平有效 (register_1_q), .LEDin32(ex_mem_1_ledout32), .LEDout32(LedData),
    .CTin16(ex_mem_1_ctout16), .CTout16_5(mem_wb_1_ctout16_5),
    .CTin4({ex_mem_1_ctout16_2[3], MEM_LH, ex_mem_1_ctout16_2[1:0]}));  // open: 传输状态Out_表明当前传输数据有效, CTout16, CTout16_2, RE2in32, ERETin1, CTout16_3, ERETin1_2, CTout16_4
  Multiplexer #(.select(1), .width(32), .disabled("Z"), .enable("false")) multiplexer_14 (
    .in0(ALURes), .in1(RD), .out(multiplexer_14_out), .sel(mem_wb_1_ctout16_6[10]));
  Adder #(.width(32)) adder_4 (.a(WB_PC), .b(32'h4), .out(adder_4_out));  // open: cin, cout
  Multiplexer #(.select(1), .width(32), .disabled("Z"), .enable("false")) multiplexer_15 (
    .in0(multiplexer_14_out), .in1(adder_4_out), .out(RDin), .sel(mem_wb_1_ctout16_6[6]));
  or or_6 (or_6_out, BLTZ, EX_BRANCH);
  Counter #(.width(16), .max('hffff), .ongoal("wrap"), .trigger("rising"), .behavior("old")) counter_4 (
    .count(EX_CTRL[15]), .Q(\无条件分支数 ), .clk(CLK), .clr(RST));  // open: load, D, carry, preset
  Counter #(.width(16), .max('hffff), .ongoal("wrap"), .trigger("rising"), .behavior("old")) counter_5 (
    .count(or_6_out), .Q(\条件分支成功数 ), .clk(CLK), .clr(RST));  // open: load, D, carry, preset
  Comparator #(.width(32), .mode("twosComplement")) comparator_3 (
    .a(EX_R1), .b({32{1'b0}}), .lt(comparator_3_lt));  // open: gt, eq
  and and_5 (and_5_out, equal, EX_CTRL[12]);
  and and_6 (and_6_out, ~equal, EX_CTRL[11]);  // AND_Gate
  Adder #(.width(16)) adder_5 (.a(\无条件分支数 ), .b(\条件分支成功数 ), .out(adder_5_out));  // open: cin, cout
  and and_7 (BLTZ, comparator_3_lt, EX_BLTZ);
  Multiplexer #(.select(2), .width(32), .disabled("Z"), .enable("false")) multiplexer_16 (
    .in0(EX_R2), .in1(ALURes), .in2(RD), .in3(EXALU), .out(R2), .sel(F));
  or or_7 (EX_BRANCH, and_5_out, and_6_out);
  Multiplier #(.width(16)) multiplier_1 (.a(adder_5_out), .b(16'h2), .out(multiplier_1_out));  // open: cin, cout
  Adder #(.width(16)) adder_6 (.a(multiplier_1_out), .b(\LoadUse次数 ), .out(\插入气泡数 ));  // open: cin, cout

  // Other names for the same wires on the sheet: SignedExt = CTRL[13]; EX_RegWrite = EX_CTRL[7];
  //   EX_MemToReg = EX_CTRL[10]; EX_JR = EX_CTRL[14]; EX_JMP = EX_CTRL[15]; MEM_PC[31:0] = M_PC

  // Notes on the sheet:
  //   中断源
  //   时空图监测，可删除
  //   中断等待指示
  //   数码管输出
  //   指令存储器
  //   contents of rom_1 (hex, n*v repeats v):
  //   20110001 8000c05 20110001 20120002 20130003 8000c09 20110001 20120002 20130003 8000c0d 20110001
  //   20120002 20130003 8000c11 20110001 20120002 20130003 c000cf7 20100001 20110001 118fc0 112020
  //   20020022 c 118882 12200001 8000c15 112020 20020022 c 20110001 118880 112020 20020022 c 12200001
  //   8000c1f 20110001 118fc0 112020 20020022 c 1188c3 112020 20020022 c 118903 112020 20020022 c 118903
  //   112020 20020022 c 118903 112020 20020022 c 118903 112020 20020022 c 118903 112020 20020022 c 118903
  //   112020 20020022 c 118903 112020 20020022 c 20100001 109fc0 139fc3 8021 2012000c 24160003 26100001
  //   3210000f 20080008 20090001 139900 2709825 132020 20020022 c 1094022 1500fff9 22100001 2018000f
  //   2188024 108700 20080008 20090001 139902 2709825 132021 20020022 c 1094022 1500fff9 108702 2c9b022
  //   12c00001 8000c50 4020 1084027 84400 3508ffff 82021 20020022 c 2010ffff 20110000 ae300000 22100001
  //   22310004 ae300000 22100001 22310004 ae300000 22100001 22310004 ae300000 22100001 22310004 ae300000
  //   22100001 22310004 ae300000 22100001 22310004 ae300000 22100001 22310004 ae300000 22100001 22310004
  //   ae300000 22100001 22310004 ae300000 22100001 22310004 ae300000 22100001 22310004 ae300000 22100001
  //   22310004 ae300000 22100001 22310004 ae300000 22100001 22310004 ae300000 22100001 22310004 ae300000
  //   22100001 22310004 22100001 8020 2011003c 8e130000 8e340000 274402a 11000002 ae330000 ae140000
  //   2231fffc 1611fff8 102020 20020022 c 22100004 2011003c 1611fff2 20020032 c 20080001 20090003 20110876
  //   118d00 112020 20020022 c 200b0008 1118807 1318807 112020 20020022 c 216bffff 1560fff9 2002000a c
  //   2008ffff 20117777 112020 20020022 c 200b0010 3a31ffff 112020 20020022 c 216bffff 1560fffa 2002000a c
  //   20090000 200b0010 34118483 20120404 118c00 129400 36318281 22520404 ad310000 2328820 21290004
  //   216bffff 1560fffb 200b0020 20090000 85310000 112020 20020022 c 21290002 216bffff 1560fff9 2002000a c
  //   2011fff1 112020 20020022 c 22310001 620fffb 2002000a c 20100000 22100001 102020 20020022 c 22100002
  //   102020 20020022 c 22100003 102020 20020022 c 22100004 102020 20020022 c 22100005 102020 20020022 c
  //   22100006 102020 20020022 c 22100007 102020 20020022 c 22100008 102020 20020022 20020022 c 3e00008
  //   OP
  //   rs
  //   rt
  //   rd
  //   控制位
  //   Func
  //   流水调试日志用
  //   暂停节拍，不能为0
  //   JMP
  //   JR
  //   OP
  //   Func
  //   Syscall
  //   戳工具置1进入计数暂停模式，ctrl+k时钟自动运行到对应节拍暂停
  //   ctrl+k关闭时钟连续运行，将控制位置零，进入单步调试模式调试
  //   Beq
  //   Bne
  //   MemToReg
  //   MemWrite
  //   AluOP
  //   AluSrcB
  //   RegWrite
  //   JAL
  //   RegDst
  //   可计数暂停的时钟源
  //   Syscall
  //   为方便自动评测，需要输出流水线各段保存的PC值，注意是PC不是PC+4，另外ID段寄存器写入信息，Mem段内存写入信息也要输出
  //   AluOP
  //   AluSrcB
  //   RegWrite
  //   MemWrite
  //   JAL
  //   Bne
endmodule

module \中断按键参考电路  (
  input  CLK,
  input  \_1号中断信号 ,
  input  \同步清零信号 ,
  output \与中断屏蔽位与 ,
  output \_1号中断等待指示灯 
);

  wire and_1_out, d_ff_1_q, or_2_out;

  or or_1 (\_1号中断等待指示灯 , \与中断屏蔽位与 , d_ff_1_q);
  D_Flip_Flop #(.trigger("rising"), .Pre_Clr_Positions("LEGACY"), .NegatePresetClear("false"), .enable("true"), .NewFFLayout("false")) d_ff_1 (
    .clk(\_1号中断信号 ), .D(1'b1), .Q(d_ff_1_q), .reset(\与中断屏蔽位与 ));  // open: Qn, preset, en
  or or_2 (or_2_out, d_ff_1_q, \与中断屏蔽位与 );
  and and_1 (and_1_out, or_2_out, ~\同步清零信号 );  // AND_Gate
  D_Flip_Flop #(.trigger("rising"), .Pre_Clr_Positions("LEGACY"), .NegatePresetClear("false"), .enable("true"), .NewFFLayout("false")) IR1 (
    .clk(CLK), .D(and_1_out), .Q(\与中断屏蔽位与 ));  // open: Qn, preset, en, reset

  // Notes on the sheet:
  //   中断信号采样参考电路
  //   Reset 
endmodule

module \单周期MIPS_单级中断  (
  input  IR1,
  input  IR2,
  input  IR3,
  output RegWrite,
  output MemWrite,
  output [31:0] PC,
  output [31:0] IR,
  output [31:0] RDin,
  output [31:0] MDin,
  output [31:0] LedData
);

  wire and_3_out, and_4_out, and_8_out, and_9_out, BLTZ, Branch, CLK, clock_2_out, comparator_1_eq,
       comparator_2_eq, comparator_3_eq, comparator_4_eq, comparator_6_lt, comparator_8_eq, comparator_8_lt,
       d_ff_1_q, decoder_1_out1, decoder_1_out2, decoder_1_out3, en, ERET, Go, IE_q, if_IR, IR1_t, IR2_t,
       IR3_t, IRA, IRB, IRC, JAL, JR, Led, LH, mips_alu_1_equal, nand_1_out, not_1_out, not_2_out, or_1_out,
       or_2_out, or_6_out, RegDst, register_3_q, RET1, RET2, RET3, SignedExt, SRAV, Syscall, W1, W2, W3,
       XORI, \中断 , \中断按键参考电路_1_与中断屏蔽位与 , \中断按键参考电路_2_与中断屏蔽位与 , \中断按键参考电路_3_与中断屏蔽位与 , \单周期硬布线控制器_1_alu_src ,
       \单周期硬布线控制器_1_beq , \单周期硬布线控制器_1_bne , \单周期硬布线控制器_1_jmp , \单周期硬布线控制器_1_memtoreg ;
  wire [1:0] priority_encoder_1_out, register_1_q;
  wire [3:0] \单周期硬布线控制器_1_alu_op ;
  wire [4:0] multiplexer_8_out, multiplexer_9_out, multiplexer_10_out, multiplexer_11_out, multiplexer_15_out;
  wire [12:0] CNT_num;
  wire [15:0] \总周期数 ;
  wire [31:0] adder_1_out, adder_2_out, bit_extender_1_out, bit_extender_2_out, bit_extender_3_out, EPC,
       mips_alu_1_result, mips_ram_1_dataout, multiplexer_1_out, multiplexer_2_out, multiplexer_4_out,
       multiplexer_5_out, multiplexer_6_out, multiplexer_13_out, multiplexer_14_out, multiplexer_16_out,
       PC_4, R1, shifter_1_out, shifter_2_out, \中断程序入口地址 ;

  Clock #(.highDuration(1), .lowDuration(1)) clock_1 ();  // open: out
  Button _1 (.out(IRA));
  Button _2 (.out(IRB));
  Button _3 (.out(IRC));
  Button \u_继续运行  (.out(Go));
  LED #(.active("true")) led_1 (.in(W1));
  LED #(.active("true")) led_2 (.in(W2));
  LED #(.active("true")) led_3 (.in(W3));
  Multiplexer #(.select(1), .width(32), .disabled("Z"), .enable("false")) multiplexer_1 (
    .in0(adder_1_out), .in1(adder_2_out), .out(multiplexer_1_out), .sel(or_6_out));
  Multiplexer #(.select(1), .width(32), .disabled("Z"), .enable("false")) multiplexer_2 (
    .in0(multiplexer_1_out), .in1(adder_2_out), .out(multiplexer_2_out), .sel(Branch));
  Hex_Digit_Display hex_digit_display_1 (.value(LedData[31:28]));  // open: dp
  Comparator #(.width(16), .mode("twosComplement")) comparator_1 (
    .a(16'h23b), .b(\总周期数 ), .eq(comparator_1_eq));  // open: gt, lt
  Comparator #(.width(16), .mode("twosComplement")) comparator_2 (
    .a(\总周期数 ), .b(16'h1), .eq(comparator_2_eq));  // open: gt, lt
  Comparator #(.width(16), .mode("twosComplement")) comparator_3 (
    .a(\总周期数 ), .b(16'h4), .eq(comparator_3_eq));  // open: gt, lt
  Comparator #(.width(16), .mode("twosComplement")) comparator_4 (
    .a(\总周期数 ), .b(16'h7), .eq(comparator_4_eq));  // open: gt, lt
  Multiplexer #(.select(1), .width(32), .disabled("Z"), .enable("false")) multiplexer_3 (
    .in0(multiplexer_2_out), .in1(multiplexer_5_out), .out(PC_4), .sel(\单周期硬布线控制器_1_jmp ));
  Multiplexer #(.select(1), .width(32), .disabled("Z"), .enable("false")) multiplexer_4 (
    .in0(PC_4), .in1(\中断程序入口地址 ), .out(multiplexer_4_out), .sel(\中断 ));
  Multiplexer #(.select(1), .width(32), .disabled("Z"), .enable("false")) multiplexer_5 (
    .in0(shifter_2_out), .in1(R1), .out(multiplexer_5_out), .sel(JR));
  Hex_Digit_Display hex_digit_display_2 (.value(LedData[23:20]));  // open: dp
  Hex_Digit_Display hex_digit_display_3 (.value(LedData[27:24]));  // open: dp
  or or_1 (or_1_out, comparator_1_eq, comparator_2_eq);
  assign IRA = or_1_out ? ~CLK : 1'bz;  // Controlled_Inverter controlled_inverter_1
  assign IRB = comparator_3_eq ? ~CLK : 1'bz;  // Controlled_Inverter controlled_inverter_2
  assign IRC = comparator_4_eq ? ~CLK : 1'bz;  // Controlled_Inverter controlled_inverter_3
  Multiplexer #(.select(1), .width(32), .disabled("Z"), .enable("false")) multiplexer_6 (
    .in0(multiplexer_4_out), .in1(EPC), .out(multiplexer_6_out), .sel(ERET));
  Register #(.width(32), .trigger("rising"), .Select("low")) u_PC (
    .D(multiplexer_6_out), .en(en), .Q(PC), .clk(CLK));  // open: clr
  \中断按键参考电路  \u_中断按键参考电路_1  (
    .CLK(CLK), .\与中断屏蔽位与 (\中断按键参考电路_1_与中断屏蔽位与 ), .\_1号中断信号 (IR1_t), .\_1号中断等待指示灯 (W1), .\同步清零信号 (RET1));
  \中断按键参考电路  \u_中断按键参考电路_2  (
    .CLK(CLK), .\与中断屏蔽位与 (\中断按键参考电路_2_与中断屏蔽位与 ), .\_1号中断信号 (IR2_t), .\_1号中断等待指示灯 (W2), .\同步清零信号 (RET2));
  \中断按键参考电路  \u_中断按键参考电路_3  (
    .CLK(CLK), .\与中断屏蔽位与 (\中断按键参考电路_3_与中断屏蔽位与 ), .\_1号中断信号 (IR3_t), .\_1号中断等待指示灯 (W3), .\同步清零信号 (RET3));
  Comparator #(.width(32), .mode("twosComplement")) comparator_5 (.a(IR), .b(32'h42000018), .eq(ERET));  // open: gt, lt
  Hex_Digit_Display hex_digit_display_4 (.value(LedData[19:16]));  // open: dp
  Hex_Digit_Display hex_digit_display_5 (.value(LedData[15:12]));  // open: dp
  Pull_Resistor #(.pull(0)) pull_resistor_1 (.node(IRA));
  Pull_Resistor #(.pull(0)) pull_resistor_2 (.node(IRB));
  Pull_Resistor #(.pull(0)) pull_resistor_3 (.node(IRC));
  Adder #(.width(32)) adder_1 (.a(PC), .b(32'h4), .out(adder_1_out));  // open: cin, cout
  Priority_Encoder #(.select(2), .disabled("Z")) priority_encoder_1 (
    .in0(1'b0), .in1(\中断按键参考电路_1_与中断屏蔽位与 ), .in2(\中断按键参考电路_2_与中断屏蔽位与 ), .in3(\中断按键参考电路_3_与中断屏蔽位与 ),
    .out(priority_encoder_1_out), .gs(if_IR), .en_in(1'b1));  // open: en_out
  Hex_Digit_Display hex_digit_display_6 (.value(LedData[11:8]));  // open: dp
  Hex_Digit_Display hex_digit_display_7 (.value(LedData[7:4]));  // open: dp
  // Probe on \总周期数 
  Comparator #(.width(32), .mode("twosComplement")) comparator_6 (
    .a(R1), .b({32{1'b0}}), .lt(comparator_6_lt));  // open: gt, eq
  Hex_Digit_Display hex_digit_display_8 (.value(LedData[3:0]));  // open: dp
  // Mips_Probe mips_probe_1: pin names not known; wires that end beside it: IR
  ROM #(.addrWidth(10), .dataWidth(32), .Select("high")) rom_1 (.addr(PC[11:2]), .data(IR));
  and and_1 (Branch, comparator_6_lt, BLTZ);
  Multiplexer #(.select(2), .width(32), .disabled("Z"), .enable("false")) multiplexer_7 (
    .in1(32'h30ac), .in2(32'h3150), .in3(32'h31f4), .out(\中断程序入口地址 ), .sel(priority_encoder_1_out));  // open: in0
  Register #(.width(32), .trigger("rising"), .Select("low")) u_EPC (
    .D(PC_4), .en(\中断 ), .Q(EPC), .clk(CLK));  // open: clr
  Register #(.width(1), .trigger("rising"), .Select("low")) IE (
    .D(\中断 ), .en(or_2_out), .Q(IE_q), .clk(CLK));  // open: clr
  or or_2 (or_2_out, \中断 , ERET);
  or or_3 (IR1_t, IR1, IRA);
  Multiplexer #(.select(1), .width(5), .disabled("Z"), .enable("false")) multiplexer_8 (
    .in0(IR[25:21]), .in1(5'b00100), .out(multiplexer_8_out), .sel(Syscall));
  Multiplexer #(.select(1), .width(5), .disabled("Z"), .enable("false")) multiplexer_9 (
    .in0(IR[20:16]), .in1(5'b00010), .out(multiplexer_9_out), .sel(Syscall));
  Multiplexer #(.select(1), .width(5), .disabled("Z"), .enable("false")) multiplexer_10 (
    .in0(IR[20:16]), .in1(IR[15:11]), .out(multiplexer_10_out), .sel(RegDst));
  or or_4 (IR2_t, IR2, IRB);
  \单周期硬布线控制器  \u_单周期硬布线控制器_1  (
    .OP(IR[31:26]), .Func(IR[5:0]), .ALU_OP(\单周期硬布线控制器_1_alu_op ), .MemToReg(\单周期硬布线控制器_1_memtoreg ),
    .MemWrite(MemWrite), .BLTZ(BLTZ), .LH(LH), .SRAV(SRAV), .XORI(XORI), .ALU_SRC(\单周期硬布线控制器_1_alu_src ),
    .RegWrite(RegWrite), .SysCALL(Syscall), .SignedExt(SignedExt), .RegDst(RegDst), .Beq(\单周期硬布线控制器_1_beq ),
    .Bne(\单周期硬布线控制器_1_bne ), .JR(JR), .JMP(\单周期硬布线控制器_1_jmp ), .JAL(JAL));
  Multiplexer #(.select(1), .width(5), .disabled("Z"), .enable("false")) multiplexer_11 (
    .in0(multiplexer_10_out), .in1({5{1'b1}}), .out(multiplexer_11_out), .sel(JAL));
  Multiplexer #(.select(1), .width(32), .disabled("Z"), .enable("false")) multiplexer_12 (
    .in0(multiplexer_16_out), .in1(adder_1_out), .out(RDin), .sel(JAL));
  Register #(.width(2), .trigger("rising"), .Select("low")) register_1 (
    .D(priority_encoder_1_out), .en(\中断 ), .Q(register_1_q), .clk(CLK));  // open: clr
  and and_2 (\中断 , ~IE_q, if_IR);  // AND_Gate
  and and_3 (and_3_out, Syscall, Led);
  assign bit_extender_1_out = {{16{1'b0}}, IR[15:0]};  // Bit_Extender bit_extender_1
  assign bit_extender_2_out = {{16{IR[15]}}, IR[15:0]};  // Bit_Extender bit_extender_2
  assign bit_extender_3_out = {{6{IR[25]}}, IR[25:0]};  // Bit_Extender bit_extender_3
  Decoder #(.select(2), .tristate("false"), .disabled("Z"), .enable("false")) decoder_1 (
    .out1(decoder_1_out1), .out2(decoder_1_out2), .out3(decoder_1_out3), .sel(register_1_q));  // open: out0
  or or_5 (IR3_t, IR3, IRC);
  and and_4 (and_4_out, \单周期硬布线控制器_1_beq , mips_alu_1_equal);
  Register #(.width(32), .trigger("rising"), .Select("low")) register_2 (
    .D(R1), .en(and_3_out), .Q(LedData), .clk(CLK));  // open: clr
  \MIPS_Regfile_上升沿  \mips_regfile_上升沿_1  (
    .Din(RDin), .Clk(CLK), .R1(R1), .R2(MDin), .WE(RegWrite), .W_num(multiplexer_11_out),
    .R1_num(multiplexer_8_out), .R2_num(multiplexer_9_out));
  Multiplexer #(.select(1), .width(32), .disabled("Z"), .enable("false")) multiplexer_13 (
    .in0(bit_extender_1_out), .in1(bit_extender_2_out), .out(multiplexer_13_out), .sel(SignedExt));
  and and_5 (RET1, decoder_1_out1, ERET);
  and and_6 (RET2, decoder_1_out2, ERET);
  and and_7 (RET3, decoder_1_out3, ERET);
  not not_1 (not_1_out, mips_alu_1_equal);
  Multiplexer #(.select(1), .width(32), .disabled("Z"), .enable("false")) multiplexer_14 (
    .in0(MDin), .in1(multiplexer_13_out), .out(multiplexer_14_out), .sel(\单周期硬布线控制器_1_alu_src ));
  Comparator #(.width(32), .mode("twosComplement")) comparator_7 (.a(32'h22), .b(MDin), .eq(Led));  // open: gt, lt
  Shifter #(.width(32), .shift("ll")) shifter_1 (.in(multiplexer_13_out), .\dist (5'b00010), .out(shifter_1_out));
  and and_8 (and_8_out, not_1_out, \单周期硬布线控制器_1_bne );
  MIPS_ALU mips_alu_1 (
    .X(R1), .Y(multiplexer_14_out), .AluOP(\单周期硬布线控制器_1_alu_op ), .Equal(mips_alu_1_equal),
    .Result(mips_alu_1_result), .shamt(multiplexer_15_out));  // open: Result_2
  not not_2 (not_2_out, Led);
  Shifter #(.width(32), .shift("ll")) shifter_2 (.in(bit_extender_3_out), .\dist (5'b00010), .out(shifter_2_out));
  Multiplexer #(.select(1), .width(5), .disabled("Z"), .enable("false")) multiplexer_15 (
    .in0(IR[10:6]), .in1(R1[4:0]), .out(multiplexer_15_out), .sel(SRAV));
  or or_6 (or_6_out, and_4_out, and_8_out);
  and and_9 (and_9_out, Syscall, not_2_out);
  Adder #(.width(32)) adder_2 (.a(shifter_1_out), .b(adder_1_out), .out(adder_2_out));  // open: cin, cout
  D_Flip_Flop #(.trigger("high"), .Pre_Clr_Positions("LEGACY"), .NegatePresetClear("false"), .enable("true"), .NewFFLayout("false")) d_ff_1 (.Q(d_ff_1_q));  // open: clk, D, Qn, preset, en, reset
  Register #(.width(1), .trigger("rising"), .Select("low")) register_3 (
    .D(Syscall), .en(and_9_out), .Q(register_3_q), .clk(CLK), .clr(Go));
  not not_3 (en, register_3_q);
  // Probe on 13'h368
  Comparator #(.width(13), .mode("twosComplement")) comparator_8 (
    .a(CNT_num), .b(13'h368), .eq(comparator_8_eq), .lt(comparator_8_lt));  // open: gt
  Clock #(.highDuration(1), .lowDuration(1)) clock_2 (.out(clock_2_out));
  MIPS_RAM mips_ram_1 (
    .\字节地址 (mips_alu_1_result[11:2]), .Din(MDin), .DataOut(mips_ram_1_dataout), .CLK(CLK), .WE(MemWrite),
    .Mode(mips_alu_1_result[1]), .LH(LH));
  Counter #(.width(16), .max('hffff), .ongoal("wrap"), .trigger("rising"), .behavior("old")) counter_1 (
    .count(en), .Q(\总周期数 ), .clk(CLK));  // open: load, D, carry, clr, preset
  nand nand_1 (nand_1_out, d_ff_1_q, comparator_8_eq);
  Counter #(.width(13), .max('h1fff), .ongoal("stay"), .trigger("rising"), .behavior("old")) counter_2 (
    .count(comparator_8_lt), .Q(CNT_num), .clk(clock_2_out));  // open: load, D, carry, clr, preset
  Multiplexer #(.select(1), .width(32), .disabled("Z"), .enable("false")) multiplexer_16 (
    .in0(mips_alu_1_result), .in1(mips_ram_1_dataout), .out(multiplexer_16_out), .sel(\单周期硬布线控制器_1_memtoreg ));
  assign CLK = nand_1_out ? clock_2_out : 1'bz;  // Controlled_Buffer controlled_buffer_1
  Pull_Resistor #(.pull(1)) pull_resistor_4 (.node(CLK));

  // Notes on the sheet:
  //   中断源
  //   中断等待指示
  //   总复位信号应将除ROM以外所有存储组件全部清零
  //   单级中断测试信号模拟器
  //   数码管输出
  //   数码管输出应该用寄存器锁存，否则显示数据只能一闪而过
  //   指令存储器
  //   指令字
  //   contents of rom_1 (hex, n*v repeats v):
  //   201d07d0 20100001 109fc0 139fc3 8021 2012000c 24160008 26100001 3210000f 20080008 20090001 139900
  //   2709825 132020 20020022 c 1094022 1500fff9 22100001 2018000f 2188024 108700 20080008 20090001 139902
  //   2709825 132021 20020022 c 1094022 1500fff9 108702 2c9b022 12c00001 8000c07 4020 1084027 84400
  //   3508ffff 82021 20020022 c 8000c01 afa20000 23bd0004 afa40000 23bd0004 afb00000 23bd0004 afb30000
  //   23bd0004 afb40000 23bd0004 afb50000 23bd0004 afb60000 23bd0004 20160001 20140003 20150001 168020
  //   108100 2149825 132020 20020022 c 1600fffa 295a022 1680fff7 23bdfffc 8fb60000 23bdfffc 8fb50000
  //   23bdfffc 8fb40000 23bdfffc 8fb30000 23bdfffc 8fb00000 23bdfffc 8fa40000 23bdfffc 8fa20000 42000018
  //   afa20000 23bd0004 afa40000 23bd0004 afb00000 23bd0004 afb30000 23bd0004 afb40000 23bd0004 afb50000
  //   23bd0004 afb60000 23bd0004 20160002 20140003 20150001 168020 108100 2149825 132020 20020022 c
  //   1600fffa 295a022 1680fff7 23bdfffc 8fb60000 23bdfffc 8fb50000 23bdfffc 8fb40000 23bdfffc 8fb30000
  //   23bdfffc 8fb00000 23bdfffc 8fa40000 23bdfffc 8fa20000 42000018 afa20000 23bd0004 afa40000 23bd0004
  //   afb00000 23bd0004 afb30000 23bd0004 afb40000 23bd0004 afb50000 23bd0004 afb60000 23bd0004 20160003
  //   20140003 20150001 168020 108100 2149825 132020 20020022 c 1600fffa 295a022 1680fff7 23bdfffc
  //   8fb60000 23bdfffc 8fb50000 23bdfffc 8fb40000 23bdfffc 8fb30000 23bdfffc 8fb00000 23bdfffc 8fa40000
  //   23bdfffc 8fa20000 42000018
  //   OP
  //   Func
  //   rs
  //   rt
  //   rd
  //   JMP
  //   JR
  //   OP
  //   Func
  //   Syscall
  //   Beq
  //   Bne
  //   MemToReg
  //   MemWrite
  //   AluOP
  //   AluSrcB
  //   RegWrite
  //   JAL
  //   RegDst
  //   为方便自动评测，需要输出PC，IR，寄存器堆写如数据RDin
  //   控制位
  //   RAM写使能MemWrite、RAM写入数据MDin等信号
  //   暂停节拍，不能为0
  //   用这个时钟源需要去掉电路中的其他时钟源
  //   戳工具置1进入计数暂停模式，ctrl+k时钟自动运行到对应节拍暂停
  //   ctrl+k关闭时钟连续运行，将控制位置零，进入单步调试模式调试
  //   可计数暂停的时钟源
endmodule

module \单周期MIPS_多级中断  (
  input  IR1,
  input  IR2,
  input  IR3,
  output RegWrite,
  output MemWrite,
  output [31:0] PC,
  output [31:0] IR,
  output [31:0] RDin,
  output [31:0] MDin,
  output [31:0] LedData
);

  wire and_1_out, and_2_out, and_3_out, and_4_out, and_5_out, and_6_out, and_7_out, and_9_out, and_10_out,
       and_11_out, and_12_out, and_13_out, and_14_out, and_15_out, and_16_out, and_17_out, B, BLTZ, CLK,
       clock_2_out, clock_3_out, clock_4_out, clock_5_out, comparator_1_eq, comparator_2_eq, comparator_3_eq,
       comparator_4_eq, comparator_5_eq, comparator_6_eq, comparator_7_eq, comparator_7_lt, comparator_9_eq,
       comparator_10_eq, comparator_11_eq, comparator_12_eq, comparator_13_lt, d_ff_1_q, d_ff_2_q, d_ff_3_q,
       d_ff_4_q, decoder_1_out1, decoder_1_out2, decoder_1_out3, decoder_2_out0, decoder_2_out1,
       decoder_2_out2, eret, Go, Halt, IE, IR1_q, IR1_RST, IR1_t, IR2_q, IR2_RST, IR2_t, IR3_q, IR3_RST,
       IR3_t, IRA, IRB, IRC, JAL, JMP, JR, LH, mfc0, mips_alu_1_equal, mtc0, nand_1_out, not_1_out,
       not_2_out, not_3_out, not_4_out, not_5_out, not_6_out, or_1_out, or_2_out, or_6_out, or_7_out,
       or_8_out, or_9_out, or_14_out, or_15_out, or_16_out, priority_encoder_1_gs, RegDst, RST, SignedExt,
       SRAV, Syscall, W1, W2, W3, XORI, \中断 , \单周期硬布线控制器_1_alu_src , \单周期硬布线控制器_1_beq , \单周期硬布线控制器_1_bne ,
       \单周期硬布线控制器_1_memtoreg ;
  wire [1:0] adder_4_out, exist, IR_Num, IR_Num_Now, IRNum1_q, IRNum2_q, IRNum3_q, multiplexer_17_out;
  wire [3:0] \单周期硬布线控制器_1_alu_op ;
  wire [4:0] multiplexer_4_out, multiplexer_5_out, multiplexer_6_out, multiplexer_7_out, multiplexer_13_out;
  wire [12:0] CNT_num;
  wire [15:0] \总周期数 ;
  wire [31:0] adder_2_out, bit_extender_1_out, bit_extender_2_out, bit_extender_3_out, bit_extender_4_out,
       EPC, EPC1_q, EPC2_q, EPC3_q, \J跳转地址 , mips_alu_1_result, mips_ram_1_dataout, multiplexer_1_out,
       multiplexer_2_out, multiplexer_8_out, multiplexer_12_out, multiplexer_18_out, PC_4, PC_B, PC_next, R1,
       shifter_1_out, shifter_2_out, shifter_3_out, \入口地址 , \立即数I扩展 ;

  Clock #(.highDuration(1), .lowDuration(1)) clock_1 ();  // open: out
  Button _1 (.out(IRA));
  Button _2 (.out(IRB));
  Button _3 (.out(IRC));
  Button \u_继续运行  (.out(Go));
  LED #(.active("true")) led_1 (.in(W1));
  LED #(.active("true")) led_2 (.in(W2));
  LED #(.active("true")) led_3 (.in(W3));
  Adder #(.width(32)) adder_1 (.a(PC), .b(32'h4), .out(PC_4));  // open: cin, cout
  Shifter #(.width(32), .shift("ll")) shifter_1 (.in(\立即数I扩展 ), .\dist (5'b00010), .out(shifter_1_out));
  Hex_Digit_Display hex_digit_display_1 (.value(LedData[31:28]));  // open: dp
  Comparator #(.width(16), .mode("twosComplement")) comparator_1 (
    .a(\总周期数 ), .b(16'h7), .eq(comparator_1_eq));  // open: gt, lt
  Comparator #(.width(16), .mode("twosComplement")) comparator_2 (
    .a(\总周期数 ), .b(16'h241), .eq(comparator_2_eq));  // open: gt, lt
  Comparator #(.width(32), .mode("twosComplement")) comparator_3 (
    .a(R1), .b(32'h22), .eq(comparator_3_eq));  // open: gt, lt
  // Mips_Probe mips_probe_1: pin names not known; wires that end beside it: IR, CLK
  not not_1 (not_1_out, Halt);
  Adder #(.width(32)) adder_2 (.a(PC_4), .b(shifter_1_out), .out(adder_2_out));  // open: cin, cout
  Clock #(.highDuration(1), .lowDuration(1)) clock_2 (.out(clock_2_out));
  LED #(.active("true")) \_1号中断等待指示灯  (.in(W1));
  Clock #(.highDuration(1), .lowDuration(1)) clock_3 (.out(clock_3_out));
  LED #(.active("true")) \_2号中断等待指示灯  (.in(W2));
  Clock #(.highDuration(1), .lowDuration(1)) clock_4 (.out(clock_4_out));
  LED #(.active("true")) \_3号中断等待指示灯  (.in(W3));
  Hex_Digit_Display hex_digit_display_2 (.value(LedData[23:20]));  // open: dp
  Hex_Digit_Display hex_digit_display_3 (.value(LedData[27:24]));  // open: dp
  Comparator #(.width(16), .mode("twosComplement")) comparator_4 (
    .a(16'h258), .b(\总周期数 ), .eq(comparator_4_eq));  // open: gt, lt
  or or_1 (or_1_out, comparator_4_eq, comparator_5_eq);
  Comparator #(.width(16), .mode("twosComplement")) comparator_5 (
    .a(\总周期数 ), .b(16'h1), .eq(comparator_5_eq));  // open: gt, lt
  Comparator #(.width(16), .mode("twosComplement")) comparator_6 (
    .a(\总周期数 ), .b(16'h4), .eq(comparator_6_eq));  // open: gt, lt
  or or_2 (or_2_out, comparator_1_eq, comparator_2_eq);
  and and_1 (and_1_out, Syscall, not_2_out);
  not not_2 (not_2_out, comparator_3_eq);
  and and_2 (and_2_out, Syscall, comparator_3_eq);
  Register #(.width(32), .trigger("rising"), .Select("low")) u_PC (
    .D(PC_next), .en(not_1_out), .Q(PC), .clk(CLK), .clr(RST));
  Multiplexer #(.select(1), .width(32), .disabled("Z"), .enable("false")) multiplexer_1 (
    .in0(PC_4), .in1(adder_2_out), .out(multiplexer_1_out), .sel(B));
  D_Flip_Flop #(.trigger("rising"), .Pre_Clr_Positions("LEGACY"), .NegatePresetClear("false"), .enable("true"), .NewFFLayout("false")) d_ff_1 (
    .clk(IR1_t), .D(1'b1), .Q(d_ff_1_q), .reset(IR1_q));  // open: Qn, preset, en
  or or_3 (W1, IR1_q, d_ff_1_q);
  D_Flip_Flop #(.trigger("rising"), .Pre_Clr_Positions("LEGACY"), .NegatePresetClear("false"), .enable("true"), .NewFFLayout("false")) d_ff_2 (
    .clk(IR2_t), .D(1'b1), .Q(d_ff_2_q), .reset(IR2_q));  // open: Qn, preset, en
  or or_4 (W2, IR2_q, d_ff_2_q);
  D_Flip_Flop #(.trigger("rising"), .Pre_Clr_Positions("LEGACY"), .NegatePresetClear("false"), .enable("true"), .NewFFLayout("false")) d_ff_3 (
    .clk(IR3_t), .D(1'b1), .Q(d_ff_3_q), .reset(IR3_q));  // open: Qn, preset, en
  or or_5 (W3, IR3_q, d_ff_3_q);
  Hex_Digit_Display hex_digit_display_4 (.value(LedData[15:12]));  // open: dp
  Hex_Digit_Display hex_digit_display_5 (.value(LedData[19:16]));  // open: dp
  Pull_Resistor #(.pull(0)) pull_resistor_1 (.node(IRA));
  assign IRA = or_1_out ? ~CLK : 1'bz;  // Controlled_Inverter controlled_inverter_1
  Pull_Resistor #(.pull(0)) pull_resistor_2 (.node(IRB));
  assign IRB = comparator_6_eq ? ~CLK : 1'bz;  // Controlled_Inverter controlled_inverter_2
  Pull_Resistor #(.pull(0)) pull_resistor_3 (.node(IRC));
  assign IRC = or_2_out ? ~CLK : 1'bz;  // Controlled_Inverter controlled_inverter_3
  Counter #(.width(1), .max('h1), .ongoal("wrap"), .trigger("rising"), .behavior("old")) counter_1 (
    .load(and_1_out), .D(and_1_out), .count(1'b0), .Q(Halt), .clk(CLK), .clr(or_6_out));  // open: carry, preset
  or or_6 (or_6_out, Go, RST);
  Register #(.width(32), .trigger("rising"), .Select("low")) register_1 (
    .D(MDin), .en(and_2_out), .Q(LedData), .clk(CLK), .clr(RST));
  Multiplexer #(.select(1), .width(32), .disabled("Z"), .enable("false")) multiplexer_2 (
    .in0(multiplexer_1_out), .in1(R1), .out(multiplexer_2_out), .sel(JR));
  or or_7 (or_7_out, d_ff_1_q, IR1_q);
  Pull_Resistor #(.pull(0)) pull_resistor_4 (.node(IR1_RST));
  or or_8 (or_8_out, d_ff_2_q, IR2_q);
  Pull_Resistor #(.pull(0)) pull_resistor_5 (.node(IR2_RST));
  or or_9 (or_9_out, d_ff_3_q, IR3_q);
  Pull_Resistor #(.pull(0)) pull_resistor_6 (.node(IR3_RST));
  Hex_Digit_Display hex_digit_display_6 (.value(LedData[11:8]));  // open: dp
  Hex_Digit_Display hex_digit_display_7 (.value(LedData[7:4]));  // open: dp
  // Probe on \总周期数 
  ROM #(.addrWidth(10), .dataWidth(32), .Select("high")) rom_1 (.addr(PC[11:2]), .data(IR));
  and and_3 (and_3_out, JMP, ~JR);  // AND_Gate
  and and_4 (and_4_out, or_7_out, ~IR1_RST);  // AND_Gate
  and and_5 (and_5_out, or_8_out, ~IR2_RST);  // AND_Gate
  and and_6 (and_6_out, or_9_out, ~IR3_RST);  // AND_Gate
  Hex_Digit_Display hex_digit_display_8 (.value(LedData[3:0]));  // open: dp
  D_Flip_Flop #(.trigger("high"), .Pre_Clr_Positions("LEGACY"), .NegatePresetClear("false"), .enable("true"), .NewFFLayout("false")) d_ff_4 (.Q(d_ff_4_q));  // open: clk, D, Qn, preset, en, reset
  Multiplexer #(.select(1), .width(32), .disabled("Z"), .enable("false")) multiplexer_3 (
    .in0(multiplexer_2_out), .in1(\J跳转地址 ), .out(PC_B), .sel(and_3_out));
  D_Flip_Flop #(.trigger("rising"), .Pre_Clr_Positions("LEGACY"), .NegatePresetClear("false"), .enable("true"), .NewFFLayout("false")) u_IR1 (
    .clk(clock_2_out), .D(and_4_out), .Q(IR1_q), .reset(RST));  // open: Qn, preset, en
  D_Flip_Flop #(.trigger("rising"), .Pre_Clr_Positions("LEGACY"), .NegatePresetClear("false"), .enable("true"), .NewFFLayout("false")) u_IR2 (
    .clk(clock_3_out), .D(and_5_out), .Q(IR2_q), .reset(RST));  // open: Qn, preset, en
  D_Flip_Flop #(.trigger("rising"), .Pre_Clr_Positions("LEGACY"), .NegatePresetClear("false"), .enable("true"), .NewFFLayout("false")) u_IR3 (
    .clk(clock_4_out), .D(and_6_out), .Q(IR3_q), .reset(RST));  // open: Qn, preset, en
  // Probe on 13'h368
  Multiplexer #(.select(1), .width(5), .disabled("Z"), .enable("false")) multiplexer_4 (
    .in0(IR[25:21]), .in1(5'b00010), .out(multiplexer_4_out), .sel(Syscall));
  Multiplexer #(.select(1), .width(5), .disabled("Z"), .enable("false")) multiplexer_5 (
    .in0(IR[20:16]), .in1(5'b00100), .out(multiplexer_5_out), .sel(Syscall));
  Multiplexer #(.select(1), .width(5), .disabled("Z"), .enable("false")) multiplexer_6 (
    .in0(IR[20:16]), .in1(IR[15:11]), .out(multiplexer_6_out), .sel(RegDst));
  assign bit_extender_1_out = {{6{1'b0}}, IR[25:0]};  // Bit_Extender bit_extender_1
  assign bit_extender_2_out = {{28{1'b0}}, PC_4[31:28]};  // Bit_Extender bit_extender_2
  or or_10 (IR1_t, IR1, IRA);
  Comparator #(.width(13), .mode("twosComplement")) comparator_7 (
    .a(CNT_num), .b(13'h368), .eq(comparator_7_eq), .lt(comparator_7_lt));  // open: gt
  Clock #(.highDuration(1), .lowDuration(1)) clock_5 (.out(clock_5_out));
  \单周期硬布线控制器  \u_单周期硬布线控制器_1  (
    .OP(IR[31:26]), .Func(IR[5:0]), .ALU_OP(\单周期硬布线控制器_1_alu_op ), .MemToReg(\单周期硬布线控制器_1_memtoreg ),
    .MemWrite(MemWrite), .BLTZ(BLTZ), .LH(LH), .SRAV(SRAV), .XORI(XORI), .ALU_SRC(\单周期硬布线控制器_1_alu_src ),
    .RegWrite(RegWrite), .SysCALL(Syscall), .SignedExt(SignedExt), .RegDst(RegDst), .Beq(\单周期硬布线控制器_1_beq ),
    .Bne(\单周期硬布线控制器_1_bne ), .JR(JR), .JMP(JMP), .JAL(JAL));
  Multiplexer #(.select(1), .width(5), .disabled("Z"), .enable("false")) multiplexer_7 (
    .in0(multiplexer_6_out), .in1({5{1'b1}}), .out(multiplexer_7_out), .sel(JAL));
  assign bit_extender_3_out = {{16{1'b0}}, IR[15:0]};  // Bit_Extender bit_extender_3
  assign bit_extender_4_out = {{16{IR[15]}}, IR[15:0]};  // Bit_Extender bit_extender_4
  Shifter #(.width(32), .shift("ll")) shifter_2 (.in(bit_extender_1_out), .\dist (5'b00010), .out(shifter_2_out));
  Shifter #(.width(32), .shift("ll")) shifter_3 (.in(bit_extender_2_out), .\dist (5'b11100), .out(shifter_3_out));
  Priority_Encoder #(.select(2), .disabled("Z")) priority_encoder_1 (
    .in1(IR1_q), .in2(IR2_q), .in3(IR3_q), .out(IR_Num), .gs(priority_encoder_1_gs));  // open: in0, en_out, en_in
  Demultiplexer #(.select(2), .width(1), .tristate("false"), .disabled("Z"), .enable("false")) demultiplexer_1 (
    .out1(IR1_RST), .out2(IR2_RST), .out3(IR3_RST), .in(eret), .sel(IR_Num));  // open: out0
  Multiplexer #(.select(1), .width(32), .disabled("Z"), .enable("false")) multiplexer_8 (
    .in0(PC_B), .in1(\入口地址 ), .out(multiplexer_8_out), .sel(\中断 ));
  or or_11 (IR2_t, IR2, IRB);
  nand nand_1 (nand_1_out, d_ff_4_q, comparator_7_eq);
  Counter #(.width(13), .max('h1fff), .ongoal("stay"), .trigger("rising"), .behavior("old")) counter_2 (
    .count(comparator_7_lt), .Q(CNT_num), .clk(clock_5_out));  // open: load, D, carry, clr, preset
  not not_3 (not_3_out, Halt);
  and and_7 (and_7_out, not_3_out, RegWrite);
  Multiplexer #(.select(1), .width(32), .disabled("Z"), .enable("false")) multiplexer_9 (
    .in0(bit_extender_3_out), .in1(bit_extender_4_out), .out(\立即数I扩展 ), .sel(SignedExt));
  Adder #(.width(32)) adder_3 (.a(shifter_2_out), .b(shifter_3_out), .out(\J跳转地址 ));  // open: cin, cout
  Multiplexer #(.select(2), .width(32), .disabled("Z"), .enable("false")) multiplexer_10 (
    .in1(32'h30ac), .in2(32'h3158), .in3(32'h3204), .out(\入口地址 ), .sel(IR_Num));  // open: in0
  and and_8 (\中断 , priority_encoder_1_gs, comparator_13_lt, IE);
  Multiplexer #(.select(1), .width(32), .disabled("Z"), .enable("false")) multiplexer_11 (
    .in0(multiplexer_8_out), .in1(EPC), .out(PC_next), .sel(eret));
  assign CLK = nand_1_out ? clock_5_out : 1'bz;  // Controlled_Buffer controlled_buffer_1
  Pull_Resistor #(.pull(1)) pull_resistor_7 (.node(CLK));
  \MIPS_Regfile_上升沿  \mips_regfile_上升沿_1  (
    .Din(RDin), .Clk(CLK), .R1(R1), .R2(MDin), .WE(and_7_out), .W_num(multiplexer_7_out),
    .R1_num(multiplexer_4_out), .R2_num(multiplexer_5_out));
  Decoder #(.select(2), .tristate("false"), .disabled("Z"), .enable("false")) decoder_1 (
    .out1(decoder_1_out1), .out2(decoder_1_out2), .out3(decoder_1_out3), .sel(IR_Num));  // open: out0
  or or_12 (IR3_t, IR3, IRC);
  Multiplexer #(.select(1), .width(32), .disabled("Z"), .enable("false")) multiplexer_12 (
    .in0(MDin), .in1(\立即数I扩展 ), .out(multiplexer_12_out), .sel(\单周期硬布线控制器_1_alu_src ));
  Multiplexer #(.select(1), .width(5), .disabled("Z"), .enable("false")) multiplexer_13 (
    .in0(IR[10:6]), .in1(R1[4:0]), .out(multiplexer_13_out), .sel(SRAV));
  Pull_Resistor #(.pull(0)) pull_resistor_8 (.node(decoder_1_out1));
  Pull_Resistor #(.pull(0)) pull_resistor_9 (.node(decoder_1_out2));
  Pull_Resistor #(.pull(0)) pull_resistor_10 (.node(decoder_1_out3));
  Decoder #(.select(2), .tristate("false"), .disabled("Z"), .enable("false")) decoder_2 (
    .out0(decoder_2_out0), .out1(decoder_2_out1), .out2(decoder_2_out2), .sel(exist));  // open: out3
  not not_4 (not_4_out, mips_alu_1_equal);
  MIPS_ALU mips_alu_1 (
    .X(R1), .Y(multiplexer_12_out), .AluOP(\单周期硬布线控制器_1_alu_op ), .Equal(mips_alu_1_equal),
    .Result(mips_alu_1_result), .shamt(multiplexer_13_out));  // open: Result_2
  Multiplexer #(.select(1), .width(32), .disabled("Z"), .enable("false")) multiplexer_14 (
    .in0(multiplexer_18_out), .in1(PC_4), .out(RDin), .sel(JAL));
  and and_9 (and_9_out, \中断 , decoder_1_out1);
  and and_10 (and_10_out, \中断 , decoder_1_out2);
  and and_11 (and_11_out, \中断 , decoder_1_out3);
  and and_12 (and_12_out, \中断 , decoder_2_out0);
  and and_13 (and_13_out, \中断 , decoder_2_out1);
  and and_14 (and_14_out, \中断 , decoder_2_out2);
  and and_15 (and_15_out, mips_alu_1_equal, \单周期硬布线控制器_1_beq );
  and and_16 (and_16_out, not_4_out, \单周期硬布线控制器_1_bne );
  Comparator #(.width(32), .mode("twosComplement")) comparator_8 (.a(IR), .b(32'h42000018), .eq(eret));  // open: gt, lt
  Register #(.width(32), .trigger("rising"), .Select("low")) EPC1 (
    .D(PC_B), .en(and_9_out), .Q(EPC1_q), .clk(CLK), .clr(RST));
  Register #(.width(32), .trigger("rising"), .Select("low")) EPC2 (
    .D(PC_B), .en(and_10_out), .Q(EPC2_q), .clk(CLK), .clr(RST));
  Register #(.width(32), .trigger("rising"), .Select("low")) EPC3 (
    .D(PC_B), .en(and_11_out), .Q(EPC3_q), .clk(CLK), .clr(RST));
  Register #(.width(2), .trigger("rising"), .Select("low")) IRNum1 (
    .D(IR_Num), .en(and_12_out), .Q(IRNum1_q), .clk(CLK), .clr(RST));
  Register #(.width(2), .trigger("rising"), .Select("low")) IRNum2 (
    .D(IR_Num), .en(and_13_out), .Q(IRNum2_q), .clk(CLK), .clr(RST));
  Register #(.width(2), .trigger("rising"), .Select("low")) IRNum3 (
    .D(IR_Num), .en(and_14_out), .Q(IRNum3_q), .clk(CLK), .clr(RST));
  or or_13 (B, BLTZ, and_15_out, and_16_out);
  Multiplexer #(.select(2), .width(32), .disabled("Z"), .enable("false")) multiplexer_15 (
    .in1(EPC1_q), .in2(EPC2_q), .in3(EPC3_q), .out(EPC), .sel(IR_Num_Now));  // open: in0
  Multiplexer #(.select(2), .width(2), .disabled("Z"), .enable("false")) multiplexer_16 (
    .in1(IRNum1_q), .in2(IRNum2_q), .in3(IRNum3_q), .out(IR_Num_Now), .sel(exist));  // open: in0
  Button \u_总复位  (.out(RST));
  not not_5 (not_5_out, Halt);
  MIPS_RAM mips_ram_1 (
    .\字节地址 (mips_alu_1_result[11:2]), .Din(MDin), .DataOut(mips_ram_1_dataout), .CLK(CLK), .WE(MemWrite),
    .Mode(mips_alu_1_result[1]), .LH(LH));
  Multiplexer #(.select(1), .width(2), .disabled("Z"), .enable("false")) multiplexer_17 (
    .in0(2'b11), .in1(2'b01), .out(multiplexer_17_out), .sel(\中断 ));
  Counter #(.width(16), .max('hffff), .ongoal("wrap"), .trigger("rising"), .behavior("old")) counter_3 (
    .Q(\总周期数 ), .clk(and_17_out), .clr(RST));  // open: load, D, count, carry, preset
  and and_17 (and_17_out, CLK, not_5_out);
  Multiplexer #(.select(1), .width(32), .disabled("Z"), .enable("false")) multiplexer_18 (
    .in0(mips_alu_1_result), .in1(mips_ram_1_dataout), .out(multiplexer_18_out), .sel(\单周期硬布线控制器_1_memtoreg ));
  Comparator #(.width(6), .mode("twosComplement")) comparator_9 (
    .a(IR[31:26]), .b(6'b010000), .eq(comparator_9_eq));  // open: gt, lt
  Comparator #(.width(5), .mode("twosComplement")) comparator_10 (
    .a(IR[25:21]), .b({5{1'b0}}), .eq(comparator_10_eq));  // open: gt, lt
  Comparator #(.width(5), .mode("twosComplement")) comparator_11 (
    .a(IR[25:21]), .b(5'b00100), .eq(comparator_11_eq));  // open: gt, lt
  or or_14 (or_14_out, mtc0, \中断 );
  Comparator #(.width(16), .mode("twosComplement")) comparator_12 (
    .a(\总周期数 ), .b({16{1'b0}}), .eq(comparator_12_eq));  // open: gt, lt
  Adder #(.width(2)) adder_4 (.a(exist), .b(multiplexer_17_out), .out(adder_4_out));  // open: cin, cout
  or or_15 (or_15_out, \中断 , eret);
  Comparator #(.width(2), .mode("unsigned")) comparator_13 (
    .a(IR_Num_Now), .b(IR_Num), .lt(comparator_13_lt));  // open: gt, eq
  Pull_Resistor #(.pull(1)) pull_resistor_11 (.node(comparator_13_lt));
  and and_18 (mfc0, comparator_9_eq, comparator_10_eq);
  and and_19 (mtc0, comparator_9_eq, comparator_11_eq);
  not not_6 (not_6_out, or_14_out);
  or or_16 (or_16_out, or_14_out, eret, mfc0, comparator_12_eq);
  Register #(.width(2), .trigger("rising"), .Select("low")) register_2 (
    .D(adder_4_out), .en(or_15_out), .Q(exist), .clk(CLK), .clr(RST));
  Register #(.width(1), .trigger("rising"), .Select("low")) u_IE (
    .D(not_6_out), .en(or_16_out), .Q(IE), .clk(CLK), .clr(RST));

  // Other names for the same wires on the sheet: Func[5:0] = IR[5:0]; rs[4:0] = IR[25:21]; OP[5:0] = IR[31:26];
  //   R2[31:0] = MDin

  // Notes on the sheet:
  //   中断源
  //   中断等待指示
  //   总复位信号应将除ROM以外所有存储组件全部清零
  //   多级中断测试信号模拟器
  //   数码管输出
  //   指令存储器
  //   数码管输出应该用寄存器锁存，否则显示数据只能一闪而过
  //   contents of rom_1 (hex, n*v repeats v):
  //   201d07d0 20100001 109fc0 139fc3 8021 2012000c 24160008 26100001 3210000f 20080008 20090001 139900
  //   2709825 132020 20020022 c 1094022 1500fff9 22100001 2018000f 2188024 108700 20080008 20090001 139902
  //   2709825 132021 20020022 c 1094022 1500fff9 108702 2c9b022 12c00001 8000c07 4020 1084027 84400
  //   3508ffff 82021 20020022 c 8000c01 afa20000 23bd0004 afa40000 23bd0004 afb00000 23bd0004 afb30000
  //   23bd0004 afb40000 23bd0004 afb50000 23bd0004 afb60000 23bd0004 40000000 20160001 20140003 20150001
  //   168020 108100 2149825 132020 20020022 c 1600fffa 295a022 1680fff7 40800000 23bdfffc 8fb60000
  //   23bdfffc 8fb50000 23bdfffc 8fb40000 23bdfffc 8fb30000 23bdfffc 8fb00000 23bdfffc 8fa40000 23bdfffc
  //   8fa20000 42000018 afa20000 23bd0004 afa40000 23bd0004 afb00000 23bd0004 afb30000 23bd0004 afb40000
  //   23bd0004 afb50000 23bd0004 afb60000 23bd0004 40000000 20160002 20140003 20150001 168020 108100
  //   2149825 132020 20020022 c 1600fffa 295a022 1680fff7 40800000 23bdfffc 8fb60000 23bdfffc 8fb50000
  //   23bdfffc 8fb40000 23bdfffc 8fb30000 23bdfffc 8fb00000 23bdfffc 8fa40000 23bdfffc 8fa20000 42000018
  //   afa20000 23bd0004 afa40000 23bd0004 afb00000 23bd0004 afb30000 23bd0004 afb40000 23bd0004 afb50000
  //   23bd0004 afb60000 23bd0004 40000000 20160003 20140003 20150001 168020 108100 2149825 132020 20020022
  //   c 1600fffa 295a022 1680fff7 40800000 23bdfffc 8fb60000 23bdfffc 8fb50000 23bdfffc 8fb40000 23bdfffc
  //   8fb30000 23bdfffc 8fb00000 23bdfffc 8fa40000 23bdfffc 8fa20000 42000018
  //   控制位
  //   暂停节拍，不能为0
  //   OP
  //   Func
  //   rs
  //   指令字
  //   rt
  //   rd
  //   shamt
  //   立即数I
  //   立即数J
  //   Reset 
  //   Reset 
  //   Reset 
  //   用这个时钟源需要去掉电路中的其他时钟源
  //   JMP
  //   JR
  //   OP
  //   Func
  //   戳工具置1进入计数暂停模式，ctrl+k时钟自动运行到对应节拍暂停
  //   ctrl+k关闭时钟连续运行，将控制位置零，进入单步调试模式调试
  //   Beq
  //   Bne
  //   MemToReg
  //   MemWrite
  //   AluOP
  //   AluSrcB
  //   RegWrite
  //   JAL
  //   RegDst
  //   Syscall
  //   可计数暂停的时钟源
  //   为方便自动评测，需要输出PC，IR，寄存器堆写如数据RDin
  //   RAM写使能MemWrite、RAM写入数据MDin等信号
endmodule

module \封装正确性测试  (
);

  wire IR1, IR2, IR3, MemW, RegW;
  wire [31:0] EX_PC, ID_PC, IF_PC, IR, LED, MDin, MDinr, MEM_PC, PC, RDin, RDinr, WB_PC;

  \单周期MIPS  \u_单周期mips_1  (
    .IR1(IR1), .IR2(IR2), .IR3(IR3), .RegWrite(RegW), .MemWrite(MemW), .PC(PC), .IR(IR), .RDin(RDin),
    .MDin(MDin), .LedData(LED));
  \气泡流水线  \u_气泡流水线_1  (
    .RegWrite(RegW), .MemWrite(MemW), .IF_PC(IF_PC), .ID_PC(ID_PC), .EX_PC(EX_PC), .M_PC(MEM_PC),
    .WB_PC(WB_PC), .RDin(RDinr), .MDin(MDinr), .LedData(LED));
  \单周期MIPS_单级中断  \u_单周期mips_单级中断_1  (
    .IR1(IR1), .IR2(IR2), .IR3(IR3), .RegWrite(RegW), .MemWrite(MemW), .PC(PC), .IR(IR), .RDin(RDin),
    .MDin(MDin), .LedData(LED));
  \理想流水线  \u_理想流水线_1  (
    .RegWrite(RegW), .MemWrite(MemW), .IF_PC(IF_PC), .ID_PC(ID_PC), .EX_PC(EX_PC), .M_PC(MEM_PC),
    .WB_PC(WB_PC), .RDin(RDinr), .MDin(MDinr), .LedData(LED));
  \气泡流水线  \u_气泡流水线_2  (
    .RegWrite(RegW), .MemWrite(MemW), .IF_PC(IF_PC), .ID_PC(ID_PC), .EX_PC(EX_PC), .M_PC(MEM_PC),
    .WB_PC(WB_PC), .RDin(RDinr), .MDin(MDinr), .LedData(LED));
  \单周期MIPS_多级中断  \u_单周期mips_多级中断_1  (
    .IR1(IR1), .IR2(IR2), .IR3(IR3), .RegWrite(RegW), .MemWrite(MemW), .PC(PC), .IR(IR), .RDin(RDin),
    .MDin(MDin), .LedData(LED));

  // Notes on the sheet:
  //   单周期封装测试
  //   气泡流水封装测试
  //   单周期+单级中断封装测试
  //   请检查上面封装有无位宽不匹配，引脚标签是否和连接的标签相对应，否则无法在educoder平台上正确测试
  //   理想流水封装测试
  //   重定向流水封装测试
  //   单周期+多级中断封装测试
endmodule

module IF_ID (
  input  [31:0] IRin32,
  input  [31:0] PCin32,
  input  CTin16,
  input  \传输状态In_表明当前传输数据有效 ,
  input  CLK,
  input  \同步清零_气泡_高电平有效 ,
  input  \使能端_低电平有效_stall_高电平有效 ,
  output [31:0] IRout32,
  output [31:0] PCout32,
  output CTout16,
  output \传输状态Out_表明当前传输数据有效 
);

  wire multiplexer_3_out, multiplexer_4_out, pull_resistor_2_node;
  wire [31:0] multiplexer_1_out, multiplexer_2_out;

  Multiplexer #(.select(1), .width(32), .disabled("Z"), .enable("false")) multiplexer_1 (
    .in0(IRin32), .in1({32{1'b0}}), .out(multiplexer_1_out), .sel(\同步清零_气泡_高电平有效 ));
  Multiplexer #(.select(1), .width(32), .disabled("Z"), .enable("false")) multiplexer_2 (
    .in0(PCin32), .in1({32{1'b0}}), .out(multiplexer_2_out), .sel(\同步清零_气泡_高电平有效 ));
  Multiplexer #(.select(1), .width(1), .disabled("Z"), .enable("false")) multiplexer_3 (
    .in0(CTin16), .in1(1'b0), .out(multiplexer_3_out), .sel(\同步清零_气泡_高电平有效 ));
  Multiplexer #(.select(1), .width(1), .disabled("Z"), .enable("false")) multiplexer_4 (
    .in0(\传输状态In_表明当前传输数据有效 ), .in1(1'b0), .out(multiplexer_4_out), .sel(\同步清零_气泡_高电平有效 ));
  Pull_Resistor #(.pull(0)) pull_resistor_1 (.node(\同步清零_气泡_高电平有效 ));
  Register #(.width(32), .trigger("rising"), .Select("low")) register_1 (
    .D(multiplexer_1_out), .en(pull_resistor_2_node), .Q(IRout32), .clk(CLK));  // open: clr
  Register #(.width(32), .trigger("rising"), .Select("low")) register_2 (
    .D(multiplexer_2_out), .en(pull_resistor_2_node), .Q(PCout32), .clk(CLK));  // open: clr
  Register #(.width(1), .trigger("rising"), .Select("low")) register_3 (
    .D(multiplexer_3_out), .en(pull_resistor_2_node), .Q(CTout16), .clk(CLK));  // open: clr
  Register #(.width(1), .trigger("rising"), .Select("low")) register_4 (
    .D(multiplexer_4_out), .en(pull_resistor_2_node), .Q(\传输状态Out_表明当前传输数据有效 ), .clk(CLK));  // open: clr
  Pull_Resistor #(.pull(0)) pull_resistor_2 (.node(pull_resistor_2_node));
  not not_1 (pull_resistor_2_node, \使能端_低电平有效_stall_高电平有效 );

  // Notes on the sheet:
  //   使能端_低电平有效_stall_高电平有效: pull=down
  //   同步清零_气泡_高电平有效: pull=down
endmodule

module ID_EX (
  input  [31:0] R1in32,
  input  [31:0] R2in32,
  input  [31:0] IRin32,
  input  [31:0] PCin32,
  input  [31:0] IMMin32,
  input  [31:0] _26in32,
  input  [4:0] WBin5,
  input  [3:0] CTRL4,
  input  [1:0] ERETin1,
  input  ERETin1_2,
  input  [4:0] SHin5,
  input  [15:0] CTin16,
  input  [1:0] FWR1in2,
  input  [1:0] FWR2in2,
  input  \传输状态In_表明当前传输数据有效 ,
  input  CLK,
  input  \同步清零_气泡_高电平有效 ,
  input  \使能端_低电平有效_stall_高电平有效 ,
  output [31:0] R1out32,
  output [31:0] R2out32,
  output [31:0] IRout32,
  output [31:0] PCout32,
  output [31:0] R1out32_2,
  output [31:0] R1out32_3,
  output [4:0] WBout5,
  output [3:0] CTRL4_2,
  output [1:0] SHout5,
  output SHout5_2,
  output [4:0] SHout5_3,
  output [15:0] CTout16,
  output [1:0] WBout5_2,
  output [1:0] SHout5_4,
  output \传输状态Out_表明当前传输数据有效 
);

  wire multiplexer_10_out, multiplexer_15_out, pull_resistor_2_node;
  wire [1:0] multiplexer_9_out, multiplexer_13_out, multiplexer_14_out;
  wire [3:0] multiplexer_8_out;
  wire [4:0] multiplexer_7_out, multiplexer_11_out;
  wire [15:0] multiplexer_12_out;
  wire [31:0] multiplexer_1_out, multiplexer_2_out, multiplexer_3_out, multiplexer_4_out, multiplexer_5_out,
       multiplexer_6_out;

  Multiplexer #(.select(1), .width(32), .disabled("Z"), .enable("false")) multiplexer_1 (
    .in0(R1in32), .in1({32{1'b0}}), .out(multiplexer_1_out), .sel(\同步清零_气泡_高电平有效 ));
  Multiplexer #(.select(1), .width(32), .disabled("Z"), .enable("false")) multiplexer_2 (
    .in0(R2in32), .in1({32{1'b0}}), .out(multiplexer_2_out), .sel(\同步清零_气泡_高电平有效 ));
  Multiplexer #(.select(1), .width(32), .disabled("Z"), .enable("false")) multiplexer_3 (
    .in0(IRin32), .in1({32{1'b0}}), .out(multiplexer_3_out), .sel(\同步清零_气泡_高电平有效 ));
  Multiplexer #(.select(1), .width(32), .disabled("Z"), .enable("false")) multiplexer_4 (
    .in0(PCin32), .in1({32{1'b0}}), .out(multiplexer_4_out), .sel(\同步清零_气泡_高电平有效 ));
  Multiplexer #(.select(1), .width(32), .disabled("Z"), .enable("false")) multiplexer_5 (
    .in0(IMMin32), .in1({32{1'b0}}), .out(multiplexer_5_out), .sel(\同步清零_气泡_高电平有效 ));
  Multiplexer #(.select(1), .width(32), .disabled("Z"), .enable("false")) multiplexer_6 (
    .in0(_26in32), .in1({32{1'b0}}), .out(multiplexer_6_out), .sel(\同步清零_气泡_高电平有效 ));
  Multiplexer #(.select(1), .width(5), .disabled("Z"), .enable("false")) multiplexer_7 (
    .in0(WBin5), .in1({5{1'b0}}), .out(multiplexer_7_out), .sel(\同步清零_气泡_高电平有效 ));
  Multiplexer #(.select(1), .width(4), .disabled("Z"), .enable("false")) multiplexer_8 (
    .in0(CTRL4), .in1(4'b0000), .out(multiplexer_8_out), .sel(\同步清零_气泡_高电平有效 ));
  Multiplexer #(.select(1), .width(2), .disabled("Z"), .enable("false")) multiplexer_9 (
    .in0(ERETin1), .in1(2'b00), .out(multiplexer_9_out), .sel(\同步清零_气泡_高电平有效 ));
  Multiplexer #(.select(1), .width(1), .disabled("Z"), .enable("false")) multiplexer_10 (
    .in0(ERETin1_2), .in1(1'b0), .out(multiplexer_10_out), .sel(\同步清零_气泡_高电平有效 ));
  Multiplexer #(.select(1), .width(5), .disabled("Z"), .enable("false")) multiplexer_11 (
    .in0(SHin5), .in1({5{1'b0}}), .out(multiplexer_11_out), .sel(\同步清零_气泡_高电平有效 ));
  Multiplexer #(.select(1), .width(16), .disabled("Z"), .enable("false")) multiplexer_12 (
    .in0(CTin16), .in1({16{1'b0}}), .out(multiplexer_12_out), .sel(\同步清零_气泡_高电平有效 ));
  Multiplexer #(.select(1), .width(2), .disabled("Z"), .enable("false")) multiplexer_13 (
    .in0(FWR1in2), .in1(2'b00), .out(multiplexer_13_out), .sel(\同步清零_气泡_高电平有效 ));
  Multiplexer #(.select(1), .width(2), .disabled("Z"), .enable("false")) multiplexer_14 (
    .in0(FWR2in2), .in1(2'b00), .out(multiplexer_14_out), .sel(\同步清零_气泡_高电平有效 ));
  Multiplexer #(.select(1), .width(1), .disabled("Z"), .enable("false")) multiplexer_15 (
    .in0(\传输状态In_表明当前传输数据有效 ), .in1(1'b0), .out(multiplexer_15_out), .sel(\同步清零_气泡_高电平有效 ));
  Pull_Resistor #(.pull(0)) pull_resistor_1 (.node(\同步清零_气泡_高电平有效 ));
  Register #(.width(32), .trigger("rising"), .Select("low")) register_1 (
    .D(multiplexer_1_out), .en(pull_resistor_2_node), .Q(R1out32), .clk(CLK));  // open: clr
  Register #(.width(32), .trigger("rising"), .Select("low")) register_2 (
    .D(multiplexer_2_out), .en(pull_resistor_2_node), .Q(R2out32), .clk(CLK));  // open: clr
  Register #(.width(32), .trigger("rising"), .Select("low")) register_3 (
    .D(multiplexer_3_out), .en(pull_resistor_2_node), .Q(IRout32), .clk(CLK));  // open: clr
  Register #(.width(32), .trigger("rising"), .Select("low")) register_4 (
    .D(multiplexer_4_out), .en(pull_resistor_2_node), .Q(PCout32), .clk(CLK));  // open: clr
  Register #(.width(32), .trigger("rising"), .Select("low")) register_5 (
    .D(multiplexer_5_out), .en(pull_resistor_2_node), .Q(R1out32_2), .clk(CLK));  // open: clr
  Register #(.width(32), .trigger("rising"), .Select("low")) register_6 (
    .D(multiplexer_6_out), .en(pull_resistor_2_node), .Q(R1out32_3), .clk(CLK));  // open: clr
  Register #(.width(5), .trigger("rising"), .Select("low")) register_7 (
    .D(multiplexer_7_out), .en(pull_resistor_2_node), .Q(WBout5), .clk(CLK));  // open: clr
  Register #(.width(4), .trigger("rising"), .Select("low")) register_8 (
    .D(multiplexer_8_out), .en(pull_resistor_2_node), .Q(CTRL4_2), .clk(CLK));  // open: clr
  Register #(.width(2), .trigger("rising"), .Select("low")) register_9 (
    .D(multiplexer_9_out), .en(pull_resistor_2_node), .Q(SHout5), .clk(CLK));  // open: clr
  Register #(.width(1), .trigger("rising"), .Select("low")) register_10 (
    .D(multiplexer_10_out), .en(pull_resistor_2_node), .Q(SHout5_2), .clk(CLK));  // open: clr
  Register #(.width(5), .trigger("rising"), .Select("low")) register_11 (
    .D(multiplexer_11_out), .en(pull_resistor_2_node), .Q(SHout5_3), .clk(CLK));  // open: clr
  Register #(.width(16), .trigger("rising"), .Select("low")) register_12 (
    .D(multiplexer_12_out), .en(pull_resistor_2_node), .Q(CTout16), .clk(CLK));  // open: clr
  Register #(.width(2), .trigger("rising"), .Select("low")) register_13 (
    .D(multiplexer_13_out), .en(pull_resistor_2_node), .Q(WBout5_2), .clk(CLK));  // open: clr
  Register #(.width(2), .trigger("rising"), .Select("low")) register_14 (
    .D(multiplexer_14_out), .en(pull_resistor_2_node), .Q(SHout5_4), .clk(CLK));  // open: clr
  Pull_Resistor #(.pull(0)) pull_resistor_2 (.node(pull_resistor_2_node));
  not not_1 (pull_resistor_2_node, \使能端_低电平有效_stall_高电平有效 );
  Register #(.width(1), .trigger("rising"), .Select("low")) register_15 (
    .D(multiplexer_15_out), .en(pull_resistor_2_node), .Q(\传输状态Out_表明当前传输数据有效 ), .clk(CLK));  // open: clr

  // Notes on the sheet:
  //   同步清零_气泡_高电平有效: pull=down
  //   使能端_低电平有效_stall_高电平有效: pull=down
endmodule

module EX_MEM (
  input  [31:0] ALUin32,
  input  [31:0] Memin32,
  input  CTin16,
  input  [3:0] CTin4,
  input  [31:0] Resullt2,
  input  ERETin2,
  input  [1:0] ERETin2_2,
  input  [31:0] IRin32,
  input  [31:0] PCin32,
  input  [4:0] WBin5,
  input  [31:0] LEDin32,
  input  [15:0] CTin16_2,
  input  \传输状态In_表明当前传输数据有效 ,
  input  CLK,
  input  \同步清零_气泡_高电平有效 ,
  input  \使能端_低电平有效_stall_高电平有效 ,
  output [31:0] ALUout32,
  output [31:0] Memout32,
  output CTout16,
  output [3:0] CTout16_2,
  output [31:0] CTout16_3,
  output CTout16_4,
  output [1:0] CTout16_5,
  output [31:0] IRout32,
  output [31:0] PCout32,
  output [4:0] WBout5,
  output [31:0] LEDout32,
  output [15:0] CTout16_6,
  output \传输状态Out_表明当前传输数据有效 
);

  wire multiplexer_3_out, multiplexer_6_out, multiplexer_13_out, pull_resistor_2_node;
  wire [1:0] multiplexer_7_out;
  wire [3:0] multiplexer_4_out;
  wire [4:0] multiplexer_10_out;
  wire [15:0] multiplexer_12_out;
  wire [31:0] multiplexer_1_out, multiplexer_2_out, multiplexer_5_out, multiplexer_8_out, multiplexer_9_out,
       multiplexer_11_out;

  Multiplexer #(.select(1), .width(32), .disabled("Z"), .enable("false")) multiplexer_1 (
    .in0(ALUin32), .in1({32{1'b0}}), .out(multiplexer_1_out), .sel(\同步清零_气泡_高电平有效 ));
  Multiplexer #(.select(1), .width(32), .disabled("Z"), .enable("false")) multiplexer_2 (
    .in0(Memin32), .in1({32{1'b0}}), .out(multiplexer_2_out), .sel(\同步清零_气泡_高电平有效 ));
  Multiplexer #(.select(1), .width(1), .disabled("Z"), .enable("false")) multiplexer_3 (
    .in0(CTin16), .in1(1'b0), .out(multiplexer_3_out), .sel(\同步清零_气泡_高电平有效 ));
  Multiplexer #(.select(1), .width(4), .disabled("Z"), .enable("false")) multiplexer_4 (
    .in0(CTin4), .in1(4'b0000), .out(multiplexer_4_out), .sel(\同步清零_气泡_高电平有效 ));
  Multiplexer #(.select(1), .width(32), .disabled("Z"), .enable("false")) multiplexer_5 (
    .in0(Resullt2), .in1({32{1'b0}}), .out(multiplexer_5_out), .sel(\同步清零_气泡_高电平有效 ));
  Multiplexer #(.select(1), .width(1), .disabled("Z"), .enable("false")) multiplexer_6 (
    .in0(ERETin2), .in1(1'b0), .out(multiplexer_6_out), .sel(\同步清零_气泡_高电平有效 ));
  Multiplexer #(.select(1), .width(2), .disabled("Z"), .enable("false")) multiplexer_7 (
    .in0(ERETin2_2), .in1(2'b00), .out(multiplexer_7_out), .sel(\同步清零_气泡_高电平有效 ));
  Multiplexer #(.select(1), .width(32), .disabled("Z"), .enable("false")) multiplexer_8 (
    .in0(IRin32), .in1({32{1'b0}}), .out(multiplexer_8_out), .sel(\同步清零_气泡_高电平有效 ));
  Multiplexer #(.select(1), .width(32), .disabled("Z"), .enable("false")) multiplexer_9 (
    .in0(PCin32), .in1({32{1'b0}}), .out(multiplexer_9_out), .sel(\同步清零_气泡_高电平有效 ));
  Multiplexer #(.select(1), .width(5), .disabled("Z"), .enable("false")) multiplexer_10 (
    .in0(WBin5), .in1({5{1'b0}}), .out(multiplexer_10_out), .sel(\同步清零_气泡_高电平有效 ));
  Multiplexer #(.select(1), .width(32), .disabled("Z"), .enable("false")) multiplexer_11 (
    .in0(LEDin32), .in1({32{1'b0}}), .out(multiplexer_11_out), .sel(\同步清零_气泡_高电平有效 ));
  Multiplexer #(.select(1), .width(16), .disabled("Z"), .enable("false")) multiplexer_12 (
    .in0(CTin16_2), .in1({16{1'b0}}), .out(multiplexer_12_out), .sel(\同步清零_气泡_高电平有效 ));
  Multiplexer #(.select(1), .width(1), .disabled("Z"), .enable("false")) multiplexer_13 (
    .in0(\传输状态In_表明当前传输数据有效 ), .in1(1'b0), .out(multiplexer_13_out), .sel(\同步清零_气泡_高电平有效 ));
  Pull_Resistor #(.pull(0)) pull_resistor_1 (.node(\同步清零_气泡_高电平有效 ));
  Pull_Resistor #(.pull(0)) pull_resistor_2 (.node(pull_resistor_2_node));
  not not_1 (pull_resistor_2_node, \使能端_低电平有效_stall_高电平有效 );
  Register #(.width(32), .trigger("rising"), .Select("low")) register_1 (
    .D(multiplexer_1_out), .en(pull_resistor_2_node), .Q(ALUout32), .clk(CLK));  // open: clr
  Register #(.width(32), .trigger("rising"), .Select("low")) register_2 (
    .D(multiplexer_2_out), .en(pull_resistor_2_node), .Q(Memout32), .clk(CLK));  // open: clr
  Register #(.width(1), .trigger("rising"), .Select("low")) register_3 (
    .D(multiplexer_3_out), .en(pull_resistor_2_node), .Q(CTout16), .clk(CLK));  // open: clr
  Register #(.width(4), .trigger("rising"), .Select("low")) register_4 (
    .D(multiplexer_4_out), .en(pull_resistor_2_node), .Q(CTout16_2), .clk(CLK));  // open: clr
  Register #(.width(32), .trigger("rising"), .Select("low")) register_5 (
    .D(multiplexer_5_out), .en(pull_resistor_2_node), .Q(CTout16_3), .clk(CLK));  // open: clr
  Register #(.width(1), .trigger("rising"), .Select("low")) register_6 (
    .D(multiplexer_6_out), .en(pull_resistor_2_node), .Q(CTout16_4), .clk(CLK));  // open: clr
  Register #(.width(2), .trigger("rising"), .Select("low")) register_7 (
    .D(multiplexer_7_out), .en(pull_resistor_2_node), .Q(CTout16_5), .clk(CLK));  // open: clr
  Register #(.width(32), .trigger("rising"), .Select("low")) register_8 (
    .D(multiplexer_8_out), .en(pull_resistor_2_node), .Q(IRout32), .clk(CLK));  // open: clr
  Register #(.width(32), .trigger("rising"), .Select("low")) register_9 (
    .D(multiplexer_9_out), .en(pull_resistor_2_node), .Q(PCout32), .clk(CLK));  // open: clr
  Register #(.width(5), .trigger("rising"), .Select("low")) register_10 (
    .D(multiplexer_10_out), .en(pull_resistor_2_node), .Q(WBout5), .clk(CLK));  // open: clr
  Register #(.width(32), .trigger("rising"), .Select("low")) register_11 (
    .D(multiplexer_11_out), .en(pull_resistor_2_node), .Q(LEDout32), .clk(CLK));  // open: clr
  Register #(.width(16), .trigger("rising"), .Select("low")) register_12 (
    .D(multiplexer_12_out), .en(pull_resistor_2_node), .Q(CTout16_6), .clk(CLK));  // open: clr
  Register #(.width(1), .trigger("rising"), .Select("low")) register_13 (
    .D(multiplexer_13_out), .en(pull_resistor_2_node), .Q(\传输状态Out_表明当前传输数据有效 ), .clk(CLK));  // open: clr

  // Notes on the sheet:
  //   使能端_低电平有效_stall_高电平有效: pull=down
  //   同步清零_气泡_高电平有效: pull=down
endmodule

module MEM_WB (
  input  [31:0] ALUin32,
  input  [31:0] MDin32,
  input  [31:0] IRin32,
  input  [31:0] PCin32,
  input  [3:0] CTin4,
  input  [31:0] RE2in32,
  input  ERETin1,
  input  [1:0] ERETin1_2,
  input  [4:0] WBin5,
  input  [31:0] LEDin32,
  input  CTin16,
  input  [15:0] CTin16_2,
  input  \传输状态In_表明当前传输数据有效 ,
  input  CLK,
  input  \同步清零_气泡_高电平有效 ,
  input  \使能端_低电平有效_stall_高电平有效 ,
  output [31:0] ALUout32,
  output [31:0] MDout32,
  output [31:0] IRout32,
  output [31:0] PCout32,
  output [3:0] CTout16,
  output [31:0] CTout16_2,
  output CTout16_3,
  output [1:0] CTout16_4,
  output [4:0] WBout5,
  output [31:0] LEDout32,
  output CTout16_5,
  output [15:0] CTout16_6,
  output \传输状态Out_表明当前传输数据有效 
);

  wire multiplexer_7_out, multiplexer_11_out, multiplexer_13_out, not_1_out;
  wire [1:0] multiplexer_8_out;
  wire [3:0] multiplexer_5_out;
  wire [4:0] multiplexer_9_out;
  wire [15:0] multiplexer_12_out;
  wire [31:0] multiplexer_1_out, multiplexer_2_out, multiplexer_3_out, multiplexer_4_out, multiplexer_6_out,
       multiplexer_10_out;

  Multiplexer #(.select(1), .width(32), .disabled("Z"), .enable("false")) multiplexer_1 (
    .in0(ALUin32), .in1({32{1'b0}}), .out(multiplexer_1_out), .sel(\同步清零_气泡_高电平有效 ));
  Multiplexer #(.select(1), .width(32), .disabled("Z"), .enable("false")) multiplexer_2 (
    .in0(MDin32), .in1({32{1'b0}}), .out(multiplexer_2_out), .sel(\同步清零_气泡_高电平有效 ));
  Multiplexer #(.select(1), .width(32), .disabled("Z"), .enable("false")) multiplexer_3 (
    .in0(IRin32), .in1({32{1'b0}}), .out(multiplexer_3_out), .sel(\同步清零_气泡_高电平有效 ));
  Multiplexer #(.select(1), .width(32), .disabled("Z"), .enable("false")) multiplexer_4 (
    .in0(PCin32), .in1({32{1'b0}}), .out(multiplexer_4_out), .sel(\同步清零_气泡_高电平有效 ));
  Multiplexer #(.select(1), .width(4), .disabled("Z"), .enable("false")) multiplexer_5 (
    .in0(CTin4), .in1(4'b0000), .out(multiplexer_5_out), .sel(\同步清零_气泡_高电平有效 ));
  Multiplexer #(.select(1), .width(32), .disabled("Z"), .enable("false")) multiplexer_6 (
    .in0(RE2in32), .in1({32{1'b0}}), .out(multiplexer_6_out), .sel(\同步清零_气泡_高电平有效 ));
  Multiplexer #(.select(1), .width(1), .disabled("Z"), .enable("false")) multiplexer_7 (
    .in0(ERETin1), .in1(1'b0), .out(multiplexer_7_out), .sel(\同步清零_气泡_高电平有效 ));
  Multiplexer #(.select(1), .width(2), .disabled("Z"), .enable("false")) multiplexer_8 (
    .in0(ERETin1_2), .in1(2'b00), .out(multiplexer_8_out), .sel(\同步清零_气泡_高电平有效 ));
  Multiplexer #(.select(1), .width(5), .disabled("Z"), .enable("false")) multiplexer_9 (
    .in0(WBin5), .in1({5{1'b0}}), .out(multiplexer_9_out), .sel(\同步清零_气泡_高电平有效 ));
  Multiplexer #(.select(1), .width(32), .disabled("Z"), .enable("false")) multiplexer_10 (
    .in0(LEDin32), .in1({32{1'b0}}), .out(multiplexer_10_out), .sel(\同步清零_气泡_高电平有效 ));
  Multiplexer #(.select(1), .width(1), .disabled("Z"), .enable("false")) multiplexer_11 (
    .in0(CTin16), .in1(1'b0), .out(multiplexer_11_out), .sel(\同步清零_气泡_高电平有效 ));
  Multiplexer #(.select(1), .width(16), .disabled("Z"), .enable("false")) multiplexer_12 (
    .in0(CTin16_2), .in1({16{1'b0}}), .out(multiplexer_12_out), .sel(\同步清零_气泡_高电平有效 ));
  Multiplexer #(.select(1), .width(1), .disabled("Z"), .enable("false")) multiplexer_13 (
    .in0(\传输状态In_表明当前传输数据有效 ), .in1(1'b0), .out(multiplexer_13_out), .sel(\同步清零_气泡_高电平有效 ));
  Pull_Resistor #(.pull(0)) pull_resistor_1 (.node(\同步清零_气泡_高电平有效 ));
  Register #(.width(32), .trigger("rising"), .Select("low")) register_1 (
    .D(multiplexer_1_out), .en(not_1_out), .Q(ALUout32), .clk(CLK));  // open: clr
  Register #(.width(32), .trigger("rising"), .Select("low")) register_2 (
    .D(multiplexer_2_out), .en(not_1_out), .Q(MDout32), .clk(CLK));  // open: clr
  Register #(.width(32), .trigger("rising"), .Select("low")) register_3 (
    .D(multiplexer_3_out), .en(not_1_out), .Q(IRout32), .clk(CLK));  // open: clr
  Register #(.width(32), .trigger("rising"), .Select("low")) register_4 (
    .D(multiplexer_4_out), .en(not_1_out), .Q(PCout32), .clk(CLK));  // open: clr
  Register #(.width(4), .trigger("rising"), .Select("low")) register_5 (
    .D(multiplexer_5_out), .en(not_1_out), .Q(CTout16), .clk(CLK));  // open: clr
  Register #(.width(32), .trigger("rising"), .Select("low")) register_6 (
    .D(multiplexer_6_out), .en(not_1_out), .Q(CTout16_2), .clk(CLK));  // open: clr
  Register #(.width(1), .trigger("rising"), .Select("low")) register_7 (
    .D(multiplexer_7_out), .en(not_1_out), .Q(CTout16_3), .clk(CLK));  // open: clr
  Register #(.width(2), .trigger("rising"), .Select("low")) register_8 (
    .D(multiplexer_8_out), .en(not_1_out), .Q(CTout16_4), .clk(CLK));  // open: clr
  not not_1 (not_1_out, \使能端_低电平有效_stall_高电平有效 );
  Register #(.width(5), .trigger("rising"), .Select("low")) register_9 (
    .D(multiplexer_9_out), .en(not_1_out), .Q(WBout5), .clk(CLK));  // open: clr
  Register #(.width(32), .trigger("rising"), .Select("low")) register_10 (
    .D(multiplexer_10_out), .en(not_1_out), .Q(LEDout32), .clk(CLK));  // open: clr
  Register #(.width(1), .trigger("rising"), .Select("low")) register_11 (
    .D(multiplexer_11_out), .en(not_1_out), .Q(CTout16_5), .clk(CLK));  // open: clr
  Register #(.width(16), .trigger("rising"), .Select("low")) register_12 (
    .D(multiplexer_12_out), .en(not_1_out), .Q(CTout16_6), .clk(CLK));  // open: clr
  Register #(.width(1), .trigger("rising"), .Select("low")) register_13 (
    .D(multiplexer_13_out), .en(not_1_out), .Q(\传输状态Out_表明当前传输数据有效 ), .clk(CLK));  // open: clr
  Pull_Resistor #(.pull(0)) pull_resistor_2 (.node(not_1_out));

  // Notes on the sheet:
  //   同步清零_气泡_高电平有效: pull=down
  //   使能端_低电平有效_stall_高电平有效: pull=down
endmodule

module \源寄存器使用情况  (
  input  OP0,
  input  OP1,
  input  OP2,
  input  OP3,
  input  OP4,
  input  OP5,
  input  F0,
  input  F1,
  input  F2,
  input  F3,
  input  F4,
  input  F5,
  output R1_used,
  output R2_used
);

  wire and_1_out, and_2_out, and_3_out, and_4_out, and_5_out, and_6_out, and_7_out, and_8_out, and_9_out,
       and_10_out, and_11_out, and_12_out, and_13_out, and_14_out, and_15_out, and_16_out, and_17_out,
       and_18_out, and_19_out, and_20_out, and_21_out, and_22_out, and_23_out, and_24_out, and_25_out,
       and_26_out, and_27_out, and_28_out, and_29_out, and_30_out, and_31_out, and_32_out, and_33_out,
       and_34_out, and_35_out, and_36_out, and_37_out, and_38_out, and_39_out, and_40_out, and_41_out,
       and_42_out, and_43_out, and_44_out, not_1_out, not_2_out, not_3_out, not_4_out, not_5_out, not_6_out,
       not_7_out, not_8_out, not_9_out, not_10_out, not_11_out, not_12_out, not_13_out, not_14_out,
       not_15_out, not_16_out, not_17_out, not_18_out, not_19_out, not_20_out, not_21_out, not_22_out,
       not_23_out, not_24_out, not_25_out, not_26_out, not_27_out, not_28_out, not_29_out, not_30_out,
       not_31_out, not_32_out, not_33_out, not_34_out, not_35_out, not_36_out, not_37_out, not_38_out,
       not_39_out, not_40_out, not_41_out, not_42_out, not_43_out, not_44_out, not_45_out, not_46_out,
       not_47_out, not_48_out, not_49_out, not_50_out, not_51_out, not_52_out, not_53_out, not_54_out,
       not_55_out, not_56_out, not_57_out, not_58_out, not_59_out, not_60_out, not_61_out, not_62_out,
       not_63_out, not_64_out, not_65_out, not_66_out, not_67_out, not_68_out, not_69_out, not_70_out,
       not_71_out, not_72_out, not_73_out, not_74_out, not_75_out, not_76_out, not_77_out, not_78_out,
       not_79_out, not_80_out, not_81_out, not_82_out, not_83_out, not_84_out, not_85_out, not_86_out,
       not_87_out, not_88_out, not_89_out, not_90_out, not_91_out, not_92_out, not_93_out, not_94_out,
       not_95_out, not_96_out, not_97_out, not_98_out, not_99_out, not_100_out, not_101_out, not_102_out,
       not_103_out, not_104_out, not_105_out, not_106_out, not_107_out, not_108_out, not_109_out,
       not_110_out, not_111_out, not_112_out, not_113_out, not_114_out, not_115_out, not_116_out,
       not_117_out, not_118_out, not_119_out, not_120_out, not_121_out, not_122_out, not_123_out,
       not_124_out, not_125_out, not_126_out, not_127_out, not_128_out, not_129_out, not_130_out,
       not_131_out, not_132_out, not_133_out, not_134_out, not_135_out, not_136_out, not_137_out,
       not_138_out, not_139_out, not_140_out, not_141_out, not_142_out, not_143_out, not_144_out,
       not_145_out, not_146_out, not_147_out, not_148_out, not_149_out, not_150_out, not_151_out,
       not_152_out, not_153_out, not_154_out, not_155_out, not_156_out, not_157_out, not_158_out,
       not_159_out, not_160_out, not_161_out, not_162_out, not_163_out, not_164_out, not_165_out,
       not_166_out, not_167_out, not_168_out, not_169_out, not_170_out, not_171_out, not_172_out,
       not_173_out, not_174_out, not_175_out, not_176_out, not_177_out, not_178_out, not_179_out,
       not_180_out, not_181_out, not_182_out, not_183_out, not_184_out, not_185_out, not_186_out,
       not_187_out, not_188_out, not_189_out, not_190_out, not_191_out, not_192_out, not_193_out,
       not_194_out, not_195_out, not_196_out, not_197_out, not_198_out, not_199_out, not_200_out,
       not_201_out, not_202_out, not_203_out, not_204_out, not_205_out, not_206_out, not_207_out,
       not_208_out, not_209_out, not_210_out, not_211_out, not_212_out, not_213_out, not_214_out,
       not_215_out, not_216_out, not_217_out, not_218_out, not_219_out, not_220_out, not_221_out,
       not_222_out, not_223_out, not_224_out, not_225_out, not_226_out, not_227_out, not_228_out,
       not_229_out, not_230_out, not_231_out, not_232_out, not_233_out, not_234_out, not_235_out,
       not_236_out, not_237_out, not_238_out, not_239_out, not_240_out, not_241_out, not_242_out,
       not_243_out, not_244_out, not_245_out, not_246_out, not_247_out, not_248_out, not_249_out,
       not_250_out, not_251_out, not_252_out, not_253_out, not_254_out, not_255_out, not_256_out,
       not_257_out, not_258_out, not_259_out, not_260_out, not_261_out, not_262_out, not_263_out,
       not_264_out, not_265_out, not_266_out, not_267_out, not_268_out, not_269_out, not_270_out,
       not_271_out, not_272_out, not_273_out, not_274_out, not_275_out, not_276_out, not_277_out,
       not_278_out, not_279_out, not_280_out, not_281_out, not_282_out, not_283_out, not_284_out,
       not_285_out, not_286_out, not_287_out, not_288_out, not_289_out, not_290_out, not_291_out,
       not_292_out, not_293_out, not_294_out, not_295_out, not_296_out, not_297_out, not_298_out,
       not_299_out, not_300_out, not_301_out, not_302_out, not_303_out, not_304_out, not_305_out,
       not_306_out, not_307_out, not_308_out, not_309_out, not_310_out, not_311_out, not_312_out,
       not_313_out, not_314_out, not_315_out, not_316_out, not_317_out, not_318_out, not_319_out,
       not_320_out, not_321_out, not_322_out, not_323_out, not_324_out, not_325_out, not_326_out,
       not_327_out, not_328_out, not_329_out;

  not not_1 (not_1_out, OP5);
  not not_2 (not_2_out, OP4);
  not not_3 (not_3_out, OP3);
  not not_4 (not_4_out, OP2);
  not not_5 (not_5_out, OP1);
  not not_6 (not_6_out, OP0);
  not not_7 (not_7_out, F5);
  not not_8 (not_8_out, F4);
  not not_9 (not_9_out, F3);
  not not_10 (not_10_out, F2);
  not not_11 (not_11_out, F1);
  not not_12 (not_12_out, F0);
  not not_13 (not_13_out, OP5);
  not not_14 (not_14_out, OP4);
  not not_15 (not_15_out, OP3);
  not not_16 (not_16_out, OP2);
  not not_17 (not_17_out, OP1);
  not not_18 (not_18_out, OP0);
  not not_19 (not_19_out, F5);
  not not_20 (not_20_out, F4);
  not not_21 (not_21_out, F3);
  not not_22 (not_22_out, F2);
  not not_23 (not_23_out, OP5);
  not not_24 (not_24_out, OP4);
  not not_25 (not_25_out, OP3);
  not not_26 (not_26_out, OP2);
  not not_27 (not_27_out, OP1);
  not not_28 (not_28_out, OP0);
  not not_29 (not_29_out, F5);
  not not_30 (not_30_out, F4);
  not not_31 (not_31_out, F3);
  not not_32 (not_32_out, F2);
  not not_33 (not_33_out, F0);
  not not_34 (not_34_out, OP5);
  not not_35 (not_35_out, OP4);
  not not_36 (not_36_out, OP3);
  not not_37 (not_37_out, OP2);
  not not_38 (not_38_out, OP1);
  not not_39 (not_39_out, OP0);
  not not_40 (not_40_out, F4);
  not not_41 (not_41_out, F3);
  not not_42 (not_42_out, F2);
  not not_43 (not_43_out, F1);
  not not_44 (not_44_out, F0);
  not not_45 (not_45_out, OP5);
  not not_46 (not_46_out, OP4);
  not not_47 (not_47_out, OP3);
  not not_48 (not_48_out, OP2);
  not not_49 (not_49_out, OP1);
  not not_50 (not_50_out, OP0);
  not not_51 (not_51_out, F4);
  not not_52 (not_52_out, F3);
  not not_53 (not_53_out, F2);
  not not_54 (not_54_out, F1);
  not not_55 (not_55_out, OP5);
  not not_56 (not_56_out, OP4);
  not not_57 (not_57_out, OP3);
  not not_58 (not_58_out, OP2);
  not not_59 (not_59_out, OP1);
  not not_60 (not_60_out, OP0);
  not not_61 (not_61_out, F4);
  not not_62 (not_62_out, F3);
  not not_63 (not_63_out, F2);
  not not_64 (not_64_out, F0);
  not not_65 (not_65_out, OP5);
  not not_66 (not_66_out, OP4);
  not not_67 (not_67_out, OP3);
  not not_68 (not_68_out, OP2);
  not not_69 (not_69_out, OP1);
  not not_70 (not_70_out, OP0);
  not not_71 (not_71_out, F4);
  not not_72 (not_72_out, F3);
  not not_73 (not_73_out, F1);
  not not_74 (not_74_out, F0);
  not not_75 (not_75_out, OP5);
  not not_76 (not_76_out, OP4);
  not not_77 (not_77_out, OP3);
  not not_78 (not_78_out, OP2);
  not not_79 (not_79_out, OP1);
  not not_80 (not_80_out, OP0);
  not not_81 (not_81_out, F4);
  not not_82 (not_82_out, F3);
  not not_83 (not_83_out, F1);
  not not_84 (not_84_out, OP5);
  not not_85 (not_85_out, OP4);
  not not_86 (not_86_out, OP3);
  not not_87 (not_87_out, OP2);
  not not_88 (not_88_out, OP1);
  not not_89 (not_89_out, OP0);
  not not_90 (not_90_out, F4);
  not not_91 (not_91_out, F3);
  not not_92 (not_92_out, OP5);
  not not_93 (not_93_out, OP4);
  not not_94 (not_94_out, OP3);
  not not_95 (not_95_out, OP2);
  not not_96 (not_96_out, OP1);
  not not_97 (not_97_out, OP0);
  not not_98 (not_98_out, F4);
  not not_99 (not_99_out, F2);
  not not_100 (not_100_out, F0);
  not not_101 (not_101_out, OP5);
  not not_102 (not_102_out, OP4);
  not not_103 (not_103_out, OP3);
  not not_104 (not_104_out, OP2);
  not not_105 (not_105_out, OP1);
  not not_106 (not_106_out, OP0);
  not not_107 (not_107_out, F4);
  not not_108 (not_108_out, F2);
  not not_109 (not_109_out, OP5);
  not not_110 (not_110_out, OP4);
  not not_111 (not_111_out, OP3);
  not not_112 (not_112_out, OP2);
  not not_113 (not_113_out, OP1);
  not not_114 (not_114_out, OP0);
  not not_115 (not_115_out, F5);
  not not_116 (not_116_out, F4);
  not not_117 (not_117_out, F2);
  not not_118 (not_118_out, F1);
  not not_119 (not_119_out, F0);
  not not_120 (not_120_out, OP5);
  not not_121 (not_121_out, OP4);
  not not_122 (not_122_out, OP3);
  not not_123 (not_123_out, OP2);
  not not_124 (not_124_out, OP1);
  not not_125 (not_125_out, OP0);
  not not_126 (not_126_out, F5);
  not not_127 (not_127_out, F4);
  not not_128 (not_128_out, F1);
  not not_129 (not_129_out, F0);
  not not_130 (not_130_out, OP5);
  not not_131 (not_131_out, OP4);
  not not_132 (not_132_out, OP3);
  not not_133 (not_133_out, OP1);
  not not_134 (not_134_out, OP0);
  not not_135 (not_135_out, OP5);
  not not_136 (not_136_out, OP4);
  not not_137 (not_137_out, OP3);
  not not_138 (not_138_out, OP1);
  not not_139 (not_139_out, OP5);
  not not_140 (not_140_out, OP4);
  not not_141 (not_141_out, OP2);
  not not_142 (not_142_out, OP1);
  not not_143 (not_143_out, OP0);
  not not_144 (not_144_out, OP5);
  not not_145 (not_145_out, OP4);
  not not_146 (not_146_out, OP1);
  not not_147 (not_147_out, OP0);
  not not_148 (not_148_out, OP5);
  not not_149 (not_149_out, OP4);
  not not_150 (not_150_out, OP2);
  not not_151 (not_151_out, OP1);
  not not_152 (not_152_out, OP5);
  not not_153 (not_153_out, OP4);
  not not_154 (not_154_out, OP2);
  not not_155 (not_155_out, OP0);
  not not_156 (not_156_out, OP5);
  not not_157 (not_157_out, OP4);
  not not_158 (not_158_out, OP1);
  not not_159 (not_159_out, OP4);
  not not_160 (not_160_out, OP3);
  not not_161 (not_161_out, OP2);
  not not_162 (not_162_out, OP4);
  not not_163 (not_163_out, OP2);
  not not_164 (not_164_out, OP5);
  not not_165 (not_165_out, OP4);
  not not_166 (not_166_out, OP3);
  not not_167 (not_167_out, OP2);
  not not_168 (not_168_out, OP1);
  not not_169 (not_169_out, OP0);
  not not_170 (not_170_out, F5);
  not not_171 (not_171_out, F4);
  not not_172 (not_172_out, F3);
  not not_173 (not_173_out, OP5);
  not not_174 (not_174_out, OP4);
  not not_175 (not_175_out, OP0);
  not not_176 (not_176_out, OP4);
  not not_177 (not_177_out, OP3);
  not not_178 (not_178_out, OP2);
  not not_179 (not_179_out, OP1);
  not not_180 (not_180_out, OP5);
  not not_181 (not_181_out, OP4);
  not not_182 (not_182_out, OP3);
  not not_183 (not_183_out, OP2);
  not not_184 (not_184_out, OP1);
  not not_185 (not_185_out, OP5);
  not not_186 (not_186_out, OP4);
  not not_187 (not_187_out, OP3);
  not not_188 (not_188_out, OP2);
  not not_189 (not_189_out, OP1);
  not not_190 (not_190_out, OP0);
  not not_191 (not_191_out, F5);
  not not_192 (not_192_out, F4);
  not not_193 (not_193_out, F3);
  not not_194 (not_194_out, F2);
  not not_195 (not_195_out, F1);
  not not_196 (not_196_out, F0);
  not not_197 (not_197_out, OP5);
  not not_198 (not_198_out, OP4);
  not not_199 (not_199_out, OP3);
  not not_200 (not_200_out, OP2);
  not not_201 (not_201_out, OP1);
  not not_202 (not_202_out, OP0);
  not not_203 (not_203_out, F5);
  not not_204 (not_204_out, F4);
  not not_205 (not_205_out, F3);
  not not_206 (not_206_out, F2);
  not not_207 (not_207_out, OP5);
  not not_208 (not_208_out, OP4);
  not not_209 (not_209_out, OP3);
  not not_210 (not_210_out, OP2);
  not not_211 (not_211_out, OP1);
  not not_212 (not_212_out, OP0);
  not not_213 (not_213_out, F5);
  not not_214 (not_214_out, F4);
  not not_215 (not_215_out, F3);
  not not_216 (not_216_out, F2);
  not not_217 (not_217_out, F0);
  not not_218 (not_218_out, OP5);
  not not_219 (not_219_out, OP4);
  not not_220 (not_220_out, OP3);
  not not_221 (not_221_out, OP2);
  not not_222 (not_222_out, OP1);
  not not_223 (not_223_out, OP0);
  not not_224 (not_224_out, F4);
  not not_225 (not_225_out, F3);
  not not_226 (not_226_out, F2);
  not not_227 (not_227_out, F1);
  not not_228 (not_228_out, F0);
  not not_229 (not_229_out, OP5);
  not not_230 (not_230_out, OP4);
  not not_231 (not_231_out, OP3);
  not not_232 (not_232_out, OP2);
  not not_233 (not_233_out, OP1);
  not not_234 (not_234_out, OP0);
  not not_235 (not_235_out, F4);
  not not_236 (not_236_out, F3);
  not not_237 (not_237_out, F2);
  not not_238 (not_238_out, F1);
  not not_239 (not_239_out, OP5);
  not not_240 (not_240_out, OP4);
  not not_241 (not_241_out, OP3);
  not not_242 (not_242_out, OP2);
  not not_243 (not_243_out, OP1);
  not not_244 (not_244_out, OP0);
  not not_245 (not_245_out, F4);
  not not_246 (not_246_out, F3);
  not not_247 (not_247_out, F2);
  not not_248 (not_248_out, F0);
  not not_249 (not_249_out, OP5);
  not not_250 (not_250_out, OP4);
  not not_251 (not_251_out, OP3);
  not not_252 (not_252_out, OP2);
  not not_253 (not_253_out, OP1);
  not not_254 (not_254_out, OP0);
  not not_255 (not_255_out, F4);
  not not_256 (not_256_out, F3);
  not not_257 (not_257_out, F1);
  not not_258 (not_258_out, F0);
  not not_259 (not_259_out, OP5);
  not not_260 (not_260_out, OP4);
  not not_261 (not_261_out, OP3);
  not not_262 (not_262_out, OP2);
  not not_263 (not_263_out, OP1);
  not not_264 (not_264_out, OP0);
  not not_265 (not_265_out, F4);
  not not_266 (not_266_out, F3);
  not not_267 (not_267_out, F1);
  not not_268 (not_268_out, OP5);
  not not_269 (not_269_out, OP4);
  not not_270 (not_270_out, OP3);
  not not_271 (not_271_out, OP2);
  not not_272 (not_272_out, OP1);
  not not_273 (not_273_out, OP0);
  not not_274 (not_274_out, F4);
  not not_275 (not_275_out, F3);
  not not_276 (not_276_out, OP5);
  not not_277 (not_277_out, OP4);
  not not_278 (not_278_out, OP3);
  not not_279 (not_279_out, OP2);
  not not_280 (not_280_out, OP1);
  not not_281 (not_281_out, OP0);
  not not_282 (not_282_out, F4);
  not not_283 (not_283_out, F2);
  not not_284 (not_284_out, F0);
  not not_285 (not_285_out, OP5);
  not not_286 (not_286_out, OP4);
  not not_287 (not_287_out, OP3);
  not not_288 (not_288_out, OP2);
  not not_289 (not_289_out, OP1);
  not not_290 (not_290_out, OP0);
  not not_291 (not_291_out, F4);
  not not_292 (not_292_out, F2);
  not not_293 (not_293_out, OP5);
  not not_294 (not_294_out, OP4);
  not not_295 (not_295_out, OP3);
  not not_296 (not_296_out, OP2);
  not not_297 (not_297_out, OP1);
  not not_298 (not_298_out, OP0);
  not not_299 (not_299_out, F5);
  not not_300 (not_300_out, F4);
  not not_301 (not_301_out, F1);
  not not_302 (not_302_out, F0);
  not not_303 (not_303_out, OP5);
  not not_304 (not_304_out, OP4);
  not not_305 (not_305_out, OP3);
  not not_306 (not_306_out, OP1);
  not not_307 (not_307_out, OP0);
  not not_308 (not_308_out, OP5);
  not not_309 (not_309_out, OP4);
  not not_310 (not_310_out, OP3);
  not not_311 (not_311_out, OP1);
  not not_312 (not_312_out, OP4);
  not not_313 (not_313_out, OP3);
  not not_314 (not_314_out, OP2);
  not not_315 (not_315_out, OP4);
  not not_316 (not_316_out, OP2);
  not not_317 (not_317_out, OP5);
  not not_318 (not_318_out, OP4);
  not not_319 (not_319_out, OP3);
  not not_320 (not_320_out, OP2);
  not not_321 (not_321_out, OP1);
  not not_322 (not_322_out, OP0);
  not not_323 (not_323_out, F5);
  not not_324 (not_324_out, F4);
  not not_325 (not_325_out, F3);
  not not_326 (not_326_out, OP4);
  not not_327 (not_327_out, OP3);
  not not_328 (not_328_out, OP2);
  not not_329 (not_329_out, OP1);
  and and_1 (and_1_out, not_1_out, not_2_out, not_3_out, not_4_out, not_5_out, not_6_out, not_7_out, not_8_out, not_9_out, not_10_out, not_11_out, not_12_out);
  and and_2 (and_2_out, not_13_out, not_14_out, not_15_out, not_16_out, not_17_out, not_18_out, not_19_out, not_20_out, not_21_out, not_22_out, F1, F0);
  and and_3 (and_3_out, not_23_out, not_24_out, not_25_out, not_26_out, not_27_out, not_28_out, not_29_out, not_30_out, not_31_out, not_32_out, F1, not_33_out);
  and and_4 (and_4_out, not_34_out, not_35_out, not_36_out, not_37_out, not_38_out, not_39_out, F5, not_40_out, not_41_out, not_42_out, not_43_out, not_44_out);
  and and_5 (and_5_out, not_45_out, not_46_out, not_47_out, not_48_out, not_49_out, not_50_out, F5, not_51_out, not_52_out, not_53_out, not_54_out, F0);
  and and_6 (and_6_out, not_55_out, not_56_out, not_57_out, not_58_out, not_59_out, not_60_out, F5, not_61_out, not_62_out, not_63_out, F1, not_64_out);
  and and_7 (and_7_out, not_65_out, not_66_out, not_67_out, not_68_out, not_69_out, not_70_out, F5, not_71_out, not_72_out, F2, not_73_out, not_74_out);
  and and_8 (and_8_out, not_75_out, not_76_out, not_77_out, not_78_out, not_79_out, not_80_out, F5, not_81_out, not_82_out, F2, not_83_out, F0);
  and and_9 (and_9_out, not_84_out, not_85_out, not_86_out, not_87_out, not_88_out, not_89_out, F5, not_90_out, not_91_out, F2, F1, F0);
  and and_10 (and_10_out, not_92_out, not_93_out, not_94_out, not_95_out, not_96_out, not_97_out, F5, not_98_out, F3, not_99_out, F1, not_100_out);
  and and_11 (and_11_out, not_101_out, not_102_out, not_103_out, not_104_out, not_105_out, not_106_out, F5, not_107_out, F3, not_108_out, F1, F0);
  and and_12 (and_12_out, not_109_out, not_110_out, not_111_out, not_112_out, not_113_out, not_114_out, not_115_out, not_116_out, F3, not_117_out, not_118_out, not_119_out);
  and and_13 (and_13_out, not_120_out, not_121_out, not_122_out, not_123_out, not_124_out, not_125_out, not_126_out, not_127_out, F3, F2, not_128_out, not_129_out);
  and and_14 (and_14_out, not_130_out, not_131_out, not_132_out, OP2, not_133_out, not_134_out);
  and and_15 (and_15_out, not_135_out, not_136_out, not_137_out, OP2, not_138_out, OP0);
  and and_16 (and_16_out, not_139_out, not_140_out, OP3, not_141_out, not_142_out, not_143_out);
  and and_17 (and_17_out, not_144_out, not_145_out, OP3, OP2, not_146_out, not_147_out);
  and and_18 (and_18_out, not_148_out, not_149_out, OP3, not_150_out, not_151_out, OP0);
  and and_19 (and_19_out, not_152_out, not_153_out, OP3, not_154_out, OP1, not_155_out);
  and and_20 (and_20_out, not_156_out, not_157_out, OP3, OP2, not_158_out, OP0);
  and and_21 (and_21_out, OP5, not_159_out, not_160_out, not_161_out, OP1, OP0);
  and and_22 (and_22_out, OP5, not_162_out, OP3, not_163_out, OP1, OP0);
  and and_23 (and_23_out, not_164_out, not_165_out, not_166_out, not_167_out, not_168_out, not_169_out, not_170_out, not_171_out, not_172_out, F2, F1, F0);
  and and_24 (and_24_out, not_173_out, not_174_out, OP3, OP2, OP1, not_175_out);
  and and_25 (and_25_out, OP5, not_176_out, not_177_out, not_178_out, not_179_out, OP0);
  and and_26 (and_26_out, not_180_out, not_181_out, not_182_out, not_183_out, not_184_out, OP0);
  and and_27 (and_27_out, not_185_out, not_186_out, not_187_out, not_188_out, not_189_out, not_190_out, not_191_out, not_192_out, not_193_out, not_194_out, not_195_out, not_196_out);
  and and_28 (and_28_out, not_197_out, not_198_out, not_199_out, not_200_out, not_201_out, not_202_out, not_203_out, not_204_out, not_205_out, not_206_out, F1, F0);
  and and_29 (and_29_out, not_207_out, not_208_out, not_209_out, not_210_out, not_211_out, not_212_out, not_213_out, not_214_out, not_215_out, not_216_out, F1, not_217_out);
  and and_30 (and_30_out, not_218_out, not_219_out, not_220_out, not_221_out, not_222_out, not_223_out, F5, not_224_out, not_225_out, not_226_out, not_227_out, not_228_out);
  and and_31 (and_31_out, not_229_out, not_230_out, not_231_out, not_232_out, not_233_out, not_234_out, F5, not_235_out, not_236_out, not_237_out, not_238_out, F0);
  and and_32 (and_32_out, not_239_out, not_240_out, not_241_out, not_242_out, not_243_out, not_244_out, F5, not_245_out, not_246_out, not_247_out, F1, not_248_out);
  and and_33 (and_33_out, not_249_out, not_250_out, not_251_out, not_252_out, not_253_out, not_254_out, F5, not_255_out, not_256_out, F2, not_257_out, not_258_out);
  and and_34 (and_34_out, not_259_out, not_260_out, not_261_out, not_262_out, not_263_out, not_264_out, F5, not_265_out, not_266_out, F2, not_267_out, F0);
  and and_35 (and_35_out, not_268_out, not_269_out, not_270_out, not_271_out, not_272_out, not_273_out, F5, not_274_out, not_275_out, F2, F1, F0);
  and and_36 (and_36_out, not_276_out, not_277_out, not_278_out, not_279_out, not_280_out, not_281_out, F5, not_282_out, F3, not_283_out, F1, not_284_out);
  and and_37 (and_37_out, not_285_out, not_286_out, not_287_out, not_288_out, not_289_out, not_290_out, F5, not_291_out, F3, not_292_out, F1, F0);
  and and_38 (and_38_out, not_293_out, not_294_out, not_295_out, not_296_out, not_297_out, not_298_out, not_299_out, not_300_out, F3, F2, not_301_out, not_302_out);
  and and_39 (and_39_out, not_303_out, not_304_out, not_305_out, OP2, not_306_out, not_307_out);
  and and_40 (and_40_out, not_308_out, not_309_out, not_310_out, OP2, not_311_out, OP0);
  and and_41 (and_41_out, OP5, not_312_out, not_313_out, not_314_out, OP1, OP0);
  and and_42 (and_42_out, OP5, not_315_out, OP3, not_316_out, OP1, OP0);
  and and_43 (and_43_out, not_317_out, not_318_out, not_319_out, not_320_out, not_321_out, not_322_out, not_323_out, not_324_out, not_325_out, F2, F1, F0);
  and and_44 (and_44_out, OP5, not_326_out, not_327_out, not_328_out, not_329_out, OP0);
  or or_1 (R1_used, and_1_out, and_2_out, and_3_out, and_4_out, and_5_out, and_6_out, and_7_out, and_8_out, and_9_out, and_10_out, and_11_out, and_12_out, and_13_out, and_14_out, and_15_out, and_16_out, and_17_out, and_18_out, and_19_out, and_20_out, and_21_out, and_22_out, and_23_out, and_24_out, and_25_out, and_26_out);
  or or_2 (R2_used, and_27_out, and_28_out, and_29_out, and_30_out, and_31_out, and_32_out, and_33_out, and_34_out, and_35_out, and_36_out, and_37_out, and_38_out, and_39_out, and_40_out, and_41_out, and_42_out, and_43_out, and_44_out);
endmodule
module \数据相关检测  (
  input  [4:0] ID_R1,
  input  [4:0] EX_WriteReg,
  input  EX_RegWrite,
  input  [4:0] MEM_WriteReg,
  input  MEM_RegWrite,
  input  [5:0] OP,
  input  [5:0] Func,
  input  [4:0] ID_R2,
  output \数据相关 
);

  wire and_1_out, and_2_out, and_3_out, and_4_out, and_5_out, and_6_out, comparator_1_eq, comparator_2_eq,
       comparator_3_eq, comparator_4_eq, comparator_5_eq, comparator_6_eq, not_1_out, not_2_out, or_1_out,
       or_2_out, \源寄存器使用情况_1_r1_used , \源寄存器使用情况_1_r2_used ;

  Comparator #(.width(5), .mode("twosComplement")) comparator_1 (
    .a(ID_R1), .b(EX_WriteReg), .eq(comparator_1_eq));  // open: gt, lt
  Comparator #(.width(5), .mode("twosComplement")) comparator_2 (
    .a(ID_R1), .b(MEM_WriteReg), .eq(comparator_2_eq));  // open: gt, lt
  Comparator #(.width(5), .mode("twosComplement")) comparator_3 (
    .a(ID_R2), .b(EX_WriteReg), .eq(comparator_3_eq));  // open: gt, lt
  Comparator #(.width(5), .mode("twosComplement")) comparator_4 (
    .a(ID_R2), .b(MEM_WriteReg), .eq(comparator_4_eq));  // open: gt, lt
  \源寄存器使用情况  \u_源寄存器使用情况_1  (
    .OP0(OP[0]), .OP1(OP[1]), .OP2(OP[2]), .OP3(OP[3]), .OP4(OP[4]), .OP5(OP[5]), .F0(Func[0]), .F1(Func[1]),
    .F2(Func[2]), .F3(Func[3]), .F4(Func[4]), .F5(Func[5]), .R1_used(\源寄存器使用情况_1_r1_used ),
    .R2_used(\源寄存器使用情况_1_r2_used ));
  not not_1 (not_1_out, comparator_5_eq);
  Comparator #(.width(5), .mode("twosComplement")) comparator_5 (
    .a(ID_R1), .b({5{1'b0}}), .eq(comparator_5_eq));  // open: gt, lt
  and and_1 (and_1_out, comparator_1_eq, EX_RegWrite);
  and and_2 (and_2_out, comparator_2_eq, MEM_RegWrite);
  and and_3 (and_3_out, comparator_3_eq, EX_RegWrite);
  and and_4 (and_4_out, comparator_4_eq, MEM_RegWrite);
  not not_2 (not_2_out, comparator_6_eq);
  Comparator #(.width(5), .mode("twosComplement")) comparator_6 (
    .a(ID_R2), .b({5{1'b0}}), .eq(comparator_6_eq));  // open: gt, lt
  or or_1 (or_1_out, and_1_out, and_2_out);
  or or_2 (or_2_out, and_3_out, and_4_out);
  and and_5 (and_5_out, not_1_out, or_1_out, \源寄存器使用情况_1_r1_used );
  and and_6 (and_6_out, \源寄存器使用情况_1_r2_used , or_2_out, not_2_out);
  or or_3 (\数据相关 , and_5_out, and_6_out);
endmodule

module \load_use相关检测  (
  input  MEM_MemToReg,
  input  [4:0] ID_R1,
  input  [4:0] EX_WriteReg,
  input  EX_RegWrite,
  input  [4:0] MEM_WriteReg,
  input  MEM_RegWrite,
  input  EX_MemToReg,
  input  [5:0] OP,
  input  [5:0] Func,
  input  [4:0] ID_R2,
  output [1:0] ForwardToR1,
  output \Load_Use相关 ,
  output [1:0] ForwardToR2
);

  wire and_1_out, and_2_out, and_3_out, and_4_out, and_5_out, and_6_out, and_7_out, and_8_out,
       comparator_1_eq, comparator_2_eq, comparator_3_eq, comparator_4_eq, comparator_5_eq, comparator_6_eq,
       not_1_out, not_2_out, or_1_out, or_2_out, or_3_out, \源寄存器使用情况_1_r1_used , \源寄存器使用情况_1_r2_used ;
  wire [1:0] multiplexer_1_out, multiplexer_2_out, multiplexer_4_out, multiplexer_6_out;

  Multiplexer #(.select(1), .width(2), .disabled("Z"), .enable("false")) multiplexer_1 (
    .in0(2'b01), .in1(2'b10), .out(multiplexer_1_out), .sel(MEM_MemToReg));
  Comparator #(.width(5), .mode("twosComplement")) comparator_1 (
    .a(ID_R1), .b(EX_WriteReg), .eq(comparator_1_eq));  // open: gt, lt
  Comparator #(.width(5), .mode("twosComplement")) comparator_2 (
    .a(ID_R1), .b(MEM_WriteReg), .eq(comparator_2_eq));  // open: gt, lt
  Comparator #(.width(5), .mode("twosComplement")) comparator_3 (
    .a(ID_R2), .b(EX_WriteReg), .eq(comparator_3_eq));  // open: gt, lt
  Comparator #(.width(5), .mode("twosComplement")) comparator_4 (
    .a(ID_R2), .b(MEM_WriteReg), .eq(comparator_4_eq));  // open: gt, lt
  Multiplexer #(.select(1), .width(2), .disabled("Z"), .enable("false")) multiplexer_2 (
    .in0(2'b01), .in1(2'b10), .out(multiplexer_2_out), .sel(MEM_MemToReg));
  Multiplexer #(.select(1), .width(2), .disabled("Z"), .enable("false")) multiplexer_3 (
    .in0(2'b00), .in1(multiplexer_4_out), .out(ForwardToR1), .sel(and_5_out));
  Multiplexer #(.select(1), .width(2), .disabled("Z"), .enable("false")) multiplexer_4 (
    .in0(multiplexer_1_out), .in1(2'b11), .out(multiplexer_4_out), .sel(comparator_1_eq));
  \源寄存器使用情况  \u_源寄存器使用情况_1  (
    .OP0(OP[0]), .OP1(OP[1]), .OP2(OP[2]), .OP3(OP[3]), .OP4(OP[4]), .OP5(OP[5]), .F0(Func[0]), .F1(Func[1]),
    .F2(Func[2]), .F3(Func[3]), .F4(Func[4]), .F5(Func[5]), .R1_used(\源寄存器使用情况_1_r1_used ),
    .R2_used(\源寄存器使用情况_1_r2_used ));
  Multiplexer #(.select(1), .width(2), .disabled("Z"), .enable("false")) multiplexer_5 (
    .in0(2'b00), .in1(multiplexer_6_out), .out(ForwardToR2), .sel(and_6_out));
  Multiplexer #(.select(1), .width(2), .disabled("Z"), .enable("false")) multiplexer_6 (
    .in0(multiplexer_2_out), .in1(2'b11), .out(multiplexer_6_out), .sel(comparator_3_eq));
  not not_1 (not_1_out, comparator_5_eq);
  Comparator #(.width(5), .mode("twosComplement")) comparator_5 (
    .a(ID_R1), .b({5{1'b0}}), .eq(comparator_5_eq));  // open: gt, lt
  and and_1 (and_1_out, comparator_1_eq, EX_RegWrite);
  and and_2 (and_2_out, comparator_2_eq, MEM_RegWrite);
  and and_3 (and_3_out, comparator_3_eq, EX_RegWrite);
  and and_4 (and_4_out, comparator_4_eq, MEM_RegWrite);
  not not_2 (not_2_out, comparator_6_eq);
  Comparator #(.width(5), .mode("twosComplement")) comparator_6 (
    .a(ID_R2), .b({5{1'b0}}), .eq(comparator_6_eq));  // open: gt, lt
  or or_1 (or_1_out, and_1_out, and_2_out);
  or or_2 (or_2_out, and_3_out, and_4_out);
  and and_5 (and_5_out, not_1_out, or_1_out, \源寄存器使用情况_1_r1_used );
  and and_6 (and_6_out, \源寄存器使用情况_1_r2_used , or_2_out, not_2_out);
  and and_7 (and_7_out, not_1_out, and_1_out, \源寄存器使用情况_1_r1_used );
  and and_8 (and_8_out, \源寄存器使用情况_1_r2_used , and_3_out, not_2_out);
  or or_3 (or_3_out, and_7_out, and_8_out);
  and and_9 (\Load_Use相关 , EX_MemToReg, or_3_out);
endmodule

module MIPS_RAM (
  input  [9:0] \字节地址 ,
  input  [31:0] Din,
  input  CLK,
  input  WE,
  input  Mode,
  input  LH,
  output [31:0] DataOut
);

  wire [7:0] Dout0, Dout1, Dout2, Dout3, \计数器_q ;
  wire [15:0] multiplexer_1_out;
  wire [31:0] bit_extender_1_out;

  RAM #(.addrWidth(10), .dataWidth(8), .bus("separate"), .Select("high")) ram_1 (
    .addr(\字节地址 ), .din(Din[31:24]), .data(Dout3), .str(WE), .clk(CLK));  // open: sel, ld, clr
  RAM #(.addrWidth(10), .dataWidth(8), .bus("separate"), .Select("high")) ram_2 (
    .addr(\字节地址 ), .din(Din[23:16]), .data(Dout2), .str(WE), .clk(CLK));  // open: sel, ld, clr
  // Probe on DataOut
  Multiplexer #(.select(1), .width(16), .disabled("Z"), .enable("false")) multiplexer_1 (
    .in0({Dout1, Dout0}), .in1({Dout3, Dout2}), .out(multiplexer_1_out), .sel(Mode));
  Multiplexer #(.select(1), .width(32), .disabled("Z"), .enable("false")) multiplexer_2 (
    .in0({Dout3, Dout2, Dout1, Dout0}), .in1(bit_extender_1_out), .out(DataOut), .sel(LH));
  assign bit_extender_1_out = {{16{multiplexer_1_out[15]}}, multiplexer_1_out};  // Bit_Extender bit_extender_1
  RAM #(.addrWidth(10), .dataWidth(8), .bus("separate"), .Select("high")) ram_3 (
    .addr(\字节地址 ), .din(Din[15:8]), .data(Dout1), .str(WE), .clk(CLK));  // open: sel, ld, clr
  Counter #(.width(8), .max('hff), .ongoal("wrap"), .trigger("rising"), .behavior("old")) \u_计数器  (
    .Q(\计数器_q ), .clk(CLK));  // open: load, D, count, carry, clr, preset
  // Probe on \计数器_q 
  RAM #(.addrWidth(10), .dataWidth(8), .bus("separate"), .Select("high")) ram_4 (
    .addr(\字节地址 ), .din(Din[7:0]), .data(Dout0), .str(WE), .clk(CLK));  // open: sel, ld, clr

  // Other names for the same wires on the sheet: Din0[7:0] = Din[7:0]; Din1[7:0] = Din[15:8]; Din2[7:0] = Din[23:16];
  //   Din3[7:0] = Din[31:24]; Dout[31:0] = DataOut

  // Notes on the sheet:
  //   输入引脚区
  //   请勿增改引脚，请勿修改子电路封装
  //   电路功能：利用下图中给定的RAM器件实现既既可以按照字节，也可以按照半字，也可以按照32位字访问的MIPS存储器
  //   输出引脚区
  //   请在下方利用上方输入输出引脚的隧道信号构建电路，ctrl+d复制选择部件
  //   为方便测试，注意Dout应一直输出数据，所有数据位不得悬空，所有RAM芯片ld控制端悬空即可
endmodule

module \流水单级中断  (
  output RegWrite,
  output MemWrite,
  output [31:0] IF_PC,
  output [31:0] ID_PC,
  output [31:0] EX_PC,
  output [31:0] M_PC,
  output [31:0] WB_PC,
  output [31:0] RDin,
  output [31:0] MDin,
  output [31:0] LedData
);

  wire and_1_out, and_2_out, and_3_out, and_8_out, and_9_out, and_10_out, BLTZ, BRANCH, CLK, clock_1_out,
       clock_2_out, CLR, comparator_2_eq, comparator_2_lt, comparator_4_lt, d_ff_1_q, decoder_1_out1,
       decoder_1_out2, decoder_1_out3, equal, ERET, EX_BLTZ, EX_BRANCH, ex_mem_1_ctout16, ex_mem_1_ctout16_4,
       \ex_mem_1_传输状态out_表明当前传输数据有效 , EX_SRAV, Go, ID_EX_shout5_2, \ID_EX_传输状态out_表明当前传输数据有效 , IE_q,
       \if_id_1_传输状态out_表明当前传输数据有效 , ir, IR1, IR2, IR3, Led, MEM_LH, Mem_MemToReg, Mem_RegWrite,
       mem_wb_1_ctout16_5, nand_1_out, not_1_out, not_2_out, or_1_out, or_3_out, or_5_out, or_6_out,
       or_7_out, or_8_out, or_9_out, register_1_q, RET1, RET2, RET3, RST, W1, W2, W3, WB_ERET,
       \中断按键参考电路_1_与中断屏蔽位与 , \中断按键参考电路_2_与中断屏蔽位与 , \中断按键参考电路_3_与中断屏蔽位与 , \开中断 , \数据相关 ;
  wire [1:0] F, ForwardR1, ForwardR2, ID_EX_wbout5_2, priority_encoder_1_out, register_2_q, undriven;
  wire [2:0] ID_EX_ctrl4_2;
  wire [3:0] CTRL4, ex_mem_1_ctout16_2;
  wire [4:0] ex_mem_1_wbout5, ID_EX_shout5_3, ID_EX_wbout5, mem_wb_1_wbout5, multiplexer_5_out,
       multiplexer_6_out, multiplexer_7_out, multiplexer_8_out, multiplexer_11_out;
  wire [12:0] CNT_num;
  wire [15:0] CTRL, EX_CTRL, ex_mem_1_ctout16_6, \LoadUse次数 , mem_wb_1_ctout16_6, \总周期数 , \无条件分支数 , \条件分支成功数 ;
  wire [31:0] adder_1_out, adder_2_out, adder_3_out, adder_4_out, ALURes, bit_extender_1_out,
       bit_extender_2_out, bit_extender_3_out, EPC, EX_IR, ex_mem_1_ledout32, EX_R1, EX_R2, EXALU,
       ID_EX_r1out32, ID_EX_r1out32_2, ID_EX_r1out32_3, ID_IR, IF_IR, MEM_IR, mips_alu_1_result,
       mips_ram_1_dataout, mips_regifile_1_r1, mips_regifile_1_r2, multiplexer_1_out, multiplexer_2_out,
       multiplexer_3_out, multiplexer_9_out, multiplexer_12_out, multiplexer_13_out, multiplexer_14_out,
       multiplexer_15_out, multiplexer_16_out, multiplexer_17_out, R2, RD, register_3_q, shifter_1_out,
       shifter_2_out, WB_IR, \中断程序入口地址 ;

  Button \u_总复位  (.out(RST));
  Button _1 (.out(IR1));
  Button _2 (.out(IR2));
  Button _3 (.out(IR3));
  // Probe on \总周期数 
  // Probe on \总周期数 
  Button \u_继续运行  (.out(Go));
  LED #(.active("true")) led_1 (.in(W1));
  LED #(.active("true")) led_2 (.in(W2));
  LED #(.active("true")) led_3 (.in(W3));
  Hex_Digit_Display hex_digit_display_1 (.value(LedData[31:28]));  // open: dp
  // Probe on IF_PC[19:0]
  // Mips_Probe mips_probe_1: pin names not known; wires that end beside it: IF_IR
  \中断按键参考电路  \u_中断按键参考电路_1  (
    .CLK(CLK), .\与中断屏蔽位与 (\中断按键参考电路_1_与中断屏蔽位与 ), .\_1号中断信号 (IR1), .\_1号中断等待指示灯 (W1), .\同步清零信号 (RET1));
  \中断按键参考电路  \u_中断按键参考电路_2  (
    .CLK(CLK), .\与中断屏蔽位与 (\中断按键参考电路_2_与中断屏蔽位与 ), .\_1号中断信号 (IR2), .\_1号中断等待指示灯 (W2), .\同步清零信号 (RET2));
  \中断按键参考电路  \u_中断按键参考电路_3  (
    .CLK(CLK), .\与中断屏蔽位与 (\中断按键参考电路_3_与中断屏蔽位与 ), .\_1号中断信号 (IR3), .\_1号中断等待指示灯 (W3), .\同步清零信号 (RET3));
  Hex_Digit_Display hex_digit_display_2 (.value(LedData[23:20]));  // open: dp
  Hex_Digit_Display hex_digit_display_3 (.value(LedData[27:24]));  // open: dp
  // Probe on ID_PC[19:0]
  // Mips_Probe mips_probe_2: pin names not known; wires that end beside it: ID_IR
  Multiplexer #(.select(1), .width(32), .disabled("Z"), .enable("false")) multiplexer_1 (
    .in0(multiplexer_3_out), .in1(EPC), .out(multiplexer_1_out), .sel(WB_ERET));
  and and_1 (and_1_out, mem_wb_1_ctout16_6[4], ~mem_wb_1_ctout16_5);  // AND_Gate
  Comparator #(.width(32), .mode("twosComplement")) comparator_1 (
    .a(ID_IR), .b(32'h42000018), .eq(ERET));  // open: gt, lt
  Hex_Digit_Display hex_digit_display_4 (.value(LedData[19:16]));  // open: dp
  Hex_Digit_Display hex_digit_display_5 (.value(LedData[15:12]));  // open: dp
  Multiplexer #(.select(1), .width(32), .disabled("Z"), .enable("false")) multiplexer_2 (
    .in0(multiplexer_1_out), .in1(\中断程序入口地址 ), .out(multiplexer_2_out), .sel(ir));
  and and_2 (and_2_out, ~\数据相关 , not_1_out);  // AND_Gate
  Register #(.width(1), .trigger("rising"), .Select("low")) register_1 (
    .D(mem_wb_1_ctout16_6[4]), .en(and_1_out), .Q(register_1_q), .clk(CLK), .clr(or_1_out));
  or or_1 (or_1_out, RST, Go);
  Multiplexer #(.select(1), .width(32), .disabled("Z"), .enable("false")) multiplexer_3 (
    .in0(adder_1_out), .in1(multiplexer_16_out), .out(multiplexer_3_out), .sel(BRANCH));
  or or_2 (BRANCH, EX_BRANCH, BLTZ, EX_CTRL[15]);
  Hex_Digit_Display hex_digit_display_6 (.value(LedData[7:4]));  // open: dp
  Hex_Digit_Display hex_digit_display_7 (.value(LedData[11:8]));  // open: dp
  Clock #(.highDuration(1), .lowDuration(1)) clock_1 (.out(clock_1_out));
  // Probe on EX_PC[19:0]
  // Mips_Probe mips_probe_3: pin names not known; wires that end beside it: clock_1_out, EX_IR, CLK
  Register #(.width(32), .trigger("rising"), .Select("low")) PC (
    .D(multiplexer_2_out), .en(and_2_out), .Q(IF_PC), .clk(CLK), .clr(RST));
  Counter #(.width(16), .max('hffff), .ongoal("wrap"), .trigger("rising"), .behavior("old")) counter_1 (
    .count(not_1_out), .Q(\总周期数 ), .clk(CLK), .clr(RST));  // open: load, D, carry, preset
  not not_1 (not_1_out, register_1_q);
  Priority_Encoder #(.select(2), .disabled("Z")) priority_encoder_1 (
    .in0(1'b0), .in1(\中断按键参考电路_1_与中断屏蔽位与 ), .in2(\中断按键参考电路_2_与中断屏蔽位与 ), .in3(\中断按键参考电路_3_与中断屏蔽位与 ),
    .out(priority_encoder_1_out), .gs(\开中断 ), .en_in(1'b1));  // open: en_out
  Hex_Digit_Display hex_digit_display_8 (.value(LedData[3:0]));  // open: dp
  Adder #(.width(32)) adder_1 (.a(IF_PC), .b(32'h4), .out(adder_1_out));  // open: cin, cout
  and and_3 (and_3_out, \数据相关 , not_1_out);
  or or_3 (or_3_out, ir, WB_ERET);
  // Probe on \总周期数 
  // Probe on M_PC[19:0]
  // Mips_Probe mips_probe_4: pin names not known; wires that end beside it: MEM_IR
  \load_use相关检测  \load_use相关检测_1  (
    .MEM_MemToReg(Mem_MemToReg), .ID_R1(multiplexer_5_out), .EX_WriteReg(ID_EX_wbout5),
    .EX_RegWrite(EX_CTRL[7]), .MEM_WriteReg(ex_mem_1_wbout5), .MEM_RegWrite(Mem_RegWrite), .OP(ID_IR[31:26]),
    .Func(ID_IR[5:0]), .ID_R2(multiplexer_6_out), .ForwardToR1(ForwardR1), .\Load_Use相关 (\数据相关 ),
    .ForwardToR2(ForwardR2), .EX_MemToReg(EX_CTRL[10]));
  ROM #(.addrWidth(10), .dataWidth(32), .Select("high")) rom_1 (.addr(IF_PC[11:2]), .data(IF_IR));
  Counter #(.width(16), .max('hffff), .ongoal("wrap"), .trigger("rising"), .behavior("old")) counter_2 (
    .count(and_3_out), .Q(\LoadUse次数 ), .clk(CLK), .clr(RST));  // open: load, D, carry, preset
  Multiplexer #(.select(2), .width(32), .disabled("Z"), .enable("false")) multiplexer_4 (
    .in1(32'h30ac), .in2(32'h3150), .in3(32'h31f4), .out(\中断程序入口地址 ), .sel(priority_encoder_1_out));  // open: in0
  Register #(.width(32), .trigger("rising"), .Select("low")) u_EPC (
    .D(EX_PC), .en(ir), .Q(EPC), .clk(CLK));  // open: clr
  Register #(.width(1), .trigger("rising"), .Select("low")) IE (
    .D(ir), .en(or_3_out), .Q(IE_q), .clk(CLK));  // open: clr
  // Probe on \总周期数 
  // Probe on \无条件分支数 
  // Probe on \条件分支成功数 
  // Probe on \LoadUse次数 
  // Probe on \LoadUse次数 
  or or_4 (CLR, ir, RST, BRANCH, WB_ERET);
  IF_ID if_id_1 (
    .IRin32(IF_IR), .PCin32(IF_PC), .\传输状态In_表明当前传输数据有效 (1'b1), .CLK(CLK), .IRout32(ID_IR), .PCout32(ID_PC),
    .\传输状态Out_表明当前传输数据有效 (\if_id_1_传输状态out_表明当前传输数据有效 ), .\同步清零_气泡_高电平有效 (CLR),
    .\使能端_低电平有效_stall_高电平有效 (or_5_out));  // open: CTin16, CTout16
  or or_5 (or_5_out, \数据相关 , register_1_q);
  not not_2 (not_2_out, IE_q);
  // Probe on IF_PC[11:0]
  // Probe on WB_PC[19:0]
  // Mips_Probe mips_probe_5: pin names not known; wires that end beside it: WB_IR
  Register #(.width(2), .trigger("rising"), .Select("low")) register_2 (
    .D(priority_encoder_1_out), .en(ir), .Q(register_2_q), .clk(CLK));  // open: clr
  and and_4 (ir, not_2_out, \开中断 );
  // Probe on ID_PC[11:0]
  // Probe on EX_PC[11:0]
  Decoder #(.select(2), .tristate("false"), .disabled("Z"), .enable("false")) decoder_1 (
    .out1(decoder_1_out1), .out2(decoder_1_out2), .out3(decoder_1_out3), .sel(register_2_q));  // open: out0
  // Probe on M_PC[11:0]
  D_Flip_Flop #(.trigger("high"), .Pre_Clr_Positions("LEGACY"), .NegatePresetClear("false"), .enable("true"), .NewFFLayout("false")) d_ff_1 (.Q(d_ff_1_q));  // open: clk, D, Qn, preset, en, reset
  // Probe on 13'hc
  Multiplexer #(.select(1), .width(5), .disabled("Z"), .enable("false")) multiplexer_5 (
    .in0(ID_IR[25:21]), .in1(5'b00100), .out(multiplexer_5_out), .sel(CTRL[4]));
  Multiplexer #(.select(1), .width(5), .disabled("Z"), .enable("false")) multiplexer_6 (
    .in0(ID_IR[20:16]), .in1(5'b00010), .out(multiplexer_6_out), .sel(CTRL[4]));
  Multiplexer #(.select(1), .width(5), .disabled("Z"), .enable("false")) multiplexer_7 (
    .in0(ID_IR[20:16]), .in1(ID_IR[15:11]), .out(multiplexer_7_out), .sel(CTRL[5]));
  Multiplexer #(.select(1), .width(5), .disabled("Z"), .enable("false")) multiplexer_8 (
    .in0(multiplexer_7_out), .in1({5{1'b1}}), .out(multiplexer_8_out), .sel(CTRL[6]));
  // Probe on WB_PC[11:0]
  Comparator #(.width(13), .mode("twosComplement")) comparator_2 (
    .a(CNT_num), .b(13'hc), .eq(comparator_2_eq), .lt(comparator_2_lt));  // open: gt
  Clock #(.highDuration(1), .lowDuration(1)) clock_2 (.out(clock_2_out));
  \单周期硬布线控制器  \u_单周期硬布线控制器_1  (
    .OP(ID_IR[31:26]), .Func(ID_IR[5:0]), .ALU_OP(CTRL[3:0]), .MemToReg(CTRL[10]), .MemWrite(CTRL[9]),
    .BLTZ(CTRL4[3]), .LH(CTRL4[2]), .SRAV(CTRL4[1]), .XORI(CTRL4[0]), .ALU_SRC(CTRL[8]), .RegWrite(CTRL[7]),
    .SysCALL(CTRL[4]), .SignedExt(CTRL[13]), .RegDst(CTRL[5]), .Beq(CTRL[12]), .Bne(CTRL[11]), .JR(CTRL[14]),
    .JMP(CTRL[15]), .JAL(CTRL[6]));
  assign bit_extender_1_out = {{16{1'b0}}, ID_IR[15:0]};  // Bit_Extender bit_extender_1
  assign bit_extender_2_out = {{16{ID_IR[15]}}, ID_IR[15:0]};  // Bit_Extender bit_extender_2
  assign bit_extender_3_out = {{6{ID_IR[25]}}, ID_IR[25:0]};  // Bit_Extender bit_extender_3
  and and_5 (RET1, decoder_1_out1, WB_ERET);
  and and_6 (RET2, decoder_1_out2, WB_ERET);
  and and_7 (RET3, decoder_1_out3, WB_ERET);
  nand nand_1 (nand_1_out, d_ff_1_q, comparator_2_eq);
  Counter #(.width(13), .max('h1fff), .ongoal("stay"), .trigger("rising"), .behavior("old")) counter_3 (
    .count(comparator_2_lt), .Q(CNT_num), .clk(clock_2_out));  // open: load, D, carry, clr, preset
  MIPS_Regifile mips_regifile_1 (
    .Din(RDin), .Clk(CLK), .R1(mips_regifile_1_r1), .R2(mips_regifile_1_r2), .WE(RegWrite),
    .W_num(mem_wb_1_wbout5), .R1_num(multiplexer_5_out), .R2_num(multiplexer_6_out));
  Multiplexer #(.select(1), .width(32), .disabled("Z"), .enable("false")) multiplexer_9 (
    .in0(bit_extender_1_out), .in1(bit_extender_2_out), .out(multiplexer_9_out), .sel(CTRL[13]));
  assign CLK = nand_1_out ? clock_2_out : 1'bz;  // Controlled_Buffer controlled_buffer_1
  Shifter #(.width(32), .shift("ll")) shifter_1 (.in(bit_extender_3_out), .\dist (5'b00010), .out(shifter_1_out));
  Pull_Resistor #(.pull(1)) pull_resistor_1 (.node(CLK));
  or or_6 (or_6_out, \数据相关 , CLR);
  ID_EX ID_EX (
    .R1in32(mips_regifile_1_r1), .R2in32(mips_regifile_1_r2), .IRin32(ID_IR), .PCin32(ID_PC),
    .IMMin32(multiplexer_9_out), .WBin5(multiplexer_8_out), .SHin5(ID_IR[10:6]), .CTin16(CTRL),
    .\传输状态In_表明当前传输数据有效 (\if_id_1_传输状态out_表明当前传输数据有效 ), .CLK(CLK), .R1out32(ID_EX_r1out32), .R2out32(EX_R2),
    .IRout32(EX_IR), .PCout32(EX_PC), .R1out32_2(ID_EX_r1out32_2), .WBout5(ID_EX_wbout5),
    .SHout5_3(ID_EX_shout5_3), .CTout16(EX_CTRL), .\传输状态Out_表明当前传输数据有效 (\ID_EX_传输状态out_表明当前传输数据有效 ),
    .\同步清零_气泡_高电平有效 (or_6_out), .\使能端_低电平有效_stall_高电平有效 (register_1_q), ._26in32(shifter_1_out),
    .R1out32_3(ID_EX_r1out32_3), .FWR1in2(ForwardR1), .WBout5_2(ID_EX_wbout5_2), .FWR2in2(ForwardR2),
    .SHout5_4(F), .CTRL4(CTRL4), .CTRL4_2({EX_BLTZ, ID_EX_ctrl4_2[2], EX_SRAV, ID_EX_ctrl4_2[0]}),
    .ERETin1_2(ERET), .SHout5_2(ID_EX_shout5_2));  // open: ERETin1, SHout5
  Register #(.width(32), .trigger("rising"), .Select("low")) register_3 (
    .D(EX_R1), .en(and_8_out), .Q(register_3_q), .clk(CLK));  // open: clr
  and and_8 (and_8_out, Led, EX_CTRL[4]);
  Multiplexer #(.select(2), .width(32), .disabled("Z"), .enable("false")) multiplexer_10 (
    .in0(ID_EX_r1out32), .in1(ALURes), .in2(RD), .in3(EXALU), .out(EX_R1), .sel(ID_EX_wbout5_2));
  Shifter #(.width(32), .shift("ll")) shifter_2 (.in(ID_EX_r1out32_2), .\dist (5'b00010), .out(shifter_2_out));
  Multiplexer #(.select(1), .width(5), .disabled("Z"), .enable("false")) multiplexer_11 (
    .in0(ID_EX_shout5_3), .in1(EX_R1[4:0]), .out(multiplexer_11_out), .sel(EX_SRAV));
  Adder #(.width(32)) adder_2 (.a(EX_PC), .b(32'h4), .out(adder_2_out));  // open: cin, cout
  Multiplexer #(.select(1), .width(32), .disabled("Z"), .enable("false")) multiplexer_12 (
    .in0(R2), .in1(ID_EX_r1out32_2), .out(multiplexer_12_out), .sel(EX_CTRL[8]));
  Comparator #(.width(32), .mode("twosComplement")) comparator_3 (.a(R2), .b(32'h22), .eq(Led));  // open: gt, lt
  Adder #(.width(32)) adder_3 (.a(shifter_2_out), .b(adder_2_out), .out(adder_3_out));  // open: cin, cout
  MIPS_ALU mips_alu_1 (
    .X(EX_R1), .Y(multiplexer_12_out), .AluOP(EX_CTRL[3:0]), .Equal(equal), .Result(mips_alu_1_result),
    .shamt(multiplexer_11_out));  // open: Result_2
  Multiplexer #(.select(1), .width(32), .disabled("Z"), .enable("false")) multiplexer_13 (
    .in0(ID_EX_r1out32_3), .in1(EX_R1), .out(multiplexer_13_out), .sel(EX_CTRL[14]));
  Multiplexer #(.select(1), .width(32), .disabled("Z"), .enable("false")) multiplexer_14 (
    .in0(adder_2_out), .in1(adder_3_out), .out(multiplexer_14_out), .sel(EX_BRANCH));
  or or_7 (or_7_out, WB_ERET, RST, ir);
  EX_MEM ex_mem_1 (
    .ALUin32(mips_alu_1_result), .Memin32(R2), .IRin32(EX_IR), .PCin32(EX_PC), .WBin5(ID_EX_wbout5),
    .CTin16_2(EX_CTRL), .\传输状态In_表明当前传输数据有效 (\ID_EX_传输状态out_表明当前传输数据有效 ), .CLK(CLK), .ALUout32(EXALU),
    .Memout32(MDin), .IRout32(MEM_IR), .PCout32(M_PC), .WBout5(ex_mem_1_wbout5),
    .CTout16_6({ex_mem_1_ctout16_6[15:11], Mem_MemToReg, MemWrite, ex_mem_1_ctout16_6[8], Mem_RegWrite, ex_mem_1_ctout16_6[6:0]}),
    .\传输状态Out_表明当前传输数据有效 (\ex_mem_1_传输状态out_表明当前传输数据有效 ), .\同步清零_气泡_高电平有效 (or_7_out),
    .\使能端_低电平有效_stall_高电平有效 (register_1_q), .LEDin32(register_3_q), .LEDout32(ex_mem_1_ledout32),
    .CTin16(Led), .CTout16(ex_mem_1_ctout16), .CTin4({EX_BLTZ, ID_EX_ctrl4_2[2], EX_SRAV, ID_EX_ctrl4_2[0]}),
    .CTout16_2({ex_mem_1_ctout16_2[3], MEM_LH, ex_mem_1_ctout16_2[1:0]}), .ERETin2(ID_EX_shout5_2),
    .CTout16_4(ex_mem_1_ctout16_4), .ERETin2_2(undriven));  // open: Resullt2, CTout16_3, CTout16_5
  Multiplexer #(.select(1), .width(32), .disabled("Z"), .enable("false")) multiplexer_15 (
    .in0(multiplexer_14_out), .in1(adder_3_out), .out(multiplexer_15_out), .sel(BLTZ));
  Multiplexer #(.select(1), .width(32), .disabled("Z"), .enable("false")) multiplexer_16 (
    .in0(multiplexer_15_out), .in1(multiplexer_13_out), .out(multiplexer_16_out), .sel(EX_CTRL[15]));
  MIPS_RAM mips_ram_1 (
    .\字节地址 (EXALU[11:2]), .Din(MDin), .DataOut(mips_ram_1_dataout), .CLK(CLK), .WE(MemWrite),
    .Mode(EXALU[1]), .LH(MEM_LH));
  or or_8 (or_8_out, WB_ERET, RST);
  MEM_WB mem_wb_1 (
    .ALUin32(EXALU), .MDin32(mips_ram_1_dataout), .IRin32(MEM_IR), .PCin32(M_PC), .WBin5(ex_mem_1_wbout5),
    .CTin16_2({ex_mem_1_ctout16_6[15:11], Mem_MemToReg, MemWrite, ex_mem_1_ctout16_6[8], Mem_RegWrite, ex_mem_1_ctout16_6[6:0]}),
    .\传输状态In_表明当前传输数据有效 (\ex_mem_1_传输状态out_表明当前传输数据有效 ), .CLK(CLK), .ALUout32(ALURes), .MDout32(RD),
    .IRout32(WB_IR), .PCout32(WB_PC), .WBout5(mem_wb_1_wbout5),
    .CTout16_6({mem_wb_1_ctout16_6[15:8], RegWrite, mem_wb_1_ctout16_6[6:0]}), .\同步清零_气泡_高电平有效 (or_8_out),
    .\使能端_低电平有效_stall_高电平有效 (register_1_q), .LEDin32(ex_mem_1_ledout32), .LEDout32(LedData),
    .CTin16(ex_mem_1_ctout16), .CTout16_5(mem_wb_1_ctout16_5),
    .CTin4({ex_mem_1_ctout16_2[3], MEM_LH, ex_mem_1_ctout16_2[1:0]}), .ERETin1(ex_mem_1_ctout16_4),
    .CTout16_3(WB_ERET));  // open: 传输状态Out_表明当前传输数据有效, CTout16, CTout16_2, RE2in32, ERETin1_2, CTout16_4
  Multiplexer #(.select(1), .width(32), .disabled("Z"), .enable("false")) multiplexer_17 (
    .in0(ALURes), .in1(RD), .out(multiplexer_17_out), .sel(mem_wb_1_ctout16_6[10]));
  Adder #(.width(32)) adder_4 (.a(WB_PC), .b(32'h4), .out(adder_4_out));  // open: cin, cout
  Multiplexer #(.select(1), .width(32), .disabled("Z"), .enable("false")) multiplexer_18 (
    .in0(multiplexer_17_out), .in1(adder_4_out), .out(RDin), .sel(mem_wb_1_ctout16_6[6]));
  Counter #(.width(16), .max('hffff), .ongoal("wrap"), .trigger("rising"), .behavior("old")) counter_4 (
    .count(EX_CTRL[15]), .Q(\无条件分支数 ), .clk(CLK), .clr(RST));  // open: load, D, carry, preset
  Counter #(.width(16), .max('hffff), .ongoal("wrap"), .trigger("rising"), .behavior("old")) counter_5 (
    .count(or_9_out), .Q(\条件分支成功数 ), .clk(CLK), .clr(RST));  // open: load, D, carry, preset
  or or_9 (or_9_out, BLTZ, EX_BRANCH);
  Comparator #(.width(32), .mode("twosComplement")) comparator_4 (
    .a(EX_R1), .b({32{1'b0}}), .lt(comparator_4_lt));  // open: gt, eq
  Multiplexer #(.select(2), .width(32), .disabled("Z"), .enable("false")) multiplexer_19 (
    .in0(EX_R2), .in1(ALURes), .in2(RD), .in3(EXALU), .out(R2), .sel(F));
  and and_9 (and_9_out, equal, EX_CTRL[12]);
  and and_10 (and_10_out, ~equal, EX_CTRL[11]);  // AND_Gate
  and and_11 (BLTZ, comparator_4_lt, EX_BLTZ);
  or or_10 (EX_BRANCH, and_9_out, and_10_out);

  // Other names for the same wires on the sheet: SignedExt = CTRL[13]; EX_RegWrite = EX_CTRL[7];
  //   EX_MemToReg = EX_CTRL[10]; EX_JR = EX_CTRL[14]; EX_JMP = EX_CTRL[15]; MEM_PC[31:0] = M_PC;
  //   插入气泡数[15:0] = \LoadUse次数 

  // Notes on the sheet:
  //   中断源
  //   时空图监测，可删除
  //   中断等待指示
  //   数码管输出
  //   指令存储器
  //   contents of rom_1 (hex, n*v repeats v):
  //   201d07d0 20100001 109fc0 139fc3 8021 2012000c 24160008 26100001 3210000f 20080008 20090001 139900
  //   2709825 132020 20020022 c 1094022 1500fff9 22100001 2018000f 2188024 108700 20080008 20090001 139902
  //   2709825 132021 20020022 c 1094022 1500fff9 108702 2c9b022 12c00001 8100007 4020 1084027 84400
  //   3508ffff 82021 20020022 c 8100001 afa20000 23bd0004 afa40000 23bd0004 afb00000 23bd0004 afb30000
  //   23bd0004 afb40000 23bd0004 afb50000 23bd0004 afb60000 23bd0004 20160001 20140003 20150001 168020
  //   108100 2149825 132020 20020022 c 1600fffa 295a022 1680fff7 23bdfffc 8fb60000 23bdfffc 8fb50000
  //   23bdfffc 8fb40000 23bdfffc 8fb30000 23bdfffc 8fb00000 23bdfffc 8fa40000 23bdfffc 8fa20000 42000018
  //   afa20000 23bd0004 afa40000 23bd0004 afb00000 23bd0004 afb30000 23bd0004 afb40000 23bd0004 afb50000
  //   23bd0004 afb60000 23bd0004 20160002 20140003 20150001 168020 108100 2149825 132020 20020022 c
  //   1600fffa 295a022 1680fff7 23bdfffc 8fb60000 23bdfffc 8fb50000 23bdfffc 8fb40000 23bdfffc 8fb30000
  //   23bdfffc 8fb00000 23bdfffc 8fa40000 23bdfffc 8fa20000 42000018 afa20000 23bd0004 afa40000 23bd0004
  //   afb00000 23bd0004 afb30000 23bd0004 afb40000 23bd0004 afb50000 23bd0004 afb60000 23bd0004 20160003
  //   20140003 20150001 168020 108100 2149825 132020 20020022 c 1600fffa 295a022 1680fff7 23bdfffc
  //   8fb60000 23bdfffc 8fb50000 23bdfffc 8fb40000 23bdfffc 8fb30000 23bdfffc 8fb00000 23bdfffc 8fa40000
  //   23bdfffc 8fa20000 42000018
  //   OP
  //   rs
  //   rt
  //   rd
  //   控制位
  //   Func
  //   流水调试日志用
  //   暂停节拍，不能为0
  //   JMP
  //   JR
  //   OP
  //   Func
  //   Syscall
  //   戳工具置1进入计数暂停模式，ctrl+k时钟自动运行到对应节拍暂停
  //   ctrl+k关闭时钟连续运行，将控制位置零，进入单步调试模式调试
  //   Beq
  //   Bne
  //   MemToReg
  //   MemWrite
  //   AluOP
  //   AluSrcB
  //   RegWrite
  //   JAL
  //   RegDst
  //   可计数暂停的时钟源
  //   Syscall
  //   为方便自动评测，需要输出流水线各段保存的PC值，注意是PC不是PC+4，另外ID段寄存器写入信息，Mem段内存写入信息也要输出
  //   AluOP
  //   AluSrcB
  //   RegWrite
  //   MemWrite
  //   JAL
  //   Bne
endmodule

module \流水多级中断  (
  output RegWrite,
  output MemWrite,
  output [31:0] IF_PC,
  output [31:0] ID_PC,
  output [31:0] EX_PC,
  output [31:0] M_PC,
  output [31:0] WB_PC,
  output [31:0] RDin,
  output [31:0] MDin,
  output [31:0] LedData
);

  wire and_1_out, and_2_out, and_3_out, and_4_out, and_5_out, and_6_out, and_7_out, and_8_out, and_9_out,
       and_10_out, BLTZ, BRANCH, CLK, clock_1_out, clock_2_out, CLR, comparator_4_eq, comparator_4_lt,
       comparator_6_lt, d_ff_4_q, demultiplexer_1_out1, demultiplexer_1_out2, demultiplexer_1_out3,
       demultiplexer_2_out1, demultiplexer_2_out2, demultiplexer_2_out3, demultiplexer_3_out1,
       demultiplexer_3_out2, demultiplexer_3_out3, en, equal, ERET, EX_BLTZ, EX_BRANCH, ex_mem_1_ctout16,
       ex_mem_1_ctout16_4, \ex_mem_1_传输状态out_表明当前传输数据有效 , EX_SRAV, Go, ID_EX_shout5_2,
       \ID_EX_传输状态out_表明当前传输数据有效 , IE, IE_q, \if_id_1_传输状态out_表明当前传输数据有效 , ir, IR1, ir1_t, IR2, ir2_t, IR3,
       ir3_t, Led, MEM_LH, Mem_MemToReg, Mem_RegWrite, mem_wb_1_ctout16_5, MFC0, MTC0, nand_1_out, or_1_out,
       or_4_out, or_5_out, or_6_out, or_7_out, or_8_out, or_9_out, or_10_out, or_11_out,
       priority_encoder_1_en_out, priority_encoder_1_gs, register_1_q, RST, WB_ERET, WB_MFC0, WB_MTC0, \数据相关 ;
  wire [1:0] ex_mem_1_ctout16_5, F, ForwardR1, ForwardR2, ID_EX_shout5, ID_EX_wbout5_2, multiplexer_11_out,
       multiplexer_20_out, register_5_q, register_6_q, register_7_q, \正在执行的中断 , \过去执行的中断 ;
  wire [2:0] ID_EX_ctrl4_2, multiplexer_9_out;
  wire [3:0] CTRL4, ex_mem_1_ctout16_2;
  wire [4:0] ex_mem_1_wbout5, ID_EX_shout5_3, ID_EX_wbout5, mem_wb_1_wbout5, multiplexer_5_out,
       multiplexer_6_out, multiplexer_7_out, multiplexer_8_out, multiplexer_14_out;
  wire [12:0] CNT_num;
  wire [15:0] CTRL, EX_CTRL, ex_mem_1_ctout16_6, \LoadUse次数 , mem_wb_1_ctout16_6, \总周期数 , \无条件分支数 , \条件分支成功数 ;
  wire [31:0] adder_1_out, adder_2_out, adder_3_out, adder_4_out, ALURes, bit_extender_1_out,
       bit_extender_2_out, bit_extender_3_out, EPC, EPC_2_q, EPC_3_q, EPC_q, EX_IR, ex_mem_1_ledout32, EX_R1,
       EX_R2, EXALU, ID_EX_r1out32, ID_EX_r1out32_2, ID_EX_r1out32_3, ID_IR, IF_IR, MEM_IR,
       mips_alu_1_result, mips_ram_1_dataout, mips_regifile_1_r1, mips_regifile_1_r2, multiplexer_1_out,
       multiplexer_2_out, multiplexer_3_out, multiplexer_10_out, multiplexer_15_out, multiplexer_16_out,
       multiplexer_17_out, multiplexer_18_out, multiplexer_19_out, multiplexer_21_out, R2, RD, register_4_q,
       shifter_1_out, shifter_2_out, WB_IR, \中断程序入口地址 ;

  Button \u_总复位  (.out(RST));
  Button _1 (.out(IR1));
  Button _2 (.out(IR2));
  Button _3 (.out(IR3));
  // Probe on \总周期数 
  // Probe on \总周期数 
  Button \u_继续运行  (.out(Go));
  LED #(.active("true")) led_1 (.in(ir1_t));
  LED #(.active("true")) led_2 (.in(ir2_t));
  LED #(.active("true")) led_3 (.in(ir3_t));
  Hex_Digit_Display hex_digit_display_1 (.value(LedData[31:28]));  // open: dp
  // Probe on IF_PC[19:0]
  // Mips_Probe mips_probe_1: pin names not known; wires that end beside it: IF_IR
  D_Flip_Flop #(.trigger("rising"), .Pre_Clr_Positions("LEGACY"), .NegatePresetClear("false"), .enable("true"), .NewFFLayout("false")) d_ff_1 (
    .clk(CLK), .D(1'b0), .Q(ir1_t), .preset(IR1), .en(demultiplexer_2_out1));  // open: Qn, reset
  D_Flip_Flop #(.trigger("rising"), .Pre_Clr_Positions("LEGACY"), .NegatePresetClear("false"), .enable("true"), .NewFFLayout("false")) d_ff_2 (
    .clk(CLK), .D(1'b0), .Q(ir2_t), .preset(IR2), .en(demultiplexer_2_out2));  // open: Qn, reset
  D_Flip_Flop #(.trigger("rising"), .Pre_Clr_Positions("LEGACY"), .NegatePresetClear("false"), .enable("true"), .NewFFLayout("false")) d_ff_3 (
    .clk(CLK), .D(1'b0), .Q(ir3_t), .preset(IR3), .en(demultiplexer_2_out3));  // open: Qn, reset
  Demultiplexer #(.select(2), .width(1), .tristate("false"), .disabled("Z"), .enable("false")) demultiplexer_1 (
    .out1(demultiplexer_1_out1), .out2(demultiplexer_1_out2), .out3(demultiplexer_1_out3), .in(ir),
    .sel(\正在执行的中断 ));  // open: out0
  Hex_Digit_Display hex_digit_display_2 (.value(LedData[27:24]));  // open: dp
  Hex_Digit_Display hex_digit_display_3 (.value(LedData[23:20]));  // open: dp
  // Probe on ID_PC[19:0]
  // Mips_Probe mips_probe_2: pin names not known; wires that end beside it: ID_IR
  Multiplexer #(.select(1), .width(32), .disabled("Z"), .enable("false")) multiplexer_1 (
    .in0(multiplexer_3_out), .in1(EPC), .out(multiplexer_1_out), .sel(WB_ERET));
  and and_1 (and_1_out, mem_wb_1_ctout16_6[4], ~mem_wb_1_ctout16_5);  // AND_Gate
  Hex_Digit_Display hex_digit_display_4 (.value(LedData[19:16]));  // open: dp
  Hex_Digit_Display hex_digit_display_5 (.value(LedData[15:12]));  // open: dp
  Multiplexer #(.select(1), .width(32), .disabled("Z"), .enable("false")) multiplexer_2 (
    .in0(multiplexer_1_out), .in1(\中断程序入口地址 ), .out(multiplexer_2_out), .sel(ir));
  and and_2 (and_2_out, ~\数据相关 , en);  // AND_Gate
  Register #(.width(1), .trigger("rising"), .Select("low")) register_1 (
    .D(mem_wb_1_ctout16_6[4]), .en(and_1_out), .Q(register_1_q), .clk(CLK), .clr(or_1_out));
  or or_1 (or_1_out, RST, Go);
  Multiplexer #(.select(1), .width(32), .disabled("Z"), .enable("false")) multiplexer_3 (
    .in0(adder_1_out), .in1(multiplexer_19_out), .out(multiplexer_3_out), .sel(BRANCH));
  or or_2 (BRANCH, EX_BRANCH, BLTZ, EX_CTRL[15]);
  Comparator #(.width(32), .mode("twosComplement")) comparator_1 (
    .a(ID_IR), .b(32'h42000018), .eq(ERET));  // open: gt, lt
  Demultiplexer #(.select(2), .width(1), .tristate("false"), .disabled("Z"), .enable("false")) demultiplexer_2 (
    .out1(demultiplexer_2_out1), .out2(demultiplexer_2_out2), .out3(demultiplexer_2_out3), .in(WB_ERET),
    .sel(\过去执行的中断 ));  // open: out0
  Hex_Digit_Display hex_digit_display_6 (.value(LedData[7:4]));  // open: dp
  Hex_Digit_Display hex_digit_display_7 (.value(LedData[11:8]));  // open: dp
  Clock #(.highDuration(1), .lowDuration(1)) clock_1 (.out(clock_1_out));
  // Probe on EX_PC[19:0]
  // Mips_Probe mips_probe_3: pin names not known; wires that end beside it: clock_1_out, EX_IR, CLK
  Register #(.width(32), .trigger("rising"), .Select("low")) PC (
    .D(multiplexer_2_out), .en(and_2_out), .Q(IF_PC), .clk(CLK), .clr(RST));
  Counter #(.width(16), .max('hffff), .ongoal("wrap"), .trigger("rising"), .behavior("old")) counter_1 (
    .count(en), .Q(\总周期数 ), .clk(CLK), .clr(RST));  // open: load, D, carry, preset
  not not_1 (en, register_1_q);
  Register #(.width(32), .trigger("rising"), .Select("low")) u_EPC (
    .D(EX_PC), .en(demultiplexer_1_out1), .Q(EPC_q), .clk(CLK));  // open: clr
  Register #(.width(32), .trigger("rising"), .Select("low")) EPC_2 (
    .D(EX_PC), .en(demultiplexer_1_out2), .Q(EPC_2_q), .clk(CLK));  // open: clr
  Register #(.width(32), .trigger("rising"), .Select("low")) EPC_3 (
    .D(EX_PC), .en(demultiplexer_1_out3), .Q(EPC_3_q), .clk(CLK));  // open: clr
  Hex_Digit_Display hex_digit_display_8 (.value(LedData[3:0]));  // open: dp
  Adder #(.width(32)) adder_1 (.a(IF_PC), .b(32'h4), .out(adder_1_out));  // open: cin, cout
  and and_3 (and_3_out, \数据相关 , en);
  // Probe on EPC_q
  // Probe on \总周期数 
  // Probe on M_PC[19:0]
  // Mips_Probe mips_probe_4: pin names not known; wires that end beside it: MEM_IR
  \load_use相关检测  \load_use相关检测_1  (
    .MEM_MemToReg(Mem_MemToReg), .ID_R1(multiplexer_5_out), .EX_WriteReg(ID_EX_wbout5),
    .EX_RegWrite(EX_CTRL[7]), .MEM_WriteReg(ex_mem_1_wbout5), .MEM_RegWrite(Mem_RegWrite), .OP(ID_IR[31:26]),
    .Func(ID_IR[5:0]), .ID_R2(multiplexer_6_out), .ForwardToR1(ForwardR1), .\Load_Use相关 (\数据相关 ),
    .ForwardToR2(ForwardR2), .EX_MemToReg(EX_CTRL[10]));
  ROM #(.addrWidth(10), .dataWidth(32), .Select("high")) rom_1 (.addr(IF_PC[11:2]), .data(IF_IR));
  Counter #(.width(16), .max('hffff), .ongoal("wrap"), .trigger("rising"), .behavior("old")) counter_2 (
    .count(and_3_out), .Q(\LoadUse次数 ), .clk(CLK), .clr(RST));  // open: load, D, carry, preset
  Comparator #(.width(11), .mode("twosComplement")) comparator_2 (
    .a(ID_IR[31:21]), .b(11'h200), .eq(MFC0));  // open: gt, lt
  // Probe on \总周期数 
  // Probe on \无条件分支数 
  // Probe on \条件分支成功数 
  // Probe on \LoadUse次数 
  // Probe on \LoadUse次数 
  or or_3 (CLR, ir, RST, BRANCH, WB_ERET);
  IF_ID if_id_1 (
    .IRin32(IF_IR), .PCin32(IF_PC), .\传输状态In_表明当前传输数据有效 (1'b1), .CLK(CLK), .IRout32(ID_IR), .PCout32(ID_PC),
    .\传输状态Out_表明当前传输数据有效 (\if_id_1_传输状态out_表明当前传输数据有效 ), .\同步清零_气泡_高电平有效 (CLR),
    .\使能端_低电平有效_stall_高电平有效 (or_4_out));  // open: CTin16, CTout16
  or or_4 (or_4_out, \数据相关 , register_1_q);
  Multiplexer #(.select(2), .width(32), .disabled("Z"), .enable("false")) multiplexer_4 (
    .in0(EX_PC), .in1(EPC_q), .in2(EPC_2_q), .in3(EPC_3_q), .out(EPC), .sel(\过去执行的中断 ));
  // Probe on IF_PC[11:0]
  // Probe on WB_PC[19:0]
  // Mips_Probe mips_probe_5: pin names not known; wires that end beside it: WB_IR
  // Probe on ID_PC[11:0]
  // Probe on EX_PC[11:0]
  or or_5 (or_5_out, WB_MFC0, WB_ERET);
  // Probe on M_PC[11:0]
  D_Flip_Flop #(.trigger("high"), .Pre_Clr_Positions("LEGACY"), .NegatePresetClear("false"), .enable("true"), .NewFFLayout("false")) d_ff_4 (.Q(d_ff_4_q));  // open: clk, D, Qn, preset, en, reset
  // Probe on 13'hc
  Multiplexer #(.select(1), .width(5), .disabled("Z"), .enable("false")) multiplexer_5 (
    .in0(ID_IR[25:21]), .in1(5'b00100), .out(multiplexer_5_out), .sel(CTRL[4]));
  Multiplexer #(.select(1), .width(5), .disabled("Z"), .enable("false")) multiplexer_6 (
    .in0(ID_IR[20:16]), .in1(5'b00010), .out(multiplexer_6_out), .sel(CTRL[4]));
  Multiplexer #(.select(1), .width(5), .disabled("Z"), .enable("false")) multiplexer_7 (
    .in0(ID_IR[20:16]), .in1(ID_IR[15:11]), .out(multiplexer_7_out), .sel(CTRL[5]));
  Multiplexer #(.select(1), .width(5), .disabled("Z"), .enable("false")) multiplexer_8 (
    .in0(multiplexer_7_out), .in1({5{1'b1}}), .out(multiplexer_8_out), .sel(CTRL[6]));
  Comparator #(.width(11), .mode("twosComplement")) comparator_3 (
    .a(ID_IR[31:21]), .b(11'h204), .eq(MTC0));  // open: gt, lt
  or or_6 (or_6_out, ir, WB_MTC0);
  not not_2 (IE, IE_q);
  Register #(.width(1), .trigger("rising"), .Select("low")) u_IE (
    .D(1'b0), .en(or_5_out), .Q(IE_q), .clk(CLK), .preset(or_6_out));  // open: clr, cs
  // Probe on WB_PC[11:0]
  Comparator #(.width(13), .mode("twosComplement")) comparator_4 (
    .a(CNT_num), .b(13'hc), .eq(comparator_4_eq), .lt(comparator_4_lt));  // open: gt
  Clock #(.highDuration(1), .lowDuration(1)) clock_2 (.out(clock_2_out));
  \单周期硬布线控制器  \u_单周期硬布线控制器_1  (
    .OP(ID_IR[31:26]), .Func(ID_IR[5:0]), .ALU_OP(CTRL[3:0]), .MemToReg(CTRL[10]), .MemWrite(CTRL[9]),
    .BLTZ(CTRL4[3]), .LH(CTRL4[2]), .SRAV(CTRL4[1]), .XORI(CTRL4[0]), .ALU_SRC(CTRL[8]), .RegWrite(CTRL[7]),
    .SysCALL(CTRL[4]), .SignedExt(CTRL[13]), .RegDst(CTRL[5]), .Beq(CTRL[12]), .Bne(CTRL[11]), .JR(CTRL[14]),
    .JMP(CTRL[15]), .JAL(CTRL[6]));
  assign bit_extender_1_out = {{16{1'b0}}, ID_IR[15:0]};  // Bit_Extender bit_extender_1
  assign bit_extender_2_out = {{16{ID_IR[15]}}, ID_IR[15:0]};  // Bit_Extender bit_extender_2
  assign bit_extender_3_out = {{6{ID_IR[25]}}, ID_IR[25:0]};  // Bit_Extender bit_extender_3
  Multiplexer #(.select(2), .width(3), .disabled("Z"), .enable("false")) multiplexer_9 (
    .in0(3'b111), .in1(3'b110), .in2(3'b100), .in3(3'b000), .out(multiplexer_9_out), .sel(\过去执行的中断 ));
  nand nand_1 (nand_1_out, d_ff_4_q, comparator_4_eq);
  Counter #(.width(13), .max('h1fff), .ongoal("stay"), .trigger("rising"), .behavior("old")) counter_3 (
    .count(comparator_4_lt), .Q(CNT_num), .clk(clock_2_out));  // open: load, D, carry, clr, preset
  MIPS_Regifile mips_regifile_1 (
    .Din(RDin), .Clk(CLK), .R1(mips_regifile_1_r1), .R2(mips_regifile_1_r2), .WE(RegWrite),
    .W_num(mem_wb_1_wbout5), .R1_num(multiplexer_5_out), .R2_num(multiplexer_6_out));
  Multiplexer #(.select(1), .width(32), .disabled("Z"), .enable("false")) multiplexer_10 (
    .in0(bit_extender_1_out), .in1(bit_extender_2_out), .out(multiplexer_10_out), .sel(CTRL[13]));
  and and_4 (and_4_out, ir1_t, multiplexer_9_out[0]);
  and and_5 (and_5_out, ir2_t, multiplexer_9_out[1]);
  and and_6 (and_6_out, ir3_t, multiplexer_9_out[2]);
  assign CLK = nand_1_out ? clock_2_out : 1'bz;  // Controlled_Buffer controlled_buffer_1
  Shifter #(.width(32), .shift("ll")) shifter_1 (.in(bit_extender_3_out), .\dist (5'b00010), .out(shifter_1_out));
  assign \正在执行的中断  = priority_encoder_1_en_out ? 2'b00 : 2'bz;  // Controlled_Buffer controlled_buffer_2
  Pull_Resistor #(.pull(1)) pull_resistor_1 (.node(CLK));
  or or_7 (or_7_out, \数据相关 , CLR);
  Priority_Encoder #(.select(2), .disabled("Z")) priority_encoder_1 (
    .in0(1'b0), .in1(and_4_out), .in2(and_5_out), .in3(and_6_out), .out(\正在执行的中断 ),
    .gs(priority_encoder_1_gs), .en_out(priority_encoder_1_en_out), .en_in(1'b1));
  and and_7 (and_7_out, priority_encoder_1_gs, IE, en);
  Multiplexer #(.select(1), .width(2), .disabled("Z"), .enable("false")) multiplexer_11 (
    .in0(\正在执行的中断 ), .in1(multiplexer_20_out), .out(multiplexer_11_out), .sel(WB_ERET));
  ID_EX ID_EX (
    .R1in32(mips_regifile_1_r1), .R2in32(mips_regifile_1_r2), .IRin32(ID_IR), .PCin32(ID_PC),
    .IMMin32(multiplexer_10_out), .WBin5(multiplexer_8_out), .SHin5(ID_IR[10:6]), .CTin16(CTRL),
    .\传输状态In_表明当前传输数据有效 (\if_id_1_传输状态out_表明当前传输数据有效 ), .CLK(CLK), .R1out32(ID_EX_r1out32), .R2out32(EX_R2),
    .IRout32(EX_IR), .PCout32(EX_PC), .R1out32_2(ID_EX_r1out32_2), .WBout5(ID_EX_wbout5),
    .SHout5_3(ID_EX_shout5_3), .CTout16(EX_CTRL), .\传输状态Out_表明当前传输数据有效 (\ID_EX_传输状态out_表明当前传输数据有效 ),
    .\同步清零_气泡_高电平有效 (or_7_out), .\使能端_低电平有效_stall_高电平有效 (register_1_q), ._26in32(shifter_1_out),
    .R1out32_3(ID_EX_r1out32_3), .FWR1in2(ForwardR1), .WBout5_2(ID_EX_wbout5_2), .FWR2in2(ForwardR2),
    .SHout5_4(F), .CTRL4(CTRL4), .CTRL4_2({EX_BLTZ, ID_EX_ctrl4_2[2], EX_SRAV, ID_EX_ctrl4_2[0]}),
    .ERETin1_2(ERET), .SHout5_2(ID_EX_shout5_2), .ERETin1({MFC0, MTC0}), .SHout5(ID_EX_shout5));
  Multiplexer #(.select(2), .width(32), .disabled("Z"), .enable("false")) multiplexer_12 (
    .in1(32'h30ac), .in2(32'h3158), .in3(32'h3204), .out(\中断程序入口地址 ), .sel(\正在执行的中断 ));  // open: in0
  Demultiplexer #(.select(2), .width(1), .tristate("false"), .disabled("Z"), .enable("false")) demultiplexer_3 (
    .out1(demultiplexer_3_out1), .out2(demultiplexer_3_out2), .out3(demultiplexer_3_out3), .in(ir),
    .sel(\正在执行的中断 ));  // open: out0
  Register #(.width(1), .trigger("falling"), .Select("low")) register_2 (
    .D(and_7_out), .Q(ir), .clk(CLK));  // open: en, clr
  Register #(.width(2), .trigger("rising"), .Select("low")) register_3 (
    .D(multiplexer_11_out), .en(or_8_out), .Q(\过去执行的中断 ), .clk(CLK));  // open: clr
  or or_8 (or_8_out, ir, WB_ERET);
  Register #(.width(32), .trigger("rising"), .Select("low")) register_4 (
    .D(EX_R1), .en(and_8_out), .Q(register_4_q), .clk(CLK));  // open: clr
  and and_8 (and_8_out, Led, EX_CTRL[4]);
  Multiplexer #(.select(2), .width(32), .disabled("Z"), .enable("false")) multiplexer_13 (
    .in0(ID_EX_r1out32), .in1(ALURes), .in2(RD), .in3(EXALU), .out(EX_R1), .sel(ID_EX_wbout5_2));
  Shifter #(.width(32), .shift("ll")) shifter_2 (.in(ID_EX_r1out32_2), .\dist (5'b00010), .out(shifter_2_out));
  Multiplexer #(.select(1), .width(5), .disabled("Z"), .enable("false")) multiplexer_14 (
    .in0(ID_EX_shout5_3), .in1(EX_R1[4:0]), .out(multiplexer_14_out), .sel(EX_SRAV));
  Adder #(.width(32)) adder_2 (.a(EX_PC), .b(32'h4), .out(adder_2_out));  // open: cin, cout
  Multiplexer #(.select(1), .width(32), .disabled("Z"), .enable("false")) multiplexer_15 (
    .in0(R2), .in1(ID_EX_r1out32_2), .out(multiplexer_15_out), .sel(EX_CTRL[8]));
  Comparator #(.width(32), .mode("twosComplement")) comparator_5 (.a(R2), .b(32'h22), .eq(Led));  // open: gt, lt
  Adder #(.width(32)) adder_3 (.a(shifter_2_out), .b(adder_2_out), .out(adder_3_out));  // open: cin, cout
  MIPS_ALU mips_alu_1 (
    .X(EX_R1), .Y(multiplexer_15_out), .AluOP(EX_CTRL[3:0]), .Equal(equal), .Result(mips_alu_1_result),
    .shamt(multiplexer_14_out));  // open: Result_2
  Multiplexer #(.select(1), .width(32), .disabled("Z"), .enable("false")) multiplexer_16 (
    .in0(ID_EX_r1out32_3), .in1(EX_R1), .out(multiplexer_16_out), .sel(EX_CTRL[14]));
  Multiplexer #(.select(1), .width(32), .disabled("Z"), .enable("false")) multiplexer_17 (
    .in0(adder_2_out), .in1(adder_3_out), .out(multiplexer_17_out), .sel(EX_BRANCH));
  Register #(.width(2), .trigger("rising"), .Select("low")) register_5 (
    .D(\过去执行的中断 ), .en(demultiplexer_3_out1), .Q(register_5_q), .clk(CLK));  // open: clr
  Register #(.width(2), .trigger("rising"), .Select("low")) register_6 (
    .D(\过去执行的中断 ), .en(demultiplexer_3_out2), .Q(register_6_q), .clk(CLK));  // open: clr
  Register #(.width(2), .trigger("rising"), .Select("low")) register_7 (
    .D(\过去执行的中断 ), .en(demultiplexer_3_out3), .Q(register_7_q), .clk(CLK));  // open: clr
  or or_9 (or_9_out, WB_ERET, RST, ir);
  EX_MEM ex_mem_1 (
    .ALUin32(mips_alu_1_result), .Memin32(R2), .IRin32(EX_IR), .PCin32(EX_PC), .WBin5(ID_EX_wbout5),
    .CTin16_2(EX_CTRL), .\传输状态In_表明当前传输数据有效 (\ID_EX_传输状态out_表明当前传输数据有效 ), .CLK(CLK), .ALUout32(EXALU),
    .Memout32(MDin), .IRout32(MEM_IR), .PCout32(M_PC), .WBout5(ex_mem_1_wbout5),
    .CTout16_6({ex_mem_1_ctout16_6[15:11], Mem_MemToReg, MemWrite, ex_mem_1_ctout16_6[8], Mem_RegWrite, ex_mem_1_ctout16_6[6:0]}),
    .\传输状态Out_表明当前传输数据有效 (\ex_mem_1_传输状态out_表明当前传输数据有效 ), .\同步清零_气泡_高电平有效 (or_9_out),
    .\使能端_低电平有效_stall_高电平有效 (register_1_q), .LEDin32(register_4_q), .LEDout32(ex_mem_1_ledout32),
    .CTin16(Led), .CTout16(ex_mem_1_ctout16), .CTin4({EX_BLTZ, ID_EX_ctrl4_2[2], EX_SRAV, ID_EX_ctrl4_2[0]}),
    .CTout16_2({ex_mem_1_ctout16_2[3], MEM_LH, ex_mem_1_ctout16_2[1:0]}), .ERETin2(ID_EX_shout5_2),
    .CTout16_4(ex_mem_1_ctout16_4), .ERETin2_2(ID_EX_shout5), .CTout16_5(ex_mem_1_ctout16_5));  // open: Resullt2, CTout16_3
  Multiplexer #(.select(1), .width(32), .disabled("Z"), .enable("false")) multiplexer_18 (
    .in0(multiplexer_17_out), .in1(adder_3_out), .out(multiplexer_18_out), .sel(BLTZ));
  Multiplexer #(.select(1), .width(32), .disabled("Z"), .enable("false")) multiplexer_19 (
    .in0(multiplexer_18_out), .in1(multiplexer_16_out), .out(multiplexer_19_out), .sel(EX_CTRL[15]));
  Multiplexer #(.select(2), .width(2), .disabled("Z"), .enable("false")) multiplexer_20 (
    .in1(register_5_q), .in2(register_6_q), .in3(register_7_q), .out(multiplexer_20_out), .sel(\过去执行的中断 ));  // open: in0
  MIPS_RAM mips_ram_1 (
    .\字节地址 (EXALU[11:2]), .Din(MDin), .DataOut(mips_ram_1_dataout), .CLK(CLK), .WE(MemWrite),
    .Mode(EXALU[1]), .LH(MEM_LH));
  or or_10 (or_10_out, WB_ERET, RST);
  MEM_WB mem_wb_1 (
    .ALUin32(EXALU), .MDin32(mips_ram_1_dataout), .IRin32(MEM_IR), .PCin32(M_PC), .WBin5(ex_mem_1_wbout5),
    .CTin16_2({ex_mem_1_ctout16_6[15:11], Mem_MemToReg, MemWrite, ex_mem_1_ctout16_6[8], Mem_RegWrite, ex_mem_1_ctout16_6[6:0]}),
    .\传输状态In_表明当前传输数据有效 (\ex_mem_1_传输状态out_表明当前传输数据有效 ), .CLK(CLK), .ALUout32(ALURes), .MDout32(RD),
    .IRout32(WB_IR), .PCout32(WB_PC), .WBout5(mem_wb_1_wbout5),
    .CTout16_6({mem_wb_1_ctout16_6[15:8], RegWrite, mem_wb_1_ctout16_6[6:0]}), .\同步清零_气泡_高电平有效 (or_10_out),
    .\使能端_低电平有效_stall_高电平有效 (register_1_q), .LEDin32(ex_mem_1_ledout32), .LEDout32(LedData),
    .CTin16(ex_mem_1_ctout16), .CTout16_5(mem_wb_1_ctout16_5),
    .CTin4({ex_mem_1_ctout16_2[3], MEM_LH, ex_mem_1_ctout16_2[1:0]}), .ERETin1(ex_mem_1_ctout16_4),
    .CTout16_3(WB_ERET), .ERETin1_2(ex_mem_1_ctout16_5), .CTout16_4({WB_MFC0, WB_MTC0}));  // open: 传输状态Out_表明当前传输数据有效, CTout16, CTout16_2, RE2in32
  Multiplexer #(.select(1), .width(32), .disabled("Z"), .enable("false")) multiplexer_21 (
    .in0(ALURes), .in1(RD), .out(multiplexer_21_out), .sel(mem_wb_1_ctout16_6[10]));
  Adder #(.width(32)) adder_4 (.a(WB_PC), .b(32'h4), .out(adder_4_out));  // open: cin, cout
  Multiplexer #(.select(1), .width(32), .disabled("Z"), .enable("false")) multiplexer_22 (
    .in0(multiplexer_21_out), .in1(adder_4_out), .out(RDin), .sel(mem_wb_1_ctout16_6[6]));
  Counter #(.width(16), .max('hffff), .ongoal("wrap"), .trigger("rising"), .behavior("old")) counter_4 (
    .count(EX_CTRL[15]), .Q(\无条件分支数 ), .clk(CLK), .clr(RST));  // open: load, D, carry, preset
  Counter #(.width(16), .max('hffff), .ongoal("wrap"), .trigger("rising"), .behavior("old")) counter_5 (
    .count(or_11_out), .Q(\条件分支成功数 ), .clk(CLK), .clr(RST));  // open: load, D, carry, preset
  or or_11 (or_11_out, BLTZ, EX_BRANCH);
  Comparator #(.width(32), .mode("twosComplement")) comparator_6 (
    .a(EX_R1), .b({32{1'b0}}), .lt(comparator_6_lt));  // open: gt, eq
  Multiplexer #(.select(2), .width(32), .disabled("Z"), .enable("false")) multiplexer_23 (
    .in0(EX_R2), .in1(ALURes), .in2(RD), .in3(EXALU), .out(R2), .sel(F));
  and and_9 (and_9_out, equal, EX_CTRL[12]);
  and and_10 (and_10_out, ~equal, EX_CTRL[11]);  // AND_Gate
  and and_11 (BLTZ, comparator_6_lt, EX_BLTZ);
  or or_12 (EX_BRANCH, and_9_out, and_10_out);

  // Other names for the same wires on the sheet: SignedExt = CTRL[13]; EX_RegWrite = EX_CTRL[7];
  //   EX_MemToReg = EX_CTRL[10]; EX_JR = EX_CTRL[14]; EX_JMP = EX_CTRL[15]; W1 = ir1_t; W2 = ir2_t; W3 = ir3_t;
  //   MEM_PC[31:0] = M_PC; 中断到来 = ir; 插入气泡数[15:0] = \LoadUse次数 

  // Notes on the sheet:
  //   中断源
  //   时空图监测，可删除
  //   中断等待指示
  //   数码管输出
  //   指令存储器
  //   contents of rom_1 (hex, n*v repeats v):
  //   201d07d0 20100001 109fc0 139fc3 8021 2012000c 24160008 26100001 3210000f 20080008 20090001 139900
  //   2709825 132020 20020022 c 1094022 1500fff9 22100001 2018000f 2188024 108700 20080008 20090001 139902
  //   2709825 132021 20020022 c 1094022 1500fff9 108702 2c9b022 12c00001 8000c07 4020 1084027 84400
  //   3508ffff 82021 20020022 c 8000c01 afa20000 23bd0004 afa40000 23bd0004 afb00000 23bd0004 afb30000
  //   23bd0004 afb40000 23bd0004 afb50000 23bd0004 afb60000 23bd0004 40000000 20160001 20140003 20150001
  //   168020 108100 2149825 132020 20020022 c 1600fffa 295a022 1680fff7 40800000 23bdfffc 8fb60000
  //   23bdfffc 8fb50000 23bdfffc 8fb40000 23bdfffc 8fb30000 23bdfffc 8fb00000 23bdfffc 8fa40000 23bdfffc
  //   8fa20000 42000018 afa20000 23bd0004 afa40000 23bd0004 afb00000 23bd0004 afb30000 23bd0004 afb40000
  //   23bd0004 afb50000 23bd0004 afb60000 23bd0004 40000000 20160002 20140003 20150001 168020 108100
  //   2149825 132020 20020022 c 1600fffa 295a022 1680fff7 40800000 23bdfffc 8fb60000 23bdfffc 8fb50000
  //   23bdfffc 8fb40000 23bdfffc 8fb30000 23bdfffc 8fb00000 23bdfffc 8fa40000 23bdfffc 8fa20000 42000018
  //   afa20000 23bd0004 afa40000 23bd0004 afb00000 23bd0004 afb30000 23bd0004 afb40000 23bd0004 afb50000
  //   23bd0004 afb60000 23bd0004 40000000 20160003 20140003 20150001 168020 108100 2149825 132020 20020022
  //   c 1600fffa 295a022 1680fff7 40800000 23bdfffc 8fb60000 23bdfffc 8fb50000 23bdfffc 8fb40000 23bdfffc
  //   8fb30000 23bdfffc 8fb00000 23bdfffc 8fa40000 23bdfffc 8fa20000 42000018
  //   OP
  //   rs
  //   rt
  //   rd
  //   控制位
  //   Func
  //   流水调试日志用
  //   暂停节拍，不能为0
  //   JMP
  //   JR
  //   OP
  //   Func
  //   Syscall
  //   中断屏蔽字
  //   戳工具置1进入计数暂停模式，ctrl+k时钟自动运行到对应节拍暂停
  //   ctrl+k关闭时钟连续运行，将控制位置零，进入单步调试模式调试
  //   Beq
  //   Bne
  //   MemToReg
  //   MemWrite
  //   AluOP
  //   AluSrcB
  //   RegWrite
  //   JAL
  //   RegDst
  //   可计数暂停的时钟源
  //   Syscall
  //   为方便自动评测，需要输出流水线各段保存的PC值，注意是PC不是PC+4，另外ID段寄存器写入信息，Mem段内存写入信息也要输出
  //   AluOP
  //   AluSrcB
  //   RegWrite
  //   MemWrite
  //   JAL
  //   Bne
endmodule

module \动态分支预测  (
  output RegWrite,
  output MemWrite,
  output [31:0] IF_PC,
  output [31:0] ID_PC,
  output [31:0] EX_PC,
  output [31:0] M_PC,
  output [31:0] WB_PC,
  output [31:0] RDin,
  output [31:0] MDin,
  output [31:0] LedData
);

  wire and_1_out, and_2_out, and_3_out, and_4_out, and_5_out, and_6_out, BLTZ, CLK, clock_1_out, clock_2_out,
       comparator_1_eq, comparator_1_lt, comparator_3_lt, d_ff_1_q, equal, EX_BLTZ, EX_BRANCH, EX_Branch_t,
       EX_BranchTaken, ex_mem_1_ctout16, \ex_mem_1_传输状态out_表明当前传输数据有效 , EX_PredictJump, EX_SRAV, Go,
       \ID_EX_传输状态out_表明当前传输数据有效 , ID_PredictJump, \if_id_1_传输状态out_表明当前传输数据有效 , IR1, IR2, IR3, Led, MEM_LH,
       Mem_MemToReg, Mem_RegWrite, mem_wb_1_ctout16_5, nand_1_out, not_1_out, or_1_out, or_3_out, or_4_out,
       or_5_out, or_6_out, or_7_out, or_9_out, PredictFailed, PredictJump, register_1_q, RST, W1, W2, W3,
       \数据相关 ;
  wire [1:0] F, ForwardR1, ForwardR2, ID_EX_wbout5_2;
  wire [2:0] ID_EX_ctrl4_2;
  wire [3:0] CTRL4, ex_mem_1_ctout16_2;
  wire [4:0] ex_mem_1_wbout5, ID_EX_shout5_3, ID_EX_wbout5, mem_wb_1_wbout5, multiplexer_5_out,
       multiplexer_6_out, multiplexer_7_out, multiplexer_8_out, multiplexer_11_out;
  wire [12:0] CNT_num;
  wire [15:0] CTRL, EX_CTRL, ex_mem_1_ctout16_6, \LoadUse次数 , mem_wb_1_ctout16_6, \总周期数 , \无条件分支数 , \条件分支成功数 ;
  wire [31:0] adder_1_out, adder_4_out, ALURes, bit_extender_1_out, bit_extender_2_out, bit_extender_3_out,
       Correct, EX_BranchAddr, EX_BRANCHPC, EX_IR, ex_mem_1_ledout32, EX_PC_4, EX_R1, EX_R2, EXALU,
       ID_EX_r1out32, ID_EX_r1out32_2, ID_EX_r1out32_3, ID_IR, IF_IR, JR_PC, JumpAddr, MEM_IR,
       mips_alu_1_result, mips_ram_1_dataout, mips_regifile_1_r1, mips_regifile_1_r2, multiplexer_1_out,
       multiplexer_2_out, multiplexer_9_out, multiplexer_12_out, multiplexer_14_out, multiplexer_15_out,
       multiplexer_16_out, multiplexer_17_out, R2, RD, register_2_q, shifter_1_out, shifter_2_out, WB_IR;

  Button \u_总复位  (.out(RST));
  Button _1 (.out(IR1));
  Button _2 (.out(IR2));
  Button _3 (.out(IR3));
  // Probe on \总周期数 
  // Probe on \总周期数 
  Button \u_继续运行  (.out(Go));
  LED #(.active("true")) led_1 (.in(W1));
  LED #(.active("true")) led_2 (.in(W2));
  LED #(.active("true")) led_3 (.in(W3));
  Hex_Digit_Display hex_digit_display_1 (.value(LedData[31:28]));  // open: dp
  // Probe on IF_PC[19:0]
  // Mips_Probe mips_probe_1: pin names not known; wires that end beside it: IF_IR
  Hex_Digit_Display hex_digit_display_2 (.value(LedData[27:24]));  // open: dp
  Hex_Digit_Display hex_digit_display_3 (.value(LedData[23:20]));  // open: dp
  // Probe on ID_PC[19:0]
  // Mips_Probe mips_probe_2: pin names not known; wires that end beside it: ID_IR
  Multiplexer #(.select(1), .width(32), .disabled("Z"), .enable("false")) multiplexer_1 (
    .in0(adder_1_out), .in1(JumpAddr), .out(multiplexer_1_out), .sel(PredictJump));
  and and_1 (and_1_out, mem_wb_1_ctout16_6[4], ~mem_wb_1_ctout16_5);  // AND_Gate
  Hex_Digit_Display hex_digit_display_4 (.value(LedData[15:12]));  // open: dp
  Hex_Digit_Display hex_digit_display_5 (.value(LedData[19:16]));  // open: dp
  Multiplexer #(.select(1), .width(32), .disabled("Z"), .enable("false")) multiplexer_2 (
    .in0(multiplexer_1_out), .in1(Correct), .out(multiplexer_2_out), .sel(PredictFailed));
  and and_2 (and_2_out, ~\数据相关 , not_1_out);  // AND_Gate
  Register #(.width(1), .trigger("rising"), .Select("low")) register_1 (
    .D(mem_wb_1_ctout16_6[4]), .en(and_1_out), .Q(register_1_q), .clk(CLK), .clr(or_1_out));
  or or_1 (or_1_out, RST, Go);
  Multiplexer #(.select(1), .width(32), .disabled("Z"), .enable("false")) multiplexer_3 (
    .in0(EX_PC_4), .in1(multiplexer_16_out), .out(Correct), .sel(EX_BranchTaken));
  or or_2 (EX_BranchTaken, EX_BRANCH, BLTZ, EX_CTRL[6], EX_CTRL[15], EX_CTRL[14]);
  BHT bht_1 (
    .JumpAddr(EX_BranchAddr), .IF_PC(IF_PC), .EX_PC(EX_PC), .EX_Branch(EX_Branch_t), .CLK(CLK),
    .in_6(EX_BranchTaken), .PredictJump(PredictJump), .JumpAddr_2(JumpAddr));
  Hex_Digit_Display hex_digit_display_6 (.value(LedData[11:8]));  // open: dp
  Hex_Digit_Display hex_digit_display_7 (.value(LedData[7:4]));  // open: dp
  Clock #(.highDuration(1), .lowDuration(1)) clock_1 (.out(clock_1_out));
  // Probe on EX_PC[19:0]
  // Mips_Probe mips_probe_3: pin names not known; wires that end beside it: clock_1_out, EX_IR, CLK
  Register #(.width(32), .trigger("rising"), .Select("low")) PC (
    .D(multiplexer_2_out), .en(and_2_out), .Q(IF_PC), .clk(CLK), .clr(RST));
  Counter #(.width(16), .max('hffff), .ongoal("wrap"), .trigger("rising"), .behavior("old")) counter_1 (
    .count(not_1_out), .Q(\总周期数 ), .clk(CLK), .clr(RST));  // open: load, D, carry, preset
  not not_1 (not_1_out, register_1_q);
  Hex_Digit_Display hex_digit_display_8 (.value(LedData[3:0]));  // open: dp
  Adder #(.width(32)) adder_1 (.a(IF_PC), .b(32'h4), .out(adder_1_out));  // open: cin, cout
  and and_3 (and_3_out, \数据相关 , not_1_out);
  // Probe on \总周期数 
  // Probe on M_PC[19:0]
  // Mips_Probe mips_probe_4: pin names not known; wires that end beside it: MEM_IR
  \load_use相关检测  \load_use相关检测_1  (
    .MEM_MemToReg(Mem_MemToReg), .ID_R1(multiplexer_5_out), .EX_WriteReg(ID_EX_wbout5),
    .EX_RegWrite(EX_CTRL[7]), .MEM_WriteReg(ex_mem_1_wbout5), .MEM_RegWrite(Mem_RegWrite), .OP(ID_IR[31:26]),
    .Func(ID_IR[5:0]), .ID_R2(multiplexer_6_out), .ForwardToR1(ForwardR1), .\Load_Use相关 (\数据相关 ),
    .ForwardToR2(ForwardR2), .EX_MemToReg(EX_CTRL[10]));
  // Mips_Probe mips_probe_5: pin names not known; wires that end beside it: IF_IR
  ROM #(.addrWidth(10), .dataWidth(32), .Select("high")) rom_1 (.addr(IF_PC[11:2]), .data(IF_IR));
  Counter #(.width(16), .max('hffff), .ongoal("wrap"), .trigger("rising"), .behavior("old")) counter_2 (
    .count(and_3_out), .Q(\LoadUse次数 ), .clk(CLK), .clr(RST));  // open: load, D, carry, preset
  or or_3 (or_3_out, EX_CTRL[14], EX_CTRL[6], EX_CTRL[15]);
  Multiplexer #(.select(1), .width(32), .disabled("Z"), .enable("false")) multiplexer_4 (
    .in0(EX_BRANCHPC), .in1(JR_PC), .out(EX_BranchAddr), .sel(or_3_out));
  // Probe on \总周期数 
  // Probe on \无条件分支数 
  // Probe on \条件分支成功数 
  // Probe on \LoadUse次数 
  // Probe on \LoadUse次数 
  or or_4 (or_4_out, RST, PredictFailed);
  IF_ID if_id_1 (
    .IRin32(IF_IR), .PCin32(IF_PC), .\传输状态In_表明当前传输数据有效 (1'b1), .CLK(CLK), .IRout32(ID_IR), .PCout32(ID_PC),
    .\传输状态Out_表明当前传输数据有效 (\if_id_1_传输状态out_表明当前传输数据有效 ), .\同步清零_气泡_高电平有效 (or_4_out),
    .\使能端_低电平有效_stall_高电平有效 (or_5_out), .CTin16(PredictJump), .CTout16(ID_PredictJump));
  or or_5 (or_5_out, \数据相关 , register_1_q);
  // Probe on IF_PC[11:0]
  // Probe on WB_PC[19:0]
  // Mips_Probe mips_probe_6: pin names not known; wires that end beside it: WB_IR
  // Probe on ID_PC[11:0]
  // Probe on EX_PC[11:0]
  // Probe on M_PC[11:0]
  D_Flip_Flop #(.trigger("high"), .Pre_Clr_Positions("LEGACY"), .NegatePresetClear("false"), .enable("true"), .NewFFLayout("false")) d_ff_1 (.Q(d_ff_1_q));  // open: clk, D, Qn, preset, en, reset
  // Probe on 13'h2e
  Multiplexer #(.select(1), .width(5), .disabled("Z"), .enable("false")) multiplexer_5 (
    .in0(ID_IR[25:21]), .in1(5'b00100), .out(multiplexer_5_out), .sel(CTRL[4]));
  Multiplexer #(.select(1), .width(5), .disabled("Z"), .enable("false")) multiplexer_6 (
    .in0(ID_IR[20:16]), .in1(5'b00010), .out(multiplexer_6_out), .sel(CTRL[4]));
  Multiplexer #(.select(1), .width(5), .disabled("Z"), .enable("false")) multiplexer_7 (
    .in0(ID_IR[20:16]), .in1(ID_IR[15:11]), .out(multiplexer_7_out), .sel(CTRL[5]));
  Multiplexer #(.select(1), .width(5), .disabled("Z"), .enable("false")) multiplexer_8 (
    .in0(multiplexer_7_out), .in1({5{1'b1}}), .out(multiplexer_8_out), .sel(CTRL[6]));
  // Probe on WB_PC[11:0]
  Comparator #(.width(13), .mode("twosComplement")) comparator_1 (
    .a(CNT_num), .b(13'h2e), .eq(comparator_1_eq), .lt(comparator_1_lt));  // open: gt
  Clock #(.highDuration(1), .lowDuration(1)) clock_2 (.out(clock_2_out));
  \单周期硬布线控制器  \u_单周期硬布线控制器_1  (
    .OP(ID_IR[31:26]), .Func(ID_IR[5:0]), .ALU_OP(CTRL[3:0]), .MemToReg(CTRL[10]), .MemWrite(CTRL[9]),
    .BLTZ(CTRL4[3]), .LH(CTRL4[2]), .SRAV(CTRL4[1]), .XORI(CTRL4[0]), .ALU_SRC(CTRL[8]), .RegWrite(CTRL[7]),
    .SysCALL(CTRL[4]), .SignedExt(CTRL[13]), .RegDst(CTRL[5]), .Beq(CTRL[12]), .Bne(CTRL[11]), .JR(CTRL[14]),
    .JMP(CTRL[15]), .JAL(CTRL[6]));
  assign bit_extender_1_out = {{16{1'b0}}, ID_IR[15:0]};  // Bit_Extender bit_extender_1
  assign bit_extender_2_out = {{16{ID_IR[15]}}, ID_IR[15:0]};  // Bit_Extender bit_extender_2
  assign bit_extender_3_out = {{6{ID_IR[25]}}, ID_IR[25:0]};  // Bit_Extender bit_extender_3
  nand nand_1 (nand_1_out, d_ff_1_q, comparator_1_eq);
  Counter #(.width(13), .max('h1fff), .ongoal("stay"), .trigger("rising"), .behavior("old")) counter_3 (
    .count(comparator_1_lt), .Q(CNT_num), .clk(clock_2_out));  // open: load, D, carry, clr, preset
  MIPS_Regifile mips_regifile_1 (
    .Din(RDin), .Clk(CLK), .R1(mips_regifile_1_r1), .R2(mips_regifile_1_r2), .WE(RegWrite),
    .W_num(mem_wb_1_wbout5), .R1_num(multiplexer_5_out), .R2_num(multiplexer_6_out));
  Multiplexer #(.select(1), .width(32), .disabled("Z"), .enable("false")) multiplexer_9 (
    .in0(bit_extender_1_out), .in1(bit_extender_2_out), .out(multiplexer_9_out), .sel(CTRL[13]));
  assign CLK = nand_1_out ? clock_2_out : 1'bz;  // Controlled_Buffer controlled_buffer_1
  Shifter #(.width(32), .shift("ll")) shifter_1 (.in(bit_extender_3_out), .\dist (5'b00010), .out(shifter_1_out));
  Pull_Resistor #(.pull(1)) pull_resistor_1 (.node(CLK));
  or or_6 (or_6_out, RST, \数据相关 , PredictFailed);
  ID_EX ID_EX (
    .R1in32(mips_regifile_1_r1), .R2in32(mips_regifile_1_r2), .IRin32(ID_IR), .PCin32(ID_PC),
    .IMMin32(multiplexer_9_out), .WBin5(multiplexer_8_out), .SHin5(ID_IR[10:6]), .CTin16(CTRL),
    .\传输状态In_表明当前传输数据有效 (\if_id_1_传输状态out_表明当前传输数据有效 ), .CLK(CLK), .R1out32(ID_EX_r1out32), .R2out32(EX_R2),
    .IRout32(EX_IR), .PCout32(EX_PC), .R1out32_2(ID_EX_r1out32_2), .WBout5(ID_EX_wbout5),
    .SHout5_3(ID_EX_shout5_3), .CTout16(EX_CTRL), .\传输状态Out_表明当前传输数据有效 (\ID_EX_传输状态out_表明当前传输数据有效 ),
    .\同步清零_气泡_高电平有效 (or_6_out), .\使能端_低电平有效_stall_高电平有效 (register_1_q), ._26in32(shifter_1_out),
    .R1out32_3(ID_EX_r1out32_3), .FWR1in2(ForwardR1), .WBout5_2(ID_EX_wbout5_2), .FWR2in2(ForwardR2),
    .SHout5_4(F), .CTRL4(CTRL4), .CTRL4_2({EX_BLTZ, ID_EX_ctrl4_2[2], EX_SRAV, ID_EX_ctrl4_2[0]}),
    .ERETin1_2(ID_PredictJump), .SHout5_2(EX_PredictJump));  // open: ERETin1, SHout5
  Register #(.width(32), .trigger("rising"), .Select("low")) register_2 (
    .D(EX_R1), .en(and_4_out), .Q(register_2_q), .clk(CLK));  // open: clr
  and and_4 (and_4_out, Led, EX_CTRL[4]);
  Multiplexer #(.select(2), .width(32), .disabled("Z"), .enable("false")) multiplexer_10 (
    .in0(ID_EX_r1out32), .in1(ALURes), .in2(RD), .in3(EXALU), .out(EX_R1), .sel(ID_EX_wbout5_2));
  Shifter #(.width(32), .shift("ll")) shifter_2 (.in(ID_EX_r1out32_2), .\dist (5'b00010), .out(shifter_2_out));
  Multiplexer #(.select(1), .width(5), .disabled("Z"), .enable("false")) multiplexer_11 (
    .in0(ID_EX_shout5_3), .in1(EX_R1[4:0]), .out(multiplexer_11_out), .sel(EX_SRAV));
  Adder #(.width(32)) adder_2 (.a(EX_PC), .b(32'h4), .out(EX_PC_4));  // open: cin, cout
  Multiplexer #(.select(1), .width(32), .disabled("Z"), .enable("false")) multiplexer_12 (
    .in0(R2), .in1(ID_EX_r1out32_2), .out(multiplexer_12_out), .sel(EX_CTRL[8]));
  Comparator #(.width(32), .mode("twosComplement")) comparator_2 (.a(R2), .b(32'h22), .eq(Led));  // open: gt, lt
  Adder #(.width(32)) adder_3 (.a(shifter_2_out), .b(EX_PC_4), .out(EX_BRANCHPC));  // open: cin, cout
  MIPS_ALU mips_alu_1 (
    .X(EX_R1), .Y(multiplexer_12_out), .AluOP(EX_CTRL[3:0]), .Equal(equal), .Result(mips_alu_1_result),
    .shamt(multiplexer_11_out));  // open: Result_2
  Multiplexer #(.select(1), .width(32), .disabled("Z"), .enable("false")) multiplexer_13 (
    .in0(ID_EX_r1out32_3), .in1(EX_R1), .out(JR_PC), .sel(EX_CTRL[14]));
  Multiplexer #(.select(1), .width(32), .disabled("Z"), .enable("false")) multiplexer_14 (
    .in0(EX_PC_4), .in1(EX_BRANCHPC), .out(multiplexer_14_out), .sel(EX_BRANCH));
  xor xor_1 (PredictFailed, EX_PredictJump, EX_BranchTaken);
  EX_MEM ex_mem_1 (
    .ALUin32(mips_alu_1_result), .Memin32(R2), .IRin32(EX_IR), .PCin32(EX_PC), .WBin5(ID_EX_wbout5),
    .CTin16_2(EX_CTRL), .\传输状态In_表明当前传输数据有效 (\ID_EX_传输状态out_表明当前传输数据有效 ), .CLK(CLK), .ALUout32(EXALU),
    .Memout32(MDin), .IRout32(MEM_IR), .PCout32(M_PC), .WBout5(ex_mem_1_wbout5),
    .CTout16_6({ex_mem_1_ctout16_6[15:11], Mem_MemToReg, MemWrite, ex_mem_1_ctout16_6[8], Mem_RegWrite, ex_mem_1_ctout16_6[6:0]}),
    .\传输状态Out_表明当前传输数据有效 (\ex_mem_1_传输状态out_表明当前传输数据有效 ), .\同步清零_气泡_高电平有效 (RST),
    .\使能端_低电平有效_stall_高电平有效 (register_1_q), .LEDin32(register_2_q), .LEDout32(ex_mem_1_ledout32),
    .CTin16(Led), .CTout16(ex_mem_1_ctout16), .CTin4({EX_BLTZ, ID_EX_ctrl4_2[2], EX_SRAV, ID_EX_ctrl4_2[0]}),
    .CTout16_2({ex_mem_1_ctout16_2[3], MEM_LH, ex_mem_1_ctout16_2[1:0]}));  // open: Resullt2, CTout16_3, ERETin2, CTout16_4, ERETin2_2, CTout16_5
  Multiplexer #(.select(1), .width(32), .disabled("Z"), .enable("false")) multiplexer_15 (
    .in0(multiplexer_14_out), .in1(EX_BRANCHPC), .out(multiplexer_15_out), .sel(BLTZ));
  Multiplexer #(.select(1), .width(32), .disabled("Z"), .enable("false")) multiplexer_16 (
    .in0(multiplexer_15_out), .in1(JR_PC), .out(multiplexer_16_out), .sel(EX_CTRL[15]));
  MIPS_RAM mips_ram_1 (
    .\字节地址 (EXALU[11:2]), .Din(MDin), .DataOut(mips_ram_1_dataout), .CLK(CLK), .WE(MemWrite),
    .Mode(EXALU[1]), .LH(MEM_LH));
  MEM_WB mem_wb_1 (
    .ALUin32(EXALU), .MDin32(mips_ram_1_dataout), .IRin32(MEM_IR), .PCin32(M_PC), .WBin5(ex_mem_1_wbout5),
    .CTin16_2({ex_mem_1_ctout16_6[15:11], Mem_MemToReg, MemWrite, ex_mem_1_ctout16_6[8], Mem_RegWrite, ex_mem_1_ctout16_6[6:0]}),
    .\传输状态In_表明当前传输数据有效 (\ex_mem_1_传输状态out_表明当前传输数据有效 ), .CLK(CLK), .ALUout32(ALURes), .MDout32(RD),
    .IRout32(WB_IR), .PCout32(WB_PC), .WBout5(mem_wb_1_wbout5),
    .CTout16_6({mem_wb_1_ctout16_6[15:8], RegWrite, mem_wb_1_ctout16_6[6:0]}), .\同步清零_气泡_高电平有效 (RST),
    .\使能端_低电平有效_stall_高电平有效 (register_1_q), .LEDin32(ex_mem_1_ledout32), .LEDout32(LedData),
    .CTin16(ex_mem_1_ctout16), .CTout16_5(mem_wb_1_ctout16_5),
    .CTin4({ex_mem_1_ctout16_2[3], MEM_LH, ex_mem_1_ctout16_2[1:0]}));  // open: 传输状态Out_表明当前传输数据有效, CTout16, CTout16_2, RE2in32, ERETin1, CTout16_3, ERETin1_2, CTout16_4
  Multiplexer #(.select(1), .width(32), .disabled("Z"), .enable("false")) multiplexer_17 (
    .in0(ALURes), .in1(RD), .out(multiplexer_17_out), .sel(mem_wb_1_ctout16_6[10]));
  Adder #(.width(32)) adder_4 (.a(WB_PC), .b(32'h4), .out(adder_4_out));  // open: cin, cout
  Multiplexer #(.select(1), .width(32), .disabled("Z"), .enable("false")) multiplexer_18 (
    .in0(multiplexer_17_out), .in1(adder_4_out), .out(RDin), .sel(mem_wb_1_ctout16_6[6]));
  Counter #(.width(16), .max('hffff), .ongoal("wrap"), .trigger("rising"), .behavior("old")) counter_4 (
    .count(EX_CTRL[15]), .Q(\无条件分支数 ), .clk(CLK), .clr(RST));  // open: load, D, carry, preset
  Counter #(.width(16), .max('hffff), .ongoal("wrap"), .trigger("rising"), .behavior("old")) counter_5 (
    .count(or_7_out), .Q(\条件分支成功数 ), .clk(CLK), .clr(RST));  // open: load, D, carry, preset
  or or_7 (or_7_out, BLTZ, EX_BRANCH);
  Comparator #(.width(32), .mode("twosComplement")) comparator_3 (
    .a(EX_R1), .b({32{1'b0}}), .lt(comparator_3_lt));  // open: gt, eq
  Multiplexer #(.select(2), .width(32), .disabled("Z"), .enable("false")) multiplexer_19 (
    .in0(EX_R2), .in1(ALURes), .in2(RD), .in3(EXALU), .out(R2), .sel(F));
  and and_5 (and_5_out, equal, EX_CTRL[12]);
  and and_6 (and_6_out, ~equal, EX_CTRL[11]);  // AND_Gate
  and and_7 (BLTZ, comparator_3_lt, EX_BLTZ);
  or or_8 (EX_BRANCH, and_5_out, and_6_out);
  or or_9 (or_9_out, EX_CTRL[11], EX_CTRL[12], EX_BLTZ);
  or or_10 (EX_Branch_t, EX_CTRL[14], or_9_out, EX_CTRL[6], EX_CTRL[15]);

  // Other names for the same wires on the sheet: SignedExt = CTRL[13]; EX_JAL = EX_CTRL[6]; EX_RegWrite = EX_CTRL[7];
  //   EX_MemToReg = EX_CTRL[10]; EX_JR = EX_CTRL[14]; EX_JMP = EX_CTRL[15]; MEM_PC[31:0] = M_PC;
  //   插入气泡数[15:0] = \LoadUse次数 

  // Notes on the sheet:
  //   中断源
  //   时空图监测，可删除
  //   中断等待指示
  //   数码管输出
  //   指令存储器
  //   contents of rom_1 (hex, n*v repeats v):
  //   20110001 8000c05 20110001 20120002 20130003 8000c09 20110001 20120002 20130003 8000c0d 20110001
  //   20120002 20130003 8000c11 20110001 20120002 20130003 c000cf7 20100001 20110001 118fc0 112020
  //   20020022 c 118882 12200001 8000c15 112020 20020022 c 20110001 118880 112020 20020022 c 12200001
  //   8000c1f 20110001 118fc0 112020 20020022 c 1188c3 112020 20020022 c 118903 112020 20020022 c 118903
  //   112020 20020022 c 118903 112020 20020022 c 118903 112020 20020022 c 118903 112020 20020022 c 118903
  //   112020 20020022 c 118903 112020 20020022 c 20100001 109fc0 139fc3 8021 2012000c 24160003 26100001
  //   3210000f 20080008 20090001 139900 2709825 132020 20020022 c 1094022 1500fff9 22100001 2018000f
  //   2188024 108700 20080008 20090001 139902 2709825 132021 20020022 c 1094022 1500fff9 108702 2c9b022
  //   12c00001 8000c50 4020 1084027 84400 3508ffff 82021 20020022 c 2010ffff 20110000 ae300000 22100001
  //   22310004 ae300000 22100001 22310004 ae300000 22100001 22310004 ae300000 22100001 22310004 ae300000
  //   22100001 22310004 ae300000 22100001 22310004 ae300000 22100001 22310004 ae300000 22100001 22310004
  //   ae300000 22100001 22310004 ae300000 22100001 22310004 ae300000 22100001 22310004 ae300000 22100001
  //   22310004 ae300000 22100001 22310004 ae300000 22100001 22310004 ae300000 22100001 22310004 ae300000
  //   22100001 22310004 22100001 8020 2011003c 8e130000 8e340000 274402a 11000002 ae330000 ae140000
  //   2231fffc 1611fff8 102020 20020022 c 22100004 2011003c 1611fff2 20020032 c 20080001 20090003 20110876
  //   118d00 112020 20020022 c 200b0008 1118807 1318807 112020 20020022 c 216bffff 1560fff9 2002000a c
  //   2008ffff 20117777 112020 20020022 c 200b0010 3a31ffff 112020 20020022 c 216bffff 1560fffa 2002000a c
  //   20090000 200b0010 34118483 20120404 118c00 129400 36318281 22520404 ad310000 2328820 21290004
  //   216bffff 1560fffb 200b0020 20090000 85310000 112020 20020022 c 21290002 216bffff 1560fff9 2002000a c
  //   2011fff1 112020 20020022 c 22310001 620fffb 2002000a c 20100000 22100001 102020 20020022 c 22100002
  //   102020 20020022 c 22100003 102020 20020022 c 22100004 102020 20020022 c 22100005 102020 20020022 c
  //   22100006 102020 20020022 c 22100007 102020 20020022 c 22100008 102020 20020022 20020022 c 3e00008
  //   OP
  //   rs
  //   rt
  //   rd
  //   控制位
  //   Func
  //   流水调试日志用
  //   暂停节拍，不能为0
  //   JMP
  //   JR
  //   OP
  //   Func
  //   Syscall
  //   戳工具置1进入计数暂停模式，ctrl+k时钟自动运行到对应节拍暂停
  //   ctrl+k关闭时钟连续运行，将控制位置零，进入单步调试模式调试
  //   Beq
  //   Bne
  //   MemToReg
  //   MemWrite
  //   AluOP
  //   AluSrcB
  //   RegWrite
  //   JAL
  //   RegDst
  //   可计数暂停的时钟源
  //   Syscall
  //   为方便自动评测，需要输出流水线各段保存的PC值，注意是PC不是PC+4，另外ID段寄存器写入信息，Mem段内存写入信息也要输出
  //   AluOP
  //   AluSrcB
  //   RegWrite
  //   MemWrite
  //   JAL
  //   Bne
endmodule

// MAX3
module \Max3_归并比较  (
  input  [15:0] Y,
  input  [15:0] X,
  input  [2:0] Y_num,
  input  [2:0] X_num,
  output [15:0] MAX,
  output [2:0] Max_num
);

  wire comparator_1_eq, comparator_1_gt, or_1_out;

  Multiplexer #(.select(1), .width(16), .disabled("Z"), .enable("false")) multiplexer_1 (
    .in0(Y), .in1(X), .out(MAX), .sel(or_1_out));
  Comparator #(.width(16), .mode("unsigned")) comparator_1 (
    .a(X), .b(Y), .gt(comparator_1_gt), .eq(comparator_1_eq));  // open: lt
  or or_1 (or_1_out, comparator_1_gt, comparator_1_eq);
  Multiplexer #(.select(1), .width(3), .disabled("Z"), .enable("false")) multiplexer_2 (
    .in0(Y_num), .in1(X_num), .out(Max_num), .sel(or_1_out));

  // Notes on the sheet:
  //   输出两个输入中的较大值，并输出较大值的3位编号
endmodule

module BHT (
  input  [31:0] IF_PC,
  input  [31:0] JumpAddr,
  input  [31:0] EX_PC,
  input  EX_Branch,
  input  CLK,
  input  in_6,
  output PredictJump,
  output [31:0] JumpAddr_2
);

  wire and_17_out, and_18_out, comparator_1_eq, comparator_2_eq, comparator_3_eq, comparator_4_eq,
       comparator_5_eq, comparator_6_eq, comparator_7_eq, comparator_8_eq, comparator_9_eq, comparator_10_eq,
       comparator_11_eq, comparator_12_eq, comparator_13_eq, comparator_14_eq, comparator_15_eq,
       comparator_16_eq, HIT, L0, l0_t, L1, l1_t, L2, l2_t, L3, l3_t, L4, l4_t, L5, l5_t, L6, l6_t, L7, l7_t,
       Miss, not_1_out, not_3_out, not_4_out, not_5_out, not_6_out, not_7_out, not_8_out, not_9_out,
       not_10_out, or_1_out, or_2_out, or_3_out, or_4_out, or_5_out, or_6_out, or_7_out, or_8_out, or_9_out,
       or_10_out, or_11_out, v0, v1, v2, v3, v4, v5, v6, v7, \全满 , \淘汰0 , \淘汰1 , \淘汰2 , \淘汰3 , \淘汰4 , \淘汰5 ,
       \淘汰6 , \淘汰7 ;
  wire [0:0] curState;
  wire [1:0] multiplexer_1_out, multiplexer_2_out, multiplexer_3_out, multiplexer_5_out, NewState, Stat_2_q,
       Stat_3_q, Stat_4_q, Stat_q, State, State_2_q, State_3_q, State_4_q, State_q;
  wire [2:0] Max, \max3_归并比较_1_max_num , \max3_归并比较_2_max_num , \max3_归并比较_3_max_num , \max3_归并比较_4_max_num ,
       \max3_归并比较_5_max_num , \max3_归并比较_6_max_num , multiplexer_6_out, priority_encoder_2_out, Valued, \淘汰 ;
  wire [15:0] c0, c1, c2, c3, c4, c5, c6, c7, \max3_归并比较_1_max , \max3_归并比较_2_max , \max3_归并比较_3_max ,
       \max3_归并比较_4_max , \max3_归并比较_5_max , \max3_归并比较_6_max ;
  wire [31:0] tag0, tag1, tag2, tag3, tag4, tag5, tag6, tag7, \数据块副本_2_q , \数据块副本_3_q , \数据块副本_4_q ,
       \数据块副本_5_q , \数据块副本_6_q , \数据块副本_7_q , \数据块副本_8_q , \数据块副本_q ;

  Register #(.width(1), .trigger("rising"), .Select("low")) valid (
    .D(1'b1), .en(\淘汰0 ), .Q(v0), .clk(CLK));  // open: clr
  Register #(.width(1), .trigger("rising"), .Select("low")) valid_2 (
    .D(1'b1), .en(\淘汰1 ), .Q(v1), .clk(CLK));  // open: clr
  Register #(.width(1), .trigger("rising"), .Select("low")) valid_3 (
    .D(1'b1), .en(\淘汰2 ), .Q(v2), .clk(CLK));  // open: clr
  Register #(.width(1), .trigger("rising"), .Select("low")) valid_4 (
    .D(1'b1), .en(\淘汰3 ), .Q(v3), .clk(CLK));  // open: clr
  Register #(.width(32), .trigger("rising"), .Select("low")) \u_标志位  (
    .D(EX_PC), .en(\淘汰0 ), .Q(tag0), .clk(CLK));  // open: clr
  Register #(.width(32), .trigger("rising"), .Select("low")) \u_标志位_2  (
    .D(EX_PC), .en(\淘汰1 ), .Q(tag1), .clk(CLK));  // open: clr
  Register #(.width(32), .trigger("rising"), .Select("low")) \u_标志位_3  (
    .D(EX_PC), .en(\淘汰2 ), .Q(tag2), .clk(CLK));  // open: clr
  Register #(.width(32), .trigger("rising"), .Select("low")) \u_标志位_4  (
    .D(EX_PC), .en(\淘汰3 ), .Q(tag3), .clk(CLK));  // open: clr
  Comparator #(.width(32), .mode("twosComplement")) comparator_1 (
    .a(IF_PC), .b(tag0), .eq(comparator_1_eq));  // open: gt, lt
  Comparator #(.width(32), .mode("twosComplement")) comparator_2 (
    .a(IF_PC), .b(tag1), .eq(comparator_2_eq));  // open: gt, lt
  Comparator #(.width(32), .mode("twosComplement")) comparator_3 (
    .a(IF_PC), .b(tag2), .eq(comparator_3_eq));  // open: gt, lt
  Comparator #(.width(32), .mode("twosComplement")) comparator_4 (
    .a(IF_PC), .b(tag3), .eq(comparator_4_eq));  // open: gt, lt
  Comparator #(.width(32), .mode("twosComplement")) comparator_5 (
    .a(IF_PC), .b(tag4), .eq(comparator_5_eq));  // open: gt, lt
  Comparator #(.width(32), .mode("twosComplement")) comparator_6 (
    .a(IF_PC), .b(tag5), .eq(comparator_6_eq));  // open: gt, lt
  Comparator #(.width(32), .mode("twosComplement")) comparator_7 (
    .a(IF_PC), .b(tag6), .eq(comparator_7_eq));  // open: gt, lt
  Comparator #(.width(32), .mode("twosComplement")) comparator_8 (
    .a(IF_PC), .b(tag7), .eq(comparator_8_eq));  // open: gt, lt
  or or_1 (or_1_out, \淘汰0 , L0);
  or or_2 (or_2_out, \淘汰1 , L1);
  or or_3 (or_3_out, \淘汰2 , L2);
  or or_4 (or_4_out, \淘汰3 , L3);
  and and_1 (L0, v0, comparator_1_eq);
  and and_2 (L1, v1, comparator_2_eq);
  and and_3 (L2, v2, comparator_3_eq);
  and and_4 (L3, v3, comparator_4_eq);
  and and_5 (L4, v4, comparator_5_eq);
  and and_6 (L5, v5, comparator_6_eq);
  and and_7 (L6, v6, comparator_7_eq);
  and and_8 (L7, v7, comparator_8_eq);
  Counter #(.width(16), .max('hffff), .ongoal("wrap"), .trigger("rising"), .behavior("new")) \u_淘汰标志位  (
    .load(or_1_out), .D({16{1'b0}}), .Q(c0), .clk(CLK));  // open: count, carry, clr, preset, down
  Counter #(.width(16), .max('hffff), .ongoal("wrap"), .trigger("rising"), .behavior("new")) \u_淘汰标志位_2  (
    .load(or_2_out), .D({16{1'b0}}), .Q(c1), .clk(CLK));  // open: count, carry, clr, preset, down
  Counter #(.width(16), .max('hffff), .ongoal("wrap"), .trigger("rising"), .behavior("new")) \u_淘汰标志位_3  (
    .load(or_3_out), .D({16{1'b0}}), .Q(c2), .clk(CLK));  // open: count, carry, clr, preset, down
  Counter #(.width(16), .max('hffff), .ongoal("wrap"), .trigger("rising"), .behavior("new")) \u_淘汰标志位_4  (
    .load(or_4_out), .D({16{1'b0}}), .Q(c3), .clk(CLK));  // open: count, carry, clr, preset, down
  or or_5 (or_5_out, L0, L1, L2, L3);
  or or_6 (or_6_out, L4, L5, L6, L7);
  or or_7 (or_7_out, or_5_out, or_6_out);
  assign JumpAddr_2 = L0 ? \数据块副本_q  : 32'bz;  // Controlled_Buffer controlled_buffer_1
  Register #(.width(32), .trigger("rising"), .Select("low")) \u_数据块副本  (
    .D(JumpAddr), .en(\淘汰0 ), .Q(\数据块副本_q ), .clk(CLK));  // open: clr
  assign JumpAddr_2 = L1 ? \数据块副本_2_q  : 32'bz;  // Controlled_Buffer controlled_buffer_2
  Register #(.width(32), .trigger("rising"), .Select("low")) \u_数据块副本_2  (
    .D(JumpAddr), .en(\淘汰1 ), .Q(\数据块副本_2_q ), .clk(CLK));  // open: clr
  Register #(.width(32), .trigger("rising"), .Select("low")) \u_数据块副本_3  (
    .D(JumpAddr), .en(\淘汰2 ), .Q(\数据块副本_3_q ), .clk(CLK));  // open: clr
  assign JumpAddr_2 = L2 ? \数据块副本_3_q  : 32'bz;  // Controlled_Buffer controlled_buffer_3
  Register #(.width(32), .trigger("rising"), .Select("low")) \u_数据块副本_4  (
    .D(JumpAddr), .en(\淘汰3 ), .Q(\数据块副本_4_q ), .clk(CLK));  // open: clr
  assign JumpAddr_2 = L3 ? \数据块副本_4_q  : 32'bz;  // Controlled_Buffer controlled_buffer_4
  assign {PredictJump, curState[0]} = not_1_out ? 2'b00 : 2'bz;  // Controlled_Buffer controlled_buffer_5
  not not_1 (not_1_out, or_7_out);
  Register #(.width(2), .trigger("rising"), .Select("low")) u_State (
    .D(NewState), .en(\淘汰0 ), .Q(State_q), .clk(CLK));  // open: clr
  Register #(.width(2), .trigger("rising"), .Select("low")) State_2 (
    .D(NewState), .en(\淘汰1 ), .Q(State_2_q), .clk(CLK));  // open: clr
  Register #(.width(2), .trigger("rising"), .Select("low")) State_3 (
    .D(NewState), .en(\淘汰2 ), .Q(State_3_q), .clk(CLK));  // open: clr
  Register #(.width(2), .trigger("rising"), .Select("low")) State_4 (
    .D(NewState), .en(\淘汰3 ), .Q(State_4_q), .clk(CLK));  // open: clr
  assign {PredictJump, curState[0]} = L0 ? State_q : 2'bz;  // Controlled_Buffer controlled_buffer_6
  assign State = l0_t ? State_q : 2'bz;  // Controlled_Buffer controlled_buffer_7
  assign {PredictJump, curState[0]} = L1 ? State_2_q : 2'bz;  // Controlled_Buffer controlled_buffer_8
  assign State = l1_t ? State_2_q : 2'bz;  // Controlled_Buffer controlled_buffer_9
  assign {PredictJump, curState[0]} = L2 ? State_3_q : 2'bz;  // Controlled_Buffer controlled_buffer_10
  assign State = l2_t ? State_3_q : 2'bz;  // Controlled_Buffer controlled_buffer_11
  assign {PredictJump, curState[0]} = L3 ? State_4_q : 2'bz;  // Controlled_Buffer controlled_buffer_12
  assign State = l3_t ? State_4_q : 2'bz;  // Controlled_Buffer controlled_buffer_13
  Comparator #(.width(32), .mode("twosComplement")) comparator_9 (
    .a(EX_PC), .b(tag0), .eq(comparator_9_eq));  // open: gt, lt
  Comparator #(.width(32), .mode("twosComplement")) comparator_10 (
    .a(EX_PC), .b(tag1), .eq(comparator_10_eq));  // open: gt, lt
  Comparator #(.width(32), .mode("twosComplement")) comparator_11 (
    .a(EX_PC), .b(tag2), .eq(comparator_11_eq));  // open: gt, lt
  Comparator #(.width(32), .mode("twosComplement")) comparator_12 (
    .a(EX_PC), .b(tag3), .eq(comparator_12_eq));  // open: gt, lt
  Comparator #(.width(32), .mode("twosComplement")) comparator_13 (
    .a(EX_PC), .b(tag4), .eq(comparator_13_eq));  // open: gt, lt
  Comparator #(.width(32), .mode("twosComplement")) comparator_14 (
    .a(EX_PC), .b(tag5), .eq(comparator_14_eq));  // open: gt, lt
  Comparator #(.width(32), .mode("twosComplement")) comparator_15 (
    .a(EX_PC), .b(tag6), .eq(comparator_15_eq));  // open: gt, lt
  Comparator #(.width(32), .mode("twosComplement")) comparator_16 (
    .a(EX_PC), .b(tag7), .eq(comparator_16_eq));  // open: gt, lt
  and and_9 (l0_t, v0, comparator_9_eq);
  and and_10 (l1_t, v1, comparator_10_eq);
  and and_11 (l2_t, v2, comparator_11_eq);
  and and_12 (l3_t, v3, comparator_12_eq);
  and and_13 (l4_t, v4, comparator_13_eq);
  and and_14 (l5_t, v5, comparator_14_eq);
  and and_15 (l6_t, v6, comparator_15_eq);
  and and_16 (l7_t, v7, comparator_16_eq);
  Register #(.width(1), .trigger("rising"), .Select("low")) valid_5 (
    .D(1'b1), .en(\淘汰7 ), .Q(v7), .clk(CLK));  // open: clr
  Register #(.width(1), .trigger("rising"), .Select("low")) valid_6 (
    .D(1'b1), .en(\淘汰4 ), .Q(v4), .clk(CLK));  // open: clr
  Register #(.width(1), .trigger("rising"), .Select("low")) valid_7 (
    .D(1'b1), .en(\淘汰5 ), .Q(v5), .clk(CLK));  // open: clr
  Register #(.width(1), .trigger("rising"), .Select("low")) valid_8 (
    .D(1'b1), .en(\淘汰6 ), .Q(v6), .clk(CLK));  // open: clr
  Priority_Encoder #(.select(3), .disabled("Z")) priority_encoder_1 (
    .in0(l0_t), .in1(l1_t), .in2(l2_t), .in3(l3_t), .in4(l4_t), .in5(l5_t), .in6(l6_t), .in7(l7_t),
    .out(Valued), .en_out(Miss), .en_in(1'b1));  // open: gs
  not not_2 (HIT, Miss);
  Register #(.width(32), .trigger("rising"), .Select("low")) \u_标志位_5  (
    .D(EX_PC), .en(\淘汰4 ), .Q(tag4), .clk(CLK));  // open: clr
  Register #(.width(32), .trigger("rising"), .Select("low")) \u_标志位_6  (
    .D(EX_PC), .en(\淘汰5 ), .Q(tag5), .clk(CLK));  // open: clr
  Register #(.width(32), .trigger("rising"), .Select("low")) \u_标志位_7  (
    .D(EX_PC), .en(\淘汰6 ), .Q(tag6), .clk(CLK));  // open: clr
  Register #(.width(32), .trigger("rising"), .Select("low")) \u_标志位_8  (
    .D(EX_PC), .en(\淘汰7 ), .Q(tag7), .clk(CLK));  // open: clr
  Counter #(.width(16), .max('hffff), .ongoal("wrap"), .trigger("rising"), .behavior("new")) \u_淘汰标志位_5  (
    .load(or_8_out), .D({16{1'b0}}), .Q(c4), .clk(CLK));  // open: count, carry, clr, preset, down
  or or_8 (or_8_out, L4, \淘汰4 );
  Counter #(.width(16), .max('hffff), .ongoal("wrap"), .trigger("rising"), .behavior("new")) \u_淘汰标志位_6  (
    .load(or_9_out), .D({16{1'b0}}), .Q(c5), .clk(CLK));  // open: count, carry, clr, preset, down
  or or_9 (or_9_out, L5, \淘汰5 );
  Counter #(.width(16), .max('hffff), .ongoal("wrap"), .trigger("rising"), .behavior("new")) \u_淘汰标志位_7  (
    .load(or_10_out), .D({16{1'b0}}), .Q(c6), .clk(CLK));  // open: count, carry, clr, preset, down
  or or_10 (or_10_out, L6, \淘汰6 );
  Counter #(.width(16), .max('hffff), .ongoal("wrap"), .trigger("rising"), .behavior("new")) \u_淘汰标志位_8  (
    .load(or_11_out), .D({16{1'b0}}), .Q(c7), .clk(CLK));  // open: count, carry, clr, preset, down
  or or_11 (or_11_out, L7, \淘汰7 );
  \Max3_归并比较  \max3_归并比较_1  (
    .Y(c1), .MAX(\max3_归并比较_1_max ), .X(c0), .Y_num(3'b001), .Max_num(\max3_归并比较_1_max_num ), .X_num(3'b000));
  \Max3_归并比较  \max3_归并比较_2  (
    .Y(c3), .MAX(\max3_归并比较_2_max ), .X(c2), .Y_num(3'b011), .Max_num(\max3_归并比较_2_max_num ), .X_num(3'b010));
  \Max3_归并比较  \max3_归并比较_3  (
    .Y(c5), .MAX(\max3_归并比较_3_max ), .X(c4), .Y_num(3'b101), .Max_num(\max3_归并比较_3_max_num ), .X_num(3'b100));
  \Max3_归并比较  \max3_归并比较_4  (
    .Y(c7), .MAX(\max3_归并比较_4_max ), .X(c6), .Y_num(3'b111), .Max_num(\max3_归并比较_4_max_num ), .X_num(3'b110));
  and and_17 (and_17_out, v0, v1, v2, v3);
  and and_18 (and_18_out, v4, v5, v6, v7);
  Multiplexer #(.select(2), .width(2), .disabled("Z"), .enable("false")) multiplexer_1 (
    .in0(2'b00), .in1(2'b00), .in2(2'b11), .in3(2'b00), .out(multiplexer_1_out), .sel(State));
  Multiplexer #(.select(2), .width(2), .disabled("Z"), .enable("false")) multiplexer_2 (
    .in0(2'b01), .in1(2'b10), .in2(2'b10), .in3(2'b10), .out(multiplexer_2_out), .sel(State));
  \Max3_归并比较  \max3_归并比较_5  (
    .Y(\max3_归并比较_2_max ), .MAX(\max3_归并比较_5_max ), .X(\max3_归并比较_1_max ), .Y_num(\max3_归并比较_2_max_num ),
    .Max_num(\max3_归并比较_5_max_num ), .X_num(\max3_归并比较_1_max_num ));
  \Max3_归并比较  \max3_归并比较_6  (
    .Y(\max3_归并比较_4_max ), .MAX(\max3_归并比较_6_max ), .X(\max3_归并比较_3_max ), .Y_num(\max3_归并比较_4_max_num ),
    .Max_num(\max3_归并比较_6_max_num ), .X_num(\max3_归并比较_3_max_num ));
  and and_19 (\全满 , and_17_out, and_18_out);
  Multiplexer #(.select(1), .width(2), .disabled("Z"), .enable("false")) multiplexer_3 (
    .in0(multiplexer_1_out), .in1(multiplexer_2_out), .out(multiplexer_3_out), .sel(in_6));
  Register #(.width(32), .trigger("rising"), .Select("low")) \u_数据块副本_5  (
    .D(JumpAddr), .en(\淘汰5 ), .Q(\数据块副本_5_q ), .clk(CLK));  // open: clr
  Register #(.width(32), .trigger("rising"), .Select("low")) \u_数据块副本_6  (
    .D(JumpAddr), .en(\淘汰6 ), .Q(\数据块副本_6_q ), .clk(CLK));  // open: clr
  Register #(.width(32), .trigger("rising"), .Select("low")) \u_数据块副本_7  (
    .D(JumpAddr), .en(\淘汰7 ), .Q(\数据块副本_7_q ), .clk(CLK));  // open: clr
  \Max3_归并比较  \max3_归并比较_7  (
    .Y(\max3_归并比较_6_max ), .X(\max3_归并比较_5_max ), .Y_num(\max3_归并比较_6_max_num ), .Max_num(Max),
    .X_num(\max3_归并比较_5_max_num ));  // open: MAX
  Multiplexer #(.select(1), .width(2), .disabled("Z"), .enable("false")) multiplexer_4 (
    .in0(multiplexer_3_out), .in1(multiplexer_5_out), .out(NewState), .sel(Miss));
  Multiplexer #(.select(1), .width(2), .disabled("Z"), .enable("false")) multiplexer_5 (
    .in0(2'b01), .in1(2'b11), .out(multiplexer_5_out), .sel(in_6));
  Register #(.width(32), .trigger("rising"), .Select("low")) \u_数据块副本_8  (
    .D(JumpAddr), .en(\淘汰4 ), .Q(\数据块副本_8_q ), .clk(CLK));  // open: clr
  assign JumpAddr_2 = L4 ? \数据块副本_8_q  : 32'bz;  // Controlled_Buffer controlled_buffer_14
  assign JumpAddr_2 = L5 ? \数据块副本_5_q  : 32'bz;  // Controlled_Buffer controlled_buffer_15
  assign JumpAddr_2 = L6 ? \数据块副本_6_q  : 32'bz;  // Controlled_Buffer controlled_buffer_16
  assign JumpAddr_2 = L7 ? \数据块副本_7_q  : 32'bz;  // Controlled_Buffer controlled_buffer_17
  not not_3 (not_3_out, v0);
  not not_4 (not_4_out, v1);
  not not_5 (not_5_out, v2);
  not not_6 (not_6_out, v3);
  not not_7 (not_7_out, v4);
  not not_8 (not_8_out, v5);
  not not_9 (not_9_out, v6);
  not not_10 (not_10_out, v7);
  Register #(.width(2), .trigger("rising"), .Select("low")) Stat (
    .D(NewState), .en(\淘汰4 ), .Q(Stat_q), .clk(CLK));  // open: clr
  Register #(.width(2), .trigger("rising"), .Select("low")) Stat_2 (
    .D(NewState), .en(\淘汰5 ), .Q(Stat_2_q), .clk(CLK));  // open: clr
  assign {PredictJump, curState[0]} = L6 ? Stat_3_q : 2'bz;  // Controlled_Buffer controlled_buffer_18
  Register #(.width(2), .trigger("rising"), .Select("low")) Stat_3 (
    .D(NewState), .en(\淘汰6 ), .Q(Stat_3_q), .clk(CLK));  // open: clr
  assign {PredictJump, curState[0]} = L7 ? Stat_4_q : 2'bz;  // Controlled_Buffer controlled_buffer_19
  Register #(.width(2), .trigger("rising"), .Select("low")) Stat_4 (
    .D(NewState), .en(\淘汰7 ), .Q(Stat_4_q), .clk(CLK));  // open: clr
  Demultiplexer #(.select(3), .width(1), .tristate("false"), .disabled(0), .enable("true")) demultiplexer_1 (
    .out0(\淘汰0 ), .out1(\淘汰1 ), .out2(\淘汰2 ), .out3(\淘汰3 ), .out4(\淘汰4 ), .out5(\淘汰5 ), .out6(\淘汰6 ),
    .out7(\淘汰7 ), .in(EX_Branch), .sel(\淘汰 ), .en(EX_Branch));
  assign {PredictJump, curState[0]} = L4 ? Stat_q : 2'bz;  // Controlled_Buffer controlled_buffer_20
  assign State = l4_t ? Stat_q : 2'bz;  // Controlled_Buffer controlled_buffer_21
  assign {PredictJump, curState[0]} = L5 ? Stat_2_q : 2'bz;  // Controlled_Buffer controlled_buffer_22
  assign State = l5_t ? Stat_2_q : 2'bz;  // Controlled_Buffer controlled_buffer_23
  assign State = l6_t ? Stat_3_q : 2'bz;  // Controlled_Buffer controlled_buffer_24
  assign State = l7_t ? Stat_4_q : 2'bz;  // Controlled_Buffer controlled_buffer_25
  Priority_Encoder #(.select(3), .disabled("Z")) priority_encoder_2 (
    .in0(not_3_out), .in1(not_4_out), .in2(not_5_out), .in3(not_6_out), .in4(not_7_out), .in5(not_8_out),
    .in6(not_9_out), .in7(not_10_out), .out(priority_encoder_2_out), .en_in(1'b1));  // open: gs, en_out
  Multiplexer #(.select(1), .width(3), .disabled("Z"), .enable("false")) multiplexer_6 (
    .in0(priority_encoder_2_out), .in1(Max), .out(multiplexer_6_out), .sel(\全满 ));
  Multiplexer #(.select(1), .width(3), .disabled("Z"), .enable("false")) multiplexer_7 (
    .in0(multiplexer_6_out), .in1(Valued), .out(\淘汰 ), .sel(HIT));

  // Other names for the same wires on the sheet: Blk[31:0] = JumpAddr; BlkReady = EX_Branch;
  //   curState[1] = PredictJump; JUMP = PredictJump; EX_Branched = in_6; DataOut[31:0] = JumpAddr_2;
  //   SlotData[31:0] = JumpAddr_2; Tag[31:0] = EX_PC

  // Notes on the sheet:
  //   输入引脚区
  //   请勿增改引脚，请勿修改子电路封装
  //   电路功能：利用上面给定的隧道构建8行的Cache，cache映射方式自选
  //   请在下方利用上方输入输出引脚的隧道信号构建电路，ctrl+d复制选择部件
  //   输出引脚区
endmodule
module BHT2 (
  input  Clk,
  input  EX_Branch,
  input  [31:0] PC,
  input  [31:0] EX_PC,
  input  [31:0] EX_BranchAddr,
  input  EX_Branched,
  output [31:0] JumpAddr,
  output PredictJump
);

  wire A0, A1, A2, A3, A4, A5, A6, A7, and_1_out, comparator_1_eq, comparator_2_eq, comparator_3_eq,
       comparator_4_eq, comparator_5_eq, comparator_6_eq, comparator_7_eq, comparator_8_eq, comparator_9_eq,
       comparator_10_eq, comparator_11_eq, comparator_12_eq, comparator_13_eq, comparator_14_eq,
       comparator_15_eq, comparator_16_eq, decoder_1_out0, decoder_1_out1, decoder_1_out2, decoder_1_out3,
       decoder_1_out4, decoder_1_out5, decoder_1_out6, decoder_1_out7, decoder_2_out0, decoder_2_out1,
       decoder_2_out2, decoder_2_out3, decoder_2_out4, decoder_2_out5, decoder_2_out6, decoder_2_out7,
       EX_Hit, EX_Miss, IF_Hit, IF_Miss, L0, L1, L2, L3, L4, L5, L6, L7, M0, M1, M2, M3, M4, M5, M6, M7,
       not_1_out, not_2_out, not_3_out, not_4_out, not_5_out, not_6_out, not_7_out, not_8_out, or_1_out,
       or_2_out, or_3_out, or_4_out, or_5_out, or_6_out, or_7_out, or_8_out, or_9_out, or_10_out, or_11_out,
       or_12_out, or_13_out, or_14_out, or_16_out, or_17_out, priority_encoder_1_gs, V0, V1, V2, V3, V4, V5,
       V6, V7, WriteL0, WriteL1, WriteL2, WriteL3, WriteL4, WriteL5, WriteL6, WriteL7;
  wire [0:0] controlled_buffer_1_out, controlled_buffer_2_out, controlled_buffer_3_out,
       controlled_buffer_4_out, controlled_buffer_5_out, controlled_buffer_6_out, controlled_buffer_7_out,
       controlled_buffer_8_out;
  wire [1:0] adder_1_out, adder_2_out, adder_3_out, adder_4_out, adder_5_out, adder_6_out, adder_7_out,
       adder_8_out, multiplexer_1_out, multiplexer_2_out, multiplexer_3_out, multiplexer_4_out,
       multiplexer_5_out, multiplexer_6_out, multiplexer_7_out, multiplexer_8_out, multiplexer_9_out,
       multiplexer_10_out, multiplexer_11_out, multiplexer_12_out, multiplexer_13_out, multiplexer_14_out,
       multiplexer_15_out, multiplexer_16_out, multiplexer_17_out, multiplexer_18_out, multiplexer_19_out,
       multiplexer_20_out, multiplexer_21_out, multiplexer_22_out, multiplexer_23_out, multiplexer_24_out,
       multiplexer_25_out, multiplexer_26_out, multiplexer_27_out, multiplexer_28_out, multiplexer_29_out,
       multiplexer_30_out, multiplexer_31_out, multiplexer_32_out, multiplexer_33_out, multiplexer_34_out,
       multiplexer_35_out, multiplexer_36_out, multiplexer_37_out, multiplexer_38_out, multiplexer_39_out,
       multiplexer_40_out, Predict0, Predict1, Predict2, Predict3, Predict4, Predict5, Predict6, Predict7;
  wire [2:0] \max3_归并比较_1_max_num , \max3_归并比较_2_max_num , \max3_归并比较_3_max_num , \max3_归并比较_4_max_num ,
       \max3_归并比较_5_max_num , \max3_归并比较_6_max_num , \max3_归并比较_7_max_num , priority_encoder_1_out;
  wire [15:0] C0, C1, C2, C3, C4, C5, C6, C7, \max3_归并比较_1_max , \max3_归并比较_2_max , \max3_归并比较_3_max ,
       \max3_归并比较_4_max , \max3_归并比较_5_max , \max3_归并比较_6_max ;
  wire [31:0] Tag0, Tag1, Tag2, Tag3, Tag4, Tag5, Tag6, Tag7, \分支目标地址_2_q , \分支目标地址_3_q , \分支目标地址_4_q ,
       \分支目标地址_5_q , \分支目标地址_6_q , \分支目标地址_7_q , \分支目标地址_8_q , \分支目标地址_q ;

  Register #(.width(1), .trigger("rising"), .Select("low")) VALID (
    .D(1'b1), .en(WriteL0), .Q(V0), .clk(Clk));  // open: clr
  Register #(.width(1), .trigger("rising"), .Select("low")) VALID_2 (
    .D(1'b1), .en(WriteL1), .Q(V1), .clk(Clk));  // open: clr
  Register #(.width(1), .trigger("rising"), .Select("low")) VALID_3 (
    .D(1'b1), .en(WriteL2), .Q(V2), .clk(Clk));  // open: clr
  Register #(.width(1), .trigger("rising"), .Select("low")) VALID_4 (
    .D(1'b1), .en(WriteL3), .Q(V3), .clk(Clk));  // open: clr
  Register #(.width(1), .trigger("rising"), .Select("low")) VALID_5 (
    .D(1'b1), .en(WriteL4), .Q(V4), .clk(Clk));  // open: clr
  Register #(.width(1), .trigger("rising"), .Select("low")) VALID_6 (
    .D(1'b1), .en(WriteL5), .Q(V5), .clk(Clk));  // open: clr
  Register #(.width(1), .trigger("rising"), .Select("low")) VALID_7 (
    .D(1'b1), .en(WriteL6), .Q(V6), .clk(Clk));  // open: clr
  Register #(.width(1), .trigger("rising"), .Select("low")) VALID_8 (
    .D(1'b1), .en(WriteL7), .Q(V7), .clk(Clk));  // open: clr
  not not_1 (not_1_out, V0);
  not not_2 (not_2_out, V1);
  not not_3 (not_3_out, V2);
  not not_4 (not_4_out, V3);
  not not_5 (not_5_out, V4);
  not not_6 (not_6_out, V5);
  not not_7 (not_7_out, V6);
  not not_8 (not_8_out, V7);
  \Max3_归并比较  \max3_归并比较_1  (
    .Y(C1), .MAX(\max3_归并比较_1_max ), .X(C0), .Y_num(3'b001), .Max_num(\max3_归并比较_1_max_num ), .X_num(3'b000));
  \Max3_归并比较  \max3_归并比较_2  (
    .Y(C3), .MAX(\max3_归并比较_2_max ), .X(C2), .Y_num(3'b011), .Max_num(\max3_归并比较_2_max_num ), .X_num(3'b010));
  \Max3_归并比较  \max3_归并比较_3  (
    .Y(C5), .MAX(\max3_归并比较_3_max ), .X(C4), .Y_num(3'b101), .Max_num(\max3_归并比较_3_max_num ), .X_num(3'b100));
  \Max3_归并比较  \max3_归并比较_4  (
    .Y(C7), .MAX(\max3_归并比较_4_max ), .X(C6), .Y_num(3'b111), .Max_num(\max3_归并比较_4_max_num ), .X_num(3'b110));
  Pull_Resistor #(.pull(0)) pull_resistor_1 (.node(PredictJump));
  assign {PredictJump, controlled_buffer_1_out[0]} = L0 ? Predict0 : 2'bz;  // Controlled_Buffer controlled_buffer_1
  assign {PredictJump, controlled_buffer_2_out[0]} = L1 ? Predict1 : 2'bz;  // Controlled_Buffer controlled_buffer_2
  assign {PredictJump, controlled_buffer_3_out[0]} = L2 ? Predict2 : 2'bz;  // Controlled_Buffer controlled_buffer_3
  assign {PredictJump, controlled_buffer_4_out[0]} = L3 ? Predict3 : 2'bz;  // Controlled_Buffer controlled_buffer_4
  assign {PredictJump, controlled_buffer_5_out[0]} = L4 ? Predict4 : 2'bz;  // Controlled_Buffer controlled_buffer_5
  assign {PredictJump, controlled_buffer_6_out[0]} = L5 ? Predict5 : 2'bz;  // Controlled_Buffer controlled_buffer_6
  assign {PredictJump, controlled_buffer_7_out[0]} = L6 ? Predict6 : 2'bz;  // Controlled_Buffer controlled_buffer_7
  assign {PredictJump, controlled_buffer_8_out[0]} = L7 ? Predict7 : 2'bz;  // Controlled_Buffer controlled_buffer_8
  Priority_Encoder #(.select(3), .disabled("Z")) priority_encoder_1 (
    .in0(not_1_out), .in1(not_2_out), .in2(not_3_out), .in3(not_4_out), .in4(not_5_out), .in5(not_6_out),
    .in6(not_7_out), .in7(not_8_out), .out(priority_encoder_1_out), .gs(priority_encoder_1_gs));  // open: en_out, en_in
  \Max3_归并比较  \max3_归并比较_5  (
    .Y(\max3_归并比较_2_max ), .MAX(\max3_归并比较_5_max ), .X(\max3_归并比较_1_max ), .Y_num(\max3_归并比较_2_max_num ),
    .Max_num(\max3_归并比较_5_max_num ), .X_num(\max3_归并比较_1_max_num ));
  \Max3_归并比较  \max3_归并比较_6  (
    .Y(\max3_归并比较_4_max ), .MAX(\max3_归并比较_6_max ), .X(\max3_归并比较_3_max ), .Y_num(\max3_归并比较_4_max_num ),
    .Max_num(\max3_归并比较_6_max_num ), .X_num(\max3_归并比较_3_max_num ));
  and and_1 (and_1_out, V0, V1, V2, V3, V4, V5, V6, V7);
  or or_1 (or_1_out, L1, L2, L3, L4, L5, L6, L7, WriteL1, WriteL2, WriteL3, WriteL4, WriteL5, WriteL6, WriteL7);
  or or_2 (or_2_out, L0, L1, L2, L3, L5, L6, L7, WriteL0, WriteL1, WriteL2, WriteL3, WriteL5, WriteL6, WriteL7);
  Register #(.width(32), .trigger("rising"), .Select("low")) \u_分支指令地址  (
    .D(EX_PC), .en(WriteL0), .Q(Tag0), .clk(Clk));  // open: clr
  Register #(.width(32), .trigger("rising"), .Select("low")) \u_分支指令地址_2  (
    .D(EX_PC), .en(WriteL1), .Q(Tag1), .clk(Clk));  // open: clr
  Register #(.width(32), .trigger("rising"), .Select("low")) \u_分支指令地址_3  (
    .D(EX_PC), .en(WriteL2), .Q(Tag2), .clk(Clk));  // open: clr
  Register #(.width(32), .trigger("rising"), .Select("low")) \u_分支指令地址_4  (
    .D(EX_PC), .en(WriteL3), .Q(Tag3), .clk(Clk));  // open: clr
  Register #(.width(32), .trigger("rising"), .Select("low")) \u_分支指令地址_5  (
    .D(EX_PC), .en(WriteL4), .Q(Tag4), .clk(Clk));  // open: clr
  Register #(.width(32), .trigger("rising"), .Select("low")) \u_分支指令地址_6  (
    .D(EX_PC), .en(WriteL5), .Q(Tag5), .clk(Clk));  // open: clr
  Register #(.width(32), .trigger("rising"), .Select("low")) \u_分支指令地址_7  (
    .D(EX_PC), .en(WriteL6), .Q(Tag6), .clk(Clk));  // open: clr
  Register #(.width(32), .trigger("rising"), .Select("low")) \u_分支指令地址_8  (
    .D(EX_PC), .en(WriteL7), .Q(Tag7), .clk(Clk));  // open: clr
  Decoder #(.select(3), .tristate("false"), .disabled(0), .enable("true")) decoder_1 (
    .out0(decoder_1_out0), .out1(decoder_1_out1), .out2(decoder_1_out2), .out3(decoder_1_out3),
    .out4(decoder_1_out4), .out5(decoder_1_out5), .out6(decoder_1_out6), .out7(decoder_1_out7),
    .sel(priority_encoder_1_out), .en(priority_encoder_1_gs));
  Decoder #(.select(3), .tristate("false"), .disabled(0), .enable("true")) decoder_2 (
    .out0(decoder_2_out0), .out1(decoder_2_out1), .out2(decoder_2_out2), .out3(decoder_2_out3),
    .out4(decoder_2_out4), .out5(decoder_2_out5), .out6(decoder_2_out6), .out7(decoder_2_out7),
    .sel(\max3_归并比较_7_max_num ), .en(and_1_out));
  \Max3_归并比较  \max3_归并比较_7  (
    .Y(\max3_归并比较_6_max ), .X(\max3_归并比较_5_max ), .Y_num(\max3_归并比较_6_max_num ),
    .Max_num(\max3_归并比较_7_max_num ), .X_num(\max3_归并比较_5_max_num ));  // open: MAX
  Multiplexer #(.select(1), .width(2), .disabled("Z"), .enable("false")) multiplexer_1 (
    .in0(2'b00), .in1(2'b01), .out(multiplexer_1_out), .sel(EX_Branched));
  Multiplexer #(.select(1), .width(2), .disabled("Z"), .enable("false")) multiplexer_2 (
    .in0(2'b11), .in1(2'b01), .out(multiplexer_2_out), .sel(EX_Branched));
  Multiplexer #(.select(1), .width(2), .disabled("Z"), .enable("false")) multiplexer_3 (
    .in0(2'b01), .in1(2'b00), .out(multiplexer_3_out), .sel(EX_Branched));
  Multiplexer #(.select(1), .width(2), .disabled("Z"), .enable("false")) multiplexer_4 (
    .in0(2'b01), .in1(2'b11), .out(multiplexer_4_out), .sel(EX_Branched));
  Multiplexer #(.select(1), .width(2), .disabled("Z"), .enable("false")) multiplexer_5 (
    .in0(2'b00), .in1(2'b01), .out(multiplexer_5_out), .sel(EX_Branched));
  Multiplexer #(.select(1), .width(2), .disabled("Z"), .enable("false")) multiplexer_6 (
    .in0(2'b11), .in1(2'b01), .out(multiplexer_6_out), .sel(EX_Branched));
  Multiplexer #(.select(1), .width(2), .disabled("Z"), .enable("false")) multiplexer_7 (
    .in0(2'b01), .in1(2'b00), .out(multiplexer_7_out), .sel(EX_Branched));
  Multiplexer #(.select(1), .width(2), .disabled("Z"), .enable("false")) multiplexer_8 (
    .in0(2'b01), .in1(2'b11), .out(multiplexer_8_out), .sel(EX_Branched));
  Counter #(.width(16), .max('hffff), .ongoal("wrap"), .trigger("rising"), .behavior("old")) \u_置换标记  (
    .count(A0), .Q(C0), .clk(Clk), .clr(L0));  // open: load, D, carry, preset
  Counter #(.width(16), .max('hffff), .ongoal("wrap"), .trigger("rising"), .behavior("old")) \u_置换标记_2  (
    .count(A1), .Q(C1), .clk(Clk), .clr(L1));  // open: load, D, carry, preset
  Counter #(.width(16), .max('hffff), .ongoal("wrap"), .trigger("rising"), .behavior("old")) \u_置换标记_3  (
    .count(A2), .Q(C2), .clk(Clk), .clr(L2));  // open: load, D, carry, preset
  Counter #(.width(16), .max('hffff), .ongoal("wrap"), .trigger("rising"), .behavior("old")) \u_置换标记_4  (
    .count(A3), .Q(C3), .clk(Clk), .clr(L3));  // open: load, D, carry, preset
  Counter #(.width(16), .max('hffff), .ongoal("wrap"), .trigger("rising"), .behavior("old")) \u_置换标记_5  (
    .count(A4), .Q(C4), .clk(Clk), .clr(L4));  // open: load, D, carry, preset
  Counter #(.width(16), .max('hffff), .ongoal("wrap"), .trigger("rising"), .behavior("old")) \u_置换标记_6  (
    .count(A5), .Q(C5), .clk(Clk), .clr(L5));  // open: load, D, carry, preset
  Counter #(.width(16), .max('hffff), .ongoal("wrap"), .trigger("rising"), .behavior("old")) \u_置换标记_7  (
    .count(A6), .Q(C6), .clk(Clk), .clr(L6));  // open: load, D, carry, preset
  Counter #(.width(16), .max('hffff), .ongoal("wrap"), .trigger("rising"), .behavior("old")) \u_置换标记_8  (
    .count(A7), .Q(C7), .clk(Clk), .clr(L7));  // open: load, D, carry, preset
  and and_2 (A0, or_1_out, V0);
  and and_3 (A4, or_2_out, V4);
  Multiplexer #(.select(2), .width(2), .disabled("Z"), .enable("false")) multiplexer_9 (
    .in0(multiplexer_1_out), .in1(multiplexer_2_out), .in2(multiplexer_3_out), .in3(multiplexer_4_out),
    .out(multiplexer_9_out), .sel(Predict0));
  Adder #(.width(2)) adder_1 (.a(Predict0), .b(multiplexer_9_out), .out(adder_1_out));  // open: cin, cout
  Adder #(.width(2)) adder_2 (.a(Predict4), .b(multiplexer_10_out), .out(adder_2_out));  // open: cin, cout
  Multiplexer #(.select(2), .width(2), .disabled("Z"), .enable("false")) multiplexer_10 (
    .in0(multiplexer_5_out), .in1(multiplexer_6_out), .in2(multiplexer_7_out), .in3(multiplexer_8_out),
    .out(multiplexer_10_out), .sel(Predict4));
  or or_3 (or_3_out, decoder_1_out0, decoder_2_out0);
  or or_4 (or_4_out, decoder_1_out1, decoder_2_out1);
  or or_5 (or_5_out, decoder_1_out2, decoder_2_out2);
  or or_6 (or_6_out, decoder_1_out3, decoder_2_out3);
  or or_7 (or_7_out, decoder_1_out4, decoder_2_out4);
  or or_8 (or_8_out, decoder_1_out5, decoder_2_out5);
  or or_9 (or_9_out, decoder_1_out6, decoder_2_out6);
  or or_10 (or_10_out, decoder_1_out7, decoder_2_out7);
  Register #(.width(2), .trigger("rising"), .Select("low")) \u_分支预测历史位  (
    .D(adder_1_out), .en(M0), .Q(Predict0), .clk(Clk));  // open: clr
  Register #(.width(2), .trigger("rising"), .Select("low")) \u_分支预测历史位_2  (
    .D(adder_2_out), .en(M4), .Q(Predict4), .clk(Clk));  // open: clr
  assign JumpAddr = L0 ? \分支目标地址_q  : 32'bz;  // Controlled_Buffer controlled_buffer_9
  Register #(.width(32), .trigger("rising"), .Select("low")) \u_分支目标地址  (
    .D(EX_BranchAddr), .en(WriteL0), .Q(\分支目标地址_q ), .clk(Clk));  // open: clr
  Register #(.width(32), .trigger("rising"), .Select("low")) \u_分支目标地址_2  (
    .D(EX_BranchAddr), .en(WriteL1), .Q(\分支目标地址_2_q ), .clk(Clk));  // open: clr
  assign JumpAddr = L1 ? \分支目标地址_2_q  : 32'bz;  // Controlled_Buffer controlled_buffer_10
  Register #(.width(32), .trigger("rising"), .Select("low")) \u_分支目标地址_3  (
    .D(EX_BranchAddr), .en(WriteL2), .Q(\分支目标地址_3_q ), .clk(Clk));  // open: clr
  assign JumpAddr = L2 ? \分支目标地址_3_q  : 32'bz;  // Controlled_Buffer controlled_buffer_11
  assign JumpAddr = L3 ? \分支目标地址_4_q  : 32'bz;  // Controlled_Buffer controlled_buffer_12
  Register #(.width(32), .trigger("rising"), .Select("low")) \u_分支目标地址_4  (
    .D(EX_BranchAddr), .en(WriteL3), .Q(\分支目标地址_4_q ), .clk(Clk));  // open: clr
  assign JumpAddr = L4 ? \分支目标地址_5_q  : 32'bz;  // Controlled_Buffer controlled_buffer_13
  Register #(.width(32), .trigger("rising"), .Select("low")) \u_分支目标地址_5  (
    .D(EX_BranchAddr), .en(WriteL4), .Q(\分支目标地址_5_q ), .clk(Clk));  // open: clr
  Register #(.width(32), .trigger("rising"), .Select("low")) \u_分支目标地址_6  (
    .D(EX_BranchAddr), .en(WriteL5), .Q(\分支目标地址_6_q ), .clk(Clk));  // open: clr
  assign JumpAddr = L5 ? \分支目标地址_6_q  : 32'bz;  // Controlled_Buffer controlled_buffer_14
  Register #(.width(32), .trigger("rising"), .Select("low")) \u_分支目标地址_7  (
    .D(EX_BranchAddr), .en(WriteL6), .Q(\分支目标地址_7_q ), .clk(Clk));  // open: clr
  assign JumpAddr = L6 ? \分支目标地址_7_q  : 32'bz;  // Controlled_Buffer controlled_buffer_15
  Register #(.width(32), .trigger("rising"), .Select("low")) \u_分支目标地址_8  (
    .D(EX_BranchAddr), .en(WriteL7), .Q(\分支目标地址_8_q ), .clk(Clk));  // open: clr
  assign JumpAddr = L7 ? \分支目标地址_8_q  : 32'bz;  // Controlled_Buffer controlled_buffer_16
  and and_4 (WriteL0, or_3_out, EX_Miss, EX_Branch);
  and and_5 (WriteL1, or_4_out, EX_Miss, EX_Branch);
  and and_6 (WriteL2, or_5_out, EX_Miss, EX_Branch);
  and and_7 (WriteL3, or_6_out, EX_Miss, EX_Branch);
  and and_8 (WriteL4, or_7_out, EX_Miss, EX_Branch);
  and and_9 (WriteL5, or_8_out, EX_Miss, EX_Branch);
  and and_10 (WriteL6, or_9_out, EX_Miss, EX_Branch);
  and and_11 (WriteL7, or_10_out, EX_Miss, EX_Branch);
  or or_11 (or_11_out, L0, L2, L3, L4, L5, L6, L7, WriteL0, WriteL2, WriteL3, WriteL4, WriteL5, WriteL6, WriteL7);
  or or_12 (or_12_out, L0, L1, L2, L3, L4, L6, L7, WriteL0, WriteL1, WriteL2, WriteL3, WriteL4, WriteL6, WriteL7);
  and and_12 (A1, or_11_out, V1);
  and and_13 (A5, or_12_out, V5);
  Multiplexer #(.select(1), .width(2), .disabled("Z"), .enable("false")) multiplexer_11 (
    .in0(2'b00), .in1(2'b01), .out(multiplexer_11_out), .sel(EX_Branched));
  Multiplexer #(.select(1), .width(2), .disabled("Z"), .enable("false")) multiplexer_12 (
    .in0(2'b11), .in1(2'b01), .out(multiplexer_12_out), .sel(EX_Branched));
  Multiplexer #(.select(1), .width(2), .disabled("Z"), .enable("false")) multiplexer_13 (
    .in0(2'b01), .in1(2'b00), .out(multiplexer_13_out), .sel(EX_Branched));
  Multiplexer #(.select(1), .width(2), .disabled("Z"), .enable("false")) multiplexer_14 (
    .in0(2'b01), .in1(2'b11), .out(multiplexer_14_out), .sel(EX_Branched));
  Multiplexer #(.select(1), .width(2), .disabled("Z"), .enable("false")) multiplexer_15 (
    .in0(2'b00), .in1(2'b01), .out(multiplexer_15_out), .sel(EX_Branched));
  Multiplexer #(.select(1), .width(2), .disabled("Z"), .enable("false")) multiplexer_16 (
    .in0(2'b11), .in1(2'b01), .out(multiplexer_16_out), .sel(EX_Branched));
  Multiplexer #(.select(1), .width(2), .disabled("Z"), .enable("false")) multiplexer_17 (
    .in0(2'b01), .in1(2'b00), .out(multiplexer_17_out), .sel(EX_Branched));
  Multiplexer #(.select(1), .width(2), .disabled("Z"), .enable("false")) multiplexer_18 (
    .in0(2'b01), .in1(2'b11), .out(multiplexer_18_out), .sel(EX_Branched));
  Multiplexer #(.select(2), .width(2), .disabled("Z"), .enable("false")) multiplexer_19 (
    .in0(multiplexer_11_out), .in1(multiplexer_12_out), .in2(multiplexer_13_out), .in3(multiplexer_14_out),
    .out(multiplexer_19_out), .sel(Predict1));
  Multiplexer #(.select(2), .width(2), .disabled("Z"), .enable("false")) multiplexer_20 (
    .in0(multiplexer_15_out), .in1(multiplexer_16_out), .in2(multiplexer_17_out), .in3(multiplexer_18_out),
    .out(multiplexer_20_out), .sel(Predict5));
  Comparator #(.width(32), .mode("twosComplement")) comparator_1 (
    .a(PC), .b(Tag0), .eq(comparator_1_eq));  // open: gt, lt
  Comparator #(.width(32), .mode("twosComplement")) comparator_2 (
    .a(PC), .b(Tag1), .eq(comparator_2_eq));  // open: gt, lt
  Comparator #(.width(32), .mode("twosComplement")) comparator_3 (
    .a(PC), .b(Tag2), .eq(comparator_3_eq));  // open: gt, lt
  Comparator #(.width(32), .mode("twosComplement")) comparator_4 (
    .a(PC), .b(Tag3), .eq(comparator_4_eq));  // open: gt, lt
  Comparator #(.width(32), .mode("twosComplement")) comparator_5 (
    .a(PC), .b(Tag4), .eq(comparator_5_eq));  // open: gt, lt
  Comparator #(.width(32), .mode("twosComplement")) comparator_6 (
    .a(PC), .b(Tag5), .eq(comparator_6_eq));  // open: gt, lt
  Comparator #(.width(32), .mode("twosComplement")) comparator_7 (
    .a(PC), .b(Tag6), .eq(comparator_7_eq));  // open: gt, lt
  Comparator #(.width(32), .mode("twosComplement")) comparator_8 (
    .a(PC), .b(Tag7), .eq(comparator_8_eq));  // open: gt, lt
  Adder #(.width(2)) adder_3 (.a(Predict1), .b(multiplexer_19_out), .out(adder_3_out));  // open: cin, cout
  Register #(.width(2), .trigger("rising"), .Select("low")) \u_分支预测历史位_3  (
    .D(adder_3_out), .en(M1), .Q(Predict1), .clk(Clk));  // open: clr
  Adder #(.width(2)) adder_4 (.a(Predict5), .b(multiplexer_20_out), .out(adder_4_out));  // open: cin, cout
  or or_13 (or_13_out, L0, L1, L3, L4, L5, L6, L7, WriteL0, WriteL1, WriteL3, WriteL4, WriteL5, WriteL6, WriteL7);
  or or_14 (or_14_out, L0, L1, L2, L3, L4, L5, L7, WriteL0, WriteL1, WriteL2, WriteL3, WriteL4, WriteL5, WriteL7);
  Register #(.width(2), .trigger("rising"), .Select("low")) \u_分支预测历史位_4  (
    .D(adder_4_out), .en(M5), .Q(Predict5), .clk(Clk));  // open: clr
  and and_14 (L0, comparator_1_eq, V0);
  and and_15 (L1, comparator_2_eq, V1);
  and and_16 (L2, comparator_3_eq, V2);
  and and_17 (L3, comparator_4_eq, V3);
  and and_18 (L4, comparator_5_eq, V4);
  and and_19 (L5, comparator_6_eq, V5);
  and and_20 (L6, comparator_7_eq, V6);
  and and_21 (L7, comparator_8_eq, V7);
  and and_22 (A2, or_13_out, V2);
  and and_23 (A6, or_14_out, V6);
  or or_15 (IF_Hit, L0, L1, L2, L3, L4, L5, L6, L7);
  Multiplexer #(.select(1), .width(2), .disabled("Z"), .enable("false")) multiplexer_21 (
    .in0(2'b00), .in1(2'b01), .out(multiplexer_21_out), .sel(EX_Branched));
  Multiplexer #(.select(1), .width(2), .disabled("Z"), .enable("false")) multiplexer_22 (
    .in0(2'b11), .in1(2'b01), .out(multiplexer_22_out), .sel(EX_Branched));
  Multiplexer #(.select(1), .width(2), .disabled("Z"), .enable("false")) multiplexer_23 (
    .in0(2'b01), .in1(2'b00), .out(multiplexer_23_out), .sel(EX_Branched));
  Multiplexer #(.select(1), .width(2), .disabled("Z"), .enable("false")) multiplexer_24 (
    .in0(2'b01), .in1(2'b11), .out(multiplexer_24_out), .sel(EX_Branched));
  Multiplexer #(.select(1), .width(2), .disabled("Z"), .enable("false")) multiplexer_25 (
    .in0(2'b00), .in1(2'b01), .out(multiplexer_25_out), .sel(EX_Branched));
  Multiplexer #(.select(1), .width(2), .disabled("Z"), .enable("false")) multiplexer_26 (
    .in0(2'b11), .in1(2'b01), .out(multiplexer_26_out), .sel(EX_Branched));
  Multiplexer #(.select(1), .width(2), .disabled("Z"), .enable("false")) multiplexer_27 (
    .in0(2'b01), .in1(2'b00), .out(multiplexer_27_out), .sel(EX_Branched));
  Multiplexer #(.select(1), .width(2), .disabled("Z"), .enable("false")) multiplexer_28 (
    .in0(2'b01), .in1(2'b11), .out(multiplexer_28_out), .sel(EX_Branched));
  not not_9 (IF_Miss, IF_Hit);
  Adder #(.width(2)) adder_5 (.a(Predict2), .b(multiplexer_29_out), .out(adder_5_out));  // open: cin, cout
  Multiplexer #(.select(2), .width(2), .disabled("Z"), .enable("false")) multiplexer_29 (
    .in0(multiplexer_21_out), .in1(multiplexer_22_out), .in2(multiplexer_23_out), .in3(multiplexer_24_out),
    .out(multiplexer_29_out), .sel(Predict2));
  Multiplexer #(.select(2), .width(2), .disabled("Z"), .enable("false")) multiplexer_30 (
    .in0(multiplexer_25_out), .in1(multiplexer_26_out), .in2(multiplexer_27_out), .in3(multiplexer_28_out),
    .out(multiplexer_30_out), .sel(Predict6));
  or or_16 (or_16_out, L0, L1, L2, L4, L5, L6, L7, WriteL0, WriteL1, WriteL2, WriteL4, WriteL5, WriteL6, WriteL7);
  or or_17 (or_17_out, L0, L1, L2, L3, L4, L5, L6, WriteL0, WriteL1, WriteL2, WriteL3, WriteL4, WriteL5, WriteL6);
  Register #(.width(2), .trigger("rising"), .Select("low")) \u_分支预测历史位_5  (
    .D(adder_5_out), .en(M2), .Q(Predict2), .clk(Clk));  // open: clr
  Register #(.width(2), .trigger("rising"), .Select("low")) \u_分支预测历史位_6  (
    .D(adder_6_out), .en(M6), .Q(Predict6), .clk(Clk));  // open: clr
  Adder #(.width(2)) adder_6 (.a(Predict6), .b(multiplexer_30_out), .out(adder_6_out));  // open: cin, cout
  Comparator #(.width(32), .mode("twosComplement")) comparator_9 (
    .a(EX_PC), .b(Tag0), .eq(comparator_9_eq));  // open: gt, lt
  Comparator #(.width(32), .mode("twosComplement")) comparator_10 (
    .a(EX_PC), .b(Tag1), .eq(comparator_10_eq));  // open: gt, lt
  Comparator #(.width(32), .mode("twosComplement")) comparator_11 (
    .a(EX_PC), .b(Tag2), .eq(comparator_11_eq));  // open: gt, lt
  Comparator #(.width(32), .mode("twosComplement")) comparator_12 (
    .a(EX_PC), .b(Tag3), .eq(comparator_12_eq));  // open: gt, lt
  Comparator #(.width(32), .mode("twosComplement")) comparator_13 (
    .a(EX_PC), .b(Tag4), .eq(comparator_13_eq));  // open: gt, lt
  Comparator #(.width(32), .mode("twosComplement")) comparator_14 (
    .a(EX_PC), .b(Tag5), .eq(comparator_14_eq));  // open: gt, lt
  Comparator #(.width(32), .mode("twosComplement")) comparator_15 (
    .a(EX_PC), .b(Tag6), .eq(comparator_15_eq));  // open: gt, lt
  Comparator #(.width(32), .mode("twosComplement")) comparator_16 (
    .a(EX_PC), .b(Tag7), .eq(comparator_16_eq));  // open: gt, lt
  and and_24 (A3, or_16_out, V3);
  and and_25 (A7, or_17_out, V7);
  and and_26 (M0, comparator_9_eq, V0);
  and and_27 (M1, comparator_10_eq, V1);
  and and_28 (M2, comparator_11_eq, V2);
  and and_29 (M3, comparator_12_eq, V3);
  and and_30 (M4, comparator_13_eq, V4);
  and and_31 (M5, comparator_14_eq, V5);
  and and_32 (M6, comparator_15_eq, V6);
  and and_33 (M7, comparator_16_eq, V7);
  Multiplexer #(.select(1), .width(2), .disabled("Z"), .enable("false")) multiplexer_31 (
    .in0(2'b00), .in1(2'b01), .out(multiplexer_31_out), .sel(EX_Branched));
  Multiplexer #(.select(1), .width(2), .disabled("Z"), .enable("false")) multiplexer_32 (
    .in0(2'b11), .in1(2'b01), .out(multiplexer_32_out), .sel(EX_Branched));
  Multiplexer #(.select(1), .width(2), .disabled("Z"), .enable("false")) multiplexer_33 (
    .in0(2'b01), .in1(2'b00), .out(multiplexer_33_out), .sel(EX_Branched));
  Multiplexer #(.select(1), .width(2), .disabled("Z"), .enable("false")) multiplexer_34 (
    .in0(2'b01), .in1(2'b11), .out(multiplexer_34_out), .sel(EX_Branched));
  Multiplexer #(.select(1), .width(2), .disabled("Z"), .enable("false")) multiplexer_35 (
    .in0(2'b00), .in1(2'b01), .out(multiplexer_35_out), .sel(EX_Branched));
  Multiplexer #(.select(1), .width(2), .disabled("Z"), .enable("false")) multiplexer_36 (
    .in0(2'b11), .in1(2'b01), .out(multiplexer_36_out), .sel(EX_Branched));
  Multiplexer #(.select(1), .width(2), .disabled("Z"), .enable("false")) multiplexer_37 (
    .in0(2'b01), .in1(2'b00), .out(multiplexer_37_out), .sel(EX_Branched));
  Multiplexer #(.select(1), .width(2), .disabled("Z"), .enable("false")) multiplexer_38 (
    .in0(2'b01), .in1(2'b11), .out(multiplexer_38_out), .sel(EX_Branched));
  Multiplexer #(.select(2), .width(2), .disabled("Z"), .enable("false")) multiplexer_39 (
    .in0(multiplexer_31_out), .in1(multiplexer_32_out), .in2(multiplexer_33_out), .in3(multiplexer_34_out),
    .out(multiplexer_39_out), .sel(Predict3));
  Multiplexer #(.select(2), .width(2), .disabled("Z"), .enable("false")) multiplexer_40 (
    .in0(multiplexer_35_out), .in1(multiplexer_36_out), .in2(multiplexer_37_out), .in3(multiplexer_38_out),
    .out(multiplexer_40_out), .sel(Predict7));
  or or_18 (EX_Hit, M0, M1, M2, M3, M4, M5, M6, M7);
  Adder #(.width(2)) adder_7 (.a(Predict3), .b(multiplexer_39_out), .out(adder_7_out));  // open: cin, cout
  Adder #(.width(2)) adder_8 (.a(Predict7), .b(multiplexer_40_out), .out(adder_8_out));  // open: cin, cout
  not not_10 (EX_Miss, EX_Hit);
  Register #(.width(2), .trigger("rising"), .Select("low")) \u_分支预测历史位_7  (
    .D(adder_7_out), .en(M3), .Q(Predict3), .clk(Clk));  // open: clr
  Register #(.width(2), .trigger("rising"), .Select("low")) \u_分支预测历史位_8  (
    .D(adder_8_out), .en(M7), .Q(Predict7), .clk(Clk));  // open: clr

  // Other names for the same wires on the sheet: Tag[31:0] = EX_PC

  // Notes on the sheet:
  //   Cache槽
  //   读缺失逻辑/块载入逻辑
  //   查找逻辑
endmodule
