// Logisim project team_work.circ as structural Verilog: 20 circuits, main circuit ◇单周期MIPS
module \单周期MIPS  (
  input  IR1,
  input  IR2,
  input  IR3,
  output RegWrite,
  output MemWrite,
  output [31:0] PC,
  output [31:0] IR,
  output [31:0] RDin,
  output [31:0] MDin,
  output [31:0] LedData
);

  wire \_0_5倍速 , \_2倍速 , AluSrcB, and_1_out, and_2_out, and_3_out, and_4_out, Beq, Bne, CLK, clock_2_out,
       comparator_1_eq, comparator_1_lt, comparator_2_eq, controlled_buffer_1_out, d_ff_1_q, Go, halt, IR1_t,
       IR2_t, IR3_t, IRA, IRB, IRC, JAL, JMP, JR, MemToReg, mips_alu_1_equal, nand_1_out, not_1_out,
       not_2_out, or_4_out, RegDst, SignedExt, Syscall, W1, W2, W3, \暂停控制电路_1_out_3 , \暂停键 ;
  wire [3:0] AluOP;
  wire [4:0] counter_3_q, multiplexer_4_out, multiplexer_5_out, multiplexer_6_out, multiplexer_7_out;
  wire [12:0] CNT_num;
  wire [13:0] counter_2_q;
  wire [15:0] \总周期数 ;
  wire [31:0] adder_1_out, adder_2_out, bit_extender_1_out, bit_extender_2_out, leddataleft_1_out_6,
       leddataleft_1_out_7, leddataleft_1_out_8, leddataleft_1_out_9, leddataleft_1_out_10,
       leddataleft_1_out_11, leddataleft_1_out_12, leddataleft_1_out_13, leddataleft_1_out_14,
       leddataleft_1_out_15, leddataleft_1_out_16, leddataleft_1_out_17, leddataleft_1_out_18,
       leddataleft_1_out_19, leddataleft_1_out_20, leddataleft_1_out_21, leddataleft_1_out_22,
       leddataleft_1_out_23, leddataleft_1_out_24, leddataleft_1_out_25, leddataleft_1_out_26,
       leddataleft_1_out_27, leddataleft_1_out_28, leddataleft_1_out_29, leddataleft_1_out_30,
       leddataleft_1_out_31, leddataleft_1_out_32, leddataleft_1_out_33, leddataleft_1_out_34,
       leddataleft_1_out_35, leddataleft_1_out_36, leddataleft_1_out_37, leddataleft_2_out_6,
       leddataleft_2_out_7, leddataleft_2_out_8, leddataleft_2_out_9, leddataleft_2_out_10,
       leddataleft_2_out_11, leddataleft_2_out_12, leddataleft_2_out_13, leddataleft_2_out_14,
       leddataleft_2_out_15, leddataleft_2_out_16, leddataleft_2_out_17, leddataleft_2_out_18,
       leddataleft_2_out_19, leddataleft_2_out_20, leddataleft_2_out_21, leddataleft_2_out_22,
       leddataleft_2_out_23, leddataleft_2_out_24, leddataleft_2_out_25, leddataleft_2_out_26,
       leddataleft_2_out_27, leddataleft_2_out_28, leddataleft_2_out_29, leddataleft_2_out_30,
       leddataleft_2_out_31, leddataleft_2_out_32, leddataleft_2_out_33, leddataleft_2_out_34,
       leddataleft_2_out_35, leddataleft_2_out_36, leddataleft_2_out_37, leddataright_1_out_6,
       leddataright_1_out_7, leddataright_1_out_8, leddataright_1_out_9, leddataright_1_out_10,
       leddataright_1_out_11, leddataright_1_out_12, leddataright_1_out_13, leddataright_1_out_14,
       leddataright_1_out_15, leddataright_1_out_16, leddataright_1_out_17, leddataright_1_out_18,
       leddataright_1_out_19, leddataright_1_out_20, leddataright_1_out_21, leddataright_1_out_22,
       leddataright_1_out_23, leddataright_1_out_24, leddataright_1_out_25, leddataright_1_out_26,
       leddataright_1_out_27, leddataright_1_out_28, leddataright_1_out_29, leddataright_1_out_30,
       leddataright_1_out_31, leddataright_1_out_32, leddataright_1_out_33, leddataright_1_out_34,
       leddataright_1_out_35, leddataright_1_out_36, leddataright_1_out_37, leddataright_2_out_6,
       leddataright_2_out_7, leddataright_2_out_8, leddataright_2_out_9, leddataright_2_out_10,
       leddataright_2_out_11, leddataright_2_out_12, leddataright_2_out_13, leddataright_2_out_14,
       leddataright_2_out_15, leddataright_2_out_16, leddataright_2_out_17, leddataright_2_out_18,
       leddataright_2_out_19, leddataright_2_out_20, leddataright_2_out_21, leddataright_2_out_22,
       leddataright_2_out_23, leddataright_2_out_24, leddataright_2_out_25, leddataright_2_out_26,
       leddataright_2_out_27, leddataright_2_out_28, leddataright_2_out_29, leddataright_2_out_30,
       leddataright_2_out_31, leddataright_2_out_32, leddataright_2_out_33, leddataright_2_out_34,
       leddataright_2_out_35, leddataright_2_out_36, leddataright_2_out_37, \led点阵行信号输入_1_out_129 ,
       \led点阵行信号输入_1_out_130 , \led点阵行信号输入_1_out_131 , \led点阵行信号输入_1_out_132 , \led点阵行信号输入_1_out_133 ,
       \led点阵行信号输入_1_out_134 , \led点阵行信号输入_1_out_135 , \led点阵行信号输入_1_out_136 , \led点阵行信号输入_1_out_137 ,
       \led点阵行信号输入_1_out_138 , \led点阵行信号输入_1_out_139 , \led点阵行信号输入_1_out_140 , \led点阵行信号输入_1_out_141 ,
       \led点阵行信号输入_1_out_142 , \led点阵行信号输入_1_out_143 , \led点阵行信号输入_1_out_144 , \led点阵行信号输入_1_out_145 ,
       \led点阵行信号输入_1_out_146 , \led点阵行信号输入_1_out_147 , \led点阵行信号输入_1_out_148 , \led点阵行信号输入_1_out_149 ,
       \led点阵行信号输入_1_out_150 , \led点阵行信号输入_1_out_151 , \led点阵行信号输入_1_out_152 , \led点阵行信号输入_1_out_153 ,
       \led点阵行信号输入_1_out_154 , \led点阵行信号输入_1_out_155 , \led点阵行信号输入_1_out_156 , \led点阵行信号输入_1_out_157 ,
       \led点阵行信号输入_1_out_158 , \led点阵行信号输入_1_out_159 , \led点阵行信号输入_1_out_160 , \led点阵行信号输入_1_out_161 ,
       \led点阵行信号输入_1_out_162 , \led点阵行信号输入_1_out_163 , \led点阵行信号输入_1_out_164 , \led点阵行信号输入_1_out_165 ,
       \led点阵行信号输入_1_out_166 , \led点阵行信号输入_1_out_167 , \led点阵行信号输入_1_out_168 , \led点阵行信号输入_1_out_169 ,
       \led点阵行信号输入_1_out_170 , \led点阵行信号输入_1_out_171 , \led点阵行信号输入_1_out_172 , \led点阵行信号输入_1_out_173 ,
       \led点阵行信号输入_1_out_174 , \led点阵行信号输入_1_out_175 , \led点阵行信号输入_1_out_176 , \led点阵行信号输入_1_out_177 ,
       \led点阵行信号输入_1_out_178 , \led点阵行信号输入_1_out_179 , \led点阵行信号输入_1_out_180 , \led点阵行信号输入_1_out_181 ,
       \led点阵行信号输入_1_out_182 , \led点阵行信号输入_1_out_183 , \led点阵行信号输入_1_out_184 , \led点阵行信号输入_1_out_185 ,
       \led点阵行信号输入_1_out_186 , \led点阵行信号输入_1_out_187 , \led点阵行信号输入_1_out_188 , \led点阵行信号输入_1_out_189 ,
       \led点阵行信号输入_1_out_190 , \led点阵行信号输入_1_out_191 , \led点阵行信号输入_1_out_192 , \led点阵行信号输入_1_out_193 ,
       \led点阵行信号输入_1_out_194 , \led点阵行信号输入_1_out_195 , \led点阵行信号输入_1_out_196 , \led点阵行信号输入_1_out_197 ,
       \led点阵行信号输入_1_out_198 , \led点阵行信号输入_1_out_199 , \led点阵行信号输入_1_out_200 , \led点阵行信号输入_1_out_201 ,
       \led点阵行信号输入_1_out_202 , \led点阵行信号输入_1_out_203 , \led点阵行信号输入_1_out_204 , \led点阵行信号输入_1_out_205 ,
       \led点阵行信号输入_1_out_206 , \led点阵行信号输入_1_out_207 , \led点阵行信号输入_1_out_208 , \led点阵行信号输入_1_out_209 ,
       \led点阵行信号输入_1_out_210 , \led点阵行信号输入_1_out_211 , \led点阵行信号输入_1_out_212 , \led点阵行信号输入_1_out_213 ,
       \led点阵行信号输入_1_out_214 , \led点阵行信号输入_1_out_215 , \led点阵行信号输入_1_out_216 , \led点阵行信号输入_1_out_217 ,
       \led点阵行信号输入_1_out_218 , \led点阵行信号输入_1_out_219 , \led点阵行信号输入_1_out_220 , \led点阵行信号输入_1_out_221 ,
       \led点阵行信号输入_1_out_222 , \led点阵行信号输入_1_out_223 , \led点阵行信号输入_1_out_224 , \led点阵行信号输入_1_out_225 ,
       \led点阵行信号输入_1_out_226 , \led点阵行信号输入_1_out_227 , \led点阵行信号输入_1_out_228 , \led点阵行信号输入_1_out_229 ,
       \led点阵行信号输入_1_out_230 , \led点阵行信号输入_1_out_231 , \led点阵行信号输入_1_out_232 , \led点阵行信号输入_1_out_233 ,
       \led点阵行信号输入_1_out_234 , \led点阵行信号输入_1_out_235 , \led点阵行信号输入_1_out_236 , \led点阵行信号输入_1_out_237 ,
       \led点阵行信号输入_1_out_238 , \led点阵行信号输入_1_out_239 , \led点阵行信号输入_1_out_240 , \led点阵行信号输入_1_out_241 ,
       \led点阵行信号输入_1_out_242 , \led点阵行信号输入_1_out_243 , \led点阵行信号输入_1_out_244 , \led点阵行信号输入_1_out_245 ,
       \led点阵行信号输入_1_out_246 , \led点阵行信号输入_1_out_247 , \led点阵行信号输入_1_out_248 , \led点阵行信号输入_1_out_249 ,
       \led点阵行信号输入_1_out_250 , \led点阵行信号输入_1_out_251 , \led点阵行信号输入_1_out_252 , \led点阵行信号输入_1_out_253 ,
       \led点阵行信号输入_1_out_254 , \led点阵行信号输入_1_out_255 , \led点阵行信号输入_1_out_256 , mips_alu_1_result,
       multiplexer_1_out, multiplexer_2_out, multiplexer_3_out, multiplexer_9_out, multiplexer_10_out,
       multiplexer_11_out, ram_1_data, rom_2_data, rom_3_data, rom_4_data, rom_5_data, shifter_1_out, V0,
       \进度条_1_out_2 , \进度条_1_out_3 ;

  Clock #(.highDuration(1), .lowDuration(1)) clock_1 ();  // open: out
  Button _1 (.out(IRA));
  Button _2 (.out(IRB));
  Button _3 (.out(IRC));
  Multiplexer #(.select(1), .width(32), .disabled("Z"), .enable("false")) multiplexer_1 (
    .in0({adder_1_out[31:28], IR[25:0], 2'b00}), .in1(V0), .out(multiplexer_1_out), .sel(JR));
  Button \u_继续运行  (.out(Go));
  LED #(.active("true")) led_1 (.in(W1));
  LED #(.active("true")) led_2 (.in(W2));
  LED #(.active("true")) led_3 (.in(W3));
  Multiplexer #(.select(1), .width(32), .disabled("Z"), .enable("false")) multiplexer_2 (
    .in0(multiplexer_3_out), .in1(multiplexer_1_out), .out(multiplexer_2_out), .sel(JMP));
  Register #(.width(32), .trigger("rising"), .Select("low")) u_PC (
    .D(multiplexer_2_out), .en(not_1_out), .Q(PC), .clk(CLK));  // open: clr
  not not_1 (not_1_out, halt);
  Multiplexer #(.select(1), .width(32), .disabled("Z"), .enable("false")) multiplexer_3 (
    .in0(adder_1_out), .in1(adder_2_out), .out(multiplexer_3_out), .sel(or_4_out));
  D_Flip_Flop #(.trigger("high"), .Pre_Clr_Positions("LEGACY"), .NegatePresetClear("false"), .enable("true"), .NewFFLayout("false")) d_ff_1 (.Q(d_ff_1_q));  // open: clk, D, Qn, preset, en, reset
  // Probe on 13'hc
  Hex_Digit_Display hex_digit_display_1 (.value(LedData[31:28]));  // open: dp
  Adder #(.width(32)) adder_1 (.a(PC), .b(32'h4), .out(adder_1_out));  // open: cin, cout
  Comparator #(.width(13), .mode("twosComplement")) comparator_1 (
    .a(CNT_num), .b(13'hc), .eq(comparator_1_eq), .lt(comparator_1_lt));  // open: gt
  Clock #(.highDuration(1), .lowDuration(1)) clock_2 (.out(clock_2_out));
  Hex_Digit_Display hex_digit_display_2 (.value(LedData[27:24]));  // open: dp
  Hex_Digit_Display hex_digit_display_3 (.value(LedData[23:20]));  // open: dp
  Counter #(.width(13), .max('h1fff), .ongoal("stay"), .trigger("rising"), .behavior("old")) counter_1 (
    .count(comparator_1_lt), .Q(CNT_num), .clk(clock_2_out));  // open: load, D, carry, clr, preset
  Hex_Digit_Display hex_digit_display_4 (.value(LedData[19:16]));  // open: dp
  Hex_Digit_Display hex_digit_display_5 (.value(LedData[15:12]));  // open: dp
  // Mips_Probe mips_probe_1: pin names not known; wires that end beside it: IR, IR[20:16]
  ROM #(.addrWidth(10), .dataWidth(32), .Select("high")) rom_1 (.addr(PC[11:2]), .data(IR));
  nand nand_1 (nand_1_out, d_ff_1_q, comparator_1_eq);
  Hex_Digit_Display hex_digit_display_6 (.value(LedData[11:8]));  // open: dp
  Hex_Digit_Display hex_digit_display_7 (.value(LedData[7:4]));  // open: dp
  // Probe on \总周期数 
  Multiplexer #(.select(1), .width(5), .disabled("Z"), .enable("false")) multiplexer_4 (
    .in0(IR[20:16]), .in1(IR[15:11]), .out(multiplexer_4_out), .sel(RegDst));
  assign controlled_buffer_1_out = nand_1_out ? clock_2_out : 1'bz;  // Controlled_Buffer controlled_buffer_1
  Pull_Resistor #(.pull(1)) pull_resistor_1 (.node(controlled_buffer_1_out));
  Hex_Digit_Display hex_digit_display_8 (.value(LedData[3:0]));  // open: dp
  Multiplexer #(.select(1), .width(5), .disabled("Z"), .enable("false")) multiplexer_5 (
    .in0(IR[25:21]), .in1(5'b00010), .out(multiplexer_5_out), .sel(Syscall));
  Multiplexer #(.select(1), .width(5), .disabled("Z"), .enable("false")) multiplexer_6 (
    .in0(IR[20:16]), .in1(5'b00100), .out(multiplexer_6_out), .sel(Syscall));
  Multiplexer #(.select(1), .width(5), .disabled("Z"), .enable("false")) multiplexer_7 (
    .in0(multiplexer_4_out), .in1({5{1'b1}}), .out(multiplexer_7_out), .sel(JAL));
  Multiplexer #(.select(1), .width(32), .disabled("Z"), .enable("false")) multiplexer_8 (
    .in0(multiplexer_11_out), .in1(adder_1_out), .out(RDin), .sel(JAL));
  assign bit_extender_1_out = {{16{1'b0}}, IR[15:0]};  // Bit_Extender bit_extender_1
  assign bit_extender_2_out = {{16{IR[15]}}, IR[15:0]};  // Bit_Extender bit_extender_2
  \暂停控制电路  \u_暂停控制电路_1  (.in_1(controlled_buffer_1_out), .in_2(\暂停键 ), .out_3(\暂停控制电路_1_out_3 ));
  Multiplexer #(.select(1), .width(32), .disabled("Z"), .enable("false")) multiplexer_9 (
    .in0(bit_extender_1_out), .in1(bit_extender_2_out), .out(multiplexer_9_out), .sel(SignedExt));
  or or_1 (IR1_t, IR1, IRA);
  MIPS_Regifile mips_regifile_1 (
    .Din(RDin), .Clk(CLK), .R1(V0), .R2(MDin), .WE(RegWrite), .W_num(multiplexer_7_out),
    .R1_num(multiplexer_5_out), .R2_num(multiplexer_6_out));
  \倍速控制  \u_倍速控制_1  (.in_1(\_0_5倍速 ), .in_2(\_2倍速 ), .in_3(\暂停控制电路_1_out_3 ), .out_4(CLK));
  or or_2 (IR2_t, IR2, IRB);
  Multiplexer #(.select(1), .width(32), .disabled("Z"), .enable("false")) multiplexer_10 (
    .in0(MDin), .in1(multiplexer_9_out), .out(multiplexer_10_out), .sel(AluSrcB));
  Shifter #(.width(32), .shift("ll")) shifter_1 (.in(bit_extender_2_out), .\dist (5'b00010), .out(shifter_1_out));
  Adder #(.width(32)) adder_2 (.a(shifter_1_out), .b(adder_1_out), .out(adder_2_out));  // open: cin, cout
  and and_1 (and_1_out, Beq, mips_alu_1_equal);
  and and_2 (and_2_out, Bne, ~mips_alu_1_equal);  // AND_Gate
  MIPS_ALU mips_alu_1 (
    .X(V0), .Y(multiplexer_10_out), .AluOP(AluOP), .Equal(mips_alu_1_equal), .Result(mips_alu_1_result),
    .shamt(IR[10:6]));  // open: Result_2
  or or_3 (IR3_t, IR3, IRC);
  or or_4 (or_4_out, and_1_out, and_2_out);
  Counter #(.width(14), .max('h3fff), .ongoal("wrap"), .trigger("rising"), .behavior("new")) counter_2 (
    .D(mips_alu_1_result[13:0]), .Q(counter_2_q), .clk(CLK));  // open: load, count, carry, clr, preset, down
  RAM #(.addrWidth(10), .dataWidth(32), .bus("separate"), .Select("high")) ram_1 (
    .addr(mips_alu_1_result[11:2]), .din(MDin), .data(ram_1_data), .str(MemWrite), .clk(CLK));  // open: sel, ld, clr
  Multiplexer #(.select(1), .width(32), .disabled("Z"), .enable("false")) multiplexer_11 (
    .in0(mips_alu_1_result), .in1(ram_1_data), .out(multiplexer_11_out), .sel(MemToReg));
  ROM #(.addrWidth(14), .dataWidth(32), .Select("high")) rom_2 (.addr(counter_2_q), .data(rom_2_data));
  Counter #(.width(5), .max('h1f), .ongoal("wrap"), .trigger("rising"), .behavior("new")) counter_3 (
    .D({5{1'b0}}), .Q(counter_3_q), .clk(CLK));  // open: load, count, carry, clr, preset, down
  ROM #(.addrWidth(14), .dataWidth(32), .Select("high")) rom_3 (.addr(counter_2_q), .data(rom_3_data));
  \单周期硬布线控制器  \u_单周期硬布线控制器_1  (
    .Func(IR[5:0]), .OP(IR[31:26]), .ALU_OP(AluOP), .MemToReg(MemToReg), .MemWrite(MemWrite),
    .ALU_SRC(AluSrcB), .RegWrite(RegWrite), .SysCALL(Syscall), .SignedExt(SignedExt), .RegDst(RegDst),
    .JR(JR), .JMP(JMP), .Beq(Beq), .JAL(JAL), .Bne(Bne));  // open: ERET
  Comparator #(.width(32), .mode("twosComplement")) comparator_2 (
    .a(V0), .b(32'h22), .eq(comparator_2_eq));  // open: gt, lt
  LedDataLeft leddataleft_1 (
    .CLK(CLK), .DATA(rom_2_data), .en(1'b1), .out_6(leddataleft_1_out_6), .out_7(leddataleft_1_out_7),
    .out_8(leddataleft_1_out_8), .out_9(leddataleft_1_out_9), .out_10(leddataleft_1_out_10),
    .out_11(leddataleft_1_out_11), .out_12(leddataleft_1_out_12), .out_13(leddataleft_1_out_13),
    .out_14(leddataleft_1_out_14), .out_15(leddataleft_1_out_15), .out_16(leddataleft_1_out_16),
    .out_17(leddataleft_1_out_17), .out_18(leddataleft_1_out_18), .out_19(leddataleft_1_out_19),
    .out_20(leddataleft_1_out_20), .out_21(leddataleft_1_out_21), .out_22(leddataleft_1_out_22),
    .out_23(leddataleft_1_out_23), .out_24(leddataleft_1_out_24), .out_25(leddataleft_1_out_25),
    .out_26(leddataleft_1_out_26), .out_27(leddataleft_1_out_27), .out_28(leddataleft_1_out_28),
    .out_29(leddataleft_1_out_29), .out_30(leddataleft_1_out_30), .out_31(leddataleft_1_out_31),
    .out_32(leddataleft_1_out_32), .out_33(leddataleft_1_out_33), .out_34(leddataleft_1_out_34),
    .out_35(leddataleft_1_out_35), .out_36(leddataleft_1_out_36), .out_37(leddataleft_1_out_37),
    .in_5(counter_3_q));  // open: CLR
  LedDataLeft leddataleft_2 (
    .CLK(CLK), .DATA(rom_3_data), .en(1'b1), .out_6(leddataleft_2_out_6), .out_7(leddataleft_2_out_7),
    .out_8(leddataleft_2_out_8), .out_9(leddataleft_2_out_9), .out_10(leddataleft_2_out_10),
    .out_11(leddataleft_2_out_11), .out_12(leddataleft_2_out_12), .out_13(leddataleft_2_out_13),
    .out_14(leddataleft_2_out_14), .out_15(leddataleft_2_out_15), .out_16(leddataleft_2_out_16),
    .out_17(leddataleft_2_out_17), .out_18(leddataleft_2_out_18), .out_19(leddataleft_2_out_19),
    .out_20(leddataleft_2_out_20), .out_21(leddataleft_2_out_21), .out_22(leddataleft_2_out_22),
    .out_23(leddataleft_2_out_23), .out_24(leddataleft_2_out_24), .out_25(leddataleft_2_out_25),
    .out_26(leddataleft_2_out_26), .out_27(leddataleft_2_out_27), .out_28(leddataleft_2_out_28),
    .out_29(leddataleft_2_out_29), .out_30(leddataleft_2_out_30), .out_31(leddataleft_2_out_31),
    .out_32(leddataleft_2_out_32), .out_33(leddataleft_2_out_33), .out_34(leddataleft_2_out_34),
    .out_35(leddataleft_2_out_35), .out_36(leddataleft_2_out_36), .out_37(leddataleft_2_out_37),
    .in_5(counter_3_q));  // open: CLR
  and and_3 (and_3_out, Syscall, comparator_2_eq);
  and and_4 (and_4_out, ~comparator_2_eq, Syscall);  // AND_Gate
  LedDataRight leddataright_1 (
    .CLK(CLK), .DATA(rom_4_data), .en(1'b1), .out_6(leddataright_1_out_6), .out_7(leddataright_1_out_7),
    .out_8(leddataright_1_out_8), .out_9(leddataright_1_out_9), .out_10(leddataright_1_out_10),
    .out_11(leddataright_1_out_11), .out_12(leddataright_1_out_12), .out_13(leddataright_1_out_13),
    .out_14(leddataright_1_out_14), .out_15(leddataright_1_out_15), .out_16(leddataright_1_out_16),
    .out_17(leddataright_1_out_17), .out_18(leddataright_1_out_18), .out_19(leddataright_1_out_19),
    .out_20(leddataright_1_out_20), .out_21(leddataright_1_out_21), .out_22(leddataright_1_out_22),
    .out_23(leddataright_1_out_23), .out_24(leddataright_1_out_24), .out_25(leddataright_1_out_25),
    .out_26(leddataright_1_out_26), .out_27(leddataright_1_out_27), .out_28(leddataright_1_out_28),
    .out_29(leddataright_1_out_29), .out_30(leddataright_1_out_30), .out_31(leddataright_1_out_31),
    .out_32(leddataright_1_out_32), .out_33(leddataright_1_out_33), .out_34(leddataright_1_out_34),
    .out_35(leddataright_1_out_35), .out_36(leddataright_1_out_36), .out_37(leddataright_1_out_37),
    .in_5(counter_3_q));  // open: CLR
  \LED点阵行信号输入  \led点阵行信号输入_1  (
    .in_1(leddataleft_1_out_6), .in_2(leddataleft_1_out_7), .in_3(leddataleft_1_out_8),
    .in_4(leddataleft_1_out_9), .in_5(leddataleft_1_out_10), .in_6(leddataleft_1_out_11),
    .in_7(leddataleft_1_out_12), .in_8(leddataleft_1_out_13), .in_9(leddataleft_1_out_14),
    .in_10(leddataleft_1_out_15), .in_11(leddataleft_1_out_16), .in_12(leddataleft_1_out_17),
    .in_13(leddataleft_1_out_18), .in_14(leddataleft_1_out_19), .in_15(leddataleft_1_out_20),
    .in_16(leddataleft_1_out_21), .in_17(leddataleft_1_out_22), .in_18(leddataleft_1_out_23),
    .in_19(leddataleft_1_out_24), .in_20(leddataleft_1_out_25), .in_21(leddataleft_1_out_26),
    .in_22(leddataleft_1_out_27), .in_23(leddataleft_1_out_28), .in_24(leddataleft_1_out_29),
    .in_25(leddataleft_1_out_30), .in_26(leddataleft_1_out_31), .in_27(leddataleft_1_out_32),
    .in_28(leddataleft_1_out_33), .in_29(leddataleft_1_out_34), .in_30(leddataleft_1_out_35),
    .in_31(leddataleft_1_out_36), .in_32(leddataleft_1_out_37), .in_33(leddataleft_2_out_6),
    .in_34(leddataleft_2_out_7), .in_35(leddataleft_2_out_8), .in_36(leddataleft_2_out_9),
    .in_37(leddataleft_2_out_10), .in_38(leddataleft_2_out_11), .in_39(leddataleft_2_out_12),
    .in_40(leddataleft_2_out_13), .in_41(leddataleft_2_out_14), .in_42(leddataleft_2_out_15),
    .in_43(leddataleft_2_out_16), .in_44(leddataleft_2_out_17), .in_45(leddataleft_2_out_18),
    .in_46(leddataleft_2_out_19), .in_47(leddataleft_2_out_20), .in_48(leddataleft_2_out_21),
    .in_49(leddataleft_2_out_22), .in_50(leddataleft_2_out_23), .in_51(leddataleft_2_out_24),
    .in_52(leddataleft_2_out_25), .in_53(leddataleft_2_out_26), .in_54(leddataleft_2_out_27),
    .in_55(leddataleft_2_out_28), .in_56(leddataleft_2_out_29), .in_57(leddataleft_2_out_30),
    .in_58(leddataleft_2_out_31), .in_59(leddataleft_2_out_32), .in_60(leddataleft_2_out_33),
    .in_61(leddataleft_2_out_34), .in_62(leddataleft_2_out_35), .in_63(leddataleft_2_out_36),
    .in_64(leddataleft_2_out_37), .in_65(leddataright_1_out_6), .in_66(leddataright_1_out_7),
    .in_67(leddataright_1_out_8), .in_68(leddataright_1_out_9), .in_69(leddataright_1_out_10),
    .in_70(leddataright_1_out_11), .in_71(leddataright_1_out_12), .in_72(leddataright_1_out_13),
    .in_73(leddataright_1_out_14), .in_74(leddataright_1_out_15), .in_75(leddataright_1_out_16),
    .in_76(leddataright_1_out_17), .in_77(leddataright_1_out_18), .in_78(leddataright_1_out_19),
    .in_79(leddataright_1_out_20), .in_80(leddataright_1_out_21), .in_81(leddataright_1_out_22),
    .in_82(leddataright_1_out_23), .in_83(leddataright_1_out_24), .in_84(leddataright_1_out_25),
    .in_85(leddataright_1_out_26), .in_86(leddataright_1_out_27), .in_87(leddataright_1_out_28),
    .in_88(leddataright_1_out_29), .in_89(leddataright_1_out_30), .in_90(leddataright_1_out_31),
    .in_91(leddataright_1_out_32), .in_92(leddataright_1_out_33), .in_93(leddataright_1_out_34),
    .in_94(leddataright_1_out_35), .in_95(leddataright_1_out_36), .in_96(leddataright_1_out_37),
    .in_97(leddataright_2_out_6), .in_98(leddataright_2_out_7), .in_99(leddataright_2_out_8),
    .in_100(leddataright_2_out_9), .in_101(leddataright_2_out_10), .in_102(leddataright_2_out_11),
    .in_103(leddataright_2_out_12), .in_104(leddataright_2_out_13), .in_105(leddataright_2_out_14),
    .in_106(leddataright_2_out_15), .in_107(leddataright_2_out_16), .in_108(leddataright_2_out_17),
    .in_109(leddataright_2_out_18), .in_110(leddataright_2_out_19), .in_111(leddataright_2_out_20),
    .in_112(leddataright_2_out_21), .in_113(leddataright_2_out_22), .in_114(leddataright_2_out_23),
    .in_115(leddataright_2_out_24), .in_116(leddataright_2_out_25), .in_117(leddataright_2_out_26),
    .in_118(leddataright_2_out_27), .in_119(leddataright_2_out_28), .in_120(leddataright_2_out_29),
    .in_121(leddataright_2_out_30), .in_122(leddataright_2_out_31), .in_123(leddataright_2_out_32),
    .in_124(leddataright_2_out_33), .in_125(leddataright_2_out_34), .in_126(leddataright_2_out_35),
    .in_127(leddataright_2_out_36), .in_128(leddataright_2_out_37), .out_129(\led点阵行信号输入_1_out_129 ),
    .out_130(\led点阵行信号输入_1_out_130 ), .out_131(\led点阵行信号输入_1_out_131 ), .out_132(\led点阵行信号输入_1_out_132 ),
    .out_133(\led点阵行信号输入_1_out_133 ), .out_134(\led点阵行信号输入_1_out_134 ), .out_135(\led点阵行信号输入_1_out_135 ),
    .out_136(\led点阵行信号输入_1_out_136 ), .out_137(\led点阵行信号输入_1_out_137 ), .out_138(\led点阵行信号输入_1_out_138 ),
    .out_139(\led点阵行信号输入_1_out_139 ), .out_140(\led点阵行信号输入_1_out_140 ), .out_141(\led点阵行信号输入_1_out_141 ),
    .out_142(\led点阵行信号输入_1_out_142 ), .out_143(\led点阵行信号输入_1_out_143 ), .out_144(\led点阵行信号输入_1_out_144 ),
    .out_145(\led点阵行信号输入_1_out_145 ), .out_146(\led点阵行信号输入_1_out_146 ), .out_147(\led点阵行信号输入_1_out_147 ),
    .out_148(\led点阵行信号输入_1_out_148 ), .out_149(\led点阵行信号输入_1_out_149 ), .out_150(\led点阵行信号输入_1_out_150 ),
    .out_151(\led点阵行信号输入_1_out_151 ), .out_152(\led点阵行信号输入_1_out_152 ), .out_153(\led点阵行信号输入_1_out_153 ),
    .out_154(\led点阵行信号输入_1_out_154 ), .out_155(\led点阵行信号输入_1_out_155 ), .out_156(\led点阵行信号输入_1_out_156 ),
    .out_157(\led点阵行信号输入_1_out_157 ), .out_158(\led点阵行信号输入_1_out_158 ), .out_159(\led点阵行信号输入_1_out_159 ),
    .out_160(\led点阵行信号输入_1_out_160 ), .out_161(\led点阵行信号输入_1_out_161 ), .out_162(\led点阵行信号输入_1_out_162 ),
    .out_163(\led点阵行信号输入_1_out_163 ), .out_164(\led点阵行信号输入_1_out_164 ), .out_165(\led点阵行信号输入_1_out_165 ),
    .out_166(\led点阵行信号输入_1_out_166 ), .out_167(\led点阵行信号输入_1_out_167 ), .out_168(\led点阵行信号输入_1_out_168 ),
    .out_169(\led点阵行信号输入_1_out_169 ), .out_170(\led点阵行信号输入_1_out_170 ), .out_171(\led点阵行信号输入_1_out_171 ),
    .out_172(\led点阵行信号输入_1_out_172 ), .out_173(\led点阵行信号输入_1_out_173 ), .out_174(\led点阵行信号输入_1_out_174 ),
    .out_175(\led点阵行信号输入_1_out_175 ), .out_176(\led点阵行信号输入_1_out_176 ), .out_177(\led点阵行信号输入_1_out_177 ),
    .out_178(\led点阵行信号输入_1_out_178 ), .out_179(\led点阵行信号输入_1_out_179 ), .out_180(\led点阵行信号输入_1_out_180 ),
    .out_181(\led点阵行信号输入_1_out_181 ), .out_182(\led点阵行信号输入_1_out_182 ), .out_183(\led点阵行信号输入_1_out_183 ),
    .out_184(\led点阵行信号输入_1_out_184 ), .out_185(\led点阵行信号输入_1_out_185 ), .out_186(\led点阵行信号输入_1_out_186 ),
    .out_187(\led点阵行信号输入_1_out_187 ), .out_188(\led点阵行信号输入_1_out_188 ), .out_189(\led点阵行信号输入_1_out_189 ),
    .out_190(\led点阵行信号输入_1_out_190 ), .out_191(\led点阵行信号输入_1_out_191 ), .out_192(\led点阵行信号输入_1_out_192 ),
    .out_193(\led点阵行信号输入_1_out_193 ), .out_194(\led点阵行信号输入_1_out_194 ), .out_195(\led点阵行信号输入_1_out_195 ),
    .out_196(\led点阵行信号输入_1_out_196 ), .out_197(\led点阵行信号输入_1_out_197 ), .out_198(\led点阵行信号输入_1_out_198 ),
    .out_199(\led点阵行信号输入_1_out_199 ), .out_200(\led点阵行信号输入_1_out_200 ), .out_201(\led点阵行信号输入_1_out_201 ),
    .out_202(\led点阵行信号输入_1_out_202 ), .out_203(\led点阵行信号输入_1_out_203 ), .out_204(\led点阵行信号输入_1_out_204 ),
    .out_205(\led点阵行信号输入_1_out_205 ), .out_206(\led点阵行信号输入_1_out_206 ), .out_207(\led点阵行信号输入_1_out_207 ),
    .out_208(\led点阵行信号输入_1_out_208 ), .out_209(\led点阵行信号输入_1_out_209 ), .out_210(\led点阵行信号输入_1_out_210 ),
    .out_211(\led点阵行信号输入_1_out_211 ), .out_212(\led点阵行信号输入_1_out_212 ), .out_213(\led点阵行信号输入_1_out_213 ),
    .out_214(\led点阵行信号输入_1_out_214 ), .out_215(\led点阵行信号输入_1_out_215 ), .out_216(\led点阵行信号输入_1_out_216 ),
    .out_217(\led点阵行信号输入_1_out_217 ), .out_218(\led点阵行信号输入_1_out_218 ), .out_219(\led点阵行信号输入_1_out_219 ),
    .out_220(\led点阵行信号输入_1_out_220 ), .out_221(\led点阵行信号输入_1_out_221 ), .out_222(\led点阵行信号输入_1_out_222 ),
    .out_223(\led点阵行信号输入_1_out_223 ), .out_224(\led点阵行信号输入_1_out_224 ), .out_225(\led点阵行信号输入_1_out_225 ),
    .out_226(\led点阵行信号输入_1_out_226 ), .out_227(\led点阵行信号输入_1_out_227 ), .out_228(\led点阵行信号输入_1_out_228 ),
    .out_229(\led点阵行信号输入_1_out_229 ), .out_230(\led点阵行信号输入_1_out_230 ), .out_231(\led点阵行信号输入_1_out_231 ),
    .out_232(\led点阵行信号输入_1_out_232 ), .out_233(\led点阵行信号输入_1_out_233 ), .out_234(\led点阵行信号输入_1_out_234 ),
    .out_235(\led点阵行信号输入_1_out_235 ), .out_236(\led点阵行信号输入_1_out_236 ), .out_237(\led点阵行信号输入_1_out_237 ),
    .out_238(\led点阵行信号输入_1_out_238 ), .out_239(\led点阵行信号输入_1_out_239 ), .out_240(\led点阵行信号输入_1_out_240 ),
    .out_241(\led点阵行信号输入_1_out_241 ), .out_242(\led点阵行信号输入_1_out_242 ), .out_243(\led点阵行信号输入_1_out_243 ),
    .out_244(\led点阵行信号输入_1_out_244 ), .out_245(\led点阵行信号输入_1_out_245 ), .out_246(\led点阵行信号输入_1_out_246 ),
    .out_247(\led点阵行信号输入_1_out_247 ), .out_248(\led点阵行信号输入_1_out_248 ), .out_249(\led点阵行信号输入_1_out_249 ),
    .out_250(\led点阵行信号输入_1_out_250 ), .out_251(\led点阵行信号输入_1_out_251 ), .out_252(\led点阵行信号输入_1_out_252 ),
    .out_253(\led点阵行信号输入_1_out_253 ), .out_254(\led点阵行信号输入_1_out_254 ), .out_255(\led点阵行信号输入_1_out_255 ),
    .out_256(\led点阵行信号输入_1_out_256 ));
  LedDataRight leddataright_2 (
    .CLK(CLK), .DATA(rom_5_data), .en(1'b1), .out_6(leddataright_2_out_6), .out_7(leddataright_2_out_7),
    .out_8(leddataright_2_out_8), .out_9(leddataright_2_out_9), .out_10(leddataright_2_out_10),
    .out_11(leddataright_2_out_11), .out_12(leddataright_2_out_12), .out_13(leddataright_2_out_13),
    .out_14(leddataright_2_out_14), .out_15(leddataright_2_out_15), .out_16(leddataright_2_out_16),
    .out_17(leddataright_2_out_17), .out_18(leddataright_2_out_18), .out_19(leddataright_2_out_19),
    .out_20(leddataright_2_out_20), .out_21(leddataright_2_out_21), .out_22(leddataright_2_out_22),
    .out_23(leddataright_2_out_23), .out_24(leddataright_2_out_24), .out_25(leddataright_2_out_25),
    .out_26(leddataright_2_out_26), .out_27(leddataright_2_out_27), .out_28(leddataright_2_out_28),
    .out_29(leddataright_2_out_29), .out_30(leddataright_2_out_30), .out_31(leddataright_2_out_31),
    .out_32(leddataright_2_out_32), .out_33(leddataright_2_out_33), .out_34(leddataright_2_out_34),
    .out_35(leddataright_2_out_35), .out_36(leddataright_2_out_36), .out_37(leddataright_2_out_37),
    .in_5(counter_3_q));  // open: CLR
  Register #(.width(32), .trigger("rising"), .Select("low")) register_1 (
    .D(MDin), .en(and_3_out), .Q(LedData), .clk(CLK));  // open: clr
  and and_5 (halt, and_4_out, ~Go);  // AND_Gate
  ROM #(.addrWidth(14), .dataWidth(32), .Select("high")) rom_4 (.addr(counter_2_q), .data(rom_4_data));
  ROM #(.addrWidth(14), .dataWidth(32), .Select("high")) rom_5 (.addr(counter_2_q), .data(rom_5_data));
  not not_2 (not_2_out, halt);
  Counter #(.width(16), .max('hffff), .ongoal("stay"), .trigger("rising"), .behavior("old")) counter_4 (
    .count(not_2_out), .Q(\总周期数 ), .clk(CLK));  // open: load, D, carry, clr, preset
  DotMatrix #(.inputtype("row"), .matrixcols(32), .matrixrows(32), .persist(0), .dotshape("circle")) dotmatrix_1 (
    .row0(\led点阵行信号输入_1_out_129 ), .row1(\led点阵行信号输入_1_out_130 ), .row2(\led点阵行信号输入_1_out_131 ),
    .row3(\led点阵行信号输入_1_out_132 ), .row4(\led点阵行信号输入_1_out_133 ), .row5(\led点阵行信号输入_1_out_134 ),
    .row6(\led点阵行信号输入_1_out_135 ), .row7(\led点阵行信号输入_1_out_136 ), .row8(\led点阵行信号输入_1_out_137 ),
    .row9(\led点阵行信号输入_1_out_138 ), .row10(\led点阵行信号输入_1_out_139 ), .row11(\led点阵行信号输入_1_out_140 ),
    .row12(\led点阵行信号输入_1_out_141 ), .row13(\led点阵行信号输入_1_out_142 ), .row14(\led点阵行信号输入_1_out_143 ),
    .row15(\led点阵行信号输入_1_out_144 ), .row16(\led点阵行信号输入_1_out_145 ), .row17(\led点阵行信号输入_1_out_146 ),
    .row18(\led点阵行信号输入_1_out_147 ), .row19(\led点阵行信号输入_1_out_148 ), .row20(\led点阵行信号输入_1_out_149 ),
    .row21(\led点阵行信号输入_1_out_150 ), .row22(\led点阵行信号输入_1_out_151 ), .row23(\led点阵行信号输入_1_out_152 ),
    .row24(\led点阵行信号输入_1_out_153 ), .row25(\led点阵行信号输入_1_out_154 ), .row26(\led点阵行信号输入_1_out_155 ),
    .row27(\led点阵行信号输入_1_out_156 ), .row28(\led点阵行信号输入_1_out_157 ), .row29(\led点阵行信号输入_1_out_158 ),
    .row30(\led点阵行信号输入_1_out_159 ), .row31(\led点阵行信号输入_1_out_160 ));
  DotMatrix #(.inputtype("row"), .matrixcols(32), .matrixrows(32), .persist(0), .dotshape("circle")) dotmatrix_2 (
    .row0(\led点阵行信号输入_1_out_161 ), .row1(\led点阵行信号输入_1_out_162 ), .row2(\led点阵行信号输入_1_out_163 ),
    .row3(\led点阵行信号输入_1_out_164 ), .row4(\led点阵行信号输入_1_out_165 ), .row5(\led点阵行信号输入_1_out_166 ),
    .row6(\led点阵行信号输入_1_out_167 ), .row7(\led点阵行信号输入_1_out_168 ), .row8(\led点阵行信号输入_1_out_169 ),
    .row9(\led点阵行信号输入_1_out_170 ), .row10(\led点阵行信号输入_1_out_171 ), .row11(\led点阵行信号输入_1_out_172 ),
    .row12(\led点阵行信号输入_1_out_173 ), .row13(\led点阵行信号输入_1_out_174 ), .row14(\led点阵行信号输入_1_out_175 ),
    .row15(\led点阵行信号输入_1_out_176 ), .row16(\led点阵行信号输入_1_out_177 ), .row17(\led点阵行信号输入_1_out_178 ),
    .row18(\led点阵行信号输入_1_out_179 ), .row19(\led点阵行信号输入_1_out_180 ), .row20(\led点阵行信号输入_1_out_181 ),
    .row21(\led点阵行信号输入_1_out_182 ), .row22(\led点阵行信号输入_1_out_183 ), .row23(\led点阵行信号输入_1_out_184 ),
    .row24(\led点阵行信号输入_1_out_185 ), .row25(\led点阵行信号输入_1_out_186 ), .row26(\led点阵行信号输入_1_out_187 ),
    .row27(\led点阵行信号输入_1_out_188 ), .row28(\led点阵行信号输入_1_out_189 ), .row29(\led点阵行信号输入_1_out_190 ),
    .row30(\led点阵行信号输入_1_out_191 ), .row31(\led点阵行信号输入_1_out_192 ));
  \进度条  \u_进度条_1  (.in_1(counter_2_q), .out_2(\进度条_1_out_2 ), .out_3(\进度条_1_out_3 ));
  DotMatrix #(.inputtype("row"), .matrixcols(32), .matrixrows(1), .persist(0), .dotshape("square")) dotmatrix_3 (.row0(\进度条_1_out_2 ));
  Button button_1 (.out(\_0_5倍速 ));
  Button button_2 (.out(\暂停键 ));
  DotMatrix #(.inputtype("row"), .matrixcols(32), .matrixrows(32), .persist(0), .dotshape("circle")) dotmatrix_4 (
    .row0(\led点阵行信号输入_1_out_193 ), .row1(\led点阵行信号输入_1_out_194 ), .row2(\led点阵行信号输入_1_out_195 ),
    .row3(\led点阵行信号输入_1_out_196 ), .row4(\led点阵行信号输入_1_out_197 ), .row5(\led点阵行信号输入_1_out_198 ),
    .row6(\led点阵行信号输入_1_out_199 ), .row7(\led点阵行信号输入_1_out_200 ), .row8(\led点阵行信号输入_1_out_201 ),
    .row9(\led点阵行信号输入_1_out_202 ), .row10(\led点阵行信号输入_1_out_203 ), .row11(\led点阵行信号输入_1_out_204 ),
    .row12(\led点阵行信号输入_1_out_205 ), .row13(\led点阵行信号输入_1_out_206 ), .row14(\led点阵行信号输入_1_out_207 ),
    .row15(\led点阵行信号输入_1_out_208 ), .row16(\led点阵行信号输入_1_out_209 ), .row17(\led点阵行信号输入_1_out_210 ),
    .row18(\led点阵行信号输入_1_out_211 ), .row19(\led点阵行信号输入_1_out_212 ), .row20(\led点阵行信号输入_1_out_213 ),
    .row21(\led点阵行信号输入_1_out_214 ), .row22(\led点阵行信号输入_1_out_215 ), .row23(\led点阵行信号输入_1_out_216 ),
    .row24(\led点阵行信号输入_1_out_217 ), .row25(\led点阵行信号输入_1_out_218 ), .row26(\led点阵行信号输入_1_out_219 ),
    .row27(\led点阵行信号输入_1_out_220 ), .row28(\led点阵行信号输入_1_out_221 ), .row29(\led点阵行信号输入_1_out_222 ),
    .row30(\led点阵行信号输入_1_out_223 ), .row31(\led点阵行信号输入_1_out_224 ));
  DotMatrix #(.inputtype("row"), .matrixcols(32), .matrixrows(32), .persist(0), .dotshape("circle")) dotmatrix_5 (
    .row0(\led点阵行信号输入_1_out_225 ), .row1(\led点阵行信号输入_1_out_226 ), .row2(\led点阵行信号输入_1_out_227 ),
    .row3(\led点阵行信号输入_1_out_228 ), .row4(\led点阵行信号输入_1_out_229 ), .row5(\led点阵行信号输入_1_out_230 ),
    .row6(\led点阵行信号输入_1_out_231 ), .row7(\led点阵行信号输入_1_out_232 ), .row8(\led点阵行信号输入_1_out_233 ),
    .row9(\led点阵行信号输入_1_out_234 ), .row10(\led点阵行信号输入_1_out_235 ), .row11(\led点阵行信号输入_1_out_236 ),
    .row12(\led点阵行信号输入_1_out_237 ), .row13(\led点阵行信号输入_1_out_238 ), .row14(\led点阵行信号输入_1_out_239 ),
    .row15(\led点阵行信号输入_1_out_240 ), .row16(\led点阵行信号输入_1_out_241 ), .row17(\led点阵行信号输入_1_out_242 ),
    .row18(\led点阵行信号输入_1_out_243 ), .row19(\led点阵行信号输入_1_out_244 ), .row20(\led点阵行信号输入_1_out_245 ),
    .row21(\led点阵行信号输入_1_out_246 ), .row22(\led点阵行信号输入_1_out_247 ), .row23(\led点阵行信号输入_1_out_248 ),
    .row24(\led点阵行信号输入_1_out_249 ), .row25(\led点阵行信号输入_1_out_250 ), .row26(\led点阵行信号输入_1_out_251 ),
    .row27(\led点阵行信号输入_1_out_252 ), .row28(\led点阵行信号输入_1_out_253 ), .row29(\led点阵行信号输入_1_out_254 ),
    .row30(\led点阵行信号输入_1_out_255 ), .row31(\led点阵行信号输入_1_out_256 ));
  DotMatrix #(.inputtype("row"), .matrixcols(32), .matrixrows(1), .persist(0), .dotshape("square")) dotmatrix_6 (.row0(\进度条_1_out_3 ));
  Button button_3 (.out(\_2倍速 ));

  // Other names for the same wires on the sheet: a0[31:0] = MDin; FUNC[5:0] = IR[5:0]; OP[5:0] = IR[31:26]

  // Notes on the sheet:
  //   中断源
  //   中断等待指示
  //   控制位
  //   暂停节拍，不能为0
  //   PC + 4
  //   J & JAL
  //   JR
  //   戳工具置1进入计数暂停模式，ctrl+k时钟自动运行到对应节拍暂停
  //   ctrl+k关闭时钟连续运行，将控制位置零，进入单步调试模式调试
  //   用这个时钟源需要去掉电路中的其他时钟源
  //   指令存储器
  //   数码管输出
  //   指令字
  //   contents of rom_1 (hex, n*v repeats v):
  //   20110001 8000c05 20110001 20120002 20130003 8000c09 20110001 20120002 20130003 8000c0d 20110001
  //   20120002 20130003 8000c11 20110001 20120002 20130003 c000cb8 20100001 20110001 118fc0 112020
  //   20020022 c 118882 12200001 8000c15 112020 20020022 c 20110001 118880 112020 20020022 c 12200001
  //   8000c1f 20110001 118fc0 112020 20020022 c 1188c3 112020 20020022 c 118903 112020 20020022 c 118903
  //   112020 20020022 c 118903 112020 20020022 c 118903 112020 20020022 c 118903 112020 20020022 c 118903
  //   112020 20020022 c 118903 112020 20020022 c 20100001 109fc0 139fc3 8021 2012000c 24160003 26100001
  //   3210000f 20080008 20090001 139900 2709825 132020 20020022 c 1094022 1500fff9 22100001 2018000f
  //   2188024 108700 20080008 20090001 139902 2709825 132021 20020022 c 1094022 1500fff9 108702 2c9b022
  //   12c00001 8000c50 4020 1084027 84400 3508ffff 82021 20020022 c 2010ffff 20110000 ae300000 22100001
  //   22310004 ae300000 22100001 22310004 ae300000 22100001 22310004 ae300000 22100001 22310004 ae300000
  //   22100001 22310004 ae300000 22100001 22310004 ae300000 22100001 22310004 ae300000 22100001 22310004
  //   ae300000 22100001 22310004 ae300000 22100001 22310004 ae300000 22100001 22310004 ae300000 22100001
  //   22310004 ae300000 22100001 22310004 ae300000 22100001 22310004 ae300000 22100001 22310004 ae300000
  //   22100001 22310004 22100001 8020 2011003c 8e130000 8e340000 274402a 11000002 ae330000 ae140000
  //   2231fffc 1611fff8 102020 20020022 c 22100004 2011003c 1611fff2 20020032 c 20100000 22100001 102020
  //   20020022 c 22100002 102020 20020022 c 22100003 102020 20020022 c 22100004 102020 20020022 c 22100005
  //   102020 20020022 c 22100006 102020 20020022 c 22100007 102020 20020022 c 22100008 102020 20020022
  //   20020022 c 3e00008
  //   OP
  //   Func
  //   rs
  //   rt
  //   rd
  //   sa
  //   imm
  //   可计数暂停的时钟源
  //   4号
  //   2号
  //   BEQ & BNE
  //   数据存储器
  //   WriteBackData
  //   为方便自动评测，需要输出PC，IR，寄存器堆写如数据RDin
  //   RAM写使能MemWrite、RAM写入数据MDin等信号
  //   JMP
  //   JR
  //   OP
  //   Func
  //   contents of rom_2 (hex, n*v repeats v):
  //   20*0 1 7 27*0 1f 1ff 7ff ff1 3fff 7fff ffff ffff 1ffbf 1ff3f 1ffff 1ffff 1ffff ffff ffff 16*0 30 3e0
  //   fef 3fff 7fff ff3f 1fc7f 3f9ff 3f3ff 3fe7ff 7fefff 7fffff ffffff fffc7f fffe7f ffff7f 13*0 f 3cff
  //   fffc 3ffe0 fff00 3ffc00 fff800 1ffe000 3ffe000 7ffc000 fff8001 1fff0007 1ffe200f 1ffe001f 39fc4038
  //   3bfcc000 3ffcc001 3ffc6003 3ffe2007 14*0 2000 c000 30000 0 0 0 c 7c b0 200 202400 204000 208000
  //   12000 8012000 8012000 1801a000 1800f301 60*0 80000 1f00000 1e00000 1800000 49*0 10000 400 78 fe 9ff
  //   3cff 3eff ffeff 183e3f 30101f 7 3 ff 2f8f e00003 19*0 100 0 0 e00000 e00000 600000 c00000 f00000
  //   1f000f0 1ffe1fc fffffe 1fffffe 3cffff8 17*0 1fc0000 df3000 3f000 e000 0 0 4207f ff8ff 7ff8ff fff8ff
  //   1ff81ff 187c3ff 1cfffff 1ffffff 3ff9fff 16*0 7 33 1 1 380 0 0 200 152*0 1 10 0 1 59*0 7 4f 4 66*0 1
  //   3 1 3 1f 7f 7f 7f 3f 3f f f 58*0 1 1 3 19*0 7 1f 7f ff 6*1ff ff 7f 3f 7f 1ff fff 20*0 400 400 600
  //   300 180 f0 20 0 0 0 1000 16*0 f 31 cf 1df 1ff 4*3ff 1ff 1ff ff 1f1 780 1c01 7807 7fff 16*0 80 100
  //   201 607 407 600 600 3a0 1f8 ff 3c 18 0 0 1e00 1000 24*0 100 62*0 e0 3f0 7f0 3f8 fd 1f 7 2003 fc07
  //   e0000000 ff800000 ffc00000 ffe00000 fff00000 fff80000 fffe0000 ffff0000 ffffc000 fffff000 fffffc00
  //   ffffff00 ffffffe1 ffffffff 3fffffff 1fffffff fffffff 7ffffff 3ffffff 1ffffff 7fffff 3fffff 1fffff
  //   fffff fffff fffff 7ffff fffff 800fffff e01fffff f07fffff ffffffff 32*0 32*ffffffff 150*0 2 f e 6 7 3
  //   f83 7e3 7f f 30*0 1 18*0 1 3 3 2 0 4 6 18004 18002 2002 0 400 0 0 c0 137*0 f800000 fe00000 7fe0000
  //   7ff0000 7ffc000 fffe000 fffe000 1fffe000 1fffe000 1fffe000 ffff000 ffffff8 7fffffe 1ffffe 1ffffe
  //   3fffffe 7fffffc 7fffffc 7ffffff 4*fffffff 8*0 1f80 600ffe0 7fdfff0 3ffffff 1ffffff 7fffff 3fffff
  //   ffffff 7ffffff fffffff fffffff 703ffff 1fff 7ff 3ff 3ff 3c0fff 3ffff9 7ffff0 1fffff8 7ffffff 7ffffff
  //   7f8001f f 0 0 ff 3ff fff 1fff 1fff fff f00 c00 1800 7f800 7f800 47800 f800 f000 3c000 130003 7 7 0 0
  //   0 20 0 0 0 780 17 6*0 1ff 7ff 4*fff 1fff 1fff 80ffff 6fffc7 3fff83 1fff83 3ffe7 fffff ffffff 1d001f
  //   1f 1f 7 7 e c c07f8 ffffc ffffc 3ffffc 7 37*0 3 1f 4*0 200 600 c00 0 400 400 12*0 1 58*0 2 4 18 30
  //   61 c3 193 3b7 7ee fce 380*0 80000 60 e0 19*0 300000 0 0 3f0000 3fc000 3fe000 3e003e 1f007f f20ff 7f
  //   6 3f1f 3fff 3fff 95*0 7c0 30*0 7fc00 fff00 62*0 1fc0000 7fe0000 320*0 f 3 1 63*0 1 29*0 f 3 13*0 8
  //   27*0 3 7 f 7 2 34*0 2 4 0 8 8 0 0 6 50*0 4 1e 3e 3e 3c 39 3c 3e 1f 1f 7 1 4*0 8 8 93*0 3 0 0 0 73fe
  //   93*0 200 0 3f00 88*0 3 f e 1e 1c 34 68 1e0 63*0 200 154*0 1800 3001800 2181800 80000 0 2800 58*0 1
  //   22*0 2 3 3 3 1 1 1 3 46 c 8001c f007e 197c0 fc0 5fe 27*0 1000 3f10 f10 0 c0 88*0 1 3 1 1 3 ff7 fff
  //   7f 241*0 10 10 8 8 20008 8008 206004 81004 10400 4200 800 0 0 0 1 52*0 8 8 8 2004 1004 10400 4200
  //   800 52*0 10 95*0 10 10 10 8 40008 20008 8000 204004 636*0 200 104 84 4 840 22 112 8 0 0 10 57*0 46
  //   22 105 8a4 6c0 100 800 123*0 3f ff 3ff 3f8 7f0 7e0 30*0 7 6 31*0 1 19*0 3 7 f 1f ff ff8 7ff00 ffc00
  //   7f800 3f000 1e000 1e000 e000 80*0 1 1 6*0 600000 988*0 80000 380*0 8000 10000 20000 40000 40000
  //   80000 0 40000 40000 20000 10000 c000 1000 18 17*0 80000 100000 200000 400000 0 4*800000 0 400000
  //   200000 100000 80000 123*0 8 0 20 83*0 4*2 0 13100 c880 12650 c081 2000 8 0 8000 3e00 800c00 53*0 2 1
  //   1 0 904 780 780 0 80 0 0 30000 16*0 3200 1300 c100 2000 6*0 180000 19*0 4 0 0 0 900 a480 45240 840
  //   c0400 0 0 10 0 238000 c0000 f0000 6000000 85*0 8 74*0 1 31*0 1 403*0 3 e 0 0 0 3 31*0 3 3 22*0 3 f
  //   38 3 e 22*0 3 c 18 0 0 0 3 e 167*0 4 22 19a 78 330 60 30*0 7 c 31*0 1 22*0 8 8 104 80 6000 800 0 0
  //   2000 53*0 10 0 800 58*0 40 61*0 100 322*0 5*1 10001 c001 3000 800 22*0 5*1 c0001 30001 c001 3000 c00
  //   21*0 1 4*0 100000 123*0 10 10 36*0 4 4 127*0 1 134*0 1 31*0 1 31*0 1 31*0 3 29*0 7 1f 1f 30*0 3 7
  //   22*0 f ff 7c0 1e00 3800 701f e078 1c0e0 1c187 1818f 20*0 3f 3ff 1fff 7fc0 1fe00 3f800 7e000 fc000
  //   1f8000 1f0000 1f0000 3f0001 20*0 f 1ff f00 383f e1e0 1c700 31c00 63000 e6003 cc01f 1cc03e 1cc07d
  //   27*0 5 30 40 80 80 50*0 3f 7ff 3f00 f800 3c000 f0000 1e0000 380000 700000 f00000 e00000 e00000
  //   1c00000 1c00002 50*0 100 0 4000 30000 40000 18000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
  //   contents of rom_3 (hex, n*v repeats v):
  //   32*0 fff8 3f9f8 3fdff 1ffff ffff 3fff 7ff 25*0 7fffff 7fffff 3fffff 1ffc3f ffe1f 7ffff 1ffff 3fff
  //   3fc 23*0 1ffa1804 1ff90e00 1ffc0381 ffe0001 7ff0000 7ffc000 3fff800 1ffffff ffffff 7fffff 3fffff
  //   1fffff 7ffff 7fff 1ff 7ff 1fff 1fff 3ff 13*0 c80f38f 64079cf 3003e03 1f07 fff 1ff 0 200000 200000
  //   100000 7c f800 0 1f 114*0 f08007 ffc01f 7fc01f c01f 401f 1f 1b 1 4000 4000 0 1f8 1f0 19*0 3c7ff80
  //   1c7ff00 c3ff00 60ff80 200700 27*0 1fe07ff 4c07ff 7ff 3ff 1003ff 7e0 147c0 3c000 18000 23*0 5*3 7
  //   1007 1003 1 161*0 60000ff 31c001f 6fc00f 23ffff ffff 57*0 3c 30 0 0 0 1f 1f 49*0 f 3f 3f 9 92*0 3fff
  //   3fff 1fff 7ff 1ff 7f 1f 28*0 8 0 0 2 30003 3e007 3fc07 1ffe1 ffe0 7f00 19*0 ffff 7fff 1fff 7ff 1ff
  //   7f 1f 1 25*0 1 3 3200c 3f01c 3f81f 1fc1f ff7f 7fff 1fff 3ff 1f 31*0 30001 1c000 51*0 7fff 7f 3f 1f
  //   3c f1 7e1 1f80 3e00 23*0 ffffffff ffffffff ffffffff fffffff ffffff 3fffff 1fffff 7ffff 7ffff 3ffff
  //   7ffff 7ffff fffff 3fffff 1ffffff fffffff 10*ffffffff fffe1fff fffc03ff fff800ff fff0007f ff00007f 7f
  //   32*0 32*ffffffff 128*0 7 7f ffe3 7803 3 e 1e 1c 24*0 3 2 30*0 60 2000000 30000 10 6*0 600 149*0
  //   e03ffff 3ffff 7ffff 3fffff 3ffffff 3ffffff 3ffffff 7ffffff e07ffff 80fffe0 3ff000 1ffe000 3ffc000
  //   7ff8000 fff0000 ff80000 fc00000 fe00000 ff00000 fe00000 12*0 f 1f 3fff 3fffff ffffff 7fffff 7007ff
  //   7ff fff 3fe3 7ffc7 3fffff ffffff 1ffffff 3ffffff 7ffffff fffffff 7e7ffff 781ffff 1ffff fffe 7fc0
  //   3c00 800 11*0 400 200 8*0 fc00 303c00 1c00 1c00 1e00 3f00 3f80 3fe0 1ffc 1ffc ffe 7ff 1ff 7f 3f 1e
  //   6*0 ffe00 1fe7c 1f 3 3 7 1f 60 180 7ff80 3fff80 ffffc0 fbffe0 c07ffd 7fe7 3fff 3fff 3fff 1fff fff
  //   3ff ff 53*0 800 5*0 180 c0 30 3 40*0 1c9e 19fe 39be 333c 737c 667c e67c c67e 1c07e 1c07b 18039 3863c
  //   3861c 3861c 1020e 7 7 3 1 46*0 800 4*0 200 0 0 10 18 8 18000 10200 200 0 100 180 180 c0 e0 70 20070
  //   60010 60000 c 63*0 c 71*0 43 180 100 4 4 154*0 38 4*0 e c 25*0 3fff fff 3ff 30 0 0 f 3c 10000000
  //   10000000 0 400 6*0 100 100 76*0 fc0 7c0 100 29*0 1fffe0 1ffe00 7f800 61*0 7ff0000 7fe0000 1fc0000
  //   542*0 3 f 1f 3f 3e 3c 3c 3c 3e 1e c 66*0 8 8 0 4 4 1 44*0 1ffff ffff 1fff 7f8 12*0 1 1 69*0 4 f 1f
  //   3e 3c 18 0 0 0 fe00 7f00 300 93*0 380 300 300 200 200 400 400 800 1000 56*0 400 400 0 0 2 2 2 152*0
  //   1800 6*0 8 4 2002 2001 1001 1fc6 ff8 82*0 780 1600 1f00e 70078 59 60f 1c011 1e0040 180 26*0 1f 7c ff
  //   ff 1f 88*0 3c fc 7f 7f 1f3 300 30*0 c00000 6*0 800 212*0 1 4*0 800 200 402 2 2 4 4 52*0 1 68*0 1800
  //   4200 10400 c1002 202000 c004 10004 20004 4 4 4 28*0 40000 56*0 800 4200 10402 c1002 2000 8004 10004
  //   4 4 4 626*0 10 8 0 48 112 222 840 4 84 104 200 53*0 800 100 680 8a4 105 22 6 120*0 7f0 7f8 3ff 1ff
  //   7f 3 26*0 7 63*0 1e000 1e000 3f000 3f800 7fc00 fff00 1fe0 ff 3f f 7 3 90*0 600000 6*0 1 1 17*0 1
  //   31*0 1 1568*0 d80000 0 2000 e000 1000 204e 1800e 4c08 1b010 0 3 2 2 50*0 70000 4*0 690 f80 1a00 0 1
  //   1 26*0 c00000 0 880000 300000 0 0 100 208 90 80 18*0 4000000 0 0 e0000 40000 118000 60000 c0020 44
  //   400bc 18128 40 0 2 2 92*0 8 51*0 1 454*0 3 1 0 0 c 7 1 25*0 3 35*0 c 7 39 1e 7 29*0 c 7 1 0 0 10 1c
  //   7 1 138*0 3a0 38 19f 32 26 27*0 7 1 63*0 18000 0 0 3000 80 100 20c 8 65*0 10 133*0 100 239*0 1 69*0
  //   1800 2000 8001 20001 4*1 24*0 1800 2000 8001 20001 80001 5*1 26*0 80000 0 0 0 1 1 16*0 1 107*0 8 0
  //   10 23*0 2 0 4 4 118*0 1 7*0 1 119*0 1 31*0 1 31*0 1 31*0 3 31*0 1f 1f 7 29*0 7 3 30*0 1818f 1c187
  //   1c0e0 e078 701f 3800 1e00 7c0 ff f 22*0 1f0001 1f0000 1f0000 1f8000 fc000 7e000 3f800 1fe00 7fc0
  //   1fff 3ff 3f 20*0 1cc07d 1cc03e cc01f e6003 63000 31c00 1c700 e1e0 383f f00 1ff f 20*0 80 80 40 30 5
  //   59*0 1c00002 1c00000 e00000 e00000 f00000 700000 380000 1e0000 f0000 3c000 f800 3f00 7ff 3f 50*0
  //   2000040 2000020 1000010 1000007 800000 800000 400000 200000 180000 40000 30000 4000 0 100 149*0 200
  //   98*0 1 25*0 1 31*0 1 36*0 400 1000 4001 10001 4*1
  //   Beq
  //   Bne
  //   MemToReg
  //   MemWrite
  //   AluOP
  //   AluSrcB
  //   RegWrite
  //   JAL
  //   RegDst
  //   Syscall
  //   $v0 == 34， 显示a0的值，否则停机
  //   总复位信号应将除ROM以外所有存储组件全部清零
  //   数码管输出应该用寄存器锁存，否则显示数据只能一闪而过
  //   halt为1 表示停机，需要按键go重启
  //   contents of rom_4 (hex, n*v repeats v):
  //   12*0 4 c c 1c 3c 3c 3e03c 3ffffffc fffffffc cffffffc 1ffffff8 7ffff0 7fff0 1fff0 7ff0 1ff8 ff8 3f8
  //   1fc 1c 13*0 c c 1c 1c 7e01c fffffc3c 7ffffffc fffffffc fffffffc ffffff00 ffffff80 ffffffe0 fff9fff0
  //   ff7c3ff0 ff870ff0 ffc007e0 ff8001f0 ff0000f8 fe000078 13*0 8 8 18 18 7ffc0030 fffff020 ffffffc0
  //   ffff0188 ffffc000 fffff800 e3ffff00 8ffff3c0 fffff860 ffe07e00 fff81f00 fffc0fc0 fff00fe0 fff80ff0
  //   fffc07f0 11*0 400000 7fffc000 fffff000 fffffe00 1f00 1c0 e0 5*0 fff00000 fffe0000 ffff8000 ffffe000
  //   7ffff000 fffffc00 fffffe00 fbffff00 f07fff00 19*0 3ffc0000 1e0000 1fe00000 3ff3e000 fc00 f001f00
  //   3c100f80 667c0 133e0 d9e0 cf0 80cf0 800604f0 117*0 c0000000 f8000000 ff7e0000 ffff8000 ffffc000
  //   ffff8000 fff80000 fff80000 fff80000 fff00000 ff800000 55*0 e0000000 fc000000 fe000000 ff000000
  //   ff000000 ff000000 fe000000 fe000000 fc000000 19*0 80000000 f8000000 1e000000 7f80000 f81cc0 3c07e0
  //   1c03e0 3e01c0 203f8080 203f8000 3f0000 7e0000 e00000 48*0 30000000 400000 10*0 60 64*0 80 80 c0 16*0
  //   fe000000 7f800000 7f00000 1fe0040 7fc030 1ffc08 fff84 1fffe4 7ffe0 1fffe0 1ffff4 3fff0 7fff0 7ffe0
  //   7ffe0 7ffe4 12*0 23e0000 60780 7c0 fe0 26e0 302e0 2e0 2f0 270 230 230 218 18 1c c 4 4*c 15*0
  //   ff800000 fff00000 ffc0000 3ff0000 7ff000 1ffe00 fffc0 3fffe0 3fffe0 fffe0 3fff0 1fff0 fff0 fff0 7ff0
  //   61ff0 21ff0 14*0 10 36*0 78000000 fe000000 fe000000 fe000000 ff000000 ffc00000 ffe00000 fff00000
  //   fff00000 fff00000 ffe00000 ffe00000 ffc00000 58*0 e0000000 f0000000 f0000000 c0000000 17*0 38000000
  //   ffc00000 fff80000 fffe0000 ffff8000 ffffc000 ffffe000 ffffe000 fffff000 fffff000 ffffe000 ffffe000
  //   ffffc000 ffffc000 ffffc000 ffff8000 ffff0000 18*0 40000000 4*0 400 600 700 700 300 300 600 0
  //   40000000 15*0 ffc00000 fff80000 fffe0000 ffff0000 ffff8000 ffffc000 ffffe000 fffff000 fffff000
  //   ff7ff000 ff7ff800 ff7ff800 fe7ff000 fefff000 fdffe000 ffffc000 ffef8000 16*0 60000 30000 c0018000
  //   41e000 30e000 187000 83800 38043800 10041800 41800 41c00 81c00 103c00 203800 30403000 60806000 26*0
  //   80 80 80 57*0 70000000 f8000000 f0000000 e0700000 c1f80000 c3f80000 ffc00000 fc000000 fdf80000
  //   ffe00000 3fffff8 1fffff0 1ffffe0 1ffffc0 1ffffc0 1ffff80 1ffff00 1fffe00 1fffc00 3fff000 7fff000
  //   3fffe000 ffffe000 fffff800 fffffe0f 9*ffffffff ffffffc0 fffffe00 fffffc00 fffffc00 ffffff00 ffffffff
  //   ffffffff ffffffff 32*0 32*ffffffff 31*0 80000000 31*0 8000000 88*0 6000000 f000000 1c000000 18000000
  //   38000000 f8000000 fe3f0000 9fff0000 30*0 80000000 d8000000 17*0 80000000 80000000 0 0 180000 200000
  //   0 0 0 8000000 18000000 1000000 0 0 380 155*0 80000000 fc000000 fe000000 ff000000 ff000000 11*0
  //   c0000000 e0000000 f0000000 fc000000 ffc00000 fff00000 fff80000 fffe0000 ffff0000 ffff8000 ffff8000
  //   9*ffffc000 ffff8000 0 0 fff00000 ffffc000 ffffe000 ffffe000 fffff000 fffff000 1fffe000 7ffe000
  //   3fff000 3fff800 3fffc00 7f80800 1fe00000 3fe7f000 7e1ffe00 fc03ff00 fc01ff00 f000ff80 7f80 7f80 3f80
  //   3fc0 3fc0 3fc0 7f80 7f80 7f00 f8007f00 700fe00 c7fe00 4*0 e7e00000 fff80000 fffc0000 fffe0000
  //   fffe0000 ffff0000 ffff8000 ffffc000 ffffe000 ffffe000 ffff0000 ffffe000 fffff800 fffffc00 fffffc00
  //   fffffe00 fe0ffe00 e007ff00 4*3ff00 7ff00 7fe00 7fe00 e007fc00 7e1ffc00 ffffc00 0 c00000 3800 800
  //   11*0 400 700 100 13*0 880 0 3fe00000 7f8fc000 fffff800 e07ff800 7ffc00 7ffc00 3ffc00 4*0 600000
  //   1fc00000 8000000 4000 f800 c0007f00 3f80 1f80 f80 780 780 7c0 3c0 3c0 1c0 e0000700 6000780 800700
  //   7fe700 18e300 47*0 300000 600000 1c00000 3800000 0 0 0 18000000 30000000 60000000 c0000000 c0000000
  //   80000000 7*0 4000 c000 38000 78000 78000 b8000 30000 60000 c0000 180000 300000 600000 275*0 200 600
  //   600 e00 1e00 1e00 3e00 1e00 e00 e00 e00 600 600 59*0 7*200 5*600 6*e00 4*1e00 11*0 200 600 600 e00
  //   1e00 3e00 7e00 3fe00 7ff00 e01ffe00 67fffe00 7fffe00 7fffe00 3fffe00 83fffe00 987ffe00 7ffe00 fffe00
  //   7fffe00 fffffe00 fffffe00 29*0 400 32*0 100 700 58*0 80 380 fc0 3fc0 1ffc0 1fffe0 28*0 80 0 fe00000
  //   3ff80000 88*0 380 380 1c0 39c0 c0 80 0 100 22*0 80 80 113*0 800000 65*0 2000000 32*0 10000000 19*0
  //   f8000000 fc000000 fc000000 3c000000 60*0 18000000 3e000000 3f000000 7f800000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
  //   contents of rom_5 (hex, n*v repeats v):
  //   c e 6 16 1e 3e 3e 3c 3c 1c 1c 1c c 4*4 15*0 2000007c 3c e000003c f00000fe f00000fc e00000fc 800000fc
  //   fc f8 18 1c 1c 1c c c 4 16*0 fffc03f8 fffc03fc fffc01fc fbf801fc fbf000f6 f9c00070 f0000030 c0000030
  //   10 10 10 18 18 8 18*0 603fff80 c03fff80 803fffc0 3fffc0 7fff80 1ffff80 fffff80 ffffff00 ffffff00
  //   fffffe00 fffffc00 fffff000 ffffe000 ffff0000 fffe0000 fff80000 ffc00000 fe000000 e0000000 13*0
  //   c00a3670 e0051010 c005101c c001b00c c001b004 8001700c 1100c 2224c 626d8 1c40b0 138c1a0 c610000
  //   71800000 0 0 2000000 6000000 111*0 ff000000 ff800000 ff800000 ffc00000 ffc00000 ff800000 ff000000
  //   fc000000 40000000 55*0 4*fc000000 f0000000 27*0 e0c00000 f1e00000 f7f80000 fffc0000 fff80000
  //   5*fff00000 400000 35*0 c00000 c00000 16*0 10000 70000 0 0 8000 4*0 40000 1f0c0000 7fc0000 1fc0000
  //   51*0 40 40 80 29*0 3fff4 3fff6 3fff4 7ffe4 1fffe4 7fffe4 1ffffe8 7ffffe0 3fffffe0 ffffff80 fffff890
  //   ffff00a0 fff000c0 ff800080 f0000000 17*0 c c c 8 8 8 c c 84 84 8c 8c 118 138 130 1b0 e0 60 14*0 1ff0
  //   1ff0 3ff0 3ff0 3fe0 ffe0 1fff0 ffff0 1ffff0 3ffff0 fffff0 13ffffe0 1fffff80 3ffffc00 bffff000 1fc000
  //   48*0 ff800000 ff000000 fe000000 fc000000 70000000 91*0 fffe0000 fffc0000 fff80000 fff00000 ffe00000
  //   ff800000 ff000000 f8000000 27*0 10000 30000 30000 40070000 c0070000 c00f0000 c01f0000 e03e0000
  //   fff80000 fff00000 3f800000 18*0 ffce0000 ff9c0000 fe180000 fc300000 fc600000 ffc00000 ff000000
  //   f0000000 24*0 c100c000 86018000 c078000 100f0000 701e0000 e01e0000 f03c0000 f0780000 fff80000
  //   ffe00000 ffc00000 fe000000 29*0 10000 80020000 c00c0000 e0380000 3fc00000 31*0 c0000000 18*0
  //   fc000000 fe000000 ff800000 c3e00000 c1f00000 e0700000 f0000000 c0000000 24*0 5*ffffffff ffffffe0
  //   4*ffffff80 ffffffc0 ffffffe0 fffffff0 fffffff8 fffffffc fffffffe 6*ffffffff ffff0fff fffc03ff
  //   fff801ff fff8007f fff0001f fff00007 fff80003 fffc0000 fffc0000 fffe0000 32*0 32*ffffffff 128*0
  //   1e000000 cf000000 fff80000 f83c0000 18180000 18000000 18000000 1c000000 38000000 38000000 22*0
  //   f8000000 40000000 20000000 29*0 200000 200000 0 0 0 8000 6000 6*0 40000000 40000000 145*0 ff000000
  //   f0000000 e0000000 e0000000 f0000000 4*f8000000 23*0 ffff0000 ffff0000 ffff0000 ffff8000 ffff8000
  //   5*ffffc000 ffff8000 ffff8000 ffff0000 fffe0000 fffc0000 fff00000 f0000000 c0000000 80000000 13*0
  //   7ffe00 3ffe00 e0600 60000 70000 78000 fc000 1fffe00 1ffffe00 4fffe00 fff00 7ff00 7ff00 7ff00 7fe00
  //   7fc00 c07f800 7ffff000 7fffe000 1f870000 cff00000 fff00000 3ffe0000 1fffc000 87ff8000 c0fc0000
  //   e0000000 5*0 7fffc00 1fff800 fff800 fffc00 fffc00 83fff800 fffff800 fffffe00 fffffe00 fffffe00
  //   3fffe00 fffe00 fffe00 7ffc00 fff800 fff000 ffffe000 ffffc000 ffff8000 ff800000 ff000000 ff000000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
  //   0.5倍速
  //   暂停
  //   2倍速
endmodule

// 单周期硬布线控制器
module \单周期硬布线控制器  (
  input  [5:0] OP,
  input  [5:0] Func,
  output [3:0] ALU_OP,
  output MemToReg,
  output MemWrite,
  output ALU_SRC,
  output RegWrite,
  output SysCALL,
  output SignedExt,
  output RegDst,
  output Beq,
  output Bne,
  output JR,
  output JMP,
  output JAL,
  output ERET
);

  wire and_1_out, and_2_out;

  \运算控制器自动生成  \u_运算控制器自动生成_1  (
    .OP0(OP[0]), .OP1(OP[1]), .OP2(OP[2]), .OP3(OP[3]), .OP4(OP[4]), .OP5(OP[5]), .F0(Func[0]), .F1(Func[1]),
    .F2(Func[2]), .F3(Func[3]), .F4(Func[4]), .F5(Func[5]), .S0(ALU_OP[0]), .S1(ALU_OP[1]), .S2(ALU_OP[2]),
    .S3(ALU_OP[3]));
  \控制信号自动生成  \u_控制信号自动生成_1  (
    .OP0(OP[0]), .OP1(OP[1]), .OP2(OP[2]), .OP3(OP[3]), .OP4(OP[4]), .OP5(OP[5]), .F0(Func[0]), .F1(Func[1]),
    .F2(Func[2]), .F3(Func[3]), .F4(Func[4]), .F5(Func[5]), .MemToReg(MemToReg), .MemWrite(MemWrite),
    .ALU_SRC(ALU_SRC), .RegWrite(RegWrite), .SysCALL(SysCALL), .SignedExt(SignedExt), .RegDst(RegDst),
    .BEQ(Beq), .BNE(Bne), .JR(JR), .JUMP(JMP), .JAL(JAL));
  and and_1 (and_1_out, ~OP[0], ~OP[1], ~OP[2], ~OP[3], OP[4], ~OP[5]);  // AND_Gate
  and and_2 (and_2_out, ~Func[0], ~Func[1], ~Func[2], Func[3], Func[4], ~Func[5]);  // AND_Gate
  and and_3 (ERET, and_1_out, and_2_out);

  // Other names for the same wires on the sheet: OP_CODE[5:0] = OP

  // Notes on the sheet:
  //   运算器控制器，根据指令生成运算器功能选择信号
  //   控制信号生成，产生数据通路需要的其他控制信号
endmodule

// 运算器控制器
module \运算控制器自动生成  (
  input  OP0,
  input  OP1,
  input  OP2,
  input  OP3,
  input  OP4,
  input  OP5,
  input  F0,
  input  F1,
  input  F2,
  input  F3,
  input  F4,
  input  F5,
  output S0,
  output S1,
  output S2,
  output S3
);

  wire and_1_out, and_2_out, and_3_out, and_4_out, and_5_out, and_6_out, and_7_out, and_8_out, and_9_out,
       and_10_out, and_11_out, and_12_out, and_13_out, and_14_out, and_15_out, and_16_out, and_17_out,
       and_18_out, and_19_out, and_20_out, and_21_out, and_22_out, and_23_out, and_24_out, and_25_out,
       and_26_out, and_27_out, and_28_out, and_29_out, and_30_out, and_31_out, and_32_out, and_33_out,
       and_34_out, not_1_out, not_2_out, not_3_out, not_4_out, not_5_out, not_6_out, not_7_out, not_8_out,
       not_9_out, not_10_out, not_11_out, not_12_out, not_13_out, not_14_out, not_15_out, not_16_out,
       not_17_out, not_18_out, not_19_out, not_20_out, not_21_out, not_22_out, not_23_out, not_24_out,
       not_25_out, not_26_out, not_27_out, not_28_out, not_29_out, not_30_out, not_31_out, not_32_out,
       not_33_out, not_34_out, not_35_out, not_36_out, not_37_out, not_38_out, not_39_out, not_40_out,
       not_41_out, not_42_out, not_43_out, not_44_out, not_45_out, not_46_out, not_47_out, not_48_out,
       not_49_out, not_50_out, not_51_out, not_52_out, not_53_out, not_54_out, not_55_out, not_56_out,
       not_57_out, not_58_out, not_59_out, not_60_out, not_61_out, not_62_out, not_63_out, not_64_out,
       not_65_out, not_66_out, not_67_out, not_68_out, not_69_out, not_70_out, not_71_out, not_72_out,
       not_73_out, not_74_out, not_75_out, not_76_out, not_77_out, not_78_out, not_79_out, not_80_out,
       not_81_out, not_82_out, not_83_out, not_84_out, not_85_out, not_86_out, not_87_out, not_88_out,
       not_89_out, not_90_out, not_91_out, not_92_out, not_93_out, not_94_out, not_95_out, not_96_out,
       not_97_out, not_98_out, not_99_out, not_100_out, not_101_out, not_102_out, not_103_out, not_104_out,
       not_105_out, not_106_out, not_107_out, not_108_out, not_109_out, not_110_out, not_111_out,
       not_112_out, not_113_out, not_114_out, not_115_out, not_116_out, not_117_out, not_118_out,
       not_119_out, not_120_out, not_121_out, not_122_out, not_123_out, not_124_out, not_125_out,
       not_126_out, not_127_out, not_128_out, not_129_out, not_130_out, not_131_out, not_132_out,
       not_133_out, not_134_out, not_135_out, not_136_out, not_137_out, not_138_out, not_139_out,
       not_140_out, not_141_out, not_142_out, not_143_out, not_144_out, not_145_out, not_146_out,
       not_147_out, not_148_out, not_149_out, not_150_out, not_151_out, not_152_out, not_153_out,
       not_154_out, not_155_out, not_156_out, not_157_out, not_158_out, not_159_out, not_160_out,
       not_161_out, not_162_out, not_163_out, not_164_out, not_165_out, not_166_out, not_167_out,
       not_168_out, not_169_out, not_170_out, not_171_out, not_172_out, not_173_out, not_174_out,
       not_175_out, not_176_out, not_177_out, not_178_out, not_179_out, not_180_out, not_181_out,
       not_182_out, not_183_out, not_184_out, not_185_out, not_186_out, not_187_out, not_188_out,
       not_189_out, not_190_out, not_191_out, not_192_out, not_193_out, not_194_out, not_195_out,
       not_196_out, not_197_out, not_198_out, not_199_out, not_200_out, not_201_out, not_202_out,
       not_203_out, not_204_out, not_205_out, not_206_out, not_207_out, not_208_out, not_209_out,
       not_210_out, not_211_out, not_212_out, not_213_out, not_214_out, not_215_out, not_216_out,
       not_217_out, not_218_out, not_219_out, not_220_out, not_221_out, not_222_out, not_223_out,
       not_224_out, not_225_out, not_226_out, not_227_out, not_228_out, not_229_out, not_230_out,
       not_231_out, not_232_out, not_233_out, not_234_out, not_235_out, not_236_out;

  not not_1 (not_1_out, OP5);
  not not_2 (not_2_out, OP4);
  not not_3 (not_3_out, OP3);
  not not_4 (not_4_out, OP2);
  not not_5 (not_5_out, OP1);
  not not_6 (not_6_out, OP0);
  not not_7 (not_7_out, F5);
  not not_8 (not_8_out, F4);
  not not_9 (not_9_out, F3);
  not not_10 (not_10_out, F2);
  not not_11 (not_11_out, OP5);
  not not_12 (not_12_out, OP4);
  not not_13 (not_13_out, OP3);
  not not_14 (not_14_out, OP2);
  not not_15 (not_15_out, OP1);
  not not_16 (not_16_out, OP0);
  not not_17 (not_17_out, F4);
  not not_18 (not_18_out, F3);
  not not_19 (not_19_out, F2);
  not not_20 (not_20_out, F1);
  not not_21 (not_21_out, F0);
  not not_22 (not_22_out, OP5);
  not not_23 (not_23_out, OP4);
  not not_24 (not_24_out, OP3);
  not not_25 (not_25_out, OP2);
  not not_26 (not_26_out, OP1);
  not not_27 (not_27_out, OP0);
  not not_28 (not_28_out, F4);
  not not_29 (not_29_out, F3);
  not not_30 (not_30_out, F2);
  not not_31 (not_31_out, F1);
  not not_32 (not_32_out, OP5);
  not not_33 (not_33_out, OP4);
  not not_34 (not_34_out, OP3);
  not not_35 (not_35_out, OP2);
  not not_36 (not_36_out, OP1);
  not not_37 (not_37_out, OP0);
  not not_38 (not_38_out, F4);
  not not_39 (not_39_out, F3);
  not not_40 (not_40_out, F1);
  not not_41 (not_41_out, F0);
  not not_42 (not_42_out, OP5);
  not not_43 (not_43_out, OP4);
  not not_44 (not_44_out, OP3);
  not not_45 (not_45_out, OP2);
  not not_46 (not_46_out, OP1);
  not not_47 (not_47_out, OP0);
  not not_48 (not_48_out, F4);
  not not_49 (not_49_out, F2);
  not not_50 (not_50_out, F0);
  not not_51 (not_51_out, OP5);
  not not_52 (not_52_out, OP4);
  not not_53 (not_53_out, OP2);
  not not_54 (not_54_out, OP1);
  not not_55 (not_55_out, OP0);
  not not_56 (not_56_out, OP5);
  not not_57 (not_57_out, OP4);
  not not_58 (not_58_out, OP1);
  not not_59 (not_59_out, OP0);
  not not_60 (not_60_out, OP5);
  not not_61 (not_61_out, OP4);
  not not_62 (not_62_out, OP2);
  not not_63 (not_63_out, OP1);
  not not_64 (not_64_out, OP5);
  not not_65 (not_65_out, OP4);
  not not_66 (not_66_out, OP2);
  not not_67 (not_67_out, OP0);
  not not_68 (not_68_out, OP4);
  not not_69 (not_69_out, OP3);
  not not_70 (not_70_out, OP2);
  not not_71 (not_71_out, OP4);
  not not_72 (not_72_out, OP2);
  not not_73 (not_73_out, OP5);
  not not_74 (not_74_out, OP4);
  not not_75 (not_75_out, OP3);
  not not_76 (not_76_out, OP2);
  not not_77 (not_77_out, OP1);
  not not_78 (not_78_out, OP0);
  not not_79 (not_79_out, F5);
  not not_80 (not_80_out, F4);
  not not_81 (not_81_out, F3);
  not not_82 (not_82_out, F2);
  not not_83 (not_83_out, F0);
  not not_84 (not_84_out, OP5);
  not not_85 (not_85_out, OP4);
  not not_86 (not_86_out, OP3);
  not not_87 (not_87_out, OP2);
  not not_88 (not_88_out, OP1);
  not not_89 (not_89_out, OP0);
  not not_90 (not_90_out, F4);
  not not_91 (not_91_out, F3);
  not not_92 (not_92_out, F2);
  not not_93 (not_93_out, F0);
  not not_94 (not_94_out, OP5);
  not not_95 (not_95_out, OP4);
  not not_96 (not_96_out, OP3);
  not not_97 (not_97_out, OP2);
  not not_98 (not_98_out, OP1);
  not not_99 (not_99_out, OP0);
  not not_100 (not_100_out, F4);
  not not_101 (not_101_out, F3);
  not not_102 (not_102_out, F1);
  not not_103 (not_103_out, F0);
  not not_104 (not_104_out, OP5);
  not not_105 (not_105_out, OP4);
  not not_106 (not_106_out, OP3);
  not not_107 (not_107_out, OP2);
  not not_108 (not_108_out, OP1);
  not not_109 (not_109_out, OP0);
  not not_110 (not_110_out, F4);
  not not_111 (not_111_out, F3);
  not not_112 (not_112_out, OP5);
  not not_113 (not_113_out, OP4);
  not not_114 (not_114_out, OP3);
  not not_115 (not_115_out, OP2);
  not not_116 (not_116_out, OP1);
  not not_117 (not_117_out, OP0);
  not not_118 (not_118_out, F4);
  not not_119 (not_119_out, F2);
  not not_120 (not_120_out, F0);
  not not_121 (not_121_out, OP5);
  not not_122 (not_122_out, OP4);
  not not_123 (not_123_out, OP1);
  not not_124 (not_124_out, OP0);
  not not_125 (not_125_out, OP5);
  not not_126 (not_126_out, OP4);
  not not_127 (not_127_out, OP2);
  not not_128 (not_128_out, OP0);
  not not_129 (not_129_out, OP5);
  not not_130 (not_130_out, OP4);
  not not_131 (not_131_out, OP3);
  not not_132 (not_132_out, OP2);
  not not_133 (not_133_out, OP1);
  not not_134 (not_134_out, OP0);
  not not_135 (not_135_out, F4);
  not not_136 (not_136_out, F3);
  not not_137 (not_137_out, F2);
  not not_138 (not_138_out, F1);
  not not_139 (not_139_out, F0);
  not not_140 (not_140_out, OP5);
  not not_141 (not_141_out, OP4);
  not not_142 (not_142_out, OP3);
  not not_143 (not_143_out, OP2);
  not not_144 (not_144_out, OP1);
  not not_145 (not_145_out, OP0);
  not not_146 (not_146_out, F4);
  not not_147 (not_147_out, F3);
  not not_148 (not_148_out, F2);
  not not_149 (not_149_out, F1);
  not not_150 (not_150_out, OP5);
  not not_151 (not_151_out, OP4);
  not not_152 (not_152_out, OP3);
  not not_153 (not_153_out, OP2);
  not not_154 (not_154_out, OP1);
  not not_155 (not_155_out, OP0);
  not not_156 (not_156_out, F4);
  not not_157 (not_157_out, F3);
  not not_158 (not_158_out, F2);
  not not_159 (not_159_out, F0);
  not not_160 (not_160_out, OP5);
  not not_161 (not_161_out, OP4);
  not not_162 (not_162_out, OP3);
  not not_163 (not_163_out, OP2);
  not not_164 (not_164_out, OP1);
  not not_165 (not_165_out, OP0);
  not not_166 (not_166_out, F4);
  not not_167 (not_167_out, F3);
  not not_168 (not_168_out, F1);
  not not_169 (not_169_out, F0);
  not not_170 (not_170_out, OP5);
  not not_171 (not_171_out, OP4);
  not not_172 (not_172_out, OP3);
  not not_173 (not_173_out, OP2);
  not not_174 (not_174_out, OP1);
  not not_175 (not_175_out, OP0);
  not not_176 (not_176_out, F4);
  not not_177 (not_177_out, F2);
  not not_178 (not_178_out, OP5);
  not not_179 (not_179_out, OP4);
  not not_180 (not_180_out, OP2);
  not not_181 (not_181_out, OP1);
  not not_182 (not_182_out, OP0);
  not not_183 (not_183_out, OP5);
  not not_184 (not_184_out, OP4);
  not not_185 (not_185_out, OP1);
  not not_186 (not_186_out, OP0);
  not not_187 (not_187_out, OP5);
  not not_188 (not_188_out, OP4);
  not not_189 (not_189_out, OP2);
  not not_190 (not_190_out, OP1);
  not not_191 (not_191_out, OP4);
  not not_192 (not_192_out, OP3);
  not not_193 (not_193_out, OP2);
  not not_194 (not_194_out, OP4);
  not not_195 (not_195_out, OP2);
  not not_196 (not_196_out, OP5);
  not not_197 (not_197_out, OP4);
  not not_198 (not_198_out, OP3);
  not not_199 (not_199_out, OP2);
  not not_200 (not_200_out, OP1);
  not not_201 (not_201_out, OP0);
  not not_202 (not_202_out, F4);
  not not_203 (not_203_out, F3);
  not not_204 (not_204_out, F1);
  not not_205 (not_205_out, OP5);
  not not_206 (not_206_out, OP4);
  not not_207 (not_207_out, OP3);
  not not_208 (not_208_out, OP2);
  not not_209 (not_209_out, OP1);
  not not_210 (not_210_out, OP0);
  not not_211 (not_211_out, F4);
  not not_212 (not_212_out, F3);
  not not_213 (not_213_out, OP5);
  not not_214 (not_214_out, OP4);
  not not_215 (not_215_out, OP3);
  not not_216 (not_216_out, OP2);
  not not_217 (not_217_out, OP1);
  not not_218 (not_218_out, OP0);
  not not_219 (not_219_out, F4);
  not not_220 (not_220_out, F2);
  not not_221 (not_221_out, F0);
  not not_222 (not_222_out, OP5);
  not not_223 (not_223_out, OP4);
  not not_224 (not_224_out, OP3);
  not not_225 (not_225_out, OP2);
  not not_226 (not_226_out, OP1);
  not not_227 (not_227_out, OP0);
  not not_228 (not_228_out, F4);
  not not_229 (not_229_out, F2);
  not not_230 (not_230_out, OP5);
  not not_231 (not_231_out, OP4);
  not not_232 (not_232_out, OP2);
  not not_233 (not_233_out, OP0);
  not not_234 (not_234_out, OP5);
  not not_235 (not_235_out, OP4);
  not not_236 (not_236_out, OP1);
  and and_1 (and_1_out, not_1_out, not_2_out, not_3_out, not_4_out, not_5_out, not_6_out, not_7_out, not_8_out, not_9_out, not_10_out, F1, F0);
  and and_2 (and_2_out, not_11_out, not_12_out, not_13_out, not_14_out, not_15_out, not_16_out, F5, not_17_out, not_18_out, not_19_out, not_20_out, not_21_out);
  and and_3 (and_3_out, not_22_out, not_23_out, not_24_out, not_25_out, not_26_out, not_27_out, F5, not_28_out, not_29_out, not_30_out, not_31_out, F0);
  and and_4 (and_4_out, not_32_out, not_33_out, not_34_out, not_35_out, not_36_out, not_37_out, F5, not_38_out, not_39_out, F2, not_40_out, not_41_out);
  and and_5 (and_5_out, not_42_out, not_43_out, not_44_out, not_45_out, not_46_out, not_47_out, F5, not_48_out, F3, not_49_out, F1, not_50_out);
  and and_6 (and_6_out, not_51_out, not_52_out, OP3, not_53_out, not_54_out, not_55_out);
  and and_7 (and_7_out, not_56_out, not_57_out, OP3, OP2, not_58_out, not_59_out);
  and and_8 (and_8_out, not_60_out, not_61_out, OP3, not_62_out, not_63_out, OP0);
  and and_9 (and_9_out, not_64_out, not_65_out, OP3, not_66_out, OP1, not_67_out);
  and and_10 (and_10_out, OP5, not_68_out, not_69_out, not_70_out, OP1, OP0);
  and and_11 (and_11_out, OP5, not_71_out, OP3, not_72_out, OP1, OP0);
  and and_12 (and_12_out, not_73_out, not_74_out, not_75_out, not_76_out, not_77_out, not_78_out, not_79_out, not_80_out, not_81_out, not_82_out, F1, not_83_out);
  and and_13 (and_13_out, not_84_out, not_85_out, not_86_out, not_87_out, not_88_out, not_89_out, F5, not_90_out, not_91_out, not_92_out, F1, not_93_out);
  and and_14 (and_14_out, not_94_out, not_95_out, not_96_out, not_97_out, not_98_out, not_99_out, F5, not_100_out, not_101_out, F2, not_102_out, not_103_out);
  and and_15 (and_15_out, not_104_out, not_105_out, not_106_out, not_107_out, not_108_out, not_109_out, F5, not_110_out, not_111_out, F2, F1, F0);
  and and_16 (and_16_out, not_112_out, not_113_out, not_114_out, not_115_out, not_116_out, not_117_out, F5, not_118_out, F3, not_119_out, F1, not_120_out);
  and and_17 (and_17_out, not_121_out, not_122_out, OP3, OP2, not_123_out, not_124_out);
  and and_18 (and_18_out, not_125_out, not_126_out, OP3, not_127_out, OP1, not_128_out);
  and and_19 (and_19_out, not_129_out, not_130_out, not_131_out, not_132_out, not_133_out, not_134_out, F5, not_135_out, not_136_out, not_137_out, not_138_out, not_139_out);
  and and_20 (and_20_out, not_140_out, not_141_out, not_142_out, not_143_out, not_144_out, not_145_out, F5, not_146_out, not_147_out, not_148_out, not_149_out, F0);
  and and_21 (and_21_out, not_150_out, not_151_out, not_152_out, not_153_out, not_154_out, not_155_out, F5, not_156_out, not_157_out, not_158_out, F1, not_159_out);
  and and_22 (and_22_out, not_160_out, not_161_out, not_162_out, not_163_out, not_164_out, not_165_out, F5, not_166_out, not_167_out, F2, not_168_out, not_169_out);
  and and_23 (and_23_out, not_170_out, not_171_out, not_172_out, not_173_out, not_174_out, not_175_out, F5, not_176_out, F3, not_177_out, F1, F0);
  and and_24 (and_24_out, not_178_out, not_179_out, OP3, not_180_out, not_181_out, not_182_out);
  and and_25 (and_25_out, not_183_out, not_184_out, OP3, OP2, not_185_out, not_186_out);
  and and_26 (and_26_out, not_187_out, not_188_out, OP3, not_189_out, not_190_out, OP0);
  and and_27 (and_27_out, OP5, not_191_out, not_192_out, not_193_out, OP1, OP0);
  and and_28 (and_28_out, OP5, not_194_out, OP3, not_195_out, OP1, OP0);
  and and_29 (and_29_out, not_196_out, not_197_out, not_198_out, not_199_out, not_200_out, not_201_out, F5, not_202_out, not_203_out, F2, not_204_out, F0);
  and and_30 (and_30_out, not_205_out, not_206_out, not_207_out, not_208_out, not_209_out, not_210_out, F5, not_211_out, not_212_out, F2, F1, F0);
  and and_31 (and_31_out, not_213_out, not_214_out, not_215_out, not_216_out, not_217_out, not_218_out, F5, not_219_out, F3, not_220_out, F1, not_221_out);
  and and_32 (and_32_out, not_222_out, not_223_out, not_224_out, not_225_out, not_226_out, not_227_out, F5, not_228_out, F3, not_229_out, F1, F0);
  and and_33 (and_33_out, not_230_out, not_231_out, OP3, not_232_out, OP1, not_233_out);
  and and_34 (and_34_out, not_234_out, not_235_out, OP3, OP2, not_236_out, OP0);
  or or_1 (S0, and_1_out, and_2_out, and_3_out, and_4_out, and_5_out, and_6_out, and_7_out, and_8_out, and_9_out, and_10_out, and_11_out);
  or or_2 (S1, and_12_out, and_13_out, and_14_out, and_15_out, and_16_out, and_17_out, and_18_out);
  or or_3 (S2, and_19_out, and_20_out, and_21_out, and_22_out, and_23_out, and_24_out, and_25_out, and_26_out, and_27_out, and_28_out);
  or or_4 (S3, and_29_out, and_30_out, and_31_out, and_32_out, and_33_out, and_34_out);
endmodule

// 控制信号生成
module \控制信号自动生成  (
  input  OP0,
  input  OP1,
  input  OP2,
  input  OP3,
  input  OP4,
  input  OP5,
  input  F0,
  input  F1,
  input  F2,
  input  F3,
  input  F4,
  input  F5,
  output MemToReg,
  output MemWrite,
  output ALU_SRC,
  output RegWrite,
  output SysCALL,
  output SignedExt,
  output RegDst,
  output BEQ,
  output BNE,
  output JR,
  output JUMP,
  output JAL
);

  wire and_3_out, and_4_out, and_5_out, and_6_out, and_7_out, and_8_out, and_9_out, and_10_out, and_11_out,
       and_12_out, and_13_out, and_15_out, and_16_out, and_17_out, and_18_out, and_19_out, and_20_out,
       and_21_out, and_22_out, and_23_out, and_24_out, and_25_out, and_26_out, and_30_out, and_31_out,
       not_1_out, not_2_out, not_3_out, not_4_out, not_5_out, not_6_out, not_7_out, not_8_out, not_9_out,
       not_10_out, not_11_out, not_12_out, not_13_out, not_14_out, not_15_out, not_16_out, not_17_out,
       not_18_out, not_19_out, not_20_out, not_21_out, not_22_out, not_23_out, not_24_out, not_25_out,
       not_26_out, not_27_out, not_28_out, not_29_out, not_30_out, not_31_out, not_32_out, not_33_out,
       not_34_out, not_35_out, not_36_out, not_37_out, not_38_out, not_39_out, not_40_out, not_41_out,
       not_42_out, not_43_out, not_44_out, not_45_out, not_46_out, not_47_out, not_48_out, not_49_out,
       not_50_out, not_51_out, not_52_out, not_53_out, not_54_out, not_55_out, not_56_out, not_57_out,
       not_58_out, not_59_out, not_60_out, not_61_out, not_62_out, not_63_out, not_64_out, not_65_out,
       not_66_out, not_67_out, not_68_out, not_69_out, not_70_out, not_71_out, not_72_out, not_73_out,
       not_74_out, not_75_out, not_76_out, not_77_out, not_78_out, not_79_out, not_80_out, not_81_out,
       not_82_out, not_83_out, not_84_out, not_85_out, not_86_out, not_87_out, not_88_out, not_89_out,
       not_90_out, not_91_out, not_92_out, not_93_out, not_94_out, not_95_out, not_96_out, not_97_out,
       not_98_out, not_99_out, not_100_out, not_101_out, not_102_out, not_103_out, not_104_out, not_105_out,
       not_106_out, not_107_out, not_108_out, not_109_out, not_110_out, not_111_out, not_112_out,
       not_113_out, not_114_out, not_115_out, not_116_out, not_117_out, not_118_out, not_119_out,
       not_120_out, not_121_out, not_122_out, not_123_out, not_124_out, not_125_out, not_126_out,
       not_127_out, not_128_out, not_129_out, not_130_out, not_131_out, not_132_out, not_133_out,
       not_134_out, not_135_out, not_136_out, not_137_out, not_138_out, not_139_out, not_140_out,
       not_141_out, not_142_out, not_143_out, not_144_out, not_145_out, not_146_out, not_147_out,
       not_148_out, not_149_out, not_150_out, not_151_out, not_152_out, not_153_out, not_154_out,
       not_155_out, not_156_out, not_157_out, not_158_out, not_159_out, not_160_out, not_161_out,
       not_162_out, not_163_out, not_164_out, not_165_out, not_166_out, not_167_out, not_168_out,
       not_169_out, not_170_out, not_171_out, not_172_out, not_173_out, not_174_out, not_175_out,
       not_176_out, not_177_out, not_178_out, not_179_out, not_180_out, not_181_out, not_182_out,
       not_183_out, not_184_out;

  not not_1 (not_1_out, OP2);
  not not_2 (not_2_out, OP3);
  not not_3 (not_3_out, OP4);
  not not_4 (not_4_out, OP2);
  not not_5 (not_5_out, OP4);
  not not_6 (not_6_out, OP0);
  not not_7 (not_7_out, OP2);
  not not_8 (not_8_out, OP4);
  not not_9 (not_9_out, OP5);
  not not_10 (not_10_out, OP1);
  not not_11 (not_11_out, OP4);
  not not_12 (not_12_out, OP5);
  not not_13 (not_13_out, OP2);
  not not_14 (not_14_out, OP4);
  not not_15 (not_15_out, OP0);
  not not_16 (not_16_out, OP1);
  not not_17 (not_17_out, OP2);
  not not_18 (not_18_out, OP4);
  not not_19 (not_19_out, OP5);
  not not_20 (not_20_out, F0);
  not not_21 (not_21_out, F2);
  not not_22 (not_22_out, F3);
  not not_23 (not_23_out, F4);
  not not_24 (not_24_out, OP0);
  not not_25 (not_25_out, OP1);
  not not_26 (not_26_out, OP2);
  not not_27 (not_27_out, OP4);
  not not_28 (not_28_out, OP5);
  not not_29 (not_29_out, F1);
  not not_30 (not_30_out, F3);
  not not_31 (not_31_out, F4);
  not not_32 (not_32_out, OP0);
  not not_33 (not_33_out, OP1);
  not not_34 (not_34_out, OP2);
  not not_35 (not_35_out, OP4);
  not not_36 (not_36_out, OP5);
  not not_37 (not_37_out, F2);
  not not_38 (not_38_out, F3);
  not not_39 (not_39_out, F4);
  not not_40 (not_40_out, F5);
  not not_41 (not_41_out, OP0);
  not not_42 (not_42_out, OP1);
  not not_43 (not_43_out, OP2);
  not not_44 (not_44_out, OP4);
  not not_45 (not_45_out, OP5);
  not not_46 (not_46_out, F2);
  not not_47 (not_47_out, F4);
  not not_48 (not_48_out, OP0);
  not not_49 (not_49_out, OP1);
  not not_50 (not_50_out, OP2);
  not not_51 (not_51_out, OP4);
  not not_52 (not_52_out, OP5);
  not not_53 (not_53_out, F3);
  not not_54 (not_54_out, F4);
  not not_55 (not_55_out, OP0);
  not not_56 (not_56_out, OP2);
  not not_57 (not_57_out, OP4);
  not not_58 (not_58_out, OP5);
  not not_59 (not_59_out, OP1);
  not not_60 (not_60_out, OP4);
  not not_61 (not_61_out, OP5);
  not not_62 (not_62_out, OP2);
  not not_63 (not_63_out, OP3);
  not not_64 (not_64_out, OP4);
  not not_65 (not_65_out, OP0);
  not not_66 (not_66_out, OP1);
  not not_67 (not_67_out, OP2);
  not not_68 (not_68_out, OP3);
  not not_69 (not_69_out, OP4);
  not not_70 (not_70_out, OP5);
  not not_71 (not_71_out, F0);
  not not_72 (not_72_out, F1);
  not not_73 (not_73_out, F4);
  not not_74 (not_74_out, F5);
  not not_75 (not_75_out, OP5);
  not not_76 (not_76_out, OP4);
  not not_77 (not_77_out, OP3);
  not not_78 (not_78_out, OP1);
  not not_79 (not_79_out, OP0);
  not not_80 (not_80_out, OP5);
  not not_81 (not_81_out, OP4);
  not not_82 (not_82_out, OP3);
  not not_83 (not_83_out, OP1);
  not not_84 (not_84_out, OP5);
  not not_85 (not_85_out, OP4);
  not not_86 (not_86_out, OP2);
  not not_87 (not_87_out, OP1);
  not not_88 (not_88_out, OP0);
  not not_89 (not_89_out, OP5);
  not not_90 (not_90_out, OP4);
  not not_91 (not_91_out, OP2);
  not not_92 (not_92_out, OP1);
  not not_93 (not_93_out, OP5);
  not not_94 (not_94_out, OP4);
  not not_95 (not_95_out, OP2);
  not not_96 (not_96_out, OP0);
  not not_97 (not_97_out, OP4);
  not not_98 (not_98_out, OP3);
  not not_99 (not_99_out, OP2);
  not not_100 (not_100_out, OP4);
  not not_101 (not_101_out, OP2);
  not not_102 (not_102_out, OP0);
  not not_103 (not_103_out, OP1);
  not not_104 (not_104_out, OP2);
  not not_105 (not_105_out, OP3);
  not not_106 (not_106_out, OP4);
  not not_107 (not_107_out, OP5);
  not not_108 (not_108_out, F0);
  not not_109 (not_109_out, F2);
  not not_110 (not_110_out, F3);
  not not_111 (not_111_out, F4);
  not not_112 (not_112_out, OP0);
  not not_113 (not_113_out, OP1);
  not not_114 (not_114_out, OP2);
  not not_115 (not_115_out, OP3);
  not not_116 (not_116_out, OP4);
  not not_117 (not_117_out, OP5);
  not not_118 (not_118_out, F1);
  not not_119 (not_119_out, F3);
  not not_120 (not_120_out, F4);
  not not_121 (not_121_out, OP0);
  not not_122 (not_122_out, OP1);
  not not_123 (not_123_out, OP2);
  not not_124 (not_124_out, OP3);
  not not_125 (not_125_out, OP4);
  not not_126 (not_126_out, OP5);
  not not_127 (not_127_out, F2);
  not not_128 (not_128_out, F3);
  not not_129 (not_129_out, F4);
  not not_130 (not_130_out, F5);
  not not_131 (not_131_out, OP0);
  not not_132 (not_132_out, OP1);
  not not_133 (not_133_out, OP2);
  not not_134 (not_134_out, OP3);
  not not_135 (not_135_out, OP4);
  not not_136 (not_136_out, OP5);
  not not_137 (not_137_out, F2);
  not not_138 (not_138_out, F4);
  not not_139 (not_139_out, OP0);
  not not_140 (not_140_out, OP1);
  not not_141 (not_141_out, OP2);
  not not_142 (not_142_out, OP3);
  not not_143 (not_143_out, OP4);
  not not_144 (not_144_out, OP5);
  not not_145 (not_145_out, F3);
  not not_146 (not_146_out, F4);
  not not_147 (not_147_out, OP0);
  not not_148 (not_148_out, OP1);
  not not_149 (not_149_out, OP3);
  not not_150 (not_150_out, OP4);
  not not_151 (not_151_out, OP5);
  not not_152 (not_152_out, OP1);
  not not_153 (not_153_out, OP3);
  not not_154 (not_154_out, OP4);
  not not_155 (not_155_out, OP5);
  not not_156 (not_156_out, OP0);
  not not_157 (not_157_out, OP1);
  not not_158 (not_158_out, OP2);
  not not_159 (not_159_out, OP3);
  not not_160 (not_160_out, OP4);
  not not_161 (not_161_out, OP5);
  not not_162 (not_162_out, F0);
  not not_163 (not_163_out, F1);
  not not_164 (not_164_out, F2);
  not not_165 (not_165_out, F4);
  not not_166 (not_166_out, F5);
  not not_167 (not_167_out, OP0);
  not not_168 (not_168_out, OP2);
  not not_169 (not_169_out, OP3);
  not not_170 (not_170_out, OP4);
  not not_171 (not_171_out, OP5);
  not not_172 (not_172_out, F0);
  not not_173 (not_173_out, F1);
  not not_174 (not_174_out, F2);
  not not_175 (not_175_out, F4);
  not not_176 (not_176_out, F5);
  not not_177 (not_177_out, OP2);
  not not_178 (not_178_out, OP3);
  not not_179 (not_179_out, OP4);
  not not_180 (not_180_out, OP5);
  not not_181 (not_181_out, OP2);
  not not_182 (not_182_out, OP3);
  not not_183 (not_183_out, OP4);
  not not_184 (not_184_out, OP5);
  and and_1 (MemToReg, OP0, OP1, not_1_out, not_2_out, not_3_out, OP5);
  and and_2 (MemWrite, OP0, OP1, not_4_out, OP3, not_5_out, OP5);
  and and_3 (and_3_out, not_6_out, not_7_out, OP3, not_8_out, not_9_out);
  and and_4 (and_4_out, not_10_out, OP3, not_11_out, not_12_out);
  or or_1 (ALU_SRC, and_3_out, and_4_out, and_5_out);
  and and_5 (and_5_out, OP0, OP1, not_13_out, not_14_out, OP5);
  and and_6 (and_6_out, not_15_out, not_16_out, not_17_out, not_18_out, not_19_out, not_20_out, not_21_out, not_22_out, not_23_out);
  and and_7 (and_7_out, not_24_out, not_25_out, not_26_out, not_27_out, not_28_out, not_29_out, not_30_out, not_31_out, F5);
  and and_8 (and_8_out, not_32_out, not_33_out, not_34_out, not_35_out, not_36_out, F1, not_37_out, not_38_out, not_39_out, not_40_out);
  and and_9 (and_9_out, not_41_out, not_42_out, not_43_out, not_44_out, not_45_out, F1, not_46_out, F3, not_47_out, F5);
  and and_10 (and_10_out, not_48_out, not_49_out, not_50_out, not_51_out, not_52_out, F0, F2, not_53_out, not_54_out, F5);
  and and_11 (and_11_out, not_55_out, not_56_out, OP3, not_57_out, not_58_out);
  and and_12 (and_12_out, not_59_out, OP3, not_60_out, not_61_out);
  and and_13 (and_13_out, OP0, OP1, not_62_out, not_63_out, not_64_out);
  and and_14 (SysCALL, not_65_out, not_66_out, not_67_out, not_68_out, not_69_out, not_70_out, not_71_out, not_72_out, F2, F3, not_73_out, not_74_out);
  and and_15 (and_15_out, not_75_out, not_76_out, not_77_out, OP2, not_78_out, not_79_out);
  and and_16 (and_16_out, not_80_out, not_81_out, not_82_out, OP2, not_83_out, OP0);
  and and_17 (and_17_out, not_84_out, not_85_out, OP3, not_86_out, not_87_out, not_88_out);
  and and_18 (and_18_out, not_89_out, not_90_out, OP3, not_91_out, not_92_out, OP0);
  and and_19 (and_19_out, not_93_out, not_94_out, OP3, not_95_out, OP1, not_96_out);
  and and_20 (and_20_out, OP5, not_97_out, not_98_out, not_99_out, OP1, OP0);
  and and_21 (and_21_out, OP5, not_100_out, OP3, not_101_out, OP1, OP0);
  and and_22 (and_22_out, not_102_out, not_103_out, not_104_out, not_105_out, not_106_out, not_107_out, not_108_out, not_109_out, not_110_out, not_111_out);
  and and_23 (and_23_out, not_112_out, not_113_out, not_114_out, not_115_out, not_116_out, not_117_out, not_118_out, not_119_out, not_120_out, F5);
  and and_24 (and_24_out, not_121_out, not_122_out, not_123_out, not_124_out, not_125_out, not_126_out, F1, not_127_out, not_128_out, not_129_out, not_130_out);
  and and_25 (and_25_out, not_131_out, not_132_out, not_133_out, not_134_out, not_135_out, not_136_out, F1, not_137_out, F3, not_138_out, F5);
  and and_26 (and_26_out, not_139_out, not_140_out, not_141_out, not_142_out, not_143_out, not_144_out, F0, F2, not_145_out, not_146_out, F5);
  and and_27 (BEQ, not_147_out, not_148_out, OP2, not_149_out, not_150_out, not_151_out);
  and and_28 (BNE, OP0, not_152_out, OP2, not_153_out, not_154_out, not_155_out);
  and and_29 (JR, not_156_out, not_157_out, not_158_out, not_159_out, not_160_out, not_161_out, not_162_out, not_163_out, not_164_out, F3, not_165_out, not_166_out);
  and and_30 (and_30_out, not_167_out, not_168_out, not_169_out, not_170_out, not_171_out, not_172_out, not_173_out, not_174_out, F3, not_175_out, not_176_out);
  and and_31 (and_31_out, OP1, not_177_out, not_178_out, not_179_out, not_180_out);
  and and_32 (JAL, OP0, OP1, not_181_out, not_182_out, not_183_out, not_184_out);
  or or_2 (RegWrite, and_6_out, and_7_out, and_8_out, and_9_out, and_10_out, and_11_out, and_12_out, and_13_out);
  or or_3 (SignedExt, and_15_out, and_16_out, and_17_out, and_18_out, and_19_out, and_20_out, and_21_out);
  or or_4 (RegDst, and_22_out, and_23_out, and_24_out, and_25_out, and_26_out);
  or or_5 (JUMP, and_30_out, and_31_out);
endmodule

// ALU
module MIPS_ALU (
  input  [4:0] shamt,
  input  [31:0] X,
  input  [31:0] Y,
  input  [3:0] AluOP,
  output Equal,
  output [31:0] Result,
  output [31:0] Result_2
);

  wire [0:0] comparator_1_lt, comparator_2_lt;
  wire [31:0] adder_1_out, AND_out, divider_1_out, divider_1_rem, multiplier_1_cout, multiplier_1_out,
       NOR_out, OR_out, shifter_1_out, shifter_2_out, shifter_3_out, subtractor_1_out, XOR_out;

  assign AND_out = X & Y;  // AND_Gate AND, 32 bits wide
  assign OR_out = X | Y;  // OR_Gate OR, 32 bits wide
  Shifter #(.width(32), .shift("ll")) shifter_1 (.in(Y), .\dist (shamt), .out(shifter_1_out));
  Shifter #(.width(32), .shift("ar")) shifter_2 (.in(Y), .\dist (shamt), .out(shifter_2_out));
  Shifter #(.width(32), .shift("lr")) shifter_3 (.in(Y), .\dist (shamt), .out(shifter_3_out));
  Multiplier #(.width(32)) multiplier_1 (.a(X), .b(Y), .out(multiplier_1_out), .cout(multiplier_1_cout));  // open: cin
  Divider #(.width(32)) divider_1 (.a(X), .b(Y), .out(divider_1_out), .rem(divider_1_rem));  // open: upper
  Adder #(.width(32)) adder_1 (.a(X), .b(Y), .out(adder_1_out));  // open: cin, cout
  Subtractor #(.width(32)) subtractor_1 (.a(X), .b(Y), .out(subtractor_1_out));  // open: bin, bout
  assign XOR_out = X ^ Y;  // XOR_Gate XOR, 32 bits wide
  assign NOR_out = ~(X | Y);  // NOR_Gate NOR, 32 bits wide
  Comparator #(.width(32), .mode("twosComplement")) comparator_1 (
    .a(X), .b(Y), .eq(Equal), .lt(comparator_1_lt[0]));  // open: gt
  Comparator #(.width(32), .mode("unsigned")) comparator_2 (.a(X), .b(Y), .lt(comparator_2_lt[0]));  // open: gt, eq
  Multiplexer #(.select(4), .width(32), .disabled("Z"), .enable("false")) multiplexer_1 (
    .in0(shifter_1_out), .in1(shifter_2_out), .in2(shifter_3_out), .in3(multiplier_1_out),
    .in4(divider_1_out), .in5(adder_1_out), .in6(subtractor_1_out), .in7(AND_out), .in8(OR_out),
    .in9(XOR_out), .in10(NOR_out), .in11({{31{1'b0}}, comparator_1_lt[0]}),
    .in12({{31{1'b0}}, comparator_2_lt[0]}), .in13({32{1'b0}}), .in14({32{1'b0}}), .in15({32{1'b0}}),
    .out(Result), .sel(AluOP));
  Multiplexer #(.select(4), .width(32), .disabled("Z"), .enable("false")) multiplexer_2 (
    .in0({32{1'b0}}), .in1({32{1'b0}}), .in2({32{1'b0}}), .in3(multiplier_1_cout), .in4(divider_1_rem),
    .in5({32{1'b0}}), .in6({32{1'b0}}), .in7({32{1'b0}}), .in8({32{1'b0}}), .in9({32{1'b0}}),
    .in10({32{1'b0}}), .in11({32{1'b0}}), .in12({32{1'b0}}), .in13({32{1'b0}}), .in14({32{1'b0}}),
    .in15({32{1'b0}}), .out(Result_2), .sel(AluOP));

  // Other names for the same wires on the sheet: Result2[31:0] = Result_2; S[3:0] = AluOP

  // Notes on the sheet:
  //   不要改变此引脚区域内容，也不要改变ALU封装形式
  //   输入引脚
  //   输出引脚
endmodule

module MIPS_Regifile (
  input  [31:0] Din,
  input  Clk,
  input  WE,
  input  [4:0] R1_num,
  input  [4:0] W_num,
  input  [4:0] R2_num,
  output [31:0] R1,
  output [31:0] R2
);

  // RegisterFile registerfile_1: pin names not known; wires that end beside it: Din, Clk, WE, W_num, R1_num, R2_num, R1, R2
endmodule

module \理想流水线  (
  output RegWrite,
  output MemWrite,
  output [31:0] IF_PC,
  output [31:0] ID_PC,
  output [31:0] EX_PC,
  output [31:0] M_PC,
  output [31:0] WB_PC,
  output [31:0] RDin,
  output [31:0] MDin,
  output [31:0] LedData
);

  wire CLK, clock_1_out, clock_2_out, comparator_1_eq, comparator_1_lt, d_ff_1_q, Go, IR1, IR2, IR3,
       nand_1_out, RST, W1, W2, W3;
  wire [12:0] CNT_num;
  wire [15:0] \LoadUse次数 , \总周期数 , \插入气泡数 , \无条件分支数 , \条件分支成功数 ;
  wire [31:0] EX_IR, ID_IR, IF_IR, MEM_IR, WB_IR;

  Button \u_总复位  (.out(RST));
  Button _1 (.out(IR1));
  Button _2 (.out(IR2));
  Button _3 (.out(IR3));
  // Probe on \总周期数 
  // Probe on \总周期数 
  Button \u_继续运行  (.out(Go));
  LED #(.active("true")) led_1 (.in(W1));
  LED #(.active("true")) led_2 (.in(W2));
  LED #(.active("true")) led_3 (.in(W3));
  Hex_Digit_Display hex_digit_display_1 (.value(LedData[31:28]));  // open: dp
  // Probe on IF_PC[19:0]
  // Mips_Probe mips_probe_1: pin names not known; wires that end beside it: IF_IR
  Hex_Digit_Display hex_digit_display_2 (.value(LedData[23:20]));  // open: dp
  Hex_Digit_Display hex_digit_display_3 (.value(LedData[27:24]));  // open: dp
  // Probe on ID_PC[19:0]
  // Mips_Probe mips_probe_2: pin names not known; wires that end beside it: ID_IR
  Hex_Digit_Display hex_digit_display_4 (.value(LedData[19:16]));  // open: dp
  Hex_Digit_Display hex_digit_display_5 (.value(LedData[15:12]));  // open: dp
  Hex_Digit_Display hex_digit_display_6 (.value(LedData[7:4]));  // open: dp
  Hex_Digit_Display hex_digit_display_7 (.value(LedData[11:8]));  // open: dp
  Clock #(.highDuration(1), .lowDuration(1)) clock_1 (.out(clock_1_out));
  // Probe on EX_PC[19:0]
  // Mips_Probe mips_probe_3: pin names not known; wires that end beside it: clock_1_out, EX_IR, CLK
  Hex_Digit_Display hex_digit_display_8 (.value(LedData[3:0]));  // open: dp
  // Probe on \总周期数 
  // Probe on M_PC[19:0]
  // Mips_Probe mips_probe_4: pin names not known; wires that end beside it: MEM_IR
  // Probe on \总周期数 
  // Probe on \无条件分支数 
  // Probe on \条件分支成功数 
  // Probe on \插入气泡数 
  // Probe on \LoadUse次数 
  // Probe on IF_PC[11:0]
  // Probe on WB_PC[19:0]
  // Mips_Probe mips_probe_5: pin names not known; wires that end beside it: WB_IR
  // Probe on ID_PC[11:0]
  // Probe on EX_PC[11:0]
  // Probe on M_PC[11:0]
  D_Flip_Flop #(.trigger("high"), .Pre_Clr_Positions("LEGACY"), .NegatePresetClear("false"), .enable("true"), .NewFFLayout("false")) d_ff_1 (.Q(d_ff_1_q));  // open: clk, D, Qn, preset, en, reset
  // Probe on 13'hc
  // Probe on WB_PC[11:0]
  Comparator #(.width(13), .mode("twosComplement")) comparator_1 (
    .a(CNT_num), .b(13'hc), .eq(comparator_1_eq), .lt(comparator_1_lt));  // open: gt
  Clock #(.highDuration(1), .lowDuration(1)) clock_2 (.out(clock_2_out));
  nand nand_1 (nand_1_out, d_ff_1_q, comparator_1_eq);
  Counter #(.width(13), .max('h1fff), .ongoal("stay"), .trigger("rising"), .behavior("old")) counter_1 (
    .count(comparator_1_lt), .Q(CNT_num), .clk(clock_2_out));  // open: load, D, carry, clr, preset
  assign CLK = nand_1_out ? clock_2_out : 1'bz;  // Controlled_Buffer controlled_buffer_1
  Pull_Resistor #(.pull(1)) pull_resistor_1 (.node(CLK));

  // Other names for the same wires on the sheet: MEM_PC[31:0] = M_PC

  // Notes on the sheet:
  //   中断源
  //   时空图监测，可删除
  //   中断等待指示
  //   数码管输出
  //   控制位
  //   流水调试日志用
  //   暂停节拍，不能为0
  //   戳工具置1进入计数暂停模式，ctrl+k时钟自动运行到对应节拍暂停
  //   ctrl+k关闭时钟连续运行，将控制位置零，进入单步调试模式调试
  //   用这个时钟源需要去掉电路中的其他时钟源
  //   可计数暂停的时钟源
  //   为方便自动评测，需要输出流水线各段保存的PC值，注意是PC不是PC+4，另外ID段寄存器写入信息，Mem段内存写入信息也要输出
endmodule

module \气泡流水线  (
  output RegWrite,
  output MemWrite,
  output [31:0] IF_PC,
  output [31:0] ID_PC,
  output [31:0] EX_PC,
  output [31:0] M_PC,
  output [31:0] WB_PC,
  output [31:0] RDin,
  output [31:0] MDin,
  output [31:0] LedData
);

  wire CLK, clock_2_out, comparator_1_eq, comparator_1_lt, d_ff_1_q, Go, IR1, IR2, IR3, nand_1_out, RST, W1,
       W2, W3;
  wire [12:0] CNT_num;
  wire [15:0] \LoadUse次数 , \总周期数 , \插入气泡数 , \无条件分支数 , \条件分支成功数 ;
  wire [31:0] EX_IR, ID_IR, IF_IR, MEM_IR, WB_IR;

  Button \u_总复位  (.out(RST));
  Button _1 (.out(IR1));
  Button _2 (.out(IR2));
  Button _3 (.out(IR3));
  // Probe on \总周期数 
  // Probe on \总周期数 
  Button \u_继续运行  (.out(Go));
  LED #(.active("true")) led_1 (.in(W1));
  LED #(.active("true")) led_2 (.in(W2));
  LED #(.active("true")) led_3 (.in(W3));
  Hex_Digit_Display hex_digit_display_1 (.value(LedData[31:28]));  // open: dp
  // Probe on IF_PC[19:0]
  // Mips_Probe mips_probe_1: pin names not known; wires that end beside it: IF_IR
  Hex_Digit_Display hex_digit_display_2 (.value(LedData[23:20]));  // open: dp
  Hex_Digit_Display hex_digit_display_3 (.value(LedData[27:24]));  // open: dp
  // Probe on ID_PC[19:0]
  // Mips_Probe mips_probe_2: pin names not known; wires that end beside it: ID_IR
  Hex_Digit_Display hex_digit_display_4 (.value(LedData[19:16]));  // open: dp
  Hex_Digit_Display hex_digit_display_5 (.value(LedData[15:12]));  // open: dp
  Hex_Digit_Display hex_digit_display_6 (.value(LedData[7:4]));  // open: dp
  Hex_Digit_Display hex_digit_display_7 (.value(LedData[11:8]));  // open: dp
  Clock #(.highDuration(1), .lowDuration(1)) clock_1 (.out(CLK));
  // Probe on EX_PC[19:0]
  // Mips_Probe mips_probe_3: pin names not known; wires that end beside it: EX_IR
  Hex_Digit_Display hex_digit_display_8 (.value(LedData[3:0]));  // open: dp
  // Probe on \总周期数 
  // Probe on M_PC[19:0]
  // Mips_Probe mips_probe_4: pin names not known; wires that end beside it: MEM_IR
  // Probe on \总周期数 
  // Probe on \无条件分支数 
  // Probe on \条件分支成功数 
  // Probe on \插入气泡数 
  // Probe on \LoadUse次数 
  // Probe on IF_PC[11:0]
  // Probe on WB_PC[19:0]
  // Mips_Probe mips_probe_5: pin names not known; wires that end beside it: WB_IR
  // Probe on ID_PC[11:0]
  // Probe on EX_PC[11:0]
  // Probe on M_PC[11:0]
  D_Flip_Flop #(.trigger("high"), .Pre_Clr_Positions("LEGACY"), .NegatePresetClear("false"), .enable("true"), .NewFFLayout("false")) d_ff_1 (.Q(d_ff_1_q));  // open: clk, D, Qn, preset, en, reset
  // Probe on 13'hc
  // Probe on WB_PC[11:0]
  Comparator #(.width(13), .mode("twosComplement")) comparator_1 (
    .a(CNT_num), .b(13'hc), .eq(comparator_1_eq), .lt(comparator_1_lt));  // open: gt
  Clock #(.highDuration(1), .lowDuration(1)) clock_2 (.out(clock_2_out));
  nand nand_1 (nand_1_out, d_ff_1_q, comparator_1_eq);
  Counter #(.width(13), .max('h1fff), .ongoal("stay"), .trigger("rising"), .behavior("old")) counter_1 (
    .count(comparator_1_lt), .Q(CNT_num), .clk(clock_2_out));  // open: load, D, carry, clr, preset
  assign CLK = nand_1_out ? clock_2_out : 1'bz;  // Controlled_Buffer controlled_buffer_1
  Pull_Resistor #(.pull(1)) pull_resistor_1 (.node(CLK));

  // Other names for the same wires on the sheet: MEM_PC[31:0] = M_PC

  // Notes on the sheet:
  //   中断源
  //   时空图监测，可删除
  //   中断等待指示
  //   数码管输出
  //   控制位
  //   流水调试日志用
  //   暂停节拍，不能为0
  //   戳工具置1进入计数暂停模式，ctrl+k时钟自动运行到对应节拍暂停
  //   ctrl+k关闭时钟连续运行，将控制位置零，进入单步调试模式调试
  //   可计数暂停的时钟源
  //   为方便自动评测，需要输出流水线各段保存的PC值，注意是PC不是PC+4，另外ID段寄存器写入信息，Mem段内存写入信息也要输出
endmodule

module \重定向流水线  (
  output RegWrite,
  output MemWrite,
  output [31:0] IF_PC,
  output [31:0] ID_PC,
  output [31:0] EX_PC,
  output [31:0] M_PC,
  output [31:0] WB_PC,
  output [31:0] RDin,
  output [31:0] MDin,
  output [31:0] LedData
);

  wire CLK, clock_2_out, comparator_1_eq, comparator_1_lt, d_ff_1_q, Go, IR1, IR2, IR3, nand_1_out, RST, W1,
       W2, W3;
  wire [12:0] CNT_num;
  wire [15:0] \LoadUse次数 , \总周期数 , \插入气泡数 , \无条件分支数 , \条件分支成功数 ;
  wire [31:0] EX_IR, ID_IR, IF_IR, MEM_IR, WB_IR;

  Button \u_总复位  (.out(RST));
  Button _1 (.out(IR1));
  Button _2 (.out(IR2));
  Button _3 (.out(IR3));
  // Probe on \总周期数 
  // Probe on \总周期数 
  Button \u_继续运行  (.out(Go));
  LED #(.active("true")) led_1 (.in(W1));
  LED #(.active("true")) led_2 (.in(W2));
  LED #(.active("true")) led_3 (.in(W3));
  Hex_Digit_Display hex_digit_display_1 (.value(LedData[31:28]));  // open: dp
  // Probe on IF_PC[19:0]
  // Mips_Probe mips_probe_1: pin names not known; wires that end beside it: IF_IR
  Hex_Digit_Display hex_digit_display_2 (.value(LedData[23:20]));  // open: dp
  Hex_Digit_Display hex_digit_display_3 (.value(LedData[27:24]));  // open: dp
  // Probe on ID_PC[19:0]
  // Mips_Probe mips_probe_2: pin names not known; wires that end beside it: ID_IR
  Hex_Digit_Display hex_digit_display_4 (.value(LedData[15:12]));  // open: dp
  Hex_Digit_Display hex_digit_display_5 (.value(LedData[19:16]));  // open: dp
  Hex_Digit_Display hex_digit_display_6 (.value(LedData[11:8]));  // open: dp
  Hex_Digit_Display hex_digit_display_7 (.value(LedData[7:4]));  // open: dp
  Clock #(.highDuration(1), .lowDuration(1)) clock_1 (.out(CLK));
  // Probe on EX_PC[19:0]
  // Mips_Probe mips_probe_3: pin names not known; wires that end beside it: EX_IR
  Hex_Digit_Display hex_digit_display_8 (.value(LedData[3:0]));  // open: dp
  // Probe on \总周期数 
  // Probe on M_PC[19:0]
  // Mips_Probe mips_probe_4: pin names not known; wires that end beside it: MEM_IR
  // Probe on \总周期数 
  // Probe on \无条件分支数 
  // Probe on \条件分支成功数 
  // Probe on \插入气泡数 
  // Probe on \LoadUse次数 
  // Probe on IF_PC[11:0]
  // Probe on WB_PC[19:0]
  // Mips_Probe mips_probe_5: pin names not known; wires that end beside it: WB_IR
  // Probe on EX_PC[11:0]
  // Probe on ID_PC[11:0]
  // Probe on M_PC[11:0]
  D_Flip_Flop #(.trigger("high"), .Pre_Clr_Positions("LEGACY"), .NegatePresetClear("false"), .enable("true"), .NewFFLayout("false")) d_ff_1 (.Q(d_ff_1_q));  // open: clk, D, Qn, preset, en, reset
  // Probe on 13'hc
  // Probe on WB_PC[11:0]
  Comparator #(.width(13), .mode("twosComplement")) comparator_1 (
    .a(CNT_num), .b(13'hc), .eq(comparator_1_eq), .lt(comparator_1_lt));  // open: gt
  Clock #(.highDuration(1), .lowDuration(1)) clock_2 (.out(clock_2_out));
  nand nand_1 (nand_1_out, d_ff_1_q, comparator_1_eq);
  Counter #(.width(13), .max('h1fff), .ongoal("stay"), .trigger("rising"), .behavior("old")) counter_1 (
    .count(comparator_1_lt), .Q(CNT_num), .clk(clock_2_out));  // open: load, D, carry, clr, preset
  assign CLK = nand_1_out ? clock_2_out : 1'bz;  // Controlled_Buffer controlled_buffer_1
  Pull_Resistor #(.pull(1)) pull_resistor_1 (.node(CLK));

  // Other names for the same wires on the sheet: MEM_PC[31:0] = M_PC

  // Notes on the sheet:
  //   中断源
  //   时空图监测，可删除
  //   中断等待指示
  //   数码管输出
  //   控制位
  //   流水调试日志用
  //   暂停节拍，不能为0
  //   戳工具置1进入计数暂停模式，ctrl+k时钟自动运行到对应节拍暂停
  //   ctrl+k关闭时钟连续运行，将控制位置零，进入单步调试模式调试
  //   可计数暂停的时钟源
  //   为方便自动评测，需要输出流水线各段保存的PC值，注意是PC不是PC+4，另外ID段寄存器写入信息，Mem段内存写入信息也要输出
endmodule

module \中断按键参考电路  (
  input  \同步清零信号 ,
  output \与中断屏蔽位与 
);

  wire \_1号中断_out , and_1_out, clock_1_out, d_ff_1_q, or_1_out, or_2_out;

  Clock #(.highDuration(1), .lowDuration(1)) clock_1 (.out(clock_1_out));
  Button \_1号中断  (.out(\_1号中断_out ));
  or or_1 (or_1_out, \与中断屏蔽位与 , d_ff_1_q);
  LED #(.active("true")) \_1号中断等待指示灯  (.in(or_1_out));
  D_Flip_Flop #(.trigger("rising"), .Pre_Clr_Positions("LEGACY"), .NegatePresetClear("false"), .enable("true"), .NewFFLayout("false")) d_ff_1 (
    .clk(\_1号中断_out ), .D(1'b1), .Q(d_ff_1_q), .reset(\与中断屏蔽位与 ));  // open: Qn, preset, en
  or or_2 (or_2_out, d_ff_1_q, \与中断屏蔽位与 );
  and and_1 (and_1_out, or_2_out, ~\同步清零信号 );  // AND_Gate
  D_Flip_Flop #(.trigger("rising"), .Pre_Clr_Positions("LEGACY"), .NegatePresetClear("false"), .enable("true"), .NewFFLayout("false")) IR1 (
    .clk(clock_1_out), .D(and_1_out), .Q(\与中断屏蔽位与 ));  // open: Qn, preset, en, reset

  // Notes on the sheet:
  //   中断信号采样参考电路
  //   Reset 
endmodule
module \单周期MIPS_单级中断  (
  input  IR1,
  input  IR2,
  input  IR3,
  output RegWrite,
  output MemWrite,
  output [31:0] PC,
  output [31:0] IR,
  output [31:0] RDin,
  output [31:0] MDin,
  output [31:0] LedData
);

  wire AluSrcB, and_1_out, and_2_out, and_3_out, and_4_out, and_5_out, and_10_out, and_11_out, Beq, Bne, CLK,
       comparator_1_eq, comparator_2_eq, comparator_3_eq, comparator_4_eq, comparator_5_eq, d_ff_1_q,
       d_ff_2_q, d_ff_3_q, decoder_1_out1, decoder_1_out2, decoder_1_out3, ERET, Go, halt, IE_ctrl, IE_q,
       IR1_q, IR1_t, IR2_q, IR2_t, IR3_q, IR3_t, IRA, IRB, IRC, JAL, JMP, JR, MemToReg, mips_alu_1_equal,
       not_1_out, not_2_out, or_4_out, or_5_out, or_6_out, or_9_out, or_11_out, or_12_out,
       priority_encoder_1_gs, RegDst, Rst1, Rst2, Rst3, SignedExt, Syscall, W1, W2, W3;
  wire [1:0] priority_encoder_1_out, register_1_q;
  wire [3:0] AluOP;
  wire [4:0] multiplexer_6_out, multiplexer_7_out, multiplexer_8_out, multiplexer_9_out;
  wire [15:0] \总周期数 ;
  wire [27:0] adder_1_out;
  wire [31:0] adder_2_out, bit_extender_1_out, bit_extender_2_out, EPC, mips_alu_1_result, multiplexer_2_out,
       multiplexer_3_out, multiplexer_4_out, multiplexer_5_out, multiplexer_11_out, multiplexer_12_out,
       multiplexer_14_out, OldEPC, ram_1_data, shifter_1_out, V0, \中断入口地址 ;
  wire [31:28] adder_1_out_2;

  Clock #(.highDuration(1), .lowDuration(1)) clock_1 (.out(CLK));
  Button _1 ();  // open: out
  Button _2 ();  // open: out
  Button _3 ();  // open: out
  Multiplexer #(.select(1), .width(32), .disabled("Z"), .enable("false")) multiplexer_1 (
    .in0(multiplexer_5_out), .in1(multiplexer_3_out), .out(OldEPC), .sel(JMP));
  Button \u_继续运行  (.out(Go));
  LED #(.active("true")) led_1 (.in(W1));
  LED #(.active("true")) led_2 (.in(W2));
  LED #(.active("true")) led_3 (.in(W3));
  Multiplexer #(.select(1), .width(32), .disabled("Z"), .enable("false")) multiplexer_2 (
    .in0(OldEPC), .in1(\中断入口地址 ), .out(multiplexer_2_out), .sel(IE_ctrl));
  Multiplexer #(.select(1), .width(32), .disabled("Z"), .enable("false")) multiplexer_3 (
    .in0({adder_1_out_2, IR[25:0], 2'b00}), .in1(V0), .out(multiplexer_3_out), .sel(JR));
  Hex_Digit_Display hex_digit_display_1 (.value(LedData[31:28]));  // open: dp
  Multiplexer #(.select(1), .width(32), .disabled("Z"), .enable("false")) multiplexer_4 (
    .in0(multiplexer_2_out), .in1(EPC), .out(multiplexer_4_out), .sel(ERET));
  Register #(.width(32), .trigger("rising"), .Select("low")) u_PC (
    .D(multiplexer_4_out), .en(not_1_out), .Q(PC), .clk(CLK));  // open: clr
  not not_1 (not_1_out, halt);
  Multiplexer #(.select(1), .width(32), .disabled("Z"), .enable("false")) multiplexer_5 (
    .in0({adder_1_out_2, adder_1_out}), .in1(adder_2_out), .out(multiplexer_5_out), .sel(or_11_out));
  or or_1 (W1, IR1_q, d_ff_1_q);
  or or_2 (W2, IR2_q, d_ff_2_q);
  or or_3 (W3, IR3_q, d_ff_3_q);
  Hex_Digit_Display hex_digit_display_2 (.value(LedData[23:20]));  // open: dp
  Hex_Digit_Display hex_digit_display_3 (.value(LedData[27:24]));  // open: dp
  Adder #(.width(32)) adder_1 (.a(PC), .b(32'h4), .out({adder_1_out_2, adder_1_out}));  // open: cin, cout
  D_Flip_Flop #(.trigger("rising"), .Pre_Clr_Positions("LEGACY"), .NegatePresetClear("false"), .enable("true"), .NewFFLayout("false")) d_ff_1 (
    .clk(IRA), .D(1'b1), .Q(d_ff_1_q), .reset(IR1_q));  // open: Qn, preset, en
  D_Flip_Flop #(.trigger("rising"), .Pre_Clr_Positions("LEGACY"), .NegatePresetClear("false"), .enable("true"), .NewFFLayout("false")) d_ff_2 (
    .clk(IRB), .D(1'b1), .Q(d_ff_2_q), .reset(IR2_q));  // open: Qn, preset, en
  D_Flip_Flop #(.trigger("rising"), .Pre_Clr_Positions("LEGACY"), .NegatePresetClear("false"), .enable("true"), .NewFFLayout("false")) d_ff_3 (
    .clk(IRC), .D(1'b1), .Q(d_ff_3_q), .reset(IR3_q));  // open: Qn, preset, en
  Hex_Digit_Display hex_digit_display_4 (.value(LedData[15:12]));  // open: dp
  Hex_Digit_Display hex_digit_display_5 (.value(LedData[19:16]));  // open: dp
  or or_4 (or_4_out, d_ff_1_q, IR1_q);
  or or_5 (or_5_out, d_ff_2_q, IR2_q);
  or or_6 (or_6_out, d_ff_3_q, IR3_q);
  Hex_Digit_Display hex_digit_display_6 (.value(LedData[11:8]));  // open: dp
  Hex_Digit_Display hex_digit_display_7 (.value(LedData[7:4]));  // open: dp
  // Probe on \总周期数 
  // Mips_Probe mips_probe_1: pin names not known; wires that end beside it: IR, IR[20:16]
  ROM #(.addrWidth(10), .dataWidth(32), .Select("high")) rom_1 (.addr(PC[11:2]), .data(IR));
  and and_1 (and_1_out, or_4_out, ~Rst1);  // AND_Gate
  and and_2 (and_2_out, or_5_out, ~Rst2);  // AND_Gate
  and and_3 (and_3_out, or_6_out, ~Rst3);  // AND_Gate
  Hex_Digit_Display hex_digit_display_8 (.value(LedData[3:0]));  // open: dp
  Multiplexer #(.select(1), .width(5), .disabled("Z"), .enable("false")) multiplexer_6 (
    .in0(IR[20:16]), .in1(IR[15:11]), .out(multiplexer_6_out), .sel(RegDst));
  D_Flip_Flop #(.trigger("rising"), .Pre_Clr_Positions("LEGACY"), .NegatePresetClear("false"), .enable("true"), .NewFFLayout("false")) u_IR1 (
    .clk(CLK), .D(and_1_out), .Q(IR1_q));  // open: Qn, preset, en, reset
  D_Flip_Flop #(.trigger("rising"), .Pre_Clr_Positions("LEGACY"), .NegatePresetClear("false"), .enable("true"), .NewFFLayout("false")) u_IR2 (
    .clk(CLK), .D(and_2_out), .Q(IR2_q));  // open: Qn, preset, en, reset
  D_Flip_Flop #(.trigger("rising"), .Pre_Clr_Positions("LEGACY"), .NegatePresetClear("false"), .enable("true"), .NewFFLayout("false")) u_IR3 (
    .clk(CLK), .D(and_3_out), .Q(IR3_q));  // open: Qn, preset, en, reset
  Multiplexer #(.select(1), .width(5), .disabled("Z"), .enable("false")) multiplexer_7 (
    .in0(IR[25:21]), .in1(5'b00010), .out(multiplexer_7_out), .sel(Syscall));
  Multiplexer #(.select(1), .width(5), .disabled("Z"), .enable("false")) multiplexer_8 (
    .in0(IR[20:16]), .in1(5'b00100), .out(multiplexer_8_out), .sel(Syscall));
  Multiplexer #(.select(1), .width(5), .disabled("Z"), .enable("false")) multiplexer_9 (
    .in0(multiplexer_6_out), .in1({5{1'b1}}), .out(multiplexer_9_out), .sel(JAL));
  Multiplexer #(.select(1), .width(32), .disabled("Z"), .enable("false")) multiplexer_10 (
    .in0(multiplexer_14_out), .in1({adder_1_out_2, adder_1_out}), .out(RDin), .sel(JAL));
  assign bit_extender_1_out = {{16{1'b0}}, IR[15:0]};  // Bit_Extender bit_extender_1
  assign bit_extender_2_out = {{16{IR[15]}}, IR[15:0]};  // Bit_Extender bit_extender_2
  or or_7 (IR1_t, IR1, IRA);
  Multiplexer #(.select(1), .width(32), .disabled("Z"), .enable("false")) multiplexer_11 (
    .in0(bit_extender_1_out), .in1(bit_extender_2_out), .out(multiplexer_11_out), .sel(SignedExt));
  or or_8 (IR2_t, IR2, IRB);
  MIPS_Regifile mips_regifile_1 (
    .Din(RDin), .Clk(CLK), .R1(V0), .R2(MDin), .WE(RegWrite), .W_num(multiplexer_9_out),
    .R1_num(multiplexer_7_out), .R2_num(multiplexer_8_out));
  Multiplexer #(.select(1), .width(32), .disabled("Z"), .enable("false")) multiplexer_12 (
    .in0(MDin), .in1(multiplexer_11_out), .out(multiplexer_12_out), .sel(AluSrcB));
  Shifter #(.width(32), .shift("ll")) shifter_1 (.in(bit_extender_2_out), .\dist (5'b00010), .out(shifter_1_out));
  Adder #(.width(32)) adder_2 (
    .a(shifter_1_out), .b({adder_1_out_2, adder_1_out}), .out(adder_2_out));  // open: cin, cout
  Register #(.width(32), .trigger("rising"), .Select("low")) \EPC寄存器  (
    .D(OldEPC), .en(IE_ctrl), .Q(EPC), .clk(CLK));  // open: clr
  or or_9 (or_9_out, ERET, IE_ctrl);
  Priority_Encoder #(.select(2), .disabled("Z")) priority_encoder_1 (
    .in0(1'b0), .in1(IR1_q), .in2(IR2_q), .in3(IR3_q), .out(priority_encoder_1_out),
    .gs(priority_encoder_1_gs));  // open: en_out, en_in
  or or_10 (IR3_t, IR3, IRC);
  and and_4 (and_4_out, Beq, mips_alu_1_equal);
  and and_5 (and_5_out, Bne, ~mips_alu_1_equal);  // AND_Gate
  MIPS_ALU mips_alu_1 (
    .X(V0), .Y(multiplexer_12_out), .AluOP(AluOP), .Equal(mips_alu_1_equal), .Result(mips_alu_1_result),
    .shamt(IR[10:6]));  // open: Result_2
  Register #(.width(1), .trigger("rising"), .Select("low")) IE (
    .D(IE_ctrl), .en(or_9_out), .Q(IE_q), .clk(CLK));  // open: clr
  Multiplexer #(.select(2), .width(32), .disabled("Z"), .enable("false")) multiplexer_13 (
    .in1(32'h30ac), .in2(32'h3150), .in3(32'h31f4), .out(\中断入口地址 ), .sel(priority_encoder_1_out));  // open: in0
  or or_11 (or_11_out, and_4_out, and_5_out);
  and and_6 (IE_ctrl, ~IE_q, priority_encoder_1_gs);  // AND_Gate
  Register #(.width(2), .trigger("rising"), .Select("low")) register_1 (
    .D(priority_encoder_1_out), .en(IE_ctrl), .Q(register_1_q), .clk(CLK));  // open: clr
  Decoder #(.select(2), .tristate("false"), .disabled("Z"), .enable("false")) decoder_1 (
    .out1(decoder_1_out1), .out2(decoder_1_out2), .out3(decoder_1_out3), .sel(register_1_q));  // open: out0
  RAM #(.addrWidth(10), .dataWidth(32), .bus("separate"), .Select("high")) ram_1 (
    .addr(mips_alu_1_result[11:2]), .din(MDin), .data(ram_1_data), .str(MemWrite), .clk(CLK));  // open: sel, ld, clr
  Multiplexer #(.select(1), .width(32), .disabled("Z"), .enable("false")) multiplexer_14 (
    .in0(mips_alu_1_result), .in1(ram_1_data), .out(multiplexer_14_out), .sel(MemToReg));
  and and_7 (Rst1, decoder_1_out1, ERET);
  and and_8 (Rst2, decoder_1_out2, ERET);
  and and_9 (Rst3, decoder_1_out3, ERET);
  \单周期硬布线控制器  \u_单周期硬布线控制器_1  (
    .Func(IR[5:0]), .OP(IR[31:26]), .ALU_OP(AluOP), .MemToReg(MemToReg), .MemWrite(MemWrite),
    .ALU_SRC(AluSrcB), .RegWrite(RegWrite), .SysCALL(Syscall), .SignedExt(SignedExt), .RegDst(RegDst),
    .JR(JR), .JMP(JMP), .Beq(Beq), .JAL(JAL), .Bne(Bne), .ERET(ERET));
  Comparator #(.width(32), .mode("twosComplement")) comparator_1 (
    .a(V0), .b(32'h22), .eq(comparator_1_eq));  // open: gt, lt
  Counter #(.width(16), .max('hffff), .ongoal("stay"), .trigger("rising"), .behavior("old")) counter_1 (
    .count(not_2_out), .Q(\总周期数 ), .clk(CLK));  // open: load, D, carry, clr, preset
  not not_2 (not_2_out, halt);
  and and_10 (and_10_out, Syscall, comparator_1_eq);
  and and_11 (and_11_out, ~comparator_1_eq, Syscall);  // AND_Gate
  Register #(.width(32), .trigger("rising"), .Select("low")) register_2 (
    .D(MDin), .en(and_10_out), .Q(LedData), .clk(CLK));  // open: clr
  and and_12 (halt, and_11_out, ~Go);  // AND_Gate
  Comparator #(.width(16), .mode("twosComplement")) comparator_2 (
    .a(16'h23b), .b(\总周期数 ), .eq(comparator_2_eq));  // open: gt, lt
  or or_12 (or_12_out, comparator_2_eq, comparator_3_eq);
  Comparator #(.width(16), .mode("twosComplement")) comparator_3 (
    .a(\总周期数 ), .b(16'h1), .eq(comparator_3_eq));  // open: gt, lt
  Comparator #(.width(16), .mode("twosComplement")) comparator_4 (
    .a(\总周期数 ), .b(16'h4), .eq(comparator_4_eq));  // open: gt, lt
  Comparator #(.width(16), .mode("twosComplement")) comparator_5 (
    .a(\总周期数 ), .b(16'h7), .eq(comparator_5_eq));  // open: gt, lt
  Pull_Resistor #(.pull(0)) pull_resistor_1 (.node(IRA));
  assign IRA = or_12_out ? ~CLK : 1'bz;  // Controlled_Inverter controlled_inverter_1
  Pull_Resistor #(.pull(0)) pull_resistor_2 (.node(IRB));
  assign IRB = comparator_4_eq ? ~CLK : 1'bz;  // Controlled_Inverter controlled_inverter_2
  Pull_Resistor #(.pull(0)) pull_resistor_3 (.node(IRC));
  assign IRC = comparator_5_eq ? ~CLK : 1'bz;  // Controlled_Inverter controlled_inverter_3

  // Other names for the same wires on the sheet: a0[31:0] = MDin; FUNC[5:0] = IR[5:0]; OP[5:0] = IR[31:26]

  // Notes on the sheet:
  //   中断源
  //   中断等待指示
  //   总复位信号应将除ROM以外所有存储组件全部清零
  //   PC + 4
  //   J & JAL
  //   JR
  //   数码管输出
  //   指令存储器
  //   中断信号产生电路
  //   数码管输出应该用寄存器锁存，否则显示数据只能一闪而过
  //   指令字
  //   contents of rom_1 (hex, n*v repeats v):
  //   201d07d0 20100001 109fc0 139fc3 8021 2012000c 24160008 26100001 3210000f 20080008 20090001 139900
  //   2709825 132020 20020022 c 1094022 1500fff9 22100001 2018000f 2188024 108700 20080008 20090001 139902
  //   2709825 132021 20020022 c 1094022 1500fff9 108702 2c9b022 12c00001 8000c07 4020 1084027 84400
  //   3508fff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
  //   OP
  //   Func
  //   rs
  //   rt
  //   rd
  //   sa
  //   imm
  //   Reset
  //   Reset
  //   Reset
  //   4号
  //   2号
  //   开中断
  //   BEQ & BNE
  //   保存断点
  //   关中断
  //   中断入口地址识别
  //   数据存储器
  //   为方便自动评测，需要输出PC，IR，寄存器堆写如数据RDin
  //   WriteBackData
  //   RAM写使能MemWrite、RAM写入数据MDin等信号
  //   IE寄存器的值为0时，此时表示可接受中断请求，处于开中断状态
  //   $v0 == 34， 显示a0的值，否则停机
  //   中断请求到来后，IE_ctrl会变为1，等待时钟到来后，会立刻保存Old_EPC的值
  //   同时，IE寄存器的值也因此从0变为1，处于关中断状态，IE_ctrl的值也会变为0
  //   直到ERET变为1的时候，IE寄存器的值才又会变为0，回到开中断状态
  //   Beq
  //   JMP
  //   JR
  //   Bne
  //   OP
  //   JAL
  //   Func
  //   Syscall
  //   中断请求清零信号
  //   MemToReg
  //   MemWrite
  //   AluOP
  //   AluSrcB
  //   RegWrite
  //   RegDst
  //   halt为1 表示停机，需要按键go重启
  //   单级中断测试信号模拟器
endmodule

module \单周期MIPS_多级中断  (
  input  IR1,
  input  IR2,
  input  IR3,
  output RegWrite,
  output MemWrite,
  output [31:0] PC,
  output [31:0] IR,
  output [31:0] RDin,
  output [31:0] MDin,
  output [31:0] LedData
);

  wire CLK, comparator_1_eq, comparator_2_eq, comparator_3_eq, comparator_4_eq, comparator_5_eq, Go, IR1_t,
       IR2_t, IR3_t, IRA, IRB, IRC, or_1_out, or_2_out, W1, W2, W3;
  wire [15:0] \总周期数 ;

  Clock #(.highDuration(1), .lowDuration(1)) clock_1 (.out(CLK));
  Button _1 ();  // open: out
  Button _2 ();  // open: out
  Button _3 ();  // open: out
  Button \u_继续运行  (.out(Go));
  LED #(.active("true")) led_1 (.in(W1));
  LED #(.active("true")) led_2 (.in(W2));
  LED #(.active("true")) led_3 (.in(W3));
  Hex_Digit_Display hex_digit_display_1 (.value(LedData[31:28]));  // open: dp
  Comparator #(.width(16), .mode("twosComplement")) comparator_1 (
    .a(\总周期数 ), .b(16'h7), .eq(comparator_1_eq));  // open: gt, lt
  Comparator #(.width(16), .mode("twosComplement")) comparator_2 (
    .a(\总周期数 ), .b(16'h241), .eq(comparator_2_eq));  // open: gt, lt
  Hex_Digit_Display hex_digit_display_2 (.value(LedData[27:24]));  // open: dp
  Hex_Digit_Display hex_digit_display_3 (.value(LedData[23:20]));  // open: dp
  Comparator #(.width(16), .mode("twosComplement")) comparator_3 (
    .a(16'h258), .b(\总周期数 ), .eq(comparator_3_eq));  // open: gt, lt
  or or_1 (or_1_out, comparator_3_eq, comparator_4_eq);
  Comparator #(.width(16), .mode("twosComplement")) comparator_4 (
    .a(\总周期数 ), .b(16'h1), .eq(comparator_4_eq));  // open: gt, lt
  Comparator #(.width(16), .mode("twosComplement")) comparator_5 (
    .a(\总周期数 ), .b(16'h4), .eq(comparator_5_eq));  // open: gt, lt
  or or_2 (or_2_out, comparator_1_eq, comparator_2_eq);
  Hex_Digit_Display hex_digit_display_4 (.value(LedData[19:16]));  // open: dp
  Hex_Digit_Display hex_digit_display_5 (.value(LedData[15:12]));  // open: dp
  Pull_Resistor #(.pull(0)) pull_resistor_1 (.node(IRA));
  assign IRA = or_1_out ? ~CLK : 1'bz;  // Controlled_Inverter controlled_inverter_1
  Pull_Resistor #(.pull(0)) pull_resistor_2 (.node(IRB));
  assign IRB = comparator_5_eq ? ~CLK : 1'bz;  // Controlled_Inverter controlled_inverter_2
  Pull_Resistor #(.pull(0)) pull_resistor_3 (.node(IRC));
  assign IRC = or_2_out ? ~CLK : 1'bz;  // Controlled_Inverter controlled_inverter_3
  Hex_Digit_Display hex_digit_display_6 (.value(LedData[11:8]));  // open: dp
  Hex_Digit_Display hex_digit_display_7 (.value(LedData[7:4]));  // open: dp
  // Probe on \总周期数 
  Hex_Digit_Display hex_digit_display_8 (.value(LedData[3:0]));  // open: dp
  or or_3 (IR1_t, IR1, IRA);
  or or_4 (IR2_t, IR2, IRB);
  or or_5 (IR3_t, IR3, IRC);

  // Notes on the sheet:
  //   中断源
  //   中断等待指示
  //   总复位信号应将除ROM以外所有存储组件全部清零
  //   多级中断测试信号模拟器
  //   数码管输出
  //   数码管输出应该用寄存器锁存，否则显示数据只能一闪而过
  //   为方便自动评测，需要输出PC，IR，寄存器堆写如数据RDin
  //   RAM写使能MemWrite、RAM写入数据MDin等信号
endmodule

module \封装正确性测试  (
);

  wire IR1, IR2, IR3, MemW, RegW;
  wire [31:0] EX_PC, ID_PC, IF_PC, IR, LED, MDin, MDinr, MEM_PC, PC, RDin, RDinr, WB_PC;

  \单周期MIPS  \u_单周期mips_1  (
    .RegWrite(RegW), .MemWrite(MemW), .PC(PC), .IR(IR), .RDin(RDin), .MDin(MDin), .LedData(LED));  // open: IR1, IR2, IR3
  \气泡流水线  \u_气泡流水线_1  (
    .RegWrite(RegW), .MemWrite(MemW), .IF_PC(IF_PC), .ID_PC(ID_PC), .EX_PC(EX_PC), .M_PC(MEM_PC),
    .WB_PC(WB_PC), .RDin(RDinr), .MDin(MDinr), .LedData(LED));
  \单周期MIPS_单级中断  \u_单周期mips_单级中断_1  (
    .IR1(IR1), .IR2(IR2), .IR3(IR3), .RegWrite(RegW), .MemWrite(MemW), .PC(PC), .IR(IR), .RDin(RDin),
    .MDin(MDin), .LedData(LED));
  \理想流水线  \u_理想流水线_1  (
    .RegWrite(RegW), .MemWrite(MemW), .IF_PC(IF_PC), .ID_PC(ID_PC), .EX_PC(EX_PC), .M_PC(MEM_PC),
    .WB_PC(WB_PC), .RDin(RDinr), .MDin(MDinr), .LedData(LED));
  \重定向流水线  \u_重定向流水线_1  (
    .RegWrite(RegW), .MemWrite(MemW), .IF_PC(IF_PC), .ID_PC(ID_PC), .EX_PC(EX_PC), .M_PC(MEM_PC),
    .WB_PC(WB_PC), .RDin(RDinr), .MDin(MDinr), .LedData(LED));
  \单周期MIPS_多级中断  \u_单周期mips_多级中断_1  (
    .IR1(IR1), .IR2(IR2), .IR3(IR3), .RegWrite(RegW), .MemWrite(MemW), .PC(PC), .IR(IR), .RDin(RDin),
    .MDin(MDin), .LedData(LED));

  // Notes on the sheet:
  //   单周期封装测试
  //   气泡流水封装测试
  //   单周期+单级中断封装测试
  //   请检查上面封装有无位宽不匹配，引脚标签是否和连接的标签相对应，否则无法在educoder平台上正确测试
  //   理想流水封装测试
  //   重定向流水封装测试
  //   单周期+多级中断封装测试
endmodule

module \LED点阵行信号输入  (
  input  [31:0] in_1,
  input  [31:0] in_2,
  input  [31:0] in_3,
  input  [31:0] in_4,
  input  [31:0] in_5,
  input  [31:0] in_6,
  input  [31:0] in_7,
  input  [31:0] in_8,
  input  [31:0] in_9,
  input  [31:0] in_10,
  input  [31:0] in_11,
  input  [31:0] in_12,
  input  [31:0] in_13,
  input  [31:0] in_14,
  input  [31:0] in_15,
  input  [31:0] in_16,
  input  [31:0] in_17,
  input  [31:0] in_18,
  input  [31:0] in_19,
  input  [31:0] in_20,
  input  [31:0] in_21,
  input  [31:0] in_22,
  input  [31:0] in_23,
  input  [31:0] in_24,
  input  [31:0] in_25,
  input  [31:0] in_26,
  input  [31:0] in_27,
  input  [31:0] in_28,
  input  [31:0] in_29,
  input  [31:0] in_30,
  input  [31:0] in_31,
  input  [31:0] in_32,
  input  [31:0] in_33,
  input  [31:0] in_34,
  input  [31:0] in_35,
  input  [31:0] in_36,
  input  [31:0] in_37,
  input  [31:0] in_38,
  input  [31:0] in_39,
  input  [31:0] in_40,
  input  [31:0] in_41,
  input  [31:0] in_42,
  input  [31:0] in_43,
  input  [31:0] in_44,
  input  [31:0] in_45,
  input  [31:0] in_46,
  input  [31:0] in_47,
  input  [31:0] in_48,
  input  [31:0] in_49,
  input  [31:0] in_50,
  input  [31:0] in_51,
  input  [31:0] in_52,
  input  [31:0] in_53,
  input  [31:0] in_54,
  input  [31:0] in_55,
  input  [31:0] in_56,
  input  [31:0] in_57,
  input  [31:0] in_58,
  input  [31:0] in_59,
  input  [31:0] in_60,
  input  [31:0] in_61,
  input  [31:0] in_62,
  input  [31:0] in_63,
  input  [31:0] in_64,
  input  [31:0] in_65,
  input  [31:0] in_66,
  input  [31:0] in_67,
  input  [31:0] in_68,
  input  [31:0] in_69,
  input  [31:0] in_70,
  input  [31:0] in_71,
  input  [31:0] in_72,
  input  [31:0] in_73,
  input  [31:0] in_74,
  input  [31:0] in_75,
  input  [31:0] in_76,
  input  [31:0] in_77,
  input  [31:0] in_78,
  input  [31:0] in_79,
  input  [31:0] in_80,
  input  [31:0] in_81,
  input  [31:0] in_82,
  input  [31:0] in_83,
  input  [31:0] in_84,
  input  [31:0] in_85,
  input  [31:0] in_86,
  input  [31:0] in_87,
  input  [31:0] in_88,
  input  [31:0] in_89,
  input  [31:0] in_90,
  input  [31:0] in_91,
  input  [31:0] in_92,
  input  [31:0] in_93,
  input  [31:0] in_94,
  input  [31:0] in_95,
  input  [31:0] in_96,
  input  [31:0] in_97,
  input  [31:0] in_98,
  input  [31:0] in_99,
  input  [31:0] in_100,
  input  [31:0] in_101,
  input  [31:0] in_102,
  input  [31:0] in_103,
  input  [31:0] in_104,
  input  [31:0] in_105,
  input  [31:0] in_106,
  input  [31:0] in_107,
  input  [31:0] in_108,
  input  [31:0] in_109,
  input  [31:0] in_110,
  input  [31:0] in_111,
  input  [31:0] in_112,
  input  [31:0] in_113,
  input  [31:0] in_114,
  input  [31:0] in_115,
  input  [31:0] in_116,
  input  [31:0] in_117,
  input  [31:0] in_118,
  input  [31:0] in_119,
  input  [31:0] in_120,
  input  [31:0] in_121,
  input  [31:0] in_122,
  input  [31:0] in_123,
  input  [31:0] in_124,
  input  [31:0] in_125,
  input  [31:0] in_126,
  input  [31:0] in_127,
  input  [31:0] in_128,
  output [31:0] out_129,
  output [31:0] out_130,
  output [31:0] out_131,
  output [31:0] out_132,
  output [31:0] out_133,
  output [31:0] out_134,
  output [31:0] out_135,
  output [31:0] out_136,
  output [31:0] out_137,
  output [31:0] out_138,
  output [31:0] out_139,
  output [31:0] out_140,
  output [31:0] out_141,
  output [31:0] out_142,
  output [31:0] out_143,
  output [31:0] out_144,
  output [31:0] out_145,
  output [31:0] out_146,
  output [31:0] out_147,
  output [31:0] out_148,
  output [31:0] out_149,
  output [31:0] out_150,
  output [31:0] out_151,
  output [31:0] out_152,
  output [31:0] out_153,
  output [31:0] out_154,
  output [31:0] out_155,
  output [31:0] out_156,
  output [31:0] out_157,
  output [31:0] out_158,
  output [31:0] out_159,
  output [31:0] out_160,
  output [31:0] out_161,
  output [31:0] out_162,
  output [31:0] out_163,
  output [31:0] out_164,
  output [31:0] out_165,
  output [31:0] out_166,
  output [31:0] out_167,
  output [31:0] out_168,
  output [31:0] out_169,
  output [31:0] out_170,
  output [31:0] out_171,
  output [31:0] out_172,
  output [31:0] out_173,
  output [31:0] out_174,
  output [31:0] out_175,
  output [31:0] out_176,
  output [31:0] out_177,
  output [31:0] out_178,
  output [31:0] out_179,
  output [31:0] out_180,
  output [31:0] out_181,
  output [31:0] out_182,
  output [31:0] out_183,
  output [31:0] out_184,
  output [31:0] out_185,
  output [31:0] out_186,
  output [31:0] out_187,
  output [31:0] out_188,
  output [31:0] out_189,
  output [31:0] out_190,
  output [31:0] out_191,
  output [31:0] out_192,
  output [31:0] out_193,
  output [31:0] out_194,
  output [31:0] out_195,
  output [31:0] out_196,
  output [31:0] out_197,
  output [31:0] out_198,
  output [31:0] out_199,
  output [31:0] out_200,
  output [31:0] out_201,
  output [31:0] out_202,
  output [31:0] out_203,
  output [31:0] out_204,
  output [31:0] out_205,
  output [31:0] out_206,
  output [31:0] out_207,
  output [31:0] out_208,
  output [31:0] out_209,
  output [31:0] out_210,
  output [31:0] out_211,
  output [31:0] out_212,
  output [31:0] out_213,
  output [31:0] out_214,
  output [31:0] out_215,
  output [31:0] out_216,
  output [31:0] out_217,
  output [31:0] out_218,
  output [31:0] out_219,
  output [31:0] out_220,
  output [31:0] out_221,
  output [31:0] out_222,
  output [31:0] out_223,
  output [31:0] out_224,
  output [31:0] out_225,
  output [31:0] out_226,
  output [31:0] out_227,
  output [31:0] out_228,
  output [31:0] out_229,
  output [31:0] out_230,
  output [31:0] out_231,
  output [31:0] out_232,
  output [31:0] out_233,
  output [31:0] out_234,
  output [31:0] out_235,
  output [31:0] out_236,
  output [31:0] out_237,
  output [31:0] out_238,
  output [31:0] out_239,
  output [31:0] out_240,
  output [31:0] out_241,
  output [31:0] out_242,
  output [31:0] out_243,
  output [31:0] out_244,
  output [31:0] out_245,
  output [31:0] out_246,
  output [31:0] out_247,
  output [31:0] out_248,
  output [31:0] out_249,
  output [31:0] out_250,
  output [31:0] out_251,
  output [31:0] out_252,
  output [31:0] out_253,
  output [31:0] out_254,
  output [31:0] out_255,
  output [31:0] out_256
);


  assign out_129 = in_1;
  assign out_130 = in_2;
  assign out_131 = in_3;
  assign out_132 = in_4;
  assign out_133 = in_5;
  assign out_134 = in_6;
  assign out_135 = in_7;
  assign out_136 = in_8;
  assign out_137 = in_9;
  assign out_138 = in_10;
  assign out_139 = in_11;
  assign out_140 = in_12;
  assign out_141 = in_13;
  assign out_142 = in_14;
  assign out_143 = in_15;
  assign out_144 = in_16;
  assign out_145 = in_17;
  assign out_146 = in_18;
  assign out_147 = in_19;
  assign out_148 = in_20;
  assign out_149 = in_21;
  assign out_150 = in_22;
  assign out_151 = in_23;
  assign out_152 = in_24;
  assign out_153 = in_25;
  assign out_154 = in_26;
  assign out_155 = in_27;
  assign out_156 = in_28;
  assign out_157 = in_29;
  assign out_158 = in_30;
  assign out_159 = in_31;
  assign out_160 = in_32;
  assign out_161 = in_33;
  assign out_162 = in_34;
  assign out_163 = in_35;
  assign out_164 = in_36;
  assign out_165 = in_37;
  assign out_166 = in_38;
  assign out_167 = in_39;
  assign out_168 = in_40;
  assign out_169 = in_41;
  assign out_170 = in_42;
  assign out_171 = in_43;
  assign out_172 = in_44;
  assign out_173 = in_45;
  assign out_174 = in_46;
  assign out_175 = in_47;
  assign out_176 = in_48;
  assign out_177 = in_49;
  assign out_178 = in_50;
  assign out_179 = in_51;
  assign out_180 = in_52;
  assign out_181 = in_53;
  assign out_182 = in_54;
  assign out_183 = in_55;
  assign out_184 = in_56;
  assign out_185 = in_57;
  assign out_186 = in_58;
  assign out_187 = in_59;
  assign out_188 = in_60;
  assign out_189 = in_61;
  assign out_190 = in_62;
  assign out_191 = in_63;
  assign out_192 = in_64;
  assign out_193 = in_65;
  assign out_194 = in_66;
  assign out_195 = in_67;
  assign out_196 = in_68;
  assign out_197 = in_69;
  assign out_198 = in_70;
  assign out_199 = in_71;
  assign out_200 = in_72;
  assign out_201 = in_73;
  assign out_202 = in_74;
  assign out_203 = in_75;
  assign out_204 = in_76;
  assign out_205 = in_77;
  assign out_206 = in_78;
  assign out_207 = in_79;
  assign out_208 = in_80;
  assign out_209 = in_81;
  assign out_210 = in_82;
  assign out_211 = in_83;
  assign out_212 = in_84;
  assign out_213 = in_85;
  assign out_214 = in_86;
  assign out_215 = in_87;
  assign out_216 = in_88;
  assign out_217 = in_89;
  assign out_218 = in_90;
  assign out_219 = in_91;
  assign out_220 = in_92;
  assign out_221 = in_93;
  assign out_222 = in_94;
  assign out_223 = in_95;
  assign out_224 = in_96;
  assign out_225 = in_97;
  assign out_226 = in_98;
  assign out_227 = in_99;
  assign out_228 = in_100;
  assign out_229 = in_101;
  assign out_230 = in_102;
  assign out_231 = in_103;
  assign out_232 = in_104;
  assign out_233 = in_105;
  assign out_234 = in_106;
  assign out_235 = in_107;
  assign out_236 = in_108;
  assign out_237 = in_109;
  assign out_238 = in_110;
  assign out_239 = in_111;
  assign out_240 = in_112;
  assign out_241 = in_113;
  assign out_242 = in_114;
  assign out_243 = in_115;
  assign out_244 = in_116;
  assign out_245 = in_117;
  assign out_246 = in_118;
  assign out_247 = in_119;
  assign out_248 = in_120;
  assign out_249 = in_121;
  assign out_250 = in_122;
  assign out_251 = in_123;
  assign out_252 = in_124;
  assign out_253 = in_125;
  assign out_254 = in_126;
  assign out_255 = in_127;
  assign out_256 = in_128;
endmodule

module \_64_64_LED点阵  (
);

  wire clock_1_out;
  wire [4:0] counter_2_q;
  wire [13:0] counter_1_q;
  wire [31:0] leddataleft_1_out_6, leddataleft_1_out_7, leddataleft_1_out_8, leddataleft_1_out_9,
       leddataleft_1_out_10, leddataleft_1_out_11, leddataleft_1_out_12, leddataleft_1_out_13,
       leddataleft_1_out_14, leddataleft_1_out_15, leddataleft_1_out_16, leddataleft_1_out_17,
       leddataleft_1_out_18, leddataleft_1_out_19, leddataleft_1_out_20, leddataleft_1_out_21,
       leddataleft_1_out_22, leddataleft_1_out_23, leddataleft_1_out_24, leddataleft_1_out_25,
       leddataleft_1_out_26, leddataleft_1_out_27, leddataleft_1_out_28, leddataleft_1_out_29,
       leddataleft_1_out_30, leddataleft_1_out_31, leddataleft_1_out_32, leddataleft_1_out_33,
       leddataleft_1_out_34, leddataleft_1_out_35, leddataleft_1_out_36, leddataleft_1_out_37,
       leddataleft_2_out_6, leddataleft_2_out_7, leddataleft_2_out_8, leddataleft_2_out_9,
       leddataleft_2_out_10, leddataleft_2_out_11, leddataleft_2_out_12, leddataleft_2_out_13,
       leddataleft_2_out_14, leddataleft_2_out_15, leddataleft_2_out_16, leddataleft_2_out_17,
       leddataleft_2_out_18, leddataleft_2_out_19, leddataleft_2_out_20, leddataleft_2_out_21,
       leddataleft_2_out_22, leddataleft_2_out_23, leddataleft_2_out_24, leddataleft_2_out_25,
       leddataleft_2_out_26, leddataleft_2_out_27, leddataleft_2_out_28, leddataleft_2_out_29,
       leddataleft_2_out_30, leddataleft_2_out_31, leddataleft_2_out_32, leddataleft_2_out_33,
       leddataleft_2_out_34, leddataleft_2_out_35, leddataleft_2_out_36, leddataleft_2_out_37,
       leddataright_1_out_6, leddataright_1_out_7, leddataright_1_out_8, leddataright_1_out_9,
       leddataright_1_out_10, leddataright_1_out_11, leddataright_1_out_12, leddataright_1_out_13,
       leddataright_1_out_14, leddataright_1_out_15, leddataright_1_out_16, leddataright_1_out_17,
       leddataright_1_out_18, leddataright_1_out_19, leddataright_1_out_20, leddataright_1_out_21,
       leddataright_1_out_22, leddataright_1_out_23, leddataright_1_out_24, leddataright_1_out_25,
       leddataright_1_out_26, leddataright_1_out_27, leddataright_1_out_28, leddataright_1_out_29,
       leddataright_1_out_30, leddataright_1_out_31, leddataright_1_out_32, leddataright_1_out_33,
       leddataright_1_out_34, leddataright_1_out_35, leddataright_1_out_36, leddataright_1_out_37,
       leddataright_2_out_6, leddataright_2_out_7, leddataright_2_out_8, leddataright_2_out_9,
       leddataright_2_out_10, leddataright_2_out_11, leddataright_2_out_12, leddataright_2_out_13,
       leddataright_2_out_14, leddataright_2_out_15, leddataright_2_out_16, leddataright_2_out_17,
       leddataright_2_out_18, leddataright_2_out_19, leddataright_2_out_20, leddataright_2_out_21,
       leddataright_2_out_22, leddataright_2_out_23, leddataright_2_out_24, leddataright_2_out_25,
       leddataright_2_out_26, leddataright_2_out_27, leddataright_2_out_28, leddataright_2_out_29,
       leddataright_2_out_30, leddataright_2_out_31, leddataright_2_out_32, leddataright_2_out_33,
       leddataright_2_out_34, leddataright_2_out_35, leddataright_2_out_36, leddataright_2_out_37,
       \led点阵行信号输入_1_out_129 , \led点阵行信号输入_1_out_130 , \led点阵行信号输入_1_out_131 , \led点阵行信号输入_1_out_132 ,
       \led点阵行信号输入_1_out_133 , \led点阵行信号输入_1_out_134 , \led点阵行信号输入_1_out_135 , \led点阵行信号输入_1_out_136 ,
       \led点阵行信号输入_1_out_137 , \led点阵行信号输入_1_out_138 , \led点阵行信号输入_1_out_139 , \led点阵行信号输入_1_out_140 ,
       \led点阵行信号输入_1_out_141 , \led点阵行信号输入_1_out_142 , \led点阵行信号输入_1_out_143 , \led点阵行信号输入_1_out_144 ,
       \led点阵行信号输入_1_out_145 , \led点阵行信号输入_1_out_146 , \led点阵行信号输入_1_out_147 , \led点阵行信号输入_1_out_148 ,
       \led点阵行信号输入_1_out_149 , \led点阵行信号输入_1_out_150 , \led点阵行信号输入_1_out_151 , \led点阵行信号输入_1_out_152 ,
       \led点阵行信号输入_1_out_153 , \led点阵行信号输入_1_out_154 , \led点阵行信号输入_1_out_155 , \led点阵行信号输入_1_out_156 ,
       \led点阵行信号输入_1_out_157 , \led点阵行信号输入_1_out_158 , \led点阵行信号输入_1_out_159 , \led点阵行信号输入_1_out_160 ,
       \led点阵行信号输入_1_out_161 , \led点阵行信号输入_1_out_162 , \led点阵行信号输入_1_out_163 , \led点阵行信号输入_1_out_164 ,
       \led点阵行信号输入_1_out_165 , \led点阵行信号输入_1_out_166 , \led点阵行信号输入_1_out_167 , \led点阵行信号输入_1_out_168 ,
       \led点阵行信号输入_1_out_169 , \led点阵行信号输入_1_out_170 , \led点阵行信号输入_1_out_171 , \led点阵行信号输入_1_out_172 ,
       \led点阵行信号输入_1_out_173 , \led点阵行信号输入_1_out_174 , \led点阵行信号输入_1_out_175 , \led点阵行信号输入_1_out_176 ,
       \led点阵行信号输入_1_out_177 , \led点阵行信号输入_1_out_178 , \led点阵行信号输入_1_out_179 , \led点阵行信号输入_1_out_180 ,
       \led点阵行信号输入_1_out_181 , \led点阵行信号输入_1_out_182 , \led点阵行信号输入_1_out_183 , \led点阵行信号输入_1_out_184 ,
       \led点阵行信号输入_1_out_185 , \led点阵行信号输入_1_out_186 , \led点阵行信号输入_1_out_187 , \led点阵行信号输入_1_out_188 ,
       \led点阵行信号输入_1_out_189 , \led点阵行信号输入_1_out_190 , \led点阵行信号输入_1_out_191 , \led点阵行信号输入_1_out_192 ,
       \led点阵行信号输入_1_out_193 , \led点阵行信号输入_1_out_194 , \led点阵行信号输入_1_out_195 , \led点阵行信号输入_1_out_196 ,
       \led点阵行信号输入_1_out_197 , \led点阵行信号输入_1_out_198 , \led点阵行信号输入_1_out_199 , \led点阵行信号输入_1_out_200 ,
       \led点阵行信号输入_1_out_201 , \led点阵行信号输入_1_out_202 , \led点阵行信号输入_1_out_203 , \led点阵行信号输入_1_out_204 ,
       \led点阵行信号输入_1_out_205 , \led点阵行信号输入_1_out_206 , \led点阵行信号输入_1_out_207 , \led点阵行信号输入_1_out_208 ,
       \led点阵行信号输入_1_out_209 , \led点阵行信号输入_1_out_210 , \led点阵行信号输入_1_out_211 , \led点阵行信号输入_1_out_212 ,
       \led点阵行信号输入_1_out_213 , \led点阵行信号输入_1_out_214 , \led点阵行信号输入_1_out_215 , \led点阵行信号输入_1_out_216 ,
       \led点阵行信号输入_1_out_217 , \led点阵行信号输入_1_out_218 , \led点阵行信号输入_1_out_219 , \led点阵行信号输入_1_out_220 ,
       \led点阵行信号输入_1_out_221 , \led点阵行信号输入_1_out_222 , \led点阵行信号输入_1_out_223 , \led点阵行信号输入_1_out_224 ,
       \led点阵行信号输入_1_out_225 , \led点阵行信号输入_1_out_226 , \led点阵行信号输入_1_out_227 , \led点阵行信号输入_1_out_228 ,
       \led点阵行信号输入_1_out_229 , \led点阵行信号输入_1_out_230 , \led点阵行信号输入_1_out_231 , \led点阵行信号输入_1_out_232 ,
       \led点阵行信号输入_1_out_233 , \led点阵行信号输入_1_out_234 , \led点阵行信号输入_1_out_235 , \led点阵行信号输入_1_out_236 ,
       \led点阵行信号输入_1_out_237 , \led点阵行信号输入_1_out_238 , \led点阵行信号输入_1_out_239 , \led点阵行信号输入_1_out_240 ,
       \led点阵行信号输入_1_out_241 , \led点阵行信号输入_1_out_242 , \led点阵行信号输入_1_out_243 , \led点阵行信号输入_1_out_244 ,
       \led点阵行信号输入_1_out_245 , \led点阵行信号输入_1_out_246 , \led点阵行信号输入_1_out_247 , \led点阵行信号输入_1_out_248 ,
       \led点阵行信号输入_1_out_249 , \led点阵行信号输入_1_out_250 , \led点阵行信号输入_1_out_251 , \led点阵行信号输入_1_out_252 ,
       \led点阵行信号输入_1_out_253 , \led点阵行信号输入_1_out_254 , \led点阵行信号输入_1_out_255 , \led点阵行信号输入_1_out_256 ,
       rom_1_data, rom_2_data, rom_3_data, rom_4_data;

  Counter #(.width(14), .max('h3fff), .ongoal("wrap"), .trigger("rising"), .behavior("new")) counter_1 (
    .D({14{1'b0}}), .Q(counter_1_q), .clk(clock_1_out));  // open: load, count, carry, clr, preset, down
  Clock #(.highDuration(1), .lowDuration(1)) clock_1 (.out(clock_1_out));
  ROM #(.addrWidth(14), .dataWidth(32), .Select("high")) rom_1 (.addr(counter_1_q), .data(rom_1_data));
  Counter #(.width(5), .max('h1f), .ongoal("wrap"), .trigger("rising"), .behavior("new")) counter_2 (
    .D({5{1'b0}}), .Q(counter_2_q), .clk(clock_1_out));  // open: load, count, carry, clr, preset, down
  ROM #(.addrWidth(14), .dataWidth(32), .Select("high")) rom_2 (.addr(counter_1_q), .data(rom_2_data));
  LedDataLeft leddataleft_1 (
    .CLK(clock_1_out), .DATA(rom_1_data), .en(1'b1), .out_6(leddataleft_1_out_6),
    .out_7(leddataleft_1_out_7), .out_8(leddataleft_1_out_8), .out_9(leddataleft_1_out_9),
    .out_10(leddataleft_1_out_10), .out_11(leddataleft_1_out_11), .out_12(leddataleft_1_out_12),
    .out_13(leddataleft_1_out_13), .out_14(leddataleft_1_out_14), .out_15(leddataleft_1_out_15),
    .out_16(leddataleft_1_out_16), .out_17(leddataleft_1_out_17), .out_18(leddataleft_1_out_18),
    .out_19(leddataleft_1_out_19), .out_20(leddataleft_1_out_20), .out_21(leddataleft_1_out_21),
    .out_22(leddataleft_1_out_22), .out_23(leddataleft_1_out_23), .out_24(leddataleft_1_out_24),
    .out_25(leddataleft_1_out_25), .out_26(leddataleft_1_out_26), .out_27(leddataleft_1_out_27),
    .out_28(leddataleft_1_out_28), .out_29(leddataleft_1_out_29), .out_30(leddataleft_1_out_30),
    .out_31(leddataleft_1_out_31), .out_32(leddataleft_1_out_32), .out_33(leddataleft_1_out_33),
    .out_34(leddataleft_1_out_34), .out_35(leddataleft_1_out_35), .out_36(leddataleft_1_out_36),
    .out_37(leddataleft_1_out_37), .in_5(counter_2_q));  // open: CLR
  LedDataLeft leddataleft_2 (
    .CLK(clock_1_out), .DATA(rom_2_data), .en(1'b1), .out_6(leddataleft_2_out_6),
    .out_7(leddataleft_2_out_7), .out_8(leddataleft_2_out_8), .out_9(leddataleft_2_out_9),
    .out_10(leddataleft_2_out_10), .out_11(leddataleft_2_out_11), .out_12(leddataleft_2_out_12),
    .out_13(leddataleft_2_out_13), .out_14(leddataleft_2_out_14), .out_15(leddataleft_2_out_15),
    .out_16(leddataleft_2_out_16), .out_17(leddataleft_2_out_17), .out_18(leddataleft_2_out_18),
    .out_19(leddataleft_2_out_19), .out_20(leddataleft_2_out_20), .out_21(leddataleft_2_out_21),
    .out_22(leddataleft_2_out_22), .out_23(leddataleft_2_out_23), .out_24(leddataleft_2_out_24),
    .out_25(leddataleft_2_out_25), .out_26(leddataleft_2_out_26), .out_27(leddataleft_2_out_27),
    .out_28(leddataleft_2_out_28), .out_29(leddataleft_2_out_29), .out_30(leddataleft_2_out_30),
    .out_31(leddataleft_2_out_31), .out_32(leddataleft_2_out_32), .out_33(leddataleft_2_out_33),
    .out_34(leddataleft_2_out_34), .out_35(leddataleft_2_out_35), .out_36(leddataleft_2_out_36),
    .out_37(leddataleft_2_out_37), .in_5(counter_2_q));  // open: CLR
  LedDataRight leddataright_1 (
    .CLK(clock_1_out), .DATA(rom_3_data), .en(1'b1), .out_6(leddataright_1_out_6),
    .out_7(leddataright_1_out_7), .out_8(leddataright_1_out_8), .out_9(leddataright_1_out_9),
    .out_10(leddataright_1_out_10), .out_11(leddataright_1_out_11), .out_12(leddataright_1_out_12),
    .out_13(leddataright_1_out_13), .out_14(leddataright_1_out_14), .out_15(leddataright_1_out_15),
    .out_16(leddataright_1_out_16), .out_17(leddataright_1_out_17), .out_18(leddataright_1_out_18),
    .out_19(leddataright_1_out_19), .out_20(leddataright_1_out_20), .out_21(leddataright_1_out_21),
    .out_22(leddataright_1_out_22), .out_23(leddataright_1_out_23), .out_24(leddataright_1_out_24),
    .out_25(leddataright_1_out_25), .out_26(leddataright_1_out_26), .out_27(leddataright_1_out_27),
    .out_28(leddataright_1_out_28), .out_29(leddataright_1_out_29), .out_30(leddataright_1_out_30),
    .out_31(leddataright_1_out_31), .out_32(leddataright_1_out_32), .out_33(leddataright_1_out_33),
    .out_34(leddataright_1_out_34), .out_35(leddataright_1_out_35), .out_36(leddataright_1_out_36),
    .out_37(leddataright_1_out_37), .in_5(counter_2_q));  // open: CLR
  \LED点阵行信号输入  \led点阵行信号输入_1  (
    .in_1(leddataleft_1_out_6), .in_2(leddataleft_1_out_7), .in_3(leddataleft_1_out_8),
    .in_4(leddataleft_1_out_9), .in_5(leddataleft_1_out_10), .in_6(leddataleft_1_out_11),
    .in_7(leddataleft_1_out_12), .in_8(leddataleft_1_out_13), .in_9(leddataleft_1_out_14),
    .in_10(leddataleft_1_out_15), .in_11(leddataleft_1_out_16), .in_12(leddataleft_1_out_17),
    .in_13(leddataleft_1_out_18), .in_14(leddataleft_1_out_19), .in_15(leddataleft_1_out_20),
    .in_16(leddataleft_1_out_21), .in_17(leddataleft_1_out_22), .in_18(leddataleft_1_out_23),
    .in_19(leddataleft_1_out_24), .in_20(leddataleft_1_out_25), .in_21(leddataleft_1_out_26),
    .in_22(leddataleft_1_out_27), .in_23(leddataleft_1_out_28), .in_24(leddataleft_1_out_29),
    .in_25(leddataleft_1_out_30), .in_26(leddataleft_1_out_31), .in_27(leddataleft_1_out_32),
    .in_28(leddataleft_1_out_33), .in_29(leddataleft_1_out_34), .in_30(leddataleft_1_out_35),
    .in_31(leddataleft_1_out_36), .in_32(leddataleft_1_out_37), .in_33(leddataleft_2_out_6),
    .in_34(leddataleft_2_out_7), .in_35(leddataleft_2_out_8), .in_36(leddataleft_2_out_9),
    .in_37(leddataleft_2_out_10), .in_38(leddataleft_2_out_11), .in_39(leddataleft_2_out_12),
    .in_40(leddataleft_2_out_13), .in_41(leddataleft_2_out_14), .in_42(leddataleft_2_out_15),
    .in_43(leddataleft_2_out_16), .in_44(leddataleft_2_out_17), .in_45(leddataleft_2_out_18),
    .in_46(leddataleft_2_out_19), .in_47(leddataleft_2_out_20), .in_48(leddataleft_2_out_21),
    .in_49(leddataleft_2_out_22), .in_50(leddataleft_2_out_23), .in_51(leddataleft_2_out_24),
    .in_52(leddataleft_2_out_25), .in_53(leddataleft_2_out_26), .in_54(leddataleft_2_out_27),
    .in_55(leddataleft_2_out_28), .in_56(leddataleft_2_out_29), .in_57(leddataleft_2_out_30),
    .in_58(leddataleft_2_out_31), .in_59(leddataleft_2_out_32), .in_60(leddataleft_2_out_33),
    .in_61(leddataleft_2_out_34), .in_62(leddataleft_2_out_35), .in_63(leddataleft_2_out_36),
    .in_64(leddataleft_2_out_37), .in_65(leddataright_1_out_6), .in_66(leddataright_1_out_7),
    .in_67(leddataright_1_out_8), .in_68(leddataright_1_out_9), .in_69(leddataright_1_out_10),
    .in_70(leddataright_1_out_11), .in_71(leddataright_1_out_12), .in_72(leddataright_1_out_13),
    .in_73(leddataright_1_out_14), .in_74(leddataright_1_out_15), .in_75(leddataright_1_out_16),
    .in_76(leddataright_1_out_17), .in_77(leddataright_1_out_18), .in_78(leddataright_1_out_19),
    .in_79(leddataright_1_out_20), .in_80(leddataright_1_out_21), .in_81(leddataright_1_out_22),
    .in_82(leddataright_1_out_23), .in_83(leddataright_1_out_24), .in_84(leddataright_1_out_25),
    .in_85(leddataright_1_out_26), .in_86(leddataright_1_out_27), .in_87(leddataright_1_out_28),
    .in_88(leddataright_1_out_29), .in_89(leddataright_1_out_30), .in_90(leddataright_1_out_31),
    .in_91(leddataright_1_out_32), .in_92(leddataright_1_out_33), .in_93(leddataright_1_out_34),
    .in_94(leddataright_1_out_35), .in_95(leddataright_1_out_36), .in_96(leddataright_1_out_37),
    .in_97(leddataright_2_out_6), .in_98(leddataright_2_out_7), .in_99(leddataright_2_out_8),
    .in_100(leddataright_2_out_9), .in_101(leddataright_2_out_10), .in_102(leddataright_2_out_11),
    .in_103(leddataright_2_out_12), .in_104(leddataright_2_out_13), .in_105(leddataright_2_out_14),
    .in_106(leddataright_2_out_15), .in_107(leddataright_2_out_16), .in_108(leddataright_2_out_17),
    .in_109(leddataright_2_out_18), .in_110(leddataright_2_out_19), .in_111(leddataright_2_out_20),
    .in_112(leddataright_2_out_21), .in_113(leddataright_2_out_22), .in_114(leddataright_2_out_23),
    .in_115(leddataright_2_out_24), .in_116(leddataright_2_out_25), .in_117(leddataright_2_out_26),
    .in_118(leddataright_2_out_27), .in_119(leddataright_2_out_28), .in_120(leddataright_2_out_29),
    .in_121(leddataright_2_out_30), .in_122(leddataright_2_out_31), .in_123(leddataright_2_out_32),
    .in_124(leddataright_2_out_33), .in_125(leddataright_2_out_34), .in_126(leddataright_2_out_35),
    .in_127(leddataright_2_out_36), .in_128(leddataright_2_out_37), .out_129(\led点阵行信号输入_1_out_129 ),
    .out_130(\led点阵行信号输入_1_out_130 ), .out_131(\led点阵行信号输入_1_out_131 ), .out_132(\led点阵行信号输入_1_out_132 ),
    .out_133(\led点阵行信号输入_1_out_133 ), .out_134(\led点阵行信号输入_1_out_134 ), .out_135(\led点阵行信号输入_1_out_135 ),
    .out_136(\led点阵行信号输入_1_out_136 ), .out_137(\led点阵行信号输入_1_out_137 ), .out_138(\led点阵行信号输入_1_out_138 ),
    .out_139(\led点阵行信号输入_1_out_139 ), .out_140(\led点阵行信号输入_1_out_140 ), .out_141(\led点阵行信号输入_1_out_141 ),
    .out_142(\led点阵行信号输入_1_out_142 ), .out_143(\led点阵行信号输入_1_out_143 ), .out_144(\led点阵行信号输入_1_out_144 ),
    .out_145(\led点阵行信号输入_1_out_145 ), .out_146(\led点阵行信号输入_1_out_146 ), .out_147(\led点阵行信号输入_1_out_147 ),
    .out_148(\led点阵行信号输入_1_out_148 ), .out_149(\led点阵行信号输入_1_out_149 ), .out_150(\led点阵行信号输入_1_out_150 ),
    .out_151(\led点阵行信号输入_1_out_151 ), .out_152(\led点阵行信号输入_1_out_152 ), .out_153(\led点阵行信号输入_1_out_153 ),
    .out_154(\led点阵行信号输入_1_out_154 ), .out_155(\led点阵行信号输入_1_out_155 ), .out_156(\led点阵行信号输入_1_out_156 ),
    .out_157(\led点阵行信号输入_1_out_157 ), .out_158(\led点阵行信号输入_1_out_158 ), .out_159(\led点阵行信号输入_1_out_159 ),
    .out_160(\led点阵行信号输入_1_out_160 ), .out_161(\led点阵行信号输入_1_out_161 ), .out_162(\led点阵行信号输入_1_out_162 ),
    .out_163(\led点阵行信号输入_1_out_163 ), .out_164(\led点阵行信号输入_1_out_164 ), .out_165(\led点阵行信号输入_1_out_165 ),
    .out_166(\led点阵行信号输入_1_out_166 ), .out_167(\led点阵行信号输入_1_out_167 ), .out_168(\led点阵行信号输入_1_out_168 ),
    .out_169(\led点阵行信号输入_1_out_169 ), .out_170(\led点阵行信号输入_1_out_170 ), .out_171(\led点阵行信号输入_1_out_171 ),
    .out_172(\led点阵行信号输入_1_out_172 ), .out_173(\led点阵行信号输入_1_out_173 ), .out_174(\led点阵行信号输入_1_out_174 ),
    .out_175(\led点阵行信号输入_1_out_175 ), .out_176(\led点阵行信号输入_1_out_176 ), .out_177(\led点阵行信号输入_1_out_177 ),
    .out_178(\led点阵行信号输入_1_out_178 ), .out_179(\led点阵行信号输入_1_out_179 ), .out_180(\led点阵行信号输入_1_out_180 ),
    .out_181(\led点阵行信号输入_1_out_181 ), .out_182(\led点阵行信号输入_1_out_182 ), .out_183(\led点阵行信号输入_1_out_183 ),
    .out_184(\led点阵行信号输入_1_out_184 ), .out_185(\led点阵行信号输入_1_out_185 ), .out_186(\led点阵行信号输入_1_out_186 ),
    .out_187(\led点阵行信号输入_1_out_187 ), .out_188(\led点阵行信号输入_1_out_188 ), .out_189(\led点阵行信号输入_1_out_189 ),
    .out_190(\led点阵行信号输入_1_out_190 ), .out_191(\led点阵行信号输入_1_out_191 ), .out_192(\led点阵行信号输入_1_out_192 ),
    .out_193(\led点阵行信号输入_1_out_193 ), .out_194(\led点阵行信号输入_1_out_194 ), .out_195(\led点阵行信号输入_1_out_195 ),
    .out_196(\led点阵行信号输入_1_out_196 ), .out_197(\led点阵行信号输入_1_out_197 ), .out_198(\led点阵行信号输入_1_out_198 ),
    .out_199(\led点阵行信号输入_1_out_199 ), .out_200(\led点阵行信号输入_1_out_200 ), .out_201(\led点阵行信号输入_1_out_201 ),
    .out_202(\led点阵行信号输入_1_out_202 ), .out_203(\led点阵行信号输入_1_out_203 ), .out_204(\led点阵行信号输入_1_out_204 ),
    .out_205(\led点阵行信号输入_1_out_205 ), .out_206(\led点阵行信号输入_1_out_206 ), .out_207(\led点阵行信号输入_1_out_207 ),
    .out_208(\led点阵行信号输入_1_out_208 ), .out_209(\led点阵行信号输入_1_out_209 ), .out_210(\led点阵行信号输入_1_out_210 ),
    .out_211(\led点阵行信号输入_1_out_211 ), .out_212(\led点阵行信号输入_1_out_212 ), .out_213(\led点阵行信号输入_1_out_213 ),
    .out_214(\led点阵行信号输入_1_out_214 ), .out_215(\led点阵行信号输入_1_out_215 ), .out_216(\led点阵行信号输入_1_out_216 ),
    .out_217(\led点阵行信号输入_1_out_217 ), .out_218(\led点阵行信号输入_1_out_218 ), .out_219(\led点阵行信号输入_1_out_219 ),
    .out_220(\led点阵行信号输入_1_out_220 ), .out_221(\led点阵行信号输入_1_out_221 ), .out_222(\led点阵行信号输入_1_out_222 ),
    .out_223(\led点阵行信号输入_1_out_223 ), .out_224(\led点阵行信号输入_1_out_224 ), .out_225(\led点阵行信号输入_1_out_225 ),
    .out_226(\led点阵行信号输入_1_out_226 ), .out_227(\led点阵行信号输入_1_out_227 ), .out_228(\led点阵行信号输入_1_out_228 ),
    .out_229(\led点阵行信号输入_1_out_229 ), .out_230(\led点阵行信号输入_1_out_230 ), .out_231(\led点阵行信号输入_1_out_231 ),
    .out_232(\led点阵行信号输入_1_out_232 ), .out_233(\led点阵行信号输入_1_out_233 ), .out_234(\led点阵行信号输入_1_out_234 ),
    .out_235(\led点阵行信号输入_1_out_235 ), .out_236(\led点阵行信号输入_1_out_236 ), .out_237(\led点阵行信号输入_1_out_237 ),
    .out_238(\led点阵行信号输入_1_out_238 ), .out_239(\led点阵行信号输入_1_out_239 ), .out_240(\led点阵行信号输入_1_out_240 ),
    .out_241(\led点阵行信号输入_1_out_241 ), .out_242(\led点阵行信号输入_1_out_242 ), .out_243(\led点阵行信号输入_1_out_243 ),
    .out_244(\led点阵行信号输入_1_out_244 ), .out_245(\led点阵行信号输入_1_out_245 ), .out_246(\led点阵行信号输入_1_out_246 ),
    .out_247(\led点阵行信号输入_1_out_247 ), .out_248(\led点阵行信号输入_1_out_248 ), .out_249(\led点阵行信号输入_1_out_249 ),
    .out_250(\led点阵行信号输入_1_out_250 ), .out_251(\led点阵行信号输入_1_out_251 ), .out_252(\led点阵行信号输入_1_out_252 ),
    .out_253(\led点阵行信号输入_1_out_253 ), .out_254(\led点阵行信号输入_1_out_254 ), .out_255(\led点阵行信号输入_1_out_255 ),
    .out_256(\led点阵行信号输入_1_out_256 ));
  LedDataRight leddataright_2 (
    .CLK(clock_1_out), .DATA(rom_4_data), .en(1'b1), .out_6(leddataright_2_out_6),
    .out_7(leddataright_2_out_7), .out_8(leddataright_2_out_8), .out_9(leddataright_2_out_9),
    .out_10(leddataright_2_out_10), .out_11(leddataright_2_out_11), .out_12(leddataright_2_out_12),
    .out_13(leddataright_2_out_13), .out_14(leddataright_2_out_14), .out_15(leddataright_2_out_15),
    .out_16(leddataright_2_out_16), .out_17(leddataright_2_out_17), .out_18(leddataright_2_out_18),
    .out_19(leddataright_2_out_19), .out_20(leddataright_2_out_20), .out_21(leddataright_2_out_21),
    .out_22(leddataright_2_out_22), .out_23(leddataright_2_out_23), .out_24(leddataright_2_out_24),
    .out_25(leddataright_2_out_25), .out_26(leddataright_2_out_26), .out_27(leddataright_2_out_27),
    .out_28(leddataright_2_out_28), .out_29(leddataright_2_out_29), .out_30(leddataright_2_out_30),
    .out_31(leddataright_2_out_31), .out_32(leddataright_2_out_32), .out_33(leddataright_2_out_33),
    .out_34(leddataright_2_out_34), .out_35(leddataright_2_out_35), .out_36(leddataright_2_out_36),
    .out_37(leddataright_2_out_37), .in_5(counter_2_q));  // open: CLR
  ROM #(.addrWidth(14), .dataWidth(32), .Select("high")) rom_3 (.addr(counter_1_q), .data(rom_3_data));
  ROM #(.addrWidth(14), .dataWidth(32), .Select("high")) rom_4 (.addr(counter_1_q), .data(rom_4_data));
  DotMatrix #(.inputtype("row"), .matrixcols(32), .matrixrows(32), .persist(0), .dotshape("circle")) dotmatrix_1 (
    .row0(\led点阵行信号输入_1_out_129 ), .row1(\led点阵行信号输入_1_out_130 ), .row2(\led点阵行信号输入_1_out_131 ),
    .row3(\led点阵行信号输入_1_out_132 ), .row4(\led点阵行信号输入_1_out_133 ), .row5(\led点阵行信号输入_1_out_134 ),
    .row6(\led点阵行信号输入_1_out_135 ), .row7(\led点阵行信号输入_1_out_136 ), .row8(\led点阵行信号输入_1_out_137 ),
    .row9(\led点阵行信号输入_1_out_138 ), .row10(\led点阵行信号输入_1_out_139 ), .row11(\led点阵行信号输入_1_out_140 ),
    .row12(\led点阵行信号输入_1_out_141 ), .row13(\led点阵行信号输入_1_out_142 ), .row14(\led点阵行信号输入_1_out_143 ),
    .row15(\led点阵行信号输入_1_out_144 ), .row16(\led点阵行信号输入_1_out_145 ), .row17(\led点阵行信号输入_1_out_146 ),
    .row18(\led点阵行信号输入_1_out_147 ), .row19(\led点阵行信号输入_1_out_148 ), .row20(\led点阵行信号输入_1_out_149 ),
    .row21(\led点阵行信号输入_1_out_150 ), .row22(\led点阵行信号输入_1_out_151 ), .row23(\led点阵行信号输入_1_out_152 ),
    .row24(\led点阵行信号输入_1_out_153 ), .row25(\led点阵行信号输入_1_out_154 ), .row26(\led点阵行信号输入_1_out_155 ),
    .row27(\led点阵行信号输入_1_out_156 ), .row28(\led点阵行信号输入_1_out_157 ), .row29(\led点阵行信号输入_1_out_158 ),
    .row30(\led点阵行信号输入_1_out_159 ), .row31(\led点阵行信号输入_1_out_160 ));
  DotMatrix #(.inputtype("row"), .matrixcols(32), .matrixrows(32), .persist(0), .dotshape("circle")) dotmatrix_2 (
    .row0(\led点阵行信号输入_1_out_161 ), .row1(\led点阵行信号输入_1_out_162 ), .row2(\led点阵行信号输入_1_out_163 ),
    .row3(\led点阵行信号输入_1_out_164 ), .row4(\led点阵行信号输入_1_out_165 ), .row5(\led点阵行信号输入_1_out_166 ),
    .row6(\led点阵行信号输入_1_out_167 ), .row7(\led点阵行信号输入_1_out_168 ), .row8(\led点阵行信号输入_1_out_169 ),
    .row9(\led点阵行信号输入_1_out_170 ), .row10(\led点阵行信号输入_1_out_171 ), .row11(\led点阵行信号输入_1_out_172 ),
    .row12(\led点阵行信号输入_1_out_173 ), .row13(\led点阵行信号输入_1_out_174 ), .row14(\led点阵行信号输入_1_out_175 ),
    .row15(\led点阵行信号输入_1_out_176 ), .row16(\led点阵行信号输入_1_out_177 ), .row17(\led点阵行信号输入_1_out_178 ),
    .row18(\led点阵行信号输入_1_out_179 ), .row19(\led点阵行信号输入_1_out_180 ), .row20(\led点阵行信号输入_1_out_181 ),
    .row21(\led点阵行信号输入_1_out_182 ), .row22(\led点阵行信号输入_1_out_183 ), .row23(\led点阵行信号输入_1_out_184 ),
    .row24(\led点阵行信号输入_1_out_185 ), .row25(\led点阵行信号输入_1_out_186 ), .row26(\led点阵行信号输入_1_out_187 ),
    .row27(\led点阵行信号输入_1_out_188 ), .row28(\led点阵行信号输入_1_out_189 ), .row29(\led点阵行信号输入_1_out_190 ),
    .row30(\led点阵行信号输入_1_out_191 ), .row31(\led点阵行信号输入_1_out_192 ));
  DotMatrix #(.inputtype("row"), .matrixcols(32), .matrixrows(32), .persist(0), .dotshape("circle")) dotmatrix_3 (
    .row0(\led点阵行信号输入_1_out_193 ), .row1(\led点阵行信号输入_1_out_194 ), .row2(\led点阵行信号输入_1_out_195 ),
    .row3(\led点阵行信号输入_1_out_196 ), .row4(\led点阵行信号输入_1_out_197 ), .row5(\led点阵行信号输入_1_out_198 ),
    .row6(\led点阵行信号输入_1_out_199 ), .row7(\led点阵行信号输入_1_out_200 ), .row8(\led点阵行信号输入_1_out_201 ),
    .row9(\led点阵行信号输入_1_out_202 ), .row10(\led点阵行信号输入_1_out_203 ), .row11(\led点阵行信号输入_1_out_204 ),
    .row12(\led点阵行信号输入_1_out_205 ), .row13(\led点阵行信号输入_1_out_206 ), .row14(\led点阵行信号输入_1_out_207 ),
    .row15(\led点阵行信号输入_1_out_208 ), .row16(\led点阵行信号输入_1_out_209 ), .row17(\led点阵行信号输入_1_out_210 ),
    .row18(\led点阵行信号输入_1_out_211 ), .row19(\led点阵行信号输入_1_out_212 ), .row20(\led点阵行信号输入_1_out_213 ),
    .row21(\led点阵行信号输入_1_out_214 ), .row22(\led点阵行信号输入_1_out_215 ), .row23(\led点阵行信号输入_1_out_216 ),
    .row24(\led点阵行信号输入_1_out_217 ), .row25(\led点阵行信号输入_1_out_218 ), .row26(\led点阵行信号输入_1_out_219 ),
    .row27(\led点阵行信号输入_1_out_220 ), .row28(\led点阵行信号输入_1_out_221 ), .row29(\led点阵行信号输入_1_out_222 ),
    .row30(\led点阵行信号输入_1_out_223 ), .row31(\led点阵行信号输入_1_out_224 ));
  DotMatrix #(.inputtype("row"), .matrixcols(32), .matrixrows(32), .persist(0), .dotshape("circle")) dotmatrix_4 (
    .row0(\led点阵行信号输入_1_out_225 ), .row1(\led点阵行信号输入_1_out_226 ), .row2(\led点阵行信号输入_1_out_227 ),
    .row3(\led点阵行信号输入_1_out_228 ), .row4(\led点阵行信号输入_1_out_229 ), .row5(\led点阵行信号输入_1_out_230 ),
    .row6(\led点阵行信号输入_1_out_231 ), .row7(\led点阵行信号输入_1_out_232 ), .row8(\led点阵行信号输入_1_out_233 ),
    .row9(\led点阵行信号输入_1_out_234 ), .row10(\led点阵行信号输入_1_out_235 ), .row11(\led点阵行信号输入_1_out_236 ),
    .row12(\led点阵行信号输入_1_out_237 ), .row13(\led点阵行信号输入_1_out_238 ), .row14(\led点阵行信号输入_1_out_239 ),
    .row15(\led点阵行信号输入_1_out_240 ), .row16(\led点阵行信号输入_1_out_241 ), .row17(\led点阵行信号输入_1_out_242 ),
    .row18(\led点阵行信号输入_1_out_243 ), .row19(\led点阵行信号输入_1_out_244 ), .row20(\led点阵行信号输入_1_out_245 ),
    .row21(\led点阵行信号输入_1_out_246 ), .row22(\led点阵行信号输入_1_out_247 ), .row23(\led点阵行信号输入_1_out_248 ),
    .row24(\led点阵行信号输入_1_out_249 ), .row25(\led点阵行信号输入_1_out_250 ), .row26(\led点阵行信号输入_1_out_251 ),
    .row27(\led点阵行信号输入_1_out_252 ), .row28(\led点阵行信号输入_1_out_253 ), .row29(\led点阵行信号输入_1_out_254 ),
    .row30(\led点阵行信号输入_1_out_255 ), .row31(\led点阵行信号输入_1_out_256 ));

  // Notes on the sheet:
  //   contents of rom_1 (hex, n*v repeats v):
  //   11*ffffffff fffffffc ffffffe8 ffffffc0 7*ffffff80 ffffffc0 ffffffc0 ffffffe0 ffffffc8 ffffffcf
  //   ffffffcf ffffffc7 ffffff82 ffffff80 ffffffc1 ffffffc0 25*ffffffff fffffff8 fffffff8 fffffff0
  //   ffffff80 ffffff00 fffffe00 fffffe00 43*ffffffff fffffffc ffffffe8 ffffffc0 7*ffffff80 ffffffc0
  //   ffffffc0 ffffffe0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
  //   contents of rom_2 (hex, n*v repeats v):
  //   ffffffc0 ffffffc0 ffffffc0 fffffe40 fffff8e0 fffdf3e0 fffdf7e0 fffce7e0 fffce7f0 fff867f0 fff867f0
  //   fff867f0 fff875f0 fffc25f8 fff825f8 fff82ff8 fff82ff8 fff82f78 fff82f3c fff83f3c fff02f9c fff00f9c
  //   fff00f8c fff00f8e ffe01fc6 ffe01fc6 ffc01fc2 fff81fe2 fffc17f1 ffc303f8 ffc037fd ffc00180 6*fffffe00
  //   f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
  //   contents of rom_3 (hex, n*v repeats v):
  //   10*ffffffff dfffffff 7ffffff 3ffffff ffffff 7fffff 3fffff 3fffff 7fffff 7fffff 7fffff ffffff ffffff
  //   1ffffff 83ffffff c7ffffff ffffffff ffffffff ffffffff 73ffffff 23ffffff 43ffffff 3ffffff 24*ffffffff
  //   3fffffff fffffff 7ffffff 1ffffff 7fffff 3fffff 3fffff 3fffff 42*ffffffff dfffffff 7ffffff 3ffffff ff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
  //   contents of rom_4 (hex, n*v repeats v):
  //   3ffffff 37fffff 3ffffff 3ffffff 3ffffff 3feffff 7feffff 7fcffff 7fcffff 7fdffff 7fdffff ffdffff
  //   ffdffff f9fbfff fbfbfff fbfbfff fff3fff f813fff e007fff 1e0c7fff 1e4cffff 1e6cffff 1c6cffff 1c6c3fff
  //   1c6c3fff 186d3fff 18679fff 1867ffff 1c67ffff 1e76ffff 1ff67fff 137fff 4*3fffff 7fffff 7fffff 7fffff
  //   fff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
endmodule

// 左
module LedDataLeft (
  input  CLK,
  input  [31:0] DATA,
  input  CLR,
  input  en,
  input  [4:0] in_5,
  output [31:0] out_6,
  output [31:0] out_7,
  output [31:0] out_8,
  output [31:0] out_9,
  output [31:0] out_10,
  output [31:0] out_11,
  output [31:0] out_12,
  output [31:0] out_13,
  output [31:0] out_14,
  output [31:0] out_15,
  output [31:0] out_16,
  output [31:0] out_17,
  output [31:0] out_18,
  output [31:0] out_19,
  output [31:0] out_20,
  output [31:0] out_21,
  output [31:0] out_22,
  output [31:0] out_23,
  output [31:0] out_24,
  output [31:0] out_25,
  output [31:0] out_26,
  output [31:0] out_27,
  output [31:0] out_28,
  output [31:0] out_29,
  output [31:0] out_30,
  output [31:0] out_31,
  output [31:0] out_32,
  output [31:0] out_33,
  output [31:0] out_34,
  output [31:0] out_35,
  output [31:0] out_36,
  output [31:0] out_37
);

  wire comparator_1_eq, d_ff_1_q, d_ff_2_q, demultiplexer_1_out0, demultiplexer_1_out1, demultiplexer_1_out2,
       demultiplexer_1_out3, demultiplexer_1_out4, demultiplexer_1_out5, demultiplexer_1_out6,
       demultiplexer_1_out7, demultiplexer_1_out8, demultiplexer_1_out9, demultiplexer_1_out10,
       demultiplexer_1_out11, demultiplexer_1_out12, demultiplexer_1_out13, demultiplexer_1_out14,
       demultiplexer_1_out15, demultiplexer_1_out16, demultiplexer_1_out17, demultiplexer_1_out18,
       demultiplexer_1_out19, demultiplexer_1_out20, demultiplexer_1_out21, demultiplexer_1_out22,
       demultiplexer_1_out23, demultiplexer_1_out24, demultiplexer_1_out25, demultiplexer_1_out26,
       demultiplexer_1_out27, demultiplexer_1_out28, demultiplexer_1_out29, demultiplexer_1_out30,
       demultiplexer_1_out31;
  wire [31:0] register_1_q, register_2_q, register_3_q, register_4_q, register_5_q, register_6_q,
       register_7_q, register_8_q, register_9_q, register_10_q, register_11_q, register_12_q, register_13_q,
       register_14_q, register_15_q, register_16_q, register_17_q, register_18_q, register_19_q,
       register_20_q, register_21_q, register_22_q, register_23_q, register_24_q, register_25_q,
       register_26_q, register_27_q, register_28_q, register_29_q, register_30_q, register_31_q,
       register_32_q;

  Demultiplexer #(.select(5), .width(1), .tristate("false"), .disabled("Z"), .enable("false")) demultiplexer_1 (
    .out0(demultiplexer_1_out0), .out1(demultiplexer_1_out1), .out2(demultiplexer_1_out2),
    .out3(demultiplexer_1_out3), .out4(demultiplexer_1_out4), .out5(demultiplexer_1_out5),
    .out6(demultiplexer_1_out6), .out7(demultiplexer_1_out7), .out8(demultiplexer_1_out8),
    .out9(demultiplexer_1_out9), .out10(demultiplexer_1_out10), .out11(demultiplexer_1_out11),
    .out12(demultiplexer_1_out12), .out13(demultiplexer_1_out13), .out14(demultiplexer_1_out14),
    .out15(demultiplexer_1_out15), .out16(demultiplexer_1_out16), .out17(demultiplexer_1_out17),
    .out18(demultiplexer_1_out18), .out19(demultiplexer_1_out19), .out20(demultiplexer_1_out20),
    .out21(demultiplexer_1_out21), .out22(demultiplexer_1_out22), .out23(demultiplexer_1_out23),
    .out24(demultiplexer_1_out24), .out25(demultiplexer_1_out25), .out26(demultiplexer_1_out26),
    .out27(demultiplexer_1_out27), .out28(demultiplexer_1_out28), .out29(demultiplexer_1_out29),
    .out30(demultiplexer_1_out30), .out31(demultiplexer_1_out31), .in(en), .sel(in_5));
  Register #(.width(32), .trigger("rising"), .Select("low")) register_1 (
    .D(DATA), .en(demultiplexer_1_out0), .Q(register_1_q), .clk(CLK));  // open: clr
  Register #(.width(32), .trigger("rising"), .Select("low")) register_2 (
    .D(DATA), .en(demultiplexer_1_out1), .Q(register_2_q), .clk(CLK));  // open: clr
  Register #(.width(32), .trigger("rising"), .Select("low")) register_3 (
    .D(DATA), .en(demultiplexer_1_out2), .Q(register_3_q), .clk(CLK));  // open: clr
  Register #(.width(32), .trigger("rising"), .Select("low")) register_4 (
    .D(DATA), .en(demultiplexer_1_out3), .Q(register_4_q), .clk(CLK));  // open: clr
  Register #(.width(32), .trigger("rising"), .Select("low")) register_5 (
    .D(DATA), .en(demultiplexer_1_out4), .Q(register_5_q), .clk(CLK));  // open: clr
  Register #(.width(32), .trigger("rising"), .Select("low")) register_6 (
    .D(DATA), .en(demultiplexer_1_out5), .Q(register_6_q), .clk(CLK));  // open: clr
  Register #(.width(32), .trigger("rising"), .Select("low")) register_7 (
    .D(DATA), .en(demultiplexer_1_out6), .Q(register_7_q), .clk(CLK));  // open: clr
  Register #(.width(32), .trigger("rising"), .Select("low")) register_8 (
    .D(DATA), .en(demultiplexer_1_out7), .Q(register_8_q), .clk(CLK));  // open: clr
  Register #(.width(32), .trigger("rising"), .Select("low")) register_9 (
    .D(DATA), .en(demultiplexer_1_out8), .Q(register_9_q), .clk(CLK));  // open: clr
  Register #(.width(32), .trigger("rising"), .Select("low")) register_10 (
    .D(DATA), .en(demultiplexer_1_out9), .Q(register_10_q), .clk(CLK));  // open: clr
  Register #(.width(32), .trigger("rising"), .Select("low")) register_11 (
    .D(DATA), .en(demultiplexer_1_out10), .Q(register_11_q), .clk(CLK));  // open: clr
  Register #(.width(32), .trigger("rising"), .Select("low")) register_12 (
    .D(DATA), .en(demultiplexer_1_out11), .Q(register_12_q), .clk(CLK));  // open: clr
  Register #(.width(32), .trigger("rising"), .Select("low")) register_13 (
    .D(DATA), .en(demultiplexer_1_out12), .Q(register_13_q), .clk(CLK));  // open: clr
  Register #(.width(32), .trigger("rising"), .Select("low")) register_14 (
    .D(DATA), .en(demultiplexer_1_out13), .Q(register_14_q), .clk(CLK));  // open: clr
  Register #(.width(32), .trigger("rising"), .Select("low")) register_15 (
    .D(DATA), .en(demultiplexer_1_out14), .Q(register_15_q), .clk(CLK));  // open: clr
  Register #(.width(32), .trigger("rising"), .Select("low")) register_16 (
    .D(DATA), .en(demultiplexer_1_out15), .Q(register_16_q), .clk(CLK));  // open: clr
  Register #(.width(32), .trigger("rising"), .Select("low")) register_17 (
    .D(DATA), .en(demultiplexer_1_out16), .Q(register_17_q), .clk(CLK));  // open: clr
  Register #(.width(32), .trigger("rising"), .Select("low")) register_18 (
    .D(DATA), .en(demultiplexer_1_out17), .Q(register_18_q), .clk(CLK));  // open: clr
  Register #(.width(32), .trigger("rising"), .Select("low")) register_19 (
    .D(DATA), .en(demultiplexer_1_out18), .Q(register_19_q), .clk(CLK));  // open: clr
  Register #(.width(32), .trigger("rising"), .Select("low")) register_20 (
    .D(DATA), .en(demultiplexer_1_out19), .Q(register_20_q), .clk(CLK));  // open: clr
  Register #(.width(32), .trigger("rising"), .Select("low")) register_21 (
    .D(DATA), .en(demultiplexer_1_out20), .Q(register_21_q), .clk(CLK));  // open: clr
  Register #(.width(32), .trigger("rising"), .Select("low")) register_22 (
    .D(DATA), .en(demultiplexer_1_out21), .Q(register_22_q), .clk(CLK));  // open: clr
  Register #(.width(32), .trigger("rising"), .Select("low")) register_23 (
    .D(DATA), .en(demultiplexer_1_out22), .Q(register_23_q), .clk(CLK));  // open: clr
  Register #(.width(32), .trigger("rising"), .Select("low")) register_24 (
    .D(DATA), .en(demultiplexer_1_out23), .Q(register_24_q), .clk(CLK));  // open: clr
  Register #(.width(32), .trigger("rising"), .Select("low")) register_25 (
    .D(DATA), .en(demultiplexer_1_out24), .Q(register_25_q), .clk(CLK));  // open: clr
  Register #(.width(32), .trigger("rising"), .Select("low")) register_26 (
    .D(DATA), .en(demultiplexer_1_out25), .Q(register_26_q), .clk(CLK));  // open: clr
  Register #(.width(32), .trigger("rising"), .Select("low")) register_27 (
    .D(DATA), .en(demultiplexer_1_out26), .Q(register_27_q), .clk(CLK));  // open: clr
  Register #(.width(32), .trigger("rising"), .Select("low")) register_28 (
    .D(DATA), .en(demultiplexer_1_out27), .Q(register_28_q), .clk(CLK));  // open: clr
  Register #(.width(32), .trigger("rising"), .Select("low")) register_29 (
    .D(DATA), .en(demultiplexer_1_out28), .Q(register_29_q), .clk(CLK));  // open: clr
  Register #(.width(32), .trigger("rising"), .Select("low")) register_30 (
    .D(DATA), .en(demultiplexer_1_out29), .Q(register_30_q), .clk(CLK));  // open: clr
  Register #(.width(32), .trigger("rising"), .Select("low")) register_31 (
    .D(DATA), .en(demultiplexer_1_out30), .Q(register_31_q), .clk(CLK));  // open: clr
  Register #(.width(32), .trigger("rising"), .Select("low")) register_32 (
    .D(DATA), .en(demultiplexer_1_out31), .Q(register_32_q), .clk(CLK));  // open: clr
  Comparator #(.width(5), .mode("twosComplement")) comparator_1 (
    .a(in_5), .b({5{1'b1}}), .eq(comparator_1_eq));  // open: gt, lt
  Register #(.width(32), .trigger("rising"), .Select("low")) register_33 (
    .D(register_1_q), .en(d_ff_1_q), .Q(out_6), .clk(CLK), .clr(CLR));
  Register #(.width(32), .trigger("rising"), .Select("low")) register_34 (
    .D(register_2_q), .en(d_ff_1_q), .Q(out_7), .clk(CLK), .clr(CLR));
  Register #(.width(32), .trigger("rising"), .Select("low")) register_35 (
    .D(register_3_q), .en(d_ff_1_q), .Q(out_8), .clk(CLK), .clr(CLR));
  Register #(.width(32), .trigger("rising"), .Select("low")) register_36 (
    .D(register_4_q), .en(d_ff_1_q), .Q(out_9), .clk(CLK), .clr(CLR));
  Register #(.width(32), .trigger("rising"), .Select("low")) register_37 (
    .D(register_5_q), .en(d_ff_1_q), .Q(out_10), .clk(CLK), .clr(CLR));
  Register #(.width(32), .trigger("rising"), .Select("low")) register_38 (
    .D(register_6_q), .en(d_ff_1_q), .Q(out_11), .clk(CLK), .clr(CLR));
  Register #(.width(32), .trigger("rising"), .Select("low")) register_39 (
    .D(register_7_q), .en(d_ff_1_q), .Q(out_12), .clk(CLK), .clr(CLR));
  Register #(.width(32), .trigger("rising"), .Select("low")) register_40 (
    .D(register_8_q), .en(d_ff_1_q), .Q(out_13), .clk(CLK), .clr(CLR));
  Register #(.width(32), .trigger("rising"), .Select("low")) register_41 (
    .D(register_9_q), .en(d_ff_1_q), .Q(out_14), .clk(CLK), .clr(CLR));
  Register #(.width(32), .trigger("rising"), .Select("low")) register_42 (
    .D(register_10_q), .en(d_ff_1_q), .Q(out_15), .clk(CLK), .clr(CLR));
  Register #(.width(32), .trigger("rising"), .Select("low")) register_43 (
    .D(register_11_q), .en(d_ff_1_q), .Q(out_16), .clk(CLK), .clr(CLR));
  Register #(.width(32), .trigger("rising"), .Select("low")) register_44 (
    .D(register_12_q), .en(d_ff_1_q), .Q(out_17), .clk(CLK), .clr(CLR));
  Register #(.width(32), .trigger("rising"), .Select("low")) register_45 (
    .D(register_13_q), .en(d_ff_1_q), .Q(out_18), .clk(CLK), .clr(CLR));
  Register #(.width(32), .trigger("rising"), .Select("low")) register_46 (
    .D(register_14_q), .en(d_ff_1_q), .Q(out_19), .clk(CLK), .clr(CLR));
  Register #(.width(32), .trigger("rising"), .Select("low")) register_47 (
    .D(register_15_q), .en(d_ff_1_q), .Q(out_20), .clk(CLK), .clr(CLR));
  Register #(.width(32), .trigger("rising"), .Select("low")) register_48 (
    .D(register_16_q), .en(d_ff_1_q), .Q(out_21), .clk(CLK), .clr(CLR));
  Register #(.width(32), .trigger("rising"), .Select("low")) register_49 (
    .D(register_17_q), .en(d_ff_1_q), .Q(out_22), .clk(CLK), .clr(CLR));
  Register #(.width(32), .trigger("rising"), .Select("low")) register_50 (
    .D(register_18_q), .en(d_ff_1_q), .Q(out_23), .clk(CLK), .clr(CLR));
  Register #(.width(32), .trigger("rising"), .Select("low")) register_51 (
    .D(register_19_q), .en(d_ff_1_q), .Q(out_24), .clk(CLK), .clr(CLR));
  Register #(.width(32), .trigger("rising"), .Select("low")) register_52 (
    .D(register_20_q), .en(d_ff_1_q), .Q(out_25), .clk(CLK), .clr(CLR));
  Register #(.width(32), .trigger("rising"), .Select("low")) register_53 (
    .D(register_21_q), .en(d_ff_1_q), .Q(out_26), .clk(CLK), .clr(CLR));
  Register #(.width(32), .trigger("rising"), .Select("low")) register_54 (
    .D(register_22_q), .en(d_ff_1_q), .Q(out_27), .clk(CLK), .clr(CLR));
  Register #(.width(32), .trigger("rising"), .Select("low")) register_55 (
    .D(register_23_q), .en(d_ff_1_q), .Q(out_28), .clk(CLK), .clr(CLR));
  Register #(.width(32), .trigger("rising"), .Select("low")) register_56 (
    .D(register_24_q), .en(d_ff_1_q), .Q(out_29), .clk(CLK), .clr(CLR));
  Register #(.width(32), .trigger("rising"), .Select("low")) register_57 (
    .D(register_25_q), .en(d_ff_1_q), .Q(out_30), .clk(CLK), .clr(CLR));
  Register #(.width(32), .trigger("rising"), .Select("low")) register_58 (
    .D(register_26_q), .en(d_ff_1_q), .Q(out_31), .clk(CLK), .clr(CLR));
  Register #(.width(32), .trigger("rising"), .Select("low")) register_59 (
    .D(register_27_q), .en(d_ff_1_q), .Q(out_32), .clk(CLK), .clr(CLR));
  Register #(.width(32), .trigger("rising"), .Select("low")) register_60 (
    .D(register_28_q), .en(d_ff_1_q), .Q(out_33), .clk(CLK), .clr(CLR));
  Register #(.width(32), .trigger("rising"), .Select("low")) register_61 (
    .D(register_29_q), .en(d_ff_1_q), .Q(out_34), .clk(CLK), .clr(CLR));
  Register #(.width(32), .trigger("rising"), .Select("low")) register_62 (
    .D(register_30_q), .en(d_ff_1_q), .Q(out_35), .clk(CLK), .clr(CLR));
  Register #(.width(32), .trigger("rising"), .Select("low")) register_63 (
    .D(register_31_q), .en(d_ff_1_q), .Q(out_36), .clk(CLK), .clr(CLR));
  Register #(.width(32), .trigger("rising"), .Select("low")) register_64 (
    .D(register_32_q), .en(d_ff_1_q), .Q(out_37), .clk(CLK), .clr(CLR));
  D_Flip_Flop #(.trigger("rising"), .Pre_Clr_Positions("LEGACY"), .NegatePresetClear("false"), .enable("true"), .NewFFLayout("true")) d_ff_1 (
    .clk(CLK), .D(comparator_1_eq), .Q(d_ff_1_q), .en(en), .reset(d_ff_2_q));  // open: Qn, preset
  D_Flip_Flop #(.trigger("rising"), .Pre_Clr_Positions("LEGACY"), .NegatePresetClear("false"), .enable("true"), .NewFFLayout("true")) d_ff_2 (
    .clk(CLK), .D(d_ff_1_q), .Q(d_ff_2_q), .en(en));  // open: Qn, preset, reset

  // Other names for the same wires on the sheet: sel[4:0] = in_5
endmodule

// 右
module LedDataRight (
  input  CLK,
  input  [31:0] DATA,
  input  CLR,
  input  en,
  input  [4:0] in_5,
  output [31:0] out_6,
  output [31:0] out_7,
  output [31:0] out_8,
  output [31:0] out_9,
  output [31:0] out_10,
  output [31:0] out_11,
  output [31:0] out_12,
  output [31:0] out_13,
  output [31:0] out_14,
  output [31:0] out_15,
  output [31:0] out_16,
  output [31:0] out_17,
  output [31:0] out_18,
  output [31:0] out_19,
  output [31:0] out_20,
  output [31:0] out_21,
  output [31:0] out_22,
  output [31:0] out_23,
  output [31:0] out_24,
  output [31:0] out_25,
  output [31:0] out_26,
  output [31:0] out_27,
  output [31:0] out_28,
  output [31:0] out_29,
  output [31:0] out_30,
  output [31:0] out_31,
  output [31:0] out_32,
  output [31:0] out_33,
  output [31:0] out_34,
  output [31:0] out_35,
  output [31:0] out_36,
  output [31:0] out_37
);

  wire comparator_1_eq, d_ff_1_q, d_ff_2_q, demultiplexer_1_out0, demultiplexer_1_out1, demultiplexer_1_out2,
       demultiplexer_1_out3, demultiplexer_1_out4, demultiplexer_1_out5, demultiplexer_1_out6,
       demultiplexer_1_out7, demultiplexer_1_out8, demultiplexer_1_out9, demultiplexer_1_out10,
       demultiplexer_1_out11, demultiplexer_1_out12, demultiplexer_1_out13, demultiplexer_1_out14,
       demultiplexer_1_out15, demultiplexer_1_out16, demultiplexer_1_out17, demultiplexer_1_out18,
       demultiplexer_1_out19, demultiplexer_1_out20, demultiplexer_1_out21, demultiplexer_1_out22,
       demultiplexer_1_out23, demultiplexer_1_out24, demultiplexer_1_out25, demultiplexer_1_out26,
       demultiplexer_1_out27, demultiplexer_1_out28, demultiplexer_1_out29, demultiplexer_1_out30,
       demultiplexer_1_out31;
  wire [31:0] register_1_q, register_2_q, register_3_q, register_4_q, register_5_q, register_6_q,
       register_7_q, register_8_q, register_9_q, register_10_q, register_11_q, register_12_q, register_13_q,
       register_14_q, register_15_q, register_16_q, register_17_q, register_18_q, register_19_q,
       register_20_q, register_21_q, register_22_q, register_23_q, register_24_q, register_25_q,
       register_26_q, register_27_q, register_28_q, register_29_q, register_30_q, register_31_q,
       register_32_q;

  Demultiplexer #(.select(5), .width(1), .tristate("false"), .disabled("Z"), .enable("false")) demultiplexer_1 (
    .out0(demultiplexer_1_out0), .out1(demultiplexer_1_out1), .out2(demultiplexer_1_out2),
    .out3(demultiplexer_1_out3), .out4(demultiplexer_1_out4), .out5(demultiplexer_1_out5),
    .out6(demultiplexer_1_out6), .out7(demultiplexer_1_out7), .out8(demultiplexer_1_out8),
    .out9(demultiplexer_1_out9), .out10(demultiplexer_1_out10), .out11(demultiplexer_1_out11),
    .out12(demultiplexer_1_out12), .out13(demultiplexer_1_out13), .out14(demultiplexer_1_out14),
    .out15(demultiplexer_1_out15), .out16(demultiplexer_1_out16), .out17(demultiplexer_1_out17),
    .out18(demultiplexer_1_out18), .out19(demultiplexer_1_out19), .out20(demultiplexer_1_out20),
    .out21(demultiplexer_1_out21), .out22(demultiplexer_1_out22), .out23(demultiplexer_1_out23),
    .out24(demultiplexer_1_out24), .out25(demultiplexer_1_out25), .out26(demultiplexer_1_out26),
    .out27(demultiplexer_1_out27), .out28(demultiplexer_1_out28), .out29(demultiplexer_1_out29),
    .out30(demultiplexer_1_out30), .out31(demultiplexer_1_out31), .in(en), .sel(in_5));
  Register #(.width(32), .trigger("rising"), .Select("low")) register_1 (
    .D(DATA), .en(demultiplexer_1_out0), .Q(register_1_q), .clk(CLK));  // open: clr
  Register #(.width(32), .trigger("rising"), .Select("low")) register_2 (
    .D(DATA), .en(demultiplexer_1_out1), .Q(register_2_q), .clk(CLK));  // open: clr
  Register #(.width(32), .trigger("rising"), .Select("low")) register_3 (
    .D(DATA), .en(demultiplexer_1_out2), .Q(register_3_q), .clk(CLK));  // open: clr
  Register #(.width(32), .trigger("rising"), .Select("low")) register_4 (
    .D(DATA), .en(demultiplexer_1_out3), .Q(register_4_q), .clk(CLK));  // open: clr
  Register #(.width(32), .trigger("rising"), .Select("low")) register_5 (
    .D(DATA), .en(demultiplexer_1_out4), .Q(register_5_q), .clk(CLK));  // open: clr
  Register #(.width(32), .trigger("rising"), .Select("low")) register_6 (
    .D(DATA), .en(demultiplexer_1_out5), .Q(register_6_q), .clk(CLK));  // open: clr
  Register #(.width(32), .trigger("rising"), .Select("low")) register_7 (
    .D(DATA), .en(demultiplexer_1_out6), .Q(register_7_q), .clk(CLK));  // open: clr
  Register #(.width(32), .trigger("rising"), .Select("low")) register_8 (
    .D(DATA), .en(demultiplexer_1_out7), .Q(register_8_q), .clk(CLK));  // open: clr
  Register #(.width(32), .trigger("rising"), .Select("low")) register_9 (
    .D(DATA), .en(demultiplexer_1_out8), .Q(register_9_q), .clk(CLK));  // open: clr
  Register #(.width(32), .trigger("rising"), .Select("low")) register_10 (
    .D(DATA), .en(demultiplexer_1_out9), .Q(register_10_q), .clk(CLK));  // open: clr
  Register #(.width(32), .trigger("rising"), .Select("low")) register_11 (
    .D(DATA), .en(demultiplexer_1_out10), .Q(register_11_q), .clk(CLK));  // open: clr
  Register #(.width(32), .trigger("rising"), .Select("low")) register_12 (
    .D(DATA), .en(demultiplexer_1_out11), .Q(register_12_q), .clk(CLK));  // open: clr
  Register #(.width(32), .trigger("rising"), .Select("low")) register_13 (
    .D(DATA), .en(demultiplexer_1_out12), .Q(register_13_q), .clk(CLK));  // open: clr
  Register #(.width(32), .trigger("rising"), .Select("low")) register_14 (
    .D(DATA), .en(demultiplexer_1_out13), .Q(register_14_q), .clk(CLK));  // open: clr
  Register #(.width(32), .trigger("rising"), .Select("low")) register_15 (
    .D(DATA), .en(demultiplexer_1_out14), .Q(register_15_q), .clk(CLK));  // open: clr
  Register #(.width(32), .trigger("rising"), .Select("low")) register_16 (
    .D(DATA), .en(demultiplexer_1_out15), .Q(register_16_q), .clk(CLK));  // open: clr
  Register #(.width(32), .trigger("rising"), .Select("low")) register_17 (
    .D(DATA), .en(demultiplexer_1_out16), .Q(register_17_q), .clk(CLK));  // open: clr
  Register #(.width(32), .trigger("rising"), .Select("low")) register_18 (
    .D(DATA), .en(demultiplexer_1_out17), .Q(register_18_q), .clk(CLK));  // open: clr
  Register #(.width(32), .trigger("rising"), .Select("low")) register_19 (
    .D(DATA), .en(demultiplexer_1_out18), .Q(register_19_q), .clk(CLK));  // open: clr
  Register #(.width(32), .trigger("rising"), .Select("low")) register_20 (
    .D(DATA), .en(demultiplexer_1_out19), .Q(register_20_q), .clk(CLK));  // open: clr
  Register #(.width(32), .trigger("rising"), .Select("low")) register_21 (
    .D(DATA), .en(demultiplexer_1_out20), .Q(register_21_q), .clk(CLK));  // open: clr
  Register #(.width(32), .trigger("rising"), .Select("low")) register_22 (
    .D(DATA), .en(demultiplexer_1_out21), .Q(register_22_q), .clk(CLK));  // open: clr
  Register #(.width(32), .trigger("rising"), .Select("low")) register_23 (
    .D(DATA), .en(demultiplexer_1_out22), .Q(register_23_q), .clk(CLK));  // open: clr
  Register #(.width(32), .trigger("rising"), .Select("low")) register_24 (
    .D(DATA), .en(demultiplexer_1_out23), .Q(register_24_q), .clk(CLK));  // open: clr
  Register #(.width(32), .trigger("rising"), .Select("low")) register_25 (
    .D(DATA), .en(demultiplexer_1_out24), .Q(register_25_q), .clk(CLK));  // open: clr
  Register #(.width(32), .trigger("rising"), .Select("low")) register_26 (
    .D(DATA), .en(demultiplexer_1_out25), .Q(register_26_q), .clk(CLK));  // open: clr
  Register #(.width(32), .trigger("rising"), .Select("low")) register_27 (
    .D(DATA), .en(demultiplexer_1_out26), .Q(register_27_q), .clk(CLK));  // open: clr
  Register #(.width(32), .trigger("rising"), .Select("low")) register_28 (
    .D(DATA), .en(demultiplexer_1_out27), .Q(register_28_q), .clk(CLK));  // open: clr
  Register #(.width(32), .trigger("rising"), .Select("low")) register_29 (
    .D(DATA), .en(demultiplexer_1_out28), .Q(register_29_q), .clk(CLK));  // open: clr
  Register #(.width(32), .trigger("rising"), .Select("low")) register_30 (
    .D(DATA), .en(demultiplexer_1_out29), .Q(register_30_q), .clk(CLK));  // open: clr
  Register #(.width(32), .trigger("rising"), .Select("low")) register_31 (
    .D(DATA), .en(demultiplexer_1_out30), .Q(register_31_q), .clk(CLK));  // open: clr
  Register #(.width(32), .trigger("rising"), .Select("low")) register_32 (
    .D(DATA), .en(demultiplexer_1_out31), .Q(register_32_q), .clk(CLK));  // open: clr
  Comparator #(.width(5), .mode("twosComplement")) comparator_1 (
    .a(in_5), .b({5{1'b1}}), .eq(comparator_1_eq));  // open: gt, lt
  Register #(.width(32), .trigger("rising"), .Select("low")) register_33 (
    .D(register_1_q), .en(d_ff_1_q), .Q(out_6), .clk(CLK), .clr(CLR));
  Register #(.width(32), .trigger("rising"), .Select("low")) register_34 (
    .D(register_2_q), .en(d_ff_1_q), .Q(out_7), .clk(CLK), .clr(CLR));
  Register #(.width(32), .trigger("rising"), .Select("low")) register_35 (
    .D(register_3_q), .en(d_ff_1_q), .Q(out_8), .clk(CLK), .clr(CLR));
  Register #(.width(32), .trigger("rising"), .Select("low")) register_36 (
    .D(register_4_q), .en(d_ff_1_q), .Q(out_9), .clk(CLK), .clr(CLR));
  Register #(.width(32), .trigger("rising"), .Select("low")) register_37 (
    .D(register_5_q), .en(d_ff_1_q), .Q(out_10), .clk(CLK), .clr(CLR));
  Register #(.width(32), .trigger("rising"), .Select("low")) register_38 (
    .D(register_6_q), .en(d_ff_1_q), .Q(out_11), .clk(CLK), .clr(CLR));
  Register #(.width(32), .trigger("rising"), .Select("low")) register_39 (
    .D(register_7_q), .en(d_ff_1_q), .Q(out_12), .clk(CLK), .clr(CLR));
  Register #(.width(32), .trigger("rising"), .Select("low")) register_40 (
    .D(register_8_q), .en(d_ff_1_q), .Q(out_13), .clk(CLK), .clr(CLR));
  Register #(.width(32), .trigger("rising"), .Select("low")) register_41 (
    .D(register_9_q), .en(d_ff_1_q), .Q(out_14), .clk(CLK), .clr(CLR));
  Register #(.width(32), .trigger("rising"), .Select("low")) register_42 (
    .D(register_10_q), .en(d_ff_1_q), .Q(out_15), .clk(CLK), .clr(CLR));
  Register #(.width(32), .trigger("rising"), .Select("low")) register_43 (
    .D(register_11_q), .en(d_ff_1_q), .Q(out_16), .clk(CLK), .clr(CLR));
  Register #(.width(32), .trigger("rising"), .Select("low")) register_44 (
    .D(register_12_q), .en(d_ff_1_q), .Q(out_17), .clk(CLK), .clr(CLR));
  Register #(.width(32), .trigger("rising"), .Select("low")) register_45 (
    .D(register_13_q), .en(d_ff_1_q), .Q(out_18), .clk(CLK), .clr(CLR));
  Register #(.width(32), .trigger("rising"), .Select("low")) register_46 (
    .D(register_14_q), .en(d_ff_1_q), .Q(out_19), .clk(CLK), .clr(CLR));
  Register #(.width(32), .trigger("rising"), .Select("low")) register_47 (
    .D(register_15_q), .en(d_ff_1_q), .Q(out_20), .clk(CLK), .clr(CLR));
  Register #(.width(32), .trigger("rising"), .Select("low")) register_48 (
    .D(register_16_q), .en(d_ff_1_q), .Q(out_21), .clk(CLK), .clr(CLR));
  Register #(.width(32), .trigger("rising"), .Select("low")) register_49 (
    .D(register_17_q), .en(d_ff_1_q), .Q(out_22), .clk(CLK), .clr(CLR));
  Register #(.width(32), .trigger("rising"), .Select("low")) register_50 (
    .D(register_18_q), .en(d_ff_1_q), .Q(out_23), .clk(CLK), .clr(CLR));
  Register #(.width(32), .trigger("rising"), .Select("low")) register_51 (
    .D(register_19_q), .en(d_ff_1_q), .Q(out_24), .clk(CLK), .clr(CLR));
  Register #(.width(32), .trigger("rising"), .Select("low")) register_52 (
    .D(register_20_q), .en(d_ff_1_q), .Q(out_25), .clk(CLK), .clr(CLR));
  Register #(.width(32), .trigger("rising"), .Select("low")) register_53 (
    .D(register_21_q), .en(d_ff_1_q), .Q(out_26), .clk(CLK), .clr(CLR));
  Register #(.width(32), .trigger("rising"), .Select("low")) register_54 (
    .D(register_22_q), .en(d_ff_1_q), .Q(out_27), .clk(CLK), .clr(CLR));
  Register #(.width(32), .trigger("rising"), .Select("low")) register_55 (
    .D(register_23_q), .en(d_ff_1_q), .Q(out_28), .clk(CLK), .clr(CLR));
  Register #(.width(32), .trigger("rising"), .Select("low")) register_56 (
    .D(register_24_q), .en(d_ff_1_q), .Q(out_29), .clk(CLK), .clr(CLR));
  Register #(.width(32), .trigger("rising"), .Select("low")) register_57 (
    .D(register_25_q), .en(d_ff_1_q), .Q(out_30), .clk(CLK), .clr(CLR));
  Register #(.width(32), .trigger("rising"), .Select("low")) register_58 (
    .D(register_26_q), .en(d_ff_1_q), .Q(out_31), .clk(CLK), .clr(CLR));
  Register #(.width(32), .trigger("rising"), .Select("low")) register_59 (
    .D(register_27_q), .en(d_ff_1_q), .Q(out_32), .clk(CLK), .clr(CLR));
  Register #(.width(32), .trigger("rising"), .Select("low")) register_60 (
    .D(register_28_q), .en(d_ff_1_q), .Q(out_33), .clk(CLK), .clr(CLR));
  Register #(.width(32), .trigger("rising"), .Select("low")) register_61 (
    .D(register_29_q), .en(d_ff_1_q), .Q(out_34), .clk(CLK), .clr(CLR));
  Register #(.width(32), .trigger("rising"), .Select("low")) register_62 (
    .D(register_30_q), .en(d_ff_1_q), .Q(out_35), .clk(CLK), .clr(CLR));
  Register #(.width(32), .trigger("rising"), .Select("low")) register_63 (
    .D(register_31_q), .en(d_ff_1_q), .Q(out_36), .clk(CLK), .clr(CLR));
  Register #(.width(32), .trigger("rising"), .Select("low")) register_64 (
    .D(register_32_q), .en(d_ff_1_q), .Q(out_37), .clk(CLK), .clr(CLR));
  D_Flip_Flop #(.trigger("rising"), .Pre_Clr_Positions("LEGACY"), .NegatePresetClear("false"), .enable("true"), .NewFFLayout("true")) d_ff_1 (
    .clk(CLK), .D(comparator_1_eq), .Q(d_ff_1_q), .en(en), .reset(d_ff_2_q));  // open: Qn, preset
  D_Flip_Flop #(.trigger("rising"), .Pre_Clr_Positions("LEGACY"), .NegatePresetClear("false"), .enable("true"), .NewFFLayout("true")) d_ff_2 (
    .clk(CLK), .D(d_ff_1_q), .Q(d_ff_2_q), .en(en));  // open: Qn, preset, reset

  // Other names for the same wires on the sheet: sel[4:0] = in_5
endmodule

module \暂停控制电路  (
  input  in_1,
  input  in_2,
  output out_3
);

  wire d_ff_1_q, not_1_out;

  D_Flip_Flop #(.trigger("rising"), .Pre_Clr_Positions("LEGACY"), .NegatePresetClear("false"), .enable("true"), .NewFFLayout("false")) d_ff_1 (
    .clk(in_2), .D(not_1_out), .Q(d_ff_1_q));  // open: Qn, preset, en, reset
  not not_1 (not_1_out, d_ff_1_q);
  and and_1 (out_3, in_1, ~d_ff_1_q);  // AND_Gate

  // Notes on the sheet:
  //   暂停控制电路
endmodule

module \进度条  (
  input  [13:0] in_1,
  output [31:0] out_2,
  output [31:0] out_3
);

  wire comparator_1_gt;
  wire [4:0] bit_extender_2_out;
  wire [31:0] bit_extender_1_out, divider_1_out, multiplexer_1_out, not_1_out, shifter_1_out,
       subtractor_1_out;

  assign bit_extender_1_out = {{18{1'b0}}, in_1};  // Bit_Extender bit_extender_1
  Divider #(.width(32)) divider_1 (.a(bit_extender_1_out), .b(32'hb2), .out(divider_1_out));  // open: upper, rem
  Subtractor #(.width(32)) subtractor_1 (.a(divider_1_out), .b(32'h20), .out(subtractor_1_out));  // open: bin, bout
  Comparator #(.width(32), .mode("twosComplement")) comparator_1 (
    .a(divider_1_out), .b(32'h20), .gt(comparator_1_gt));  // open: eq, lt
  Multiplexer #(.select(1), .width(32), .disabled("Z"), .enable("false")) multiplexer_1 (
    .in0(divider_1_out), .in1(subtractor_1_out), .out(multiplexer_1_out), .sel(comparator_1_gt));
  Bit_Extender #(.in_width(32), .out_width(5), .\type ("zero")) bit_extender_2 (
    .in(multiplexer_1_out), .out(bit_extender_2_out));
  Shifter #(.width(32), .shift("lr")) shifter_1 (.in({32{1'b1}}), .\dist (bit_extender_2_out), .out(shifter_1_out));
  assign not_1_out = ~shifter_1_out;  // NOT_Gate not_1, 32 bits wide
  Multiplexer #(.select(1), .width(32), .disabled("Z"), .enable("false")) multiplexer_2 (
    .in0(not_1_out), .in1({32{1'b1}}), .out(out_2), .sel(comparator_1_gt));
  Multiplexer #(.select(1), .width(32), .disabled("Z"), .enable("false")) multiplexer_3 (
    .in0({32{1'b0}}), .in1(not_1_out), .out(out_3), .sel(comparator_1_gt));

  // Notes on the sheet:
  //   进度条控制电路
endmodule

module \倍速控制  (
  input  in_1,
  input  in_2,
  input  in_3,
  output out_4
);

  wire and_1_out, and_2_out, and_3_out, and_4_out, counter_1_carry, counter_2_carry, d_ff_1_q, d_ff_2_q,
       not_1_out, not_2_out;

  not not_1 (not_1_out, d_ff_1_q);
  not not_2 (not_2_out, d_ff_2_q);
  D_Flip_Flop #(.trigger("rising"), .Pre_Clr_Positions("LEGACY"), .NegatePresetClear("false"), .enable("true"), .NewFFLayout("false")) d_ff_1 (
    .clk(in_1), .D(not_1_out), .Q(d_ff_1_q));  // open: Qn, preset, en, reset
  D_Flip_Flop #(.trigger("rising"), .Pre_Clr_Positions("LEGACY"), .NegatePresetClear("false"), .enable("true"), .NewFFLayout("false")) d_ff_2 (
    .clk(in_2), .D(not_2_out), .Q(d_ff_2_q));  // open: Qn, preset, en, reset
  Counter #(.width(8), .max('h2), .ongoal("wrap"), .trigger("rising"), .behavior("new")) counter_1 (
    .carry(counter_1_carry), .clk(counter_2_carry));  // open: load, D, count, Q, clr, preset, down
  Counter #(.width(8), .max('h2), .ongoal("wrap"), .trigger("rising"), .behavior("new")) counter_2 (
    .carry(counter_2_carry), .clk(in_3));  // open: load, D, count, Q, clr, preset, down
  and and_1 (and_1_out, ~d_ff_1_q, ~d_ff_2_q);  // AND_Gate
  and and_2 (and_2_out, d_ff_1_q, counter_1_carry);
  and and_3 (and_3_out, in_3, d_ff_2_q);
  and and_4 (and_4_out, and_1_out, counter_2_carry);
  or or_1 (out_4, and_4_out, and_2_out, and_3_out);

  // Notes on the sheet:
  //   倍速控制电路
endmodule
